// Logisim project IDCT.circ as structural Verilog
module HA (
  input  in2___b,
  input  in1___a,
  output out2___sum,
  output out1___cout
);

  wire transistor_3_out, transistor_5_out, transistor_6_out, transistor_13_out;

  Transistor #(.gate("br")) transistor_1 (.in(1'b1), .out(out2___sum), .gate(transistor_3_out));
  Transistor #(.gate("br")) transistor_2 (.in(1'b1), .out(out1___cout), .gate(transistor_6_out));
  Transistor #(.gate("br")) transistor_3 (.in(in2___b), .out(transistor_3_out), .gate(transistor_5_out));
  Transistor #(.gate("br")) transistor_4 (.in(transistor_5_out), .out(transistor_3_out), .gate(in2___b));
  Transistor #(.gate("br")) transistor_5 (.in(1'b1), .out(transistor_5_out), .gate(in1___a));
  Transistor #(.gate("br")) transistor_6 (.in(1'b1), .out(transistor_6_out), .gate(in2___b));
  Transistor #(.gate("br")) transistor_7 (.in(1'b1), .out(transistor_6_out), .gate(in1___a));
  Transistor #(.\type ("n")) transistor_8 (.in(1'b0), .out(out2___sum), .gate(transistor_3_out));
  Transistor #(.\type ("n")) transistor_9 (.in(1'b0), .out(out1___cout), .gate(transistor_6_out));
  Transistor #(.\type ("n")) transistor_10 (.in(in2___b), .out(transistor_3_out), .gate(in1___a));
  Transistor #(.\type ("n")) transistor_11 (.in(in1___a), .out(transistor_3_out), .gate(in2___b));
  Transistor #(.\type ("n")) transistor_12 (.in(1'b0), .out(transistor_5_out), .gate(in1___a));
  Transistor #(.\type ("n")) transistor_13 (.in(1'b0), .out(transistor_13_out), .gate(in2___b));
  Transistor #(.\type ("n")) transistor_14 (.in(transistor_13_out), .out(transistor_6_out), .gate(in1___a));

  // Notes on the sheet:
  //   HALF ADDER
endmodule

module FA (
  input  in3___cin,
  input  in2___b,
  input  in1___a,
  output out2___sum,
  output out1___cout
);

  wire transistor_1_out, transistor_3_out, transistor_6_out, transistor_8_out, transistor_9_out,
       transistor_11_out;

  Transistor #(.gate("br")) transistor_1 (.in(in3___cin), .out(transistor_1_out), .gate(transistor_9_out));
  Transistor #(.gate("br")) transistor_2 (.in(transistor_3_out), .out(transistor_1_out), .gate(transistor_11_out));
  Transistor #(.gate("br")) transistor_3 (.in(1'b1), .out(transistor_3_out), .gate(in3___cin));
  Transistor #(.gate("br")) transistor_4 (.in(1'b1), .out(out2___sum), .gate(transistor_1_out));
  Transistor #(.gate("br")) transistor_5 (.in(1'b1), .out(out1___cout), .gate(transistor_6_out));
  Transistor #(.gate("br")) transistor_6 (.in(transistor_3_out), .out(transistor_6_out), .gate(transistor_9_out));
  Transistor #(.gate("br")) transistor_7 (.in(transistor_8_out), .out(transistor_6_out), .gate(transistor_11_out));
  Transistor #(.gate("br")) transistor_8 (.in(1'b1), .out(transistor_8_out), .gate(in2___b));
  Transistor #(.gate("br")) transistor_9 (.in(transistor_8_out), .out(transistor_9_out), .gate(in1___a));
  Transistor #(.gate("br")) transistor_10 (.in(in1___a), .out(transistor_9_out), .gate(transistor_8_out));
  Transistor #(.gate("br")) transistor_11 (.in(in1___a), .out(transistor_11_out), .gate(in2___b));
  Transistor #(.gate("br")) transistor_12 (.in(in2___b), .out(transistor_11_out), .gate(in1___a));
  Transistor #(.\type ("n")) transistor_13 (.in(in3___cin), .out(transistor_1_out), .gate(transistor_11_out));
  Transistor #(.\type ("n")) transistor_14 (.in(transistor_3_out), .out(transistor_1_out), .gate(transistor_9_out));
  Transistor #(.\type ("n")) transistor_15 (.in(1'b0), .out(transistor_3_out), .gate(in3___cin));
  Transistor #(.\type ("n")) transistor_16 (.in(1'b0), .out(out2___sum), .gate(transistor_1_out));
  Transistor #(.\type ("n")) transistor_17 (.in(1'b0), .out(out1___cout), .gate(transistor_6_out));
  Transistor #(.\type ("n")) transistor_18 (.in(transistor_3_out), .out(transistor_6_out), .gate(transistor_11_out));
  Transistor #(.\type ("n")) transistor_19 (.in(transistor_8_out), .out(transistor_6_out), .gate(transistor_9_out));
  Transistor #(.\type ("n")) transistor_20 (.in(1'b0), .out(transistor_8_out), .gate(in2___b));
  Transistor #(.\type ("n")) transistor_21 (.in(transistor_8_out), .out(transistor_11_out), .gate(in1___a));
  Transistor #(.\type ("n")) transistor_22 (.in(in1___a), .out(transistor_11_out), .gate(transistor_8_out));
  Transistor #(.\type ("n")) transistor_23 (.in(in1___a), .out(transistor_9_out), .gate(in2___b));
  Transistor #(.\type ("n")) transistor_24 (.in(in2___b), .out(transistor_9_out), .gate(in1___a));

  // Notes on the sheet:
  //   FULL ADDER
  //   xor
  //   xnor
endmodule

module CA (
  input  a,
  input  b,
  output out1___sum,
  output out2___cout
);

  wire transistor_3_out, transistor_5_out, transistor_6_out, transistor_7_out;

  Transistor #(.gate("br")) transistor_1 (.in(1'b1), .out(out1___sum), .gate(transistor_3_out));
  Transistor #(.gate("br")) transistor_2 (.in(1'b1), .out(out2___cout), .gate(transistor_7_out));
  Transistor #(.gate("br")) transistor_3 (.in(a), .out(transistor_3_out), .gate(b));
  Transistor #(.gate("br")) transistor_4 (.in(b), .out(transistor_3_out), .gate(a));
  Transistor #(.gate("br")) transistor_5 (.in(1'b1), .out(transistor_5_out), .gate(b));
  Transistor #(.gate("br")) transistor_6 (.in(1'b1), .out(transistor_6_out), .gate(a));
  Transistor #(.gate("br")) transistor_7 (.in(transistor_6_out), .out(transistor_7_out), .gate(b));
  Transistor #(.\type ("n")) transistor_8 (.in(1'b0), .out(out1___sum), .gate(transistor_3_out));
  Transistor #(.\type ("n")) transistor_9 (.in(1'b0), .out(out2___cout), .gate(transistor_7_out));
  Transistor #(.\type ("n")) transistor_10 (.in(a), .out(transistor_3_out), .gate(transistor_5_out));
  Transistor #(.\type ("n")) transistor_11 (.in(transistor_5_out), .out(transistor_3_out), .gate(a));
  Transistor #(.\type ("n")) transistor_12 (.in(1'b0), .out(transistor_5_out), .gate(b));
  Transistor #(.\type ("n")) transistor_13 (.in(1'b0), .out(transistor_7_out), .gate(a));
  Transistor #(.\type ("n")) transistor_14 (.in(1'b0), .out(transistor_7_out), .gate(b));

  // Notes on the sheet:
  //   CARRY ADDER
  //   (full adder with cin = 1)
  //   out1 = XNOR(a,b)
  //   out2 = OR(a,b)
endmodule

module MUX_ARRAY (
  input  C1,
  input  C2,
  input  in,
  input  _01,
  input  _00,
  input  _11,
  input  _10,
  input  _21,
  input  _20,
  input  _31,
  input  _30,
  input  D1,
  input  D2,
  output _02,
  output _12,
  output _22,
  output _32,
  output out
);

  wire transistor_2_out, transistor_5_out, transistor_7_out, transistor_8_out, transistor_9_out,
       transistor_13_out, transistor_14_out, transistor_15_out, transistor_18_out, transistor_21_out,
       transistor_26_out, transistor_29_out, transistor_31_out, transistor_32_out, transistor_33_out,
       transistor_37_out, transistor_38_out, transistor_40_out, transistor_43_out, transistor_45_out,
       transistor_49_out;

  Transistor #(.gate("br")) transistor_1 (.in(transistor_7_out), .out(_02), .gate(transistor_9_out));
  Transistor #(.gate("br")) transistor_2 (.in(1'b1), .out(transistor_2_out), .gate(in));
  Transistor #(.gate("br")) transistor_3 (.in(transistor_2_out), .out(_02), .gate(D1));
  Transistor #(.\type ("n")) transistor_4 (.in(transistor_5_out), .out(_02), .gate(D2));
  Transistor #(.\type ("n")) transistor_5 (.in(1'b0), .out(transistor_5_out), .gate(in));
  Transistor #(.\type ("n")) transistor_6 (.in(transistor_8_out), .out(_02), .gate(D1));
  Transistor #(.gate("br")) transistor_7 (.in(1'b1), .out(transistor_7_out), .gate(D2));
  Transistor #(.\type ("n")) transistor_8 (.in(1'b0), .out(transistor_8_out), .gate(transistor_9_out));
  Transistor #(.gate("br")) transistor_9 (.in(_01), .out(transistor_9_out), .gate(C1));
  Transistor #(.gate("br")) transistor_10 (.in(_00), .out(transistor_9_out), .gate(C2));
  Transistor #(.\type ("n")) transistor_11 (.in(_01), .out(transistor_9_out), .gate(C2));
  Transistor #(.\type ("n")) transistor_12 (.in(_00), .out(transistor_9_out), .gate(C1));
  Transistor #(.gate("br")) transistor_13 (.in(1'b1), .out(transistor_13_out), .gate(transistor_9_out));
  Transistor #(.\type ("n")) transistor_14 (.in(1'b0), .out(transistor_14_out), .gate(transistor_9_out));
  Transistor #(.gate("br")) transistor_15 (.in(1'b1), .out(transistor_15_out), .gate(D2));
  Transistor #(.gate("br")) transistor_16 (.in(transistor_13_out), .out(_12), .gate(D1));
  Transistor #(.gate("br")) transistor_17 (.in(transistor_15_out), .out(_12), .gate(transistor_21_out));
  Transistor #(.\type ("n")) transistor_18 (.in(1'b0), .out(transistor_18_out), .gate(transistor_21_out));
  Transistor #(.\type ("n")) transistor_19 (.in(transistor_18_out), .out(_12), .gate(D1));
  Transistor #(.\type ("n")) transistor_20 (.in(transistor_14_out), .out(_12), .gate(D2));
  Transistor #(.gate("br")) transistor_21 (.in(_11), .out(transistor_21_out), .gate(C1));
  Transistor #(.gate("br")) transistor_22 (.in(_10), .out(transistor_21_out), .gate(C2));
  Transistor #(.\type ("n")) transistor_23 (.in(_11), .out(transistor_21_out), .gate(C2));
  Transistor #(.\type ("n")) transistor_24 (.in(_10), .out(transistor_21_out), .gate(C1));
  Transistor #(.gate("br")) transistor_25 (.in(transistor_31_out), .out(_22), .gate(transistor_33_out));
  Transistor #(.gate("br")) transistor_26 (.in(1'b1), .out(transistor_26_out), .gate(transistor_21_out));
  Transistor #(.gate("br")) transistor_27 (.in(transistor_26_out), .out(_22), .gate(D1));
  Transistor #(.\type ("n")) transistor_28 (.in(transistor_32_out), .out(_22), .gate(D1));
  Transistor #(.\type ("n")) transistor_29 (.in(1'b0), .out(transistor_29_out), .gate(transistor_21_out));
  Transistor #(.\type ("n")) transistor_30 (.in(transistor_29_out), .out(_22), .gate(D2));
  Transistor #(.gate("br")) transistor_31 (.in(1'b1), .out(transistor_31_out), .gate(D2));
  Transistor #(.\type ("n")) transistor_32 (.in(1'b0), .out(transistor_32_out), .gate(transistor_33_out));
  Transistor #(.gate("br")) transistor_33 (.in(_21), .out(transistor_33_out), .gate(C1));
  Transistor #(.gate("br")) transistor_34 (.in(_20), .out(transistor_33_out), .gate(C2));
  Transistor #(.\type ("n")) transistor_35 (.in(_21), .out(transistor_33_out), .gate(C2));
  Transistor #(.\type ("n")) transistor_36 (.in(_20), .out(transistor_33_out), .gate(C1));
  Transistor #(.gate("br")) transistor_37 (.in(1'b1), .out(transistor_37_out), .gate(transistor_33_out));
  Transistor #(.\type ("n")) transistor_38 (.in(1'b0), .out(transistor_38_out), .gate(transistor_33_out));
  Transistor #(.gate("br")) transistor_39 (.in(transistor_37_out), .out(_32), .gate(D1));
  Transistor #(.gate("br")) transistor_40 (.in(1'b1), .out(transistor_40_out), .gate(D2));
  Transistor #(.gate("br")) transistor_41 (.in(transistor_40_out), .out(_32), .gate(transistor_45_out));
  Transistor #(.\type ("n")) transistor_42 (.in(transistor_38_out), .out(_32), .gate(D2));
  Transistor #(.\type ("n")) transistor_43 (.in(1'b0), .out(transistor_43_out), .gate(transistor_45_out));
  Transistor #(.\type ("n")) transistor_44 (.in(transistor_43_out), .out(_32), .gate(D1));
  Transistor #(.gate("br")) transistor_45 (.in(_30), .out(transistor_45_out), .gate(C2));
  Transistor #(.gate("br")) transistor_46 (.in(_31), .out(transistor_45_out), .gate(C1));
  Transistor #(.\type ("n")) transistor_47 (.in(_31), .out(transistor_45_out), .gate(C2));
  Transistor #(.\type ("n")) transistor_48 (.in(_30), .out(transistor_45_out), .gate(C1));
  Transistor #(.gate("br")) transistor_49 (.in(1'b1), .out(transistor_49_out), .gate(transistor_45_out));
  Transistor #(.\type ("n")) transistor_50 (.in(1'b0), .out(transistor_49_out), .gate(transistor_45_out));
  Transistor #(.gate("br")) transistor_51 (.in(1'b1), .out(out), .gate(transistor_49_out));
  Transistor #(.\type ("n")) transistor_52 (.in(1'b0), .out(out), .gate(transistor_49_out));

  // Notes on the sheet:
  //   MUX ARRAY
endmodule

module MUX_ARRAY_LOGIC (
  input  C1,
  input  D1,
  input  in,
  input  _01,
  input  _00,
  input  _11,
  input  _10,
  input  _21,
  input  _20,
  input  _31,
  input  _30,
  output _02,
  output _12,
  output _22,
  output _32,
  output out
);

  wire multiplexer_1_out, multiplexer_2_out, multiplexer_3_out, multiplexer_5_out, multiplexer_6_out,
       multiplexer_7_out, multiplexer_8_out;

  Multiplexer multiplexer_1 (.in0(_01), .in1(_00), .out(multiplexer_1_out), .sel(C1));  // open: en
  Multiplexer multiplexer_2 (.in0(_11), .in1(_10), .out(multiplexer_2_out), .sel(C1));  // open: en
  Multiplexer multiplexer_3 (.in0(_21), .in1(_20), .out(multiplexer_3_out), .sel(C1));  // open: en
  Multiplexer multiplexer_4 (.in0(_31), .in1(_30), .out(out), .sel(C1));  // open: en
  Multiplexer multiplexer_5 (.in0(in), .in1(multiplexer_1_out), .out(multiplexer_5_out), .sel(D1));  // open: en
  Multiplexer multiplexer_6 (
    .in0(multiplexer_1_out), .in1(multiplexer_2_out), .out(multiplexer_6_out), .sel(D1));  // open: en
  Multiplexer multiplexer_7 (
    .in0(multiplexer_2_out), .in1(multiplexer_3_out), .out(multiplexer_7_out), .sel(D1));  // open: en
  Multiplexer multiplexer_8 (.in0(multiplexer_3_out), .in1(out), .out(multiplexer_8_out), .sel(D1));  // open: en
  not not_1 (_02, multiplexer_5_out);
  not not_2 (_12, multiplexer_6_out);
  not not_3 (_22, multiplexer_7_out);
  not not_4 (_32, multiplexer_8_out);

  // Notes on the sheet:
  //   MUX ARRAY
endmodule

module WS1 (
  input  in5,
  input  in4,
  input  in3,
  input  in2,
  input  in1,
  output out2,
  output out3,
  output out1
);

  wire transistor_1_out, transistor_3_out, transistor_5_out, transistor_6_out, transistor_9_out,
       transistor_11_out, transistor_13_out, transistor_15_out, transistor_19_out, transistor_23_out,
       transistor_27_out, transistor_39_out, transistor_43_out;

  Transistor #(.gate("br")) transistor_1 (.in(1'b1), .out(transistor_1_out), .gate(transistor_3_out));
  Transistor #(.\type ("n")) transistor_2 (.in(1'b0), .out(transistor_1_out), .gate(transistor_3_out));
  Transistor #(.gate("br")) transistor_3 (.in(1'b1), .out(transistor_3_out), .gate(in5));
  Transistor #(.\type ("n")) transistor_4 (.in(1'b0), .out(transistor_3_out), .gate(in5));
  Transistor #(.gate("br")) transistor_5 (.in(in4), .out(transistor_5_out), .gate(transistor_3_out));
  Transistor #(.gate("br")) transistor_6 (.in(1'b1), .out(transistor_6_out), .gate(in4));
  Transistor #(.gate("br")) transistor_7 (.in(transistor_6_out), .out(transistor_5_out), .gate(in5));
  Transistor #(.\type ("n")) transistor_8 (.in(in4), .out(transistor_5_out), .gate(in5));
  Transistor #(.\type ("n")) transistor_9 (.in(1'b0), .out(transistor_9_out), .gate(in4));
  Transistor #(.\type ("n")) transistor_10 (.in(transistor_9_out), .out(transistor_5_out), .gate(transistor_3_out));
  Transistor #(.gate("br")) transistor_11 (.in(1'b1), .out(transistor_11_out), .gate(transistor_5_out));
  Transistor #(.\type ("n")) transistor_12 (.in(1'b0), .out(transistor_11_out), .gate(transistor_5_out));
  Transistor #(.gate("br")) transistor_13 (.in(1'b1), .out(transistor_13_out), .gate(transistor_11_out));
  Transistor #(.\type ("n")) transistor_14 (.in(1'b0), .out(transistor_13_out), .gate(transistor_11_out));
  Transistor transistor_15 (.in(in3), .out(transistor_15_out), .gate(transistor_13_out));
  Transistor #(.gate("br")) transistor_16 (.in(transistor_13_out), .out(transistor_15_out), .gate(in3));
  Transistor #(.\type ("n")) transistor_17 (.in(transistor_11_out), .out(transistor_15_out), .gate(in3));
  Transistor #(.\type ("n"), .gate("br")) transistor_18 (.in(in3), .out(transistor_15_out), .gate(transistor_11_out));
  Transistor #(.gate("br")) transistor_19 (.in(transistor_1_out), .out(transistor_19_out), .gate(transistor_11_out));
  Transistor #(.gate("br")) transistor_20 (.in(in3), .out(transistor_19_out), .gate(transistor_5_out));
  Transistor #(.\type ("n")) transistor_21 (.in(in3), .out(transistor_19_out), .gate(transistor_11_out));
  Transistor #(.\type ("n")) transistor_22 (.in(transistor_1_out), .out(transistor_19_out), .gate(transistor_5_out));
  Transistor #(.gate("br")) transistor_23 (.in(in2), .out(transistor_23_out), .gate(transistor_5_out));
  Transistor #(.gate("br")) transistor_24 (.in(transistor_1_out), .out(transistor_23_out), .gate(transistor_11_out));
  Transistor #(.\type ("n")) transistor_25 (.in(transistor_1_out), .out(transistor_23_out), .gate(transistor_5_out));
  Transistor #(.\type ("n")) transistor_26 (.in(in2), .out(transistor_23_out), .gate(transistor_11_out));
  Transistor #(.gate("br")) transistor_27 (.in(transistor_13_out), .out(transistor_27_out), .gate(in2));
  Transistor transistor_28 (.in(in2), .out(transistor_27_out), .gate(transistor_13_out));
  Transistor #(.\type ("n"), .gate("br")) transistor_29 (.in(in2), .out(transistor_27_out), .gate(transistor_11_out));
  Transistor #(.\type ("n")) transistor_30 (.in(transistor_11_out), .out(transistor_27_out), .gate(in2));
  Transistor #(.gate("br")) transistor_31 (.in(1'b1), .out(out2), .gate(transistor_23_out));
  Transistor #(.gate("br")) transistor_32 (.in(1'b1), .out(out2), .gate(transistor_23_out));
  Transistor #(.\type ("n")) transistor_33 (.in(1'b0), .out(out2), .gate(transistor_23_out));
  Transistor #(.\type ("n")) transistor_34 (.in(1'b0), .out(out2), .gate(transistor_23_out));
  Transistor #(.gate("br")) transistor_35 (.in(1'b1), .out(out3), .gate(transistor_19_out));
  Transistor #(.gate("br")) transistor_36 (.in(1'b1), .out(out3), .gate(transistor_19_out));
  Transistor #(.\type ("n")) transistor_37 (.in(1'b0), .out(out3), .gate(transistor_19_out));
  Transistor #(.\type ("n")) transistor_38 (.in(1'b0), .out(out3), .gate(transistor_19_out));
  Transistor #(.gate("br")) transistor_39 (.in(transistor_15_out), .out(transistor_39_out), .gate(transistor_43_out));
  Transistor #(.gate("br")) transistor_40 (.in(transistor_27_out), .out(transistor_39_out), .gate(in1));
  Transistor #(.\type ("n")) transistor_41 (.in(transistor_27_out), .out(transistor_39_out), .gate(transistor_43_out));
  Transistor #(.\type ("n")) transistor_42 (.in(transistor_15_out), .out(transistor_39_out), .gate(in1));
  Transistor #(.gate("br")) transistor_43 (.in(1'b1), .out(transistor_43_out), .gate(in1));
  Transistor #(.\type ("n")) transistor_44 (.in(1'b0), .out(transistor_43_out), .gate(in1));
  Transistor #(.gate("br")) transistor_45 (.in(1'b1), .out(out1), .gate(transistor_39_out));
  Transistor #(.gate("br")) transistor_46 (.in(1'b1), .out(out1), .gate(transistor_39_out));
  Transistor #(.\type ("n")) transistor_47 (.in(1'b0), .out(out1), .gate(transistor_39_out));
  Transistor #(.\type ("n")) transistor_48 (.in(1'b0), .out(out1), .gate(transistor_39_out));

  // Notes on the sheet:
  //   in5'
  //   XNOR
  //   x
  //   !x
  //   x2
  //   s1
  //   s0
endmodule

module WS2 (
  input  in5,
  input  in4,
  input  in3,
  input  in2,
  input  in1,
  output out2,
  output out3,
  output out1
);

  wire transistor_1_out, transistor_3_out, transistor_5_out, transistor_6_out, transistor_7_out,
       transistor_11_out, transistor_13_out, transistor_15_out, transistor_19_out, transistor_23_out,
       transistor_27_out, transistor_39_out, transistor_43_out;

  Transistor #(.gate("br")) transistor_1 (.in(1'b1), .out(transistor_1_out), .gate(in5));
  Transistor #(.\type ("n")) transistor_2 (.in(1'b0), .out(transistor_1_out), .gate(in5));
  Transistor #(.gate("br")) transistor_3 (.in(1'b1), .out(transistor_3_out), .gate(in5));
  Transistor #(.\type ("n")) transistor_4 (.in(1'b0), .out(transistor_3_out), .gate(in5));
  Transistor #(.gate("br")) transistor_5 (.in(1'b1), .out(transistor_5_out), .gate(in4));
  Transistor #(.\type ("n")) transistor_6 (.in(1'b0), .out(transistor_6_out), .gate(in4));
  Transistor #(.gate("br")) transistor_7 (.in(transistor_5_out), .out(transistor_7_out), .gate(in5));
  Transistor #(.gate("br")) transistor_8 (.in(in4), .out(transistor_7_out), .gate(transistor_3_out));
  Transistor #(.\type ("n")) transistor_9 (.in(transistor_6_out), .out(transistor_7_out), .gate(transistor_3_out));
  Transistor #(.\type ("n")) transistor_10 (.in(in4), .out(transistor_7_out), .gate(in5));
  Transistor #(.gate("br")) transistor_11 (.in(1'b1), .out(transistor_11_out), .gate(transistor_7_out));
  Transistor #(.\type ("n")) transistor_12 (.in(1'b0), .out(transistor_11_out), .gate(transistor_7_out));
  Transistor #(.gate("br")) transistor_13 (.in(1'b1), .out(transistor_13_out), .gate(transistor_11_out));
  Transistor #(.\type ("n")) transistor_14 (.in(1'b0), .out(transistor_13_out), .gate(transistor_11_out));
  Transistor #(.gate("br")) transistor_15 (.in(transistor_11_out), .out(transistor_15_out), .gate(in3));
  Transistor #(.\type ("n")) transistor_16 (.in(transistor_13_out), .out(transistor_15_out), .gate(in3));
  Transistor #(.gate("br")) transistor_17 (.in(in3), .out(transistor_15_out), .gate(transistor_11_out));
  Transistor #(.\type ("n")) transistor_18 (.in(in3), .out(transistor_15_out), .gate(transistor_13_out));
  Transistor #(.gate("br")) transistor_19 (.in(transistor_1_out), .out(transistor_19_out), .gate(transistor_11_out));
  Transistor #(.gate("br")) transistor_20 (.in(in3), .out(transistor_19_out), .gate(transistor_7_out));
  Transistor #(.\type ("n")) transistor_21 (.in(in3), .out(transistor_19_out), .gate(transistor_11_out));
  Transistor #(.\type ("n")) transistor_22 (.in(transistor_1_out), .out(transistor_19_out), .gate(transistor_7_out));
  Transistor #(.gate("br")) transistor_23 (.in(transistor_1_out), .out(transistor_23_out), .gate(transistor_11_out));
  Transistor #(.gate("br")) transistor_24 (.in(in2), .out(transistor_23_out), .gate(transistor_7_out));
  Transistor #(.\type ("n")) transistor_25 (.in(in2), .out(transistor_23_out), .gate(transistor_11_out));
  Transistor #(.\type ("n")) transistor_26 (.in(transistor_1_out), .out(transistor_23_out), .gate(transistor_7_out));
  Transistor #(.gate("br")) transistor_27 (.in(transistor_11_out), .out(transistor_27_out), .gate(in2));
  Transistor #(.gate("br")) transistor_28 (.in(in2), .out(transistor_27_out), .gate(transistor_11_out));
  Transistor #(.\type ("n")) transistor_29 (.in(transistor_13_out), .out(transistor_27_out), .gate(in2));
  Transistor #(.\type ("n")) transistor_30 (.in(in2), .out(transistor_27_out), .gate(transistor_13_out));
  Transistor #(.gate("br")) transistor_31 (.in(1'b1), .out(out2), .gate(transistor_23_out));
  Transistor #(.gate("br")) transistor_32 (.in(1'b1), .out(out2), .gate(transistor_23_out));
  Transistor #(.\type ("n")) transistor_33 (.in(1'b0), .out(out2), .gate(transistor_23_out));
  Transistor #(.\type ("n")) transistor_34 (.in(1'b0), .out(out2), .gate(transistor_23_out));
  Transistor #(.gate("br")) transistor_35 (.in(1'b1), .out(out3), .gate(transistor_19_out));
  Transistor #(.gate("br")) transistor_36 (.in(1'b1), .out(out3), .gate(transistor_19_out));
  Transistor #(.\type ("n")) transistor_37 (.in(1'b0), .out(out3), .gate(transistor_19_out));
  Transistor #(.\type ("n")) transistor_38 (.in(1'b0), .out(out3), .gate(transistor_19_out));
  Transistor #(.gate("br")) transistor_39 (.in(transistor_27_out), .out(transistor_39_out), .gate(in1));
  Transistor #(.gate("br")) transistor_40 (.in(transistor_15_out), .out(transistor_39_out), .gate(transistor_43_out));
  Transistor #(.\type ("n")) transistor_41 (.in(transistor_15_out), .out(transistor_39_out), .gate(in1));
  Transistor #(.\type ("n")) transistor_42 (.in(transistor_27_out), .out(transistor_39_out), .gate(transistor_43_out));
  Transistor #(.gate("br")) transistor_43 (.in(1'b1), .out(transistor_43_out), .gate(in1));
  Transistor #(.\type ("n")) transistor_44 (.in(1'b0), .out(transistor_43_out), .gate(in1));
  Transistor #(.gate("br")) transistor_45 (.in(1'b1), .out(out1), .gate(transistor_39_out));
  Transistor #(.gate("br")) transistor_46 (.in(1'b1), .out(out1), .gate(transistor_39_out));
  Transistor #(.\type ("n")) transistor_47 (.in(1'b0), .out(out1), .gate(transistor_39_out));
  Transistor #(.\type ("n")) transistor_48 (.in(1'b0), .out(out1), .gate(transistor_39_out));

  // Notes on the sheet:
  //   !in5'
  //   XNOR
  //   x
  //   !x
  //   x2
  //   s1
  //   s0
endmodule

module IMUX (
  input  sel,
  input  b___in0,
  input  c___in1,
  output out
);

  wire transistor_2_out, transistor_3_out;

  Transistor #(.gate("br")) transistor_1 (.in(1'b1), .out(out), .gate(transistor_3_out));
  Transistor #(.gate("br")) transistor_2 (.in(1'b1), .out(transistor_2_out), .gate(sel));
  Transistor #(.gate("br")) transistor_3 (.in(b___in0), .out(transistor_3_out), .gate(sel));
  Transistor #(.gate("br")) transistor_4 (.in(c___in1), .out(transistor_3_out), .gate(transistor_2_out));
  Transistor #(.\type ("n")) transistor_5 (.in(1'b0), .out(out), .gate(transistor_3_out));
  Transistor #(.\type ("n")) transistor_6 (.in(1'b0), .out(transistor_2_out), .gate(sel));
  Transistor #(.\type ("n")) transistor_7 (.in(b___in0), .out(transistor_3_out), .gate(transistor_2_out));
  Transistor #(.\type ("n")) transistor_8 (.in(c___in1), .out(transistor_3_out), .gate(sel));

  // Notes on the sheet:
  //   INVERTING MUX
endmodule

module _12_OAI (
  input  a,
  input  b,
  input  c,
  output out
);

  wire transistor_3_out, transistor_5_out;

  Transistor #(.gate("br")) transistor_1 (.in(1'b1), .out(out), .gate(a));
  Transistor #(.gate("br")) transistor_2 (.in(transistor_3_out), .out(out), .gate(b));
  Transistor #(.gate("br")) transistor_3 (.in(1'b1), .out(transistor_3_out), .gate(c));
  Transistor #(.\type ("n")) transistor_4 (.in(transistor_5_out), .out(out), .gate(a));
  Transistor #(.\type ("n")) transistor_5 (.in(1'b0), .out(transistor_5_out), .gate(b));
  Transistor #(.\type ("n")) transistor_6 (.in(1'b0), .out(transistor_5_out), .gate(c));

  // Notes on the sheet:
  //   12-OAI
  //   out = ~ (a & (b|c))
endmodule
