// Logisim project 004.circ as structural Verilog: 7 circuits, main circuit main
module main (
  input  in1,
  input  in2,
  input  in3,
  input  in4,
  input  in5,
  input  in6,
  input  in7,
  input  in8,
  input  in9,
  input  in10
);

  wire _104_out, not_1_out, not_2_out, not_3_out, not_4_out, not_5_out, not_6_out, not_7_out, not_8_out,
       not_9_out, not_10_out;

  // OR_Gate _212 has open pins: in0=in1, out=open
  not not_1 (not_1_out, in1);
  buf _104 (_104_out, not_1_out);  // OR_Gate
  // OR_Gate _011 has open pins: in0=in2, out=open
  not not_2 (not_2_out, in2);
  // OR_Gate _211 has open pins: in0=not_2_out, out=open
  // NAND_Gate _215 has open pins: in0=in3, out=open
  not not_3 (not_3_out, in3);
  // NAND_Gate _009 has open pins: in0=not_3_out, in1=not_5_out, out=open
  not not_4 (not_4_out, in4);
  not not_5 (not_5_out, in5);
  not not_6 (not_6_out, in6);
  not not_7 (not_7_out, in7);
  not not_8 (not_8_out, in8);
  not not_9 (not_9_out, in9);
  not not_10 (not_10_out, in10);
  // Buffer _103 has open pins: in=_104_out, out=open
  // NAND_Gate _105 has open pins: in0=not_3_out, in1=not_5_out, out=open
  // OR_Gate _208 has open pins: in0=in1, out=open
  // OR_Gate _106 has open pins: in0=not_1_out, out=open
  // OR_Gate _012 has open pins: in0=in2, out=open
  // NAND_Gate _421 has open pins: in0=not_2_out, out=open
  // NAND_Gate _423 has open pins: in0=in3, out=open
  // NAND_Gate _302 has open pins: in0=in4, out=open
  // NAND_Gate _503 has open pins: in0=not_4_out, out=open
  // OR_Gate _316 has open pins: in0=in1, out=open
  // NAND_Gate _116 has open pins: in0=not_1_out, in1=not_5_out, out=open
  // OR_Gate _310 has open pins: in0=in2, out=open
  // OR_Gate _710 has open pins: in0=not_2_out, out=open
  // NAND_Gate _428 has open pins: in0=in3, out=open
  NAND_XOR nand_xor_1 (.d(not_3_out));  // open: a, b, c, out
  // NAND_Gate _404 has open pins: in0=in4, out=open
  // NAND_Gate _414 has open pins: in0=not_4_out, out=open
  // OR_Gate _305 has open pins: in0=not_5_out, out=open
  NAND_NOR nand_nor_1 (.a(in1));  // open: out_5, b, c, d
  // NAND_Gate _425 has open pins: in0=not_1_out, out=open
  // OR_Gate _016 has open pins: in0=in2, out=open
  _12_OAI u_12_oai_1 (.a(not_2_out));  // open: out, b, c
  // OR_Gate _433 has open pins: in0=in3, out=open
  // OR_Gate _321 has open pins: in0=not_3_out, out=open
  // NAND_Gate _502 has open pins: in0=in4, out=open
  // NAND_Gate _424 has open pins: in0=not_4_out, out=open
  // OR_Gate _306 has open pins: in0=not_5_out, out=open
  // NAND_Gate _463 has open pins: in0=not_1_out, out=open
  // OR_Gate _315 has open pins: in0=in2, out=open
  // OR_Gate _232 has open pins: in0=not_2_out, out=open
  // OR_Gate _336 has open pins: in0=in3, out=open
  _22_OAI u_22_oai_1 (.a(not_3_out));  // open: b, c, d, out
  // OR_Gate _216 has open pins: in0=in4, out=open
  // OR_Gate _048 has open pins: in0=not_1_out, out=open
  // OR_Gate _609 has open pins: in0=in2, out=open
  // OR_Gate _713 has open pins: in0=not_2_out, out=open
  NOR_NAND _633 (.d(in3));  // open: a, b, c, out_5
  // OR_Gate _221 has open pins: in0=in4, out=open
  _22_OAI _516 (.d(not_4_out));  // open: a, b, c, out
  // OR_Gate _320 has open pins: in0=not_5_out, out=open
  _22_OAI _515 (.b(in1), .c(in3));  // open: a, d, out
  // NAND_Gate _537 has open pins: in0=not_3_out, out=open
  // NOR_Gate _142 has open pins: in0=not_5_out, out=open
  // OR_Gate _226 has open pins: in0=in4, out=open
  _12_OAI _355 (.c(not_5_out));  // open: out, a, b
  // NAND_Gate _608 has open pins: in0=in1, in1=not_3_out, out=open
  // OR_Gate _610 has open pins: in0=not_4_out, out=open
  NOR_NAND nor_nand_1 (.d(in1));  // open: a, b, c, out_5
  // OR_Gate _554 has open pins: in0=not_1_out, out=open
  // NAND_Gate _614 has open pins: in0=in2, in1=not_4_out, out=open
  // NAND_Gate _717 has open pins: in0=not_2_out, out=open
  // OR_Gate _462 has open pins: in0=in3, out=open
  // NAND_Gate _722 has open pins: in0=not_3_out, out=open
  // NAND_Gate _525 has open pins: in0=in4, out=open
  // OR_Gate _619 has open pins: in0=not_4_out, out=open
  // OR_Gate _461 has open pins: in0=not_5_out, out=open
  _12_OAI u_12_oai_2 (.a(not_1_out));  // open: out, b, c
  _12_OAI u_12_oai_3 (.a(in2));  // open: out, b, c
  // NAND_Gate _720 has open pins: in0=not_2_out, in1=not_3_out, out=open
  _12_OAI _723 (.c(not_5_out));  // open: out, a, b
  // NAND_Gate _432 has open pins: in0=in1, out=open
  // NOR_Gate _448 has open pins: in0=not_1_out, out=open
  // OR_Gate _328 has open pins: in0=in2, out=open
  // OR_Gate _437 has open pins: in0=in4, out=open
  // NOR_Gate _549 has open pins: in0=not_4_out, out=open
  _12_OAI u_12_oai_4 (.a(in1));  // open: out, b, c
  // OR_Gate _029 has open pins: in0=not_1_out, out=open
  // NOR_Gate _632 has open pins: in0=in2, out=open
  // NAND_Gate _647 has open pins: in0=not_2_out, in1=in3, out=open
  // NAND_Gate _261 has open pins: in0=in3, out=open
  // OR_Gate _556 has open pins: in0=not_3_out, out=open
  // OR_Gate _335 has open pins: in0=in4, out=open
  // NOR_Gate _453 has open pins: in0=not_4_out, out=open
  // OR_Gate _712 has open pins: in0=not_5_out, out=open
  // OR_Gate _627 has open pins: in0=in1, out=open
  _12_OAI u_12_oai_5 (.a(in1));  // open: out, b, c
  // OR_Gate _112 has open pins: in0=not_1_out, out=open
  // OR_Gate _050 has open pins: in0=not_2_out, out=open
  // OR_Gate _356 has open pins: in0=not_3_out, out=open
  // NOR_Gate _643 has open pins: in0=not_5_out, out=open
  // OR_Gate _219 has open pins: in0=not_1_out, out=open
  // NAND_Gate _649 has open pins: in0=in2, in1=in3, out=open
  // OR_Gate _445 has open pins: in0=in4, out=open
  // NAND_Gate _015 has open pins: in0=not_1_out, in1=not_5_out, out=open
  // OR_Gate _044 has open pins: in0=not_2_out, out=open
  // NOR_Gate _456 has open pins: in0=in1, out=open
  NOR_AND nor_and_1 (.b(in2), .c(in2));  // open: out_5, a, d
  _12_OAI u_12_oai_6 (.c(in2));  // open: out, a, b
  // OR_Gate _716 has open pins: in0=in4, out=open
  // NAND_Gate _347 has open pins: in0=not_4_out, out=open
  // OR_Gate _638 has open pins: in0=not_5_out, out=open
  NOR_AND nor_and_2 (.a(in1), .c(in1));  // open: out_5, b, d
  // OR_Gate _307 has open pins: in0=not_1_out, out=open
  // OR_Gate _141 has open pins: in0=not_2_out, out=open
  NOR_NAND _346 (.d(in4));  // open: a, b, c, out_5
  // NAND_Gate _513 has open pins: in0=not_1_out, out=open
  // NOR_Gate _247 has open pins: in0=in2, out=open
  // NOR_Gate _628 has open pins: in0=not_2_out, out=open
  // OR_Gate _539 has open pins: in0=not_4_out, out=open
  // NAND_Gate _352 has open pins: in0=in1, in1=in3, out=open
  // NAND_Gate _518 has open pins: in0=not_1_out, in1=in3, out=open
  // OR_Gate _256 has open pins: in0=in4, out=open
  // NAND_Gate _237 has open pins: in0=in2, in1=not_5_out, out=open
  // NAND_Gate _342 has open pins: in0=in2, out=open
  // OR_Gate _148 has open pins: in0=in4, out=open
  // OR_Gate _637 has open pins: in0=in4, out=open

  // Notes on the sheet:
  //   x14
  //   x17
  //   x16
  //   x13
  //   x8
  //   x9
  //   x15
  //   x10
  //   x10
endmodule

module _12_OAI (
  input  a,
  input  b,
  input  c,
  output out
);

  wire transistor_3_out, transistor_5_out;

  Transistor #(.gate("br")) transistor_1 (.in(1'b1), .out(out), .gate(a));
  Transistor #(.gate("br")) transistor_2 (.in(transistor_3_out), .out(out), .gate(b));
  Transistor #(.gate("br")) transistor_3 (.in(1'b1), .out(transistor_3_out), .gate(c));
  Transistor #(.\type ("n")) transistor_4 (.in(transistor_5_out), .out(out), .gate(a));
  Transistor #(.\type ("n")) transistor_5 (.in(1'b0), .out(transistor_5_out), .gate(b));
  Transistor #(.\type ("n")) transistor_6 (.in(1'b0), .out(transistor_5_out), .gate(c));
endmodule

module NAND_NOR (
  input  a,
  input  b,
  input  c,
  input  d,
  output out_5
);

  wire transistor_3_out, transistor_5_out, transistor_6_out;

  Transistor #(.gate("br")) transistor_1 (.in(1'b1), .out(out_5), .gate(a));
  Transistor #(.gate("br")) transistor_2 (.in(1'b1), .out(out_5), .gate(b));
  Transistor #(.gate("br")) transistor_3 (.in(1'b1), .out(transistor_3_out), .gate(c));
  Transistor #(.gate("br")) transistor_4 (.in(transistor_3_out), .out(out_5), .gate(d));
  Transistor #(.\type ("n")) transistor_5 (.in(1'b0), .out(transistor_5_out), .gate(a));
  Transistor #(.\type ("n")) transistor_6 (.in(transistor_5_out), .out(transistor_6_out), .gate(b));
  Transistor #(.\type ("n")) transistor_7 (.in(transistor_6_out), .out(out_5), .gate(c));
  Transistor #(.\type ("n")) transistor_8 (.in(transistor_6_out), .out(out_5), .gate(d));

  // Notes on the sheet:
  //   NAND
  //   NOR
  //   out = NAND(a,b) | NOR(c,d)
endmodule

module _22_OAI (
  input  a,
  input  b,
  input  c,
  input  d,
  output out
);

  wire transistor_1_out, transistor_4_out, transistor_7_out;

  Transistor #(.gate("br")) transistor_1 (.in(1'b1), .out(transistor_1_out), .gate(a));
  Transistor #(.gate("br")) transistor_2 (.in(transistor_1_out), .out(out), .gate(b));
  Transistor #(.gate("br")) transistor_3 (.in(transistor_4_out), .out(out), .gate(c));
  Transistor #(.gate("br")) transistor_4 (.in(1'b1), .out(transistor_4_out), .gate(d));
  Transistor #(.\type ("n")) transistor_5 (.in(transistor_7_out), .out(out), .gate(a));
  Transistor #(.\type ("n")) transistor_6 (.in(transistor_7_out), .out(out), .gate(b));
  Transistor #(.\type ("n")) transistor_7 (.in(1'b0), .out(transistor_7_out), .gate(c));
  Transistor #(.\type ("n")) transistor_8 (.in(1'b0), .out(transistor_7_out), .gate(d));

  // Notes on the sheet:
  //   out = NAND(a|b, c|d)
endmodule

module NOR_NAND (
  input  a,
  input  b,
  input  c,
  input  d,
  output out_5
);

  wire nand_1_out, nor_1_out;

  nor nor_1 (nor_1_out, a, b);
  nand nand_1 (nand_1_out, c, d);
  and and_1 (out_5, nor_1_out, nand_1_out);
endmodule

module NOR_AND (
  input  a,
  input  b,
  input  c,
  input  d,
  output out_5
);

  wire and_1_out, nor_1_out;

  and and_1 (and_1_out, c, d);
  nor nor_1 (nor_1_out, a, b);
  or or_1 (out_5, nor_1_out, and_1_out);
endmodule

module NAND_XOR (
  input  a,
  input  b,
  input  c,
  input  d,
  output out
);

  wire nand_1_out, xor_1_out;

  nand nand_1 (nand_1_out, a, b);
  xor xor_1 (xor_1_out, c, d);
  and and_1 (out, nand_1_out, xor_1_out);
endmodule
