// Logisim project 4-MUX.circ as structural Verilog: 1 circuit, main circuit 4-MUX
module _4_MUX (
  input  s1,
  input  _3,
  input  _2,
  input  _1,
  input  _0,
  input  s0,
  output out
);

  wire transistor_2_out, transistor_3_out, transistor_5_out, transistor_6_out, transistor_8_out,
       transistor_9_out, transistor_10_out, transistor_12_out, transistor_13_out, transistor_18_out,
       transistor_21_out, transistor_22_out, transistor_25_out;

  Transistor #(.gate("br")) transistor_1 (.in(1'b1), .out(out), .gate(transistor_3_out));
  Transistor #(.gate("br")) transistor_2 (.in(1'b1), .out(transistor_2_out), .gate(s1));
  Transistor #(.gate("br")) transistor_3 (.in(transistor_6_out), .out(transistor_3_out), .gate(transistor_2_out));
  Transistor #(.gate("br")) transistor_4 (.in(transistor_10_out), .out(transistor_3_out), .gate(s1));
  Transistor #(.gate("br")) transistor_5 (.in(1'b1), .out(transistor_5_out), .gate(_3));
  Transistor #(.gate("br")) transistor_6 (.in(transistor_5_out), .out(transistor_6_out), .gate(transistor_13_out));
  Transistor #(.gate("br")) transistor_7 (.in(transistor_8_out), .out(transistor_6_out), .gate(s0));
  Transistor #(.gate("br")) transistor_8 (.in(1'b1), .out(transistor_8_out), .gate(_2));
  Transistor #(.gate("br")) transistor_9 (.in(1'b1), .out(transistor_9_out), .gate(_1));
  Transistor #(.gate("br")) transistor_10 (.in(transistor_9_out), .out(transistor_10_out), .gate(transistor_13_out));
  Transistor #(.gate("br")) transistor_11 (.in(transistor_12_out), .out(transistor_10_out), .gate(s0));
  Transistor #(.gate("br")) transistor_12 (.in(1'b1), .out(transistor_12_out), .gate(_0));
  Transistor #(.gate("br")) transistor_13 (.in(1'b1), .out(transistor_13_out), .gate(s0));
  Transistor #(.\type ("n")) transistor_14 (.in(1'b0), .out(out), .gate(transistor_3_out));
  Transistor #(.\type ("n")) transistor_15 (.in(1'b0), .out(transistor_2_out), .gate(s1));
  Transistor #(.\type ("n")) transistor_16 (.in(transistor_6_out), .out(transistor_3_out), .gate(s1));
  Transistor #(.\type ("n")) transistor_17 (.in(transistor_10_out), .out(transistor_3_out), .gate(transistor_2_out));
  Transistor #(.\type ("n")) transistor_18 (.in(1'b0), .out(transistor_18_out), .gate(_3));
  Transistor #(.\type ("n")) transistor_19 (.in(transistor_18_out), .out(transistor_6_out), .gate(s0));
  Transistor #(.\type ("n")) transistor_20 (.in(transistor_21_out), .out(transistor_6_out), .gate(transistor_13_out));
  Transistor #(.\type ("n")) transistor_21 (.in(1'b0), .out(transistor_21_out), .gate(_2));
  Transistor #(.\type ("n")) transistor_22 (.in(1'b0), .out(transistor_22_out), .gate(_1));
  Transistor #(.\type ("n")) transistor_23 (.in(transistor_22_out), .out(transistor_10_out), .gate(s0));
  Transistor #(.\type ("n")) transistor_24 (.in(transistor_25_out), .out(transistor_10_out), .gate(transistor_13_out));
  Transistor #(.\type ("n")) transistor_25 (.in(1'b0), .out(transistor_25_out), .gate(_0));
  Transistor #(.\type ("n")) transistor_26 (.in(1'b0), .out(transistor_13_out), .gate(s0));
endmodule
