// Logisim project 4-NOR.circ as structural Verilog: 1 circuit, main circuit main
module main (
  input  a,
  input  b,
  input  c,
  input  d,
  output out
);

  wire transistor_2_out, transistor_3_out, transistor_4_out, transistor_6_out, transistor_7_out,
       transistor_12_out;

  Transistor #(.gate("br")) transistor_1 (.in(1'b1), .out(out), .gate(transistor_4_out));
  Transistor #(.gate("br")) transistor_2 (.in(transistor_3_out), .out(transistor_2_out), .gate(a));
  Transistor #(.gate("br")) transistor_3 (.in(1'b1), .out(transistor_3_out), .gate(b));
  Transistor #(.gate("br")) transistor_4 (.in(1'b1), .out(transistor_4_out), .gate(transistor_2_out));
  Transistor #(.gate("br")) transistor_5 (.in(1'b1), .out(transistor_4_out), .gate(transistor_7_out));
  Transistor #(.gate("br")) transistor_6 (.in(1'b1), .out(transistor_6_out), .gate(c));
  Transistor #(.gate("br")) transistor_7 (.in(transistor_6_out), .out(transistor_7_out), .gate(d));
  Transistor #(.\type ("n")) transistor_8 (.in(1'b0), .out(out), .gate(transistor_4_out));
  Transistor #(.\type ("n")) transistor_9 (.in(1'b0), .out(transistor_2_out), .gate(a));
  Transistor #(.\type ("n")) transistor_10 (.in(1'b0), .out(transistor_2_out), .gate(b));
  Transistor #(.\type ("n")) transistor_11 (.in(transistor_12_out), .out(transistor_4_out), .gate(transistor_2_out));
  Transistor #(.\type ("n")) transistor_12 (.in(1'b0), .out(transistor_12_out), .gate(transistor_7_out));
  Transistor #(.\type ("n")) transistor_13 (.in(1'b0), .out(transistor_7_out), .gate(c));
  Transistor #(.\type ("n")) transistor_14 (.in(1'b0), .out(transistor_7_out), .gate(d));
endmodule
