// Logisim project DFFRS3X.circ as structural Verilog: 1 circuit, main circuit main
module main (
  input  in,
  input  nres,
  input  nset,
  output out
);

  wire CLK_out, multiplexer_1_out, multiplexer_2_out, nand_1_out, nand_2_out, nand_3_out, nand_4_out,
       not_1_out, not_2_out;

  Clock #(.highDuration(4), .lowDuration(4)) CLK (.out(CLK_out));
  not not_1 (not_1_out, CLK_out);
  not not_2 (not_2_out, in);
  nand nand_1 (nand_1_out, nand_2_out, nres);
  Multiplexer multiplexer_1 (.in0(nand_1_out), .in1(not_2_out), .out(multiplexer_1_out), .sel(not_1_out));  // open: en
  nand nand_2 (nand_2_out, multiplexer_1_out, nset);
  nand nand_3 (nand_3_out, nand_4_out, nset);
  Multiplexer multiplexer_2 (.in0(nand_3_out), .in1(nand_2_out), .out(multiplexer_2_out), .sel(CLK_out));  // open: en
  nand nand_4 (nand_4_out, multiplexer_2_out, nres);
  not not_3 (out, nand_4_out);
endmodule
