// Logisim project DFFS.circ as structural Verilog: 1 circuit, main circuit main
module main (
  input  nSET,
  input  D,
  output out_3
);

  wire clock_1_out, multiplexer_1_out, multiplexer_2_out, nand_1_out, nand_2_out, not_1_out, not_2_out,
       not_3_out;

  Clock clock_1 (.out(clock_1_out));
  not not_1 (not_1_out, D);
  nand nand_1 (nand_1_out, nSET, not_3_out);
  nand nand_2 (nand_2_out, nSET, multiplexer_1_out);
  not not_2 (not_2_out, nand_2_out);
  Multiplexer multiplexer_1 (.in0(not_2_out), .in1(not_1_out), .out(multiplexer_1_out), .sel(clock_1_out));  // open: en
  Multiplexer multiplexer_2 (
    .in0(nand_2_out), .in1(nand_1_out), .out(multiplexer_2_out), .sel(clock_1_out));  // open: en
  not not_3 (not_3_out, multiplexer_2_out);
  not not_4 (out_3, not_3_out);
endmodule
