// Logisim project XNOR1_trans.circ as structural Verilog: 1 circuit, main circuit main
module main (
  input  a,
  input  b,
  output out
);

  wire transistor_2_out, transistor_3_out, transistor_5_out, transistor_6_out;

  Transistor #(.gate("br")) transistor_1 (.in(1'b1), .out(out), .gate(transistor_3_out));
  Transistor #(.gate("br")) transistor_2 (.in(1'b1), .out(transistor_2_out), .gate(a));
  Transistor #(.gate("br")) transistor_3 (.in(transistor_6_out), .out(transistor_3_out), .gate(transistor_2_out));
  Transistor #(.gate("br")) transistor_4 (.in(transistor_5_out), .out(transistor_3_out), .gate(a));
  Transistor #(.gate("br")) transistor_5 (.in(1'b1), .out(transistor_5_out), .gate(transistor_6_out));
  Transistor #(.gate("br")) transistor_6 (.in(1'b1), .out(transistor_6_out), .gate(b));
  Transistor #(.\type ("n")) transistor_7 (.in(1'b0), .out(out), .gate(transistor_3_out));
  Transistor #(.\type ("n")) transistor_8 (.in(1'b0), .out(transistor_2_out), .gate(a));
  Transistor #(.\type ("n")) transistor_9 (.in(transistor_6_out), .out(transistor_3_out), .gate(a));
  Transistor #(.\type ("n")) transistor_10 (.in(transistor_5_out), .out(transistor_3_out), .gate(transistor_2_out));
  Transistor #(.\type ("n")) transistor_11 (.in(1'b0), .out(transistor_5_out), .gate(transistor_6_out));
  Transistor #(.\type ("n")) transistor_12 (.in(1'b0), .out(transistor_6_out), .gate(b));
endmodule
