// Logisim project 8-MUX.circ as structural Verilog: 1 circuit, main circuit main
module main (
  input  in5,
  input  in4,
  input  in7,
  input  in6,
  input  s0,
  input  s1,
  input  in2,
  input  in3,
  input  in0,
  input  in1,
  input  s2,
  output out
);

  wire transistor_1_out, transistor_2_out, transistor_4_out, transistor_5_out, transistor_6_out,
       transistor_8_out, transistor_9_out, transistor_11_out, transistor_12_out, transistor_13_out,
       transistor_16_out, transistor_18_out, transistor_19_out, transistor_21_out, transistor_22_out,
       transistor_23_out, transistor_25_out, transistor_26_out, transistor_27_out, transistor_28_out,
       transistor_31_out, transistor_32_out, transistor_35_out, transistor_45_out, transistor_48_out,
       transistor_49_out, transistor_52_out;

  Transistor #(.gate("br")) transistor_1 (.in(1'b1), .out(transistor_1_out), .gate(in5));
  Transistor #(.gate("br")) transistor_2 (.in(transistor_1_out), .out(transistor_2_out), .gate(transistor_27_out));
  Transistor #(.gate("br")) transistor_3 (.in(transistor_4_out), .out(transistor_2_out), .gate(transistor_26_out));
  Transistor #(.gate("br")) transistor_4 (.in(1'b1), .out(transistor_4_out), .gate(in4));
  Transistor #(.gate("br")) transistor_5 (.in(1'b1), .out(transistor_5_out), .gate(in7));
  Transistor #(.gate("br")) transistor_6 (.in(transistor_5_out), .out(transistor_6_out), .gate(transistor_27_out));
  Transistor #(.gate("br")) transistor_7 (.in(transistor_8_out), .out(transistor_6_out), .gate(transistor_26_out));
  Transistor #(.gate("br")) transistor_8 (.in(1'b1), .out(transistor_8_out), .gate(in6));
  Transistor #(.gate("br")) transistor_9 (.in(transistor_6_out), .out(transistor_9_out), .gate(transistor_11_out));
  Transistor #(.gate("br")) transistor_10 (.in(transistor_2_out), .out(transistor_9_out), .gate(s1));
  Transistor #(.gate("br")) transistor_11 (.in(1'b1), .out(transistor_11_out), .gate(s1));
  Transistor #(.gate("br")) transistor_12 (.in(1'b1), .out(transistor_12_out), .gate(s0));
  Transistor #(.gate("br")) transistor_13 (.in(transistor_9_out), .out(transistor_13_out), .gate(transistor_12_out));
  Transistor #(.gate("br")) transistor_14 (.in(transistor_16_out), .out(transistor_13_out), .gate(s0));
  Transistor #(.gate("br")) transistor_15 (.in(1'b1), .out(out), .gate(transistor_13_out));
  Transistor #(.gate("br")) transistor_16 (.in(transistor_23_out), .out(transistor_16_out), .gate(s1));
  Transistor #(.gate("br")) transistor_17 (.in(transistor_19_out), .out(transistor_16_out), .gate(transistor_11_out));
  Transistor #(.gate("br")) transistor_18 (.in(1'b1), .out(transistor_18_out), .gate(in2));
  Transistor #(.gate("br")) transistor_19 (.in(transistor_18_out), .out(transistor_19_out), .gate(transistor_26_out));
  Transistor #(.gate("br")) transistor_20 (.in(transistor_21_out), .out(transistor_19_out), .gate(transistor_27_out));
  Transistor #(.gate("br")) transistor_21 (.in(1'b1), .out(transistor_21_out), .gate(in3));
  Transistor #(.gate("br")) transistor_22 (.in(1'b1), .out(transistor_22_out), .gate(in0));
  Transistor #(.gate("br")) transistor_23 (.in(transistor_22_out), .out(transistor_23_out), .gate(transistor_26_out));
  Transistor #(.gate("br")) transistor_24 (.in(transistor_25_out), .out(transistor_23_out), .gate(transistor_27_out));
  Transistor #(.gate("br")) transistor_25 (.in(1'b1), .out(transistor_25_out), .gate(in1));
  Transistor #(.gate("br")) transistor_26 (.in(1'b1), .out(transistor_26_out), .gate(transistor_27_out));
  Transistor #(.gate("br")) transistor_27 (.in(1'b1), .out(transistor_27_out), .gate(s2));
  Transistor #(.\type ("n")) transistor_28 (.in(1'b0), .out(transistor_28_out), .gate(in5));
  Transistor #(.\type ("n")) transistor_29 (.in(transistor_28_out), .out(transistor_2_out), .gate(transistor_26_out));
  Transistor #(.\type ("n")) transistor_30 (.in(transistor_31_out), .out(transistor_2_out), .gate(transistor_27_out));
  Transistor #(.\type ("n")) transistor_31 (.in(1'b0), .out(transistor_31_out), .gate(in4));
  Transistor #(.\type ("n")) transistor_32 (.in(1'b0), .out(transistor_32_out), .gate(in7));
  Transistor #(.\type ("n")) transistor_33 (.in(transistor_32_out), .out(transistor_6_out), .gate(transistor_26_out));
  Transistor #(.\type ("n")) transistor_34 (.in(transistor_35_out), .out(transistor_6_out), .gate(transistor_27_out));
  Transistor #(.\type ("n")) transistor_35 (.in(1'b0), .out(transistor_35_out), .gate(in6));
  Transistor #(.\type ("n")) transistor_36 (.in(transistor_6_out), .out(transistor_9_out), .gate(s1));
  Transistor #(.\type ("n")) transistor_37 (.in(transistor_2_out), .out(transistor_9_out), .gate(transistor_11_out));
  Transistor #(.\type ("n")) transistor_38 (.in(1'b0), .out(transistor_11_out), .gate(s1));
  Transistor #(.\type ("n")) transistor_39 (.in(1'b0), .out(transistor_12_out), .gate(s0));
  Transistor #(.\type ("n")) transistor_40 (.in(transistor_9_out), .out(transistor_13_out), .gate(s0));
  Transistor #(.\type ("n")) transistor_41 (.in(transistor_16_out), .out(transistor_13_out), .gate(transistor_12_out));
  Transistor #(.\type ("n")) transistor_42 (.in(1'b0), .out(out), .gate(transistor_13_out));
  Transistor #(.\type ("n")) transistor_43 (.in(transistor_23_out), .out(transistor_16_out), .gate(transistor_11_out));
  Transistor #(.\type ("n")) transistor_44 (.in(transistor_19_out), .out(transistor_16_out), .gate(s1));
  Transistor #(.\type ("n")) transistor_45 (.in(1'b0), .out(transistor_45_out), .gate(in2));
  Transistor #(.\type ("n")) transistor_46 (.in(transistor_45_out), .out(transistor_19_out), .gate(transistor_27_out));
  Transistor #(.\type ("n")) transistor_47 (.in(transistor_48_out), .out(transistor_19_out), .gate(transistor_26_out));
  Transistor #(.\type ("n")) transistor_48 (.in(1'b0), .out(transistor_48_out), .gate(in3));
  Transistor #(.\type ("n")) transistor_49 (.in(1'b0), .out(transistor_49_out), .gate(in0));
  Transistor #(.\type ("n")) transistor_50 (.in(transistor_49_out), .out(transistor_23_out), .gate(transistor_27_out));
  Transistor #(.\type ("n")) transistor_51 (.in(transistor_52_out), .out(transistor_23_out), .gate(transistor_26_out));
  Transistor #(.\type ("n")) transistor_52 (.in(1'b0), .out(transistor_52_out), .gate(in1));
  Transistor #(.\type ("n")) transistor_53 (.in(1'b0), .out(transistor_26_out), .gate(transistor_27_out));
  Transistor #(.\type ("n")) transistor_54 (.in(1'b0), .out(transistor_27_out), .gate(s2));
endmodule
