// Logisim project ADDC.circ as structural Verilog: 1 circuit, main circuit main
module main (
  input  a,
  input  b,
  input  cin,
  output sum,
  output cout
);

  wire transistor_3_out, transistor_4_out, transistor_6_out, transistor_7_out, transistor_9_out,
       transistor_10_out, transistor_11_out, transistor_13_out, transistor_25_out;

  Transistor #(.gate("br")) transistor_1 (.in(1'b1), .out(sum), .gate(transistor_4_out));
  Transistor #(.gate("br")) transistor_2 (.in(1'b1), .out(sum), .gate(transistor_4_out));
  Transistor #(.gate("br")) transistor_3 (.in(1'b1), .out(transistor_3_out), .gate(transistor_11_out));
  Transistor #(.gate("br")) transistor_4 (.in(transistor_3_out), .out(transistor_4_out), .gate(a));
  Transistor #(.gate("br")) transistor_5 (.in(transistor_11_out), .out(transistor_4_out), .gate(transistor_6_out));
  Transistor #(.gate("br")) transistor_6 (.in(1'b1), .out(transistor_6_out), .gate(a));
  Transistor #(.gate("br")) transistor_7 (.in(transistor_6_out), .out(transistor_7_out), .gate(transistor_3_out));
  Transistor #(.gate("br")) transistor_8 (.in(transistor_9_out), .out(transistor_7_out), .gate(transistor_11_out));
  Transistor #(.gate("br")) transistor_9 (.in(1'b1), .out(transistor_9_out), .gate(b));
  Transistor #(.gate("br")) transistor_10 (.in(1'b1), .out(transistor_10_out), .gate(transistor_13_out));
  Transistor #(.gate("br")) transistor_11 (.in(transistor_10_out), .out(transistor_11_out), .gate(b));
  Transistor #(.gate("br")) transistor_12 (.in(transistor_13_out), .out(transistor_11_out), .gate(transistor_9_out));
  Transistor #(.gate("br")) transistor_13 (.in(1'b1), .out(transistor_13_out), .gate(cin));
  Transistor #(.gate("br")) transistor_14 (.in(1'b1), .out(cout), .gate(transistor_7_out));
  Transistor #(.gate("br")) transistor_15 (.in(1'b1), .out(cout), .gate(transistor_7_out));
  Transistor #(.\type ("n")) transistor_16 (.in(1'b0), .out(sum), .gate(transistor_4_out));
  Transistor #(.\type ("n")) transistor_17 (.in(1'b0), .out(sum), .gate(transistor_4_out));
  Transistor #(.\type ("n")) transistor_18 (.in(1'b0), .out(transistor_3_out), .gate(transistor_11_out));
  Transistor #(.\type ("n")) transistor_19 (.in(transistor_3_out), .out(transistor_4_out), .gate(transistor_6_out));
  Transistor #(.\type ("n")) transistor_20 (.in(transistor_11_out), .out(transistor_4_out), .gate(a));
  Transistor #(.\type ("n")) transistor_21 (.in(1'b0), .out(transistor_6_out), .gate(a));
  Transistor #(.\type ("n")) transistor_22 (.in(transistor_6_out), .out(transistor_7_out), .gate(transistor_11_out));
  Transistor #(.\type ("n")) transistor_23 (.in(transistor_9_out), .out(transistor_7_out), .gate(transistor_3_out));
  Transistor #(.\type ("n")) transistor_24 (.in(1'b0), .out(transistor_9_out), .gate(b));
  Transistor #(.\type ("n")) transistor_25 (.in(1'b0), .out(transistor_25_out), .gate(transistor_13_out));
  Transistor #(.\type ("n")) transistor_26 (.in(transistor_25_out), .out(transistor_11_out), .gate(transistor_9_out));
  Transistor #(.\type ("n")) transistor_27 (.in(transistor_13_out), .out(transistor_11_out), .gate(b));
  Transistor #(.\type ("n")) transistor_28 (.in(1'b0), .out(transistor_13_out), .gate(cin));
  Transistor #(.\type ("n")) transistor_29 (.in(1'b0), .out(cout), .gate(transistor_7_out));
  Transistor #(.\type ("n")) transistor_30 (.in(1'b0), .out(cout), .gate(transistor_7_out));
endmodule
