// Logisim project DFF.circ as structural Verilog: 1 circuit, main circuit main
module main (
  input  D,
  output Q
);

  wire T_out, transistor_2_out, transistor_3_out, transistor_4_out, transistor_5_out, transistor_6_out,
       transistor_8_out, transistor_9_out, transistor_10_out, transistor_12_out, transistor_17_out,
       transistor_21_out;

  Transistor #(.gate("br")) transistor_1 (.in(1'b1), .out(Q), .gate(transistor_4_out));
  Transistor #(.gate("br")) transistor_2 (.in(1'b1), .out(transistor_2_out), .gate(transistor_3_out));
  Transistor #(.gate("br")) transistor_3 (.in(1'b1), .out(transistor_3_out), .gate(T_out));
  Transistor #(.gate("br")) transistor_4 (.in(1'b1), .out(transistor_4_out), .gate(transistor_6_out));
  Transistor #(.gate("br")) transistor_5 (.in(1'b1), .out(transistor_5_out), .gate(transistor_4_out));
  Transistor transistor_6 (.in(transistor_5_out), .out(transistor_6_out), .gate(transistor_2_out));
  Transistor #(.gate("br")) transistor_7 (.in(transistor_8_out), .out(transistor_6_out), .gate(transistor_3_out));
  Transistor #(.gate("br")) transistor_8 (.in(1'b1), .out(transistor_8_out), .gate(transistor_10_out));
  Transistor #(.gate("br")) transistor_9 (.in(1'b1), .out(transistor_9_out), .gate(transistor_8_out));
  Transistor #(.gate("br")) transistor_10 (.in(transistor_9_out), .out(transistor_10_out), .gate(transistor_3_out));
  Transistor transistor_11 (.in(transistor_12_out), .out(transistor_10_out), .gate(transistor_2_out));
  Transistor #(.gate("br")) transistor_12 (.in(1'b1), .out(transistor_12_out), .gate(D));
  Clock #(.highDuration(8), .lowDuration(8)) T (.out(T_out));
  Transistor #(.\type ("n")) transistor_13 (.in(1'b0), .out(Q), .gate(transistor_4_out));
  Transistor #(.\type ("n")) transistor_14 (.in(1'b0), .out(transistor_2_out), .gate(transistor_3_out));
  Transistor #(.\type ("n")) transistor_15 (.in(1'b0), .out(transistor_3_out), .gate(T_out));
  Transistor #(.\type ("n")) transistor_16 (.in(1'b0), .out(transistor_4_out), .gate(transistor_6_out));
  Transistor #(.\type ("n")) transistor_17 (.in(1'b0), .out(transistor_17_out), .gate(transistor_4_out));
  Transistor #(.\type ("n"), .gate("br")) transistor_18 (
    .in(transistor_17_out), .out(transistor_6_out), .gate(transistor_3_out));
  Transistor #(.\type ("n")) transistor_19 (.in(transistor_8_out), .out(transistor_6_out), .gate(transistor_2_out));
  Transistor #(.\type ("n")) transistor_20 (.in(1'b0), .out(transistor_8_out), .gate(transistor_10_out));
  Transistor #(.\type ("n")) transistor_21 (.in(1'b0), .out(transistor_21_out), .gate(transistor_8_out));
  Transistor #(.\type ("n")) transistor_22 (.in(transistor_21_out), .out(transistor_10_out), .gate(transistor_2_out));
  Transistor #(.\type ("n"), .gate("br")) transistor_23 (
    .in(transistor_12_out), .out(transistor_10_out), .gate(transistor_3_out));
  Transistor #(.\type ("n")) transistor_24 (.in(1'b0), .out(transistor_12_out), .gate(D));

  // Notes on the sheet:
  //   C0
  //   C1
endmodule
