// Logisim project DFFR.circ as structural Verilog: 2 circuits, main circuit main
module main (
  input  in2,
  input  value,
  output out
);

  wire CLK_out, transistor_2_out, transistor_3_out, transistor_4_out, transistor_6_out, transistor_7_out,
       transistor_9_out, transistor_10_out, transistor_12_out, transistor_14_out, transistor_19_out,
       transistor_20_out, transistor_24_out, transistor_25_out;

  Transistor #(.gate("br")) transistor_1 (.in(1'b1), .out(out), .gate(transistor_4_out));
  Transistor #(.gate("br")) transistor_2 (.in(1'b1), .out(transistor_2_out), .gate(transistor_3_out));
  Transistor #(.gate("br")) transistor_3 (.in(1'b1), .out(transistor_3_out), .gate(CLK_out));
  Transistor #(.gate("br")) transistor_4 (.in(1'b1), .out(transistor_4_out), .gate(transistor_7_out));
  Transistor #(.gate("br")) transistor_5 (.in(1'b1), .out(transistor_4_out), .gate(in2));
  Transistor #(.gate("br")) transistor_6 (.in(1'b1), .out(transistor_6_out), .gate(transistor_4_out));
  Transistor #(.gate("br")) transistor_7 (.in(transistor_6_out), .out(transistor_7_out), .gate(transistor_2_out));
  Transistor #(.gate("br")) transistor_8 (.in(transistor_9_out), .out(transistor_7_out), .gate(transistor_3_out));
  Transistor #(.gate("br")) transistor_9 (.in(1'b1), .out(transistor_9_out), .gate(transistor_12_out));
  Transistor #(.gate("br")) transistor_10 (.in(1'b1), .out(transistor_10_out), .gate(in2));
  Transistor #(.gate("br")) transistor_11 (.in(1'b1), .out(transistor_10_out), .gate(transistor_9_out));
  Transistor #(.gate("br")) transistor_12 (.in(transistor_10_out), .out(transistor_12_out), .gate(transistor_3_out));
  Transistor #(.gate("br")) transistor_13 (.in(transistor_14_out), .out(transistor_12_out), .gate(transistor_2_out));
  Transistor #(.gate("br")) transistor_14 (.in(1'b1), .out(transistor_14_out), .gate(value));
  Clock #(.highDuration(4), .lowDuration(4)) CLK (.out(CLK_out));
  Transistor #(.\type ("n")) transistor_15 (.in(1'b0), .out(out), .gate(transistor_4_out));
  Transistor #(.\type ("n")) transistor_16 (.in(1'b0), .out(transistor_2_out), .gate(transistor_3_out));
  Transistor #(.\type ("n")) transistor_17 (.in(1'b0), .out(transistor_3_out), .gate(CLK_out));
  Transistor #(.\type ("n")) transistor_18 (.in(transistor_19_out), .out(transistor_4_out), .gate(transistor_7_out));
  Transistor #(.\type ("n")) transistor_19 (.in(1'b0), .out(transistor_19_out), .gate(in2));
  Transistor #(.\type ("n")) transistor_20 (.in(1'b0), .out(transistor_20_out), .gate(transistor_4_out));
  Transistor #(.\type ("n")) transistor_21 (.in(transistor_20_out), .out(transistor_7_out), .gate(transistor_3_out));
  Transistor #(.\type ("n")) transistor_22 (.in(transistor_9_out), .out(transistor_7_out), .gate(transistor_2_out));
  Transistor #(.\type ("n")) transistor_23 (.in(1'b0), .out(transistor_9_out), .gate(transistor_12_out));
  Transistor #(.\type ("n")) transistor_24 (.in(1'b0), .out(transistor_24_out), .gate(in2));
  Transistor #(.\type ("n")) transistor_25 (.in(transistor_24_out), .out(transistor_25_out), .gate(transistor_9_out));
  Transistor #(.\type ("n")) transistor_26 (.in(transistor_25_out), .out(transistor_12_out), .gate(transistor_2_out));
  Transistor #(.\type ("n")) transistor_27 (.in(transistor_14_out), .out(transistor_12_out), .gate(transistor_3_out));
  Transistor #(.\type ("n")) transistor_28 (.in(1'b0), .out(transistor_14_out), .gate(value));

  // Notes on the sheet:
  //   2
  //   1
endmodule

module \logic  (
  input  in,
  input  nres,
  output out_3
);

  wire CLK_out, multiplexer_1_out, multiplexer_2_out, nand_1_out, nand_2_out, not_1_out, not_2_out,
       not_3_out, not_4_out;

  Clock #(.highDuration(4), .lowDuration(4)) CLK (.out(CLK_out));
  not not_1 (not_1_out, CLK_out);
  not not_2 (not_2_out, in);
  Multiplexer multiplexer_1 (.in0(nand_1_out), .in1(not_2_out), .out(multiplexer_1_out), .sel(not_1_out));  // open: en
  nand nand_1 (nand_1_out, not_3_out, nres);
  not not_3 (not_3_out, multiplexer_1_out);
  not not_4 (not_4_out, nand_2_out);
  Multiplexer multiplexer_2 (.in0(not_4_out), .in1(not_3_out), .out(multiplexer_2_out), .sel(CLK_out));  // open: en
  nand nand_2 (nand_2_out, multiplexer_2_out, nres);
  not not_5 (out_3, nand_2_out);
endmodule
