// Logisim project 22-AOI3X_trans.circ as structural Verilog: 1 circuit, main circuit main
module main (
  input  a,
  input  b,
  input  c,
  input  d,
  output out,
  output nout
);

  wire transistor_3_out, transistor_13_out, transistor_16_out, transistor_17_out, transistor_20_out,
       transistor_21_out, transistor_24_out;

  Transistor #(.gate("br")) transistor_1 (.in(transistor_3_out), .out(out), .gate(b));
  Transistor #(.gate("br")) transistor_2 (.in(transistor_3_out), .out(out), .gate(a));
  Transistor #(.gate("br")) transistor_3 (.in(1'b1), .out(transistor_3_out), .gate(d));
  Transistor #(.gate("br")) transistor_4 (.in(1'b1), .out(transistor_3_out), .gate(c));
  Transistor #(.gate("br")) transistor_5 (.in(1'b1), .out(transistor_3_out), .gate(c));
  Transistor #(.gate("br")) transistor_6 (.in(1'b1), .out(transistor_3_out), .gate(d));
  Transistor #(.gate("br")) transistor_7 (.in(transistor_3_out), .out(out), .gate(a));
  Transistor #(.gate("br")) transistor_8 (.in(1'b1), .out(out), .gate(b));
  Transistor #(.gate("br")) transistor_9 (.in(1'b1), .out(out), .gate(b));
  Transistor #(.gate("br")) transistor_10 (.in(transistor_3_out), .out(out), .gate(a));
  Transistor #(.gate("br")) transistor_11 (.in(1'b1), .out(transistor_3_out), .gate(d));
  Transistor #(.gate("br")) transistor_12 (.in(1'b1), .out(transistor_3_out), .gate(c));
  Transistor #(.\type ("n")) transistor_13 (.in(1'b0), .out(transistor_13_out), .gate(b));
  Transistor #(.\type ("n")) transistor_14 (.in(transistor_13_out), .out(nout), .gate(a));
  Transistor #(.\type ("n")) transistor_15 (.in(transistor_16_out), .out(nout), .gate(d));
  Transistor #(.\type ("n")) transistor_16 (.in(1'b0), .out(transistor_16_out), .gate(c));
  Transistor #(.\type ("n")) transistor_17 (.in(1'b0), .out(transistor_17_out), .gate(c));
  Transistor #(.\type ("n")) transistor_18 (.in(transistor_17_out), .out(nout), .gate(d));
  Transistor #(.\type ("n")) transistor_19 (.in(transistor_20_out), .out(nout), .gate(a));
  Transistor #(.\type ("n")) transistor_20 (.in(1'b0), .out(transistor_20_out), .gate(b));
  Transistor #(.\type ("n")) transistor_21 (.in(1'b0), .out(transistor_21_out), .gate(b));
  Transistor #(.\type ("n")) transistor_22 (.in(transistor_21_out), .out(nout), .gate(a));
  Transistor #(.\type ("n")) transistor_23 (.in(transistor_24_out), .out(nout), .gate(d));
  Transistor #(.\type ("n")) transistor_24 (.in(1'b0), .out(transistor_24_out), .gate(c));
endmodule
