// Logisim project 222-AOI.circ as structural Verilog: 1 circuit, main circuit main
module main (
  input  a,
  input  a_2,
  input  b,
  input  b_2,
  input  c,
  input  c_2,
  input  d,
  input  d_2,
  input  e,
  input  e_2,
  input  f,
  input  f_2,
  output out_13,
  output out_14
);

  wire and_1_out, and_2_out, and_3_out, transistor_2_out, transistor_3_out, transistor_5_out,
       transistor_7_out, transistor_12_out, transistor_13_out, transistor_16_out;

  Transistor #(.gate("br")) transistor_1 (.in(1'b1), .out(out_13), .gate(transistor_2_out));
  Transistor #(.gate("br")) transistor_2 (.in(1'b1), .out(transistor_2_out), .gate(transistor_3_out));
  Transistor #(.gate("br")) transistor_3 (.in(transistor_7_out), .out(transistor_3_out), .gate(a));
  Transistor #(.gate("br")) transistor_4 (.in(transistor_7_out), .out(transistor_3_out), .gate(b_2));
  Transistor #(.gate("br")) transistor_5 (.in(1'b1), .out(transistor_5_out), .gate(c_2));
  Transistor #(.gate("br")) transistor_6 (.in(1'b1), .out(transistor_5_out), .gate(d_2));
  Transistor #(.gate("br")) transistor_7 (.in(transistor_5_out), .out(transistor_7_out), .gate(e));
  Transistor #(.gate("br")) transistor_8 (.in(transistor_5_out), .out(transistor_7_out), .gate(f));
  Transistor #(.\type ("n")) transistor_9 (.in(1'b0), .out(out_13), .gate(transistor_2_out));
  Transistor #(.\type ("n")) transistor_10 (.in(1'b0), .out(transistor_2_out), .gate(transistor_3_out));
  Transistor #(.\type ("n")) transistor_11 (.in(transistor_12_out), .out(transistor_3_out), .gate(a));
  Transistor #(.\type ("n")) transistor_12 (.in(1'b0), .out(transistor_12_out), .gate(b_2));
  Transistor #(.\type ("n")) transistor_13 (.in(1'b0), .out(transistor_13_out), .gate(c_2));
  Transistor #(.\type ("n")) transistor_14 (.in(transistor_13_out), .out(transistor_3_out), .gate(d_2));
  Transistor #(.\type ("n")) transistor_15 (.in(transistor_16_out), .out(transistor_3_out), .gate(e));
  Transistor #(.\type ("n")) transistor_16 (.in(1'b0), .out(transistor_16_out), .gate(f));
  and and_1 (and_1_out, a_2, b);
  and and_2 (and_2_out, c, d);
  and and_3 (and_3_out, e_2, f_2);
  nor nor_1 (out_14, and_1_out, and_2_out, and_3_out);
endmodule
