// Logisim project 3-MUX.circ as structural Verilog: 1 circuit, main circuit main
module main (
  input  in2,
  input  sel1,
  input  in1,
  input  in0,
  input  sel0,
  output out
);

  wire transistor_2_out, transistor_3_out, transistor_5_out, transistor_6_out, transistor_7_out,
       transistor_9_out, transistor_10_out, transistor_12_out, transistor_16_out, transistor_19_out;

  Transistor #(.gate("br")) transistor_1 (.in(1'b1), .out(out), .gate(transistor_3_out));
  Transistor #(.gate("br")) transistor_2 (.in(1'b1), .out(transistor_2_out), .gate(in2));
  Transistor #(.gate("br")) transistor_3 (.in(transistor_2_out), .out(transistor_3_out), .gate(transistor_5_out));
  Transistor #(.gate("br")) transistor_4 (.in(transistor_7_out), .out(transistor_3_out), .gate(sel1));
  Transistor #(.gate("br")) transistor_5 (.in(1'b1), .out(transistor_5_out), .gate(sel1));
  Transistor #(.gate("br")) transistor_6 (.in(1'b1), .out(transistor_6_out), .gate(in1));
  Transistor #(.gate("br")) transistor_7 (.in(transistor_6_out), .out(transistor_7_out), .gate(transistor_10_out));
  Transistor #(.gate("br")) transistor_8 (.in(transistor_9_out), .out(transistor_7_out), .gate(sel0));
  Transistor #(.gate("br")) transistor_9 (.in(1'b1), .out(transistor_9_out), .gate(in0));
  Transistor #(.gate("br")) transistor_10 (.in(1'b1), .out(transistor_10_out), .gate(sel0));
  Transistor #(.\type ("n")) transistor_11 (.in(1'b0), .out(out), .gate(transistor_3_out));
  Transistor #(.\type ("n")) transistor_12 (.in(1'b0), .out(transistor_12_out), .gate(in2));
  Transistor #(.\type ("n")) transistor_13 (.in(transistor_12_out), .out(transistor_3_out), .gate(sel1));
  Transistor #(.\type ("n"), .gate("br")) transistor_14 (
    .in(transistor_7_out), .out(transistor_3_out), .gate(transistor_5_out));
  Transistor #(.\type ("n")) transistor_15 (.in(1'b0), .out(transistor_5_out), .gate(sel1));
  Transistor #(.\type ("n")) transistor_16 (.in(1'b0), .out(transistor_16_out), .gate(in1));
  Transistor #(.\type ("n")) transistor_17 (.in(transistor_16_out), .out(transistor_7_out), .gate(sel0));
  Transistor #(.\type ("n"), .gate("br")) transistor_18 (
    .in(transistor_19_out), .out(transistor_7_out), .gate(transistor_10_out));
  Transistor #(.\type ("n")) transistor_19 (.in(1'b0), .out(transistor_19_out), .gate(in0));
  Transistor #(.\type ("n")) transistor_20 (.in(1'b0), .out(transistor_10_out), .gate(sel0));

  // Notes on the sheet:
  //   t
  //   if (Sel1 == 1) out = in1
  //   if (Sel1 == 0) out = NOT(t)
  //   if (Sel0 == 1) t = NOT(in2)
  //   if (Sel0 == 0) t = NOT(in3)
  //   00: out = in0
  //   01: out = in1
  //   1X: out = in2
endmodule
