// Logisim project 3-XOR.circ as structural Verilog: 1 circuit, main circuit main
module main (
  input  a,
  input  b,
  input  c,
  output out
);

  wire transistor_2_out, transistor_3_out, transistor_5_out, transistor_6_out, transistor_7_out,
       transistor_9_out, transistor_18_out, transistor_19_out;

  Transistor #(.gate("br")) transistor_1 (.in(1'b1), .out(out), .gate(transistor_3_out));
  Transistor #(.gate("br")) transistor_2 (.in(1'b1), .out(transistor_2_out), .gate(a));
  Transistor #(.gate("br")) transistor_3 (.in(transistor_7_out), .out(transistor_3_out), .gate(a));
  Transistor #(.gate("br")) transistor_4 (.in(transistor_5_out), .out(transistor_3_out), .gate(transistor_2_out));
  Transistor #(.gate("br")) transistor_5 (.in(1'b1), .out(transistor_5_out), .gate(transistor_7_out));
  Transistor #(.gate("br")) transistor_6 (.in(1'b1), .out(transistor_6_out), .gate(c));
  Transistor #(.gate("br")) transistor_7 (.in(transistor_6_out), .out(transistor_7_out), .gate(b));
  Transistor #(.gate("br")) transistor_8 (.in(1'b1), .out(transistor_7_out), .gate(transistor_9_out));
  Transistor #(.gate("br")) transistor_9 (.in(1'b1), .out(transistor_9_out), .gate(c));
  Transistor #(.gate("br")) transistor_10 (.in(1'b1), .out(transistor_9_out), .gate(b));
  Transistor #(.\type ("n")) transistor_11 (.in(1'b0), .out(out), .gate(transistor_3_out));
  Transistor #(.\type ("n")) transistor_12 (.in(1'b0), .out(transistor_2_out), .gate(a));
  Transistor #(.\type ("n")) transistor_13 (.in(transistor_7_out), .out(transistor_3_out), .gate(transistor_2_out));
  Transistor #(.\type ("n")) transistor_14 (.in(transistor_5_out), .out(transistor_3_out), .gate(a));
  Transistor #(.\type ("n")) transistor_15 (.in(1'b0), .out(transistor_5_out), .gate(transistor_7_out));
  Transistor #(.\type ("n")) transistor_16 (.in(transistor_18_out), .out(transistor_7_out), .gate(c));
  Transistor #(.\type ("n")) transistor_17 (.in(transistor_18_out), .out(transistor_7_out), .gate(b));
  Transistor #(.\type ("n")) transistor_18 (.in(1'b0), .out(transistor_18_out), .gate(transistor_9_out));
  Transistor #(.\type ("n")) transistor_19 (.in(1'b0), .out(transistor_19_out), .gate(c));
  Transistor #(.\type ("n")) transistor_20 (.in(transistor_19_out), .out(transistor_9_out), .gate(b));
endmodule
