// Logisim project 4-MUX2X.circ as structural Verilog: 1 circuit, main circuit main
module main (
  input  sel_1,
  input  mux_3,
  input  mux_2,
  input  mux_1,
  input  mux_0,
  input  sel_0,
  output out_7
);

  wire transistor_4_out, transistor_5_out, transistor_7_out, transistor_8_out, transistor_10_out,
       transistor_11_out, transistor_12_out, transistor_14_out, transistor_15_out, transistor_22_out,
       transistor_25_out, transistor_26_out, transistor_29_out;

  Transistor #(.gate("br")) transistor_1 (.in(1'b1), .out(out_7), .gate(transistor_5_out));
  Transistor #(.gate("br")) transistor_2 (.in(1'b1), .out(out_7), .gate(transistor_5_out));
  Transistor #(.gate("br")) transistor_3 (.in(1'b1), .out(out_7), .gate(transistor_5_out));
  Transistor #(.gate("br")) transistor_4 (.in(1'b1), .out(transistor_4_out), .gate(sel_1));
  Transistor #(.gate("br")) transistor_5 (.in(transistor_8_out), .out(transistor_5_out), .gate(transistor_4_out));
  Transistor #(.gate("br")) transistor_6 (.in(transistor_12_out), .out(transistor_5_out), .gate(sel_1));
  Transistor #(.gate("br")) transistor_7 (.in(1'b1), .out(transistor_7_out), .gate(mux_3));
  Transistor #(.gate("br")) transistor_8 (.in(transistor_7_out), .out(transistor_8_out), .gate(transistor_15_out));
  Transistor #(.gate("br")) transistor_9 (.in(transistor_10_out), .out(transistor_8_out), .gate(sel_0));
  Transistor #(.gate("br")) transistor_10 (.in(1'b1), .out(transistor_10_out), .gate(mux_2));
  Transistor #(.gate("br")) transistor_11 (.in(1'b1), .out(transistor_11_out), .gate(mux_1));
  Transistor #(.gate("br")) transistor_12 (.in(transistor_11_out), .out(transistor_12_out), .gate(transistor_15_out));
  Transistor #(.gate("br")) transistor_13 (.in(transistor_14_out), .out(transistor_12_out), .gate(sel_0));
  Transistor #(.gate("br")) transistor_14 (.in(1'b1), .out(transistor_14_out), .gate(mux_0));
  Transistor #(.gate("br")) transistor_15 (.in(1'b1), .out(transistor_15_out), .gate(sel_0));
  Transistor #(.\type ("n")) transistor_16 (.in(1'b0), .out(out_7), .gate(transistor_5_out));
  Transistor #(.\type ("n")) transistor_17 (.in(1'b0), .out(out_7), .gate(transistor_5_out));
  Transistor #(.\type ("n")) transistor_18 (.in(1'b0), .out(out_7), .gate(transistor_5_out));
  Transistor #(.\type ("n")) transistor_19 (.in(1'b0), .out(transistor_4_out), .gate(sel_1));
  Transistor #(.\type ("n")) transistor_20 (.in(transistor_8_out), .out(transistor_5_out), .gate(sel_1));
  Transistor #(.\type ("n")) transistor_21 (.in(transistor_12_out), .out(transistor_5_out), .gate(transistor_4_out));
  Transistor #(.\type ("n")) transistor_22 (.in(1'b0), .out(transistor_22_out), .gate(mux_3));
  Transistor #(.\type ("n")) transistor_23 (.in(transistor_22_out), .out(transistor_8_out), .gate(sel_0));
  Transistor #(.\type ("n")) transistor_24 (.in(transistor_25_out), .out(transistor_8_out), .gate(transistor_15_out));
  Transistor #(.\type ("n")) transistor_25 (.in(1'b0), .out(transistor_25_out), .gate(mux_2));
  Transistor #(.\type ("n")) transistor_26 (.in(1'b0), .out(transistor_26_out), .gate(mux_1));
  Transistor #(.\type ("n")) transistor_27 (.in(transistor_26_out), .out(transistor_12_out), .gate(sel_0));
  Transistor #(.\type ("n")) transistor_28 (.in(transistor_29_out), .out(transistor_12_out), .gate(transistor_15_out));
  Transistor #(.\type ("n")) transistor_29 (.in(1'b0), .out(transistor_29_out), .gate(mux_0));
  Transistor #(.\type ("n")) transistor_30 (.in(1'b0), .out(transistor_15_out), .gate(sel_0));
endmodule
