// Logisim project 5-NOR.circ as structural Verilog: 1 circuit, main circuit main
module main (
  input  in_1,
  input  in_2,
  input  in_3,
  input  in_4,
  input  in_5,
  output out_6
);

  wire transistor_2_out, transistor_3_out, transistor_4_out, transistor_5_out, transistor_7_out,
       transistor_8_out, transistor_14_out;

  Transistor #(.gate("br")) transistor_1 (.in(1'b1), .out(out_6), .gate(transistor_5_out));
  Transistor #(.gate("br")) transistor_2 (.in(transistor_3_out), .out(transistor_2_out), .gate(in_1));
  Transistor #(.gate("br")) transistor_3 (.in(transistor_4_out), .out(transistor_3_out), .gate(in_2));
  Transistor #(.gate("br")) transistor_4 (.in(1'b1), .out(transistor_4_out), .gate(in_3));
  Transistor #(.gate("br")) transistor_5 (.in(1'b1), .out(transistor_5_out), .gate(transistor_2_out));
  Transistor #(.gate("br")) transistor_6 (.in(1'b1), .out(transistor_5_out), .gate(transistor_8_out));
  Transistor #(.gate("br")) transistor_7 (.in(1'b1), .out(transistor_7_out), .gate(in_4));
  Transistor #(.gate("br")) transistor_8 (.in(transistor_7_out), .out(transistor_8_out), .gate(in_5));
  Transistor #(.\type ("n")) transistor_9 (.in(1'b0), .out(out_6), .gate(transistor_5_out));
  Transistor #(.\type ("n")) transistor_10 (.in(1'b0), .out(transistor_2_out), .gate(in_1));
  Transistor #(.\type ("n")) transistor_11 (.in(1'b0), .out(transistor_2_out), .gate(in_2));
  Transistor #(.\type ("n")) transistor_12 (.in(1'b0), .out(transistor_2_out), .gate(in_3));
  Transistor #(.\type ("n")) transistor_13 (.in(transistor_14_out), .out(transistor_5_out), .gate(transistor_2_out));
  Transistor #(.\type ("n")) transistor_14 (.in(1'b0), .out(transistor_14_out), .gate(transistor_8_out));
  Transistor #(.\type ("n")) transistor_15 (.in(1'b0), .out(transistor_8_out), .gate(in_4));
  Transistor #(.\type ("n")) transistor_16 (.in(1'b0), .out(transistor_8_out), .gate(in_5));
endmodule
