// Logisim project DEMUX.circ as structural Verilog: 1 circuit, main circuit main
module main (
  input  in,
  output out1,
  output out0
);

  wire transistor_2_out;

  Transistor #(.gate("br")) transistor_1 (.in(1'b1), .out(out1), .gate(transistor_2_out));
  Transistor #(.gate("br")) transistor_2 (.in(1'b1), .out(transistor_2_out), .gate(in));
  Transistor #(.gate("br")) transistor_3 (.in(1'b1), .out(out0), .gate(in));
  Transistor #(.\type ("n")) transistor_4 (.in(1'b0), .out(out1), .gate(transistor_2_out));
  Transistor #(.\type ("n")) transistor_5 (.in(1'b0), .out(transistor_2_out), .gate(in));
  Transistor #(.\type ("n")) transistor_6 (.in(1'b0), .out(out0), .gate(in));
endmodule
