// Logisim project DFFR_MUX.circ as structural Verilog: 4 circuits, main circuit main
module main (
  input  nres,
  input  mux_0,
  input  mux_1,
  input  sel,
  output out
);

  wire c_out, transistor_2_out, transistor_3_out, transistor_4_out, transistor_6_out, transistor_7_out,
       transistor_9_out, transistor_10_out, transistor_12_out, transistor_14_out, transistor_15_out,
       transistor_18_out, transistor_23_out, transistor_24_out, transistor_28_out, transistor_29_out,
       transistor_33_out, transistor_35_out;

  Clock c (.out(c_out));
  Transistor #(.gate("br")) transistor_1 (.in(1'b1), .out(out), .gate(transistor_4_out));
  Transistor #(.gate("br")) transistor_2 (.in(1'b1), .out(transistor_2_out), .gate(transistor_3_out));
  Transistor #(.gate("br")) transistor_3 (.in(1'b1), .out(transistor_3_out), .gate(c_out));
  Transistor #(.gate("br")) transistor_4 (.in(1'b1), .out(transistor_4_out), .gate(transistor_7_out));
  Transistor #(.gate("br")) transistor_5 (.in(1'b1), .out(transistor_4_out), .gate(nres));
  Transistor #(.gate("br")) transistor_6 (.in(1'b1), .out(transistor_6_out), .gate(transistor_4_out));
  Transistor #(.gate("br")) transistor_7 (.in(transistor_6_out), .out(transistor_7_out), .gate(transistor_2_out));
  Transistor #(.gate("br")) transistor_8 (.in(transistor_9_out), .out(transistor_7_out), .gate(transistor_3_out));
  Transistor #(.gate("br")) transistor_9 (.in(1'b1), .out(transistor_9_out), .gate(transistor_12_out));
  Transistor #(.gate("br")) transistor_10 (.in(1'b1), .out(transistor_10_out), .gate(nres));
  Transistor #(.gate("br")) transistor_11 (.in(1'b1), .out(transistor_10_out), .gate(transistor_9_out));
  Transistor #(.gate("br")) transistor_12 (.in(transistor_10_out), .out(transistor_12_out), .gate(transistor_3_out));
  Transistor #(.gate("br")) transistor_13 (.in(transistor_14_out), .out(transistor_12_out), .gate(transistor_2_out));
  Transistor #(.gate("br")) transistor_14 (.in(transistor_15_out), .out(transistor_14_out), .gate(mux_0));
  Transistor #(.gate("br")) transistor_15 (.in(1'b1), .out(transistor_15_out), .gate(mux_1));
  Transistor #(.gate("br")) transistor_16 (.in(transistor_15_out), .out(transistor_14_out), .gate(transistor_18_out));
  Transistor #(.gate("br")) transistor_17 (.in(1'b1), .out(transistor_15_out), .gate(sel));
  Transistor #(.gate("br")) transistor_18 (.in(1'b1), .out(transistor_18_out), .gate(sel));
  Transistor #(.\type ("n")) transistor_19 (.in(1'b0), .out(out), .gate(transistor_4_out));
  Transistor #(.\type ("n")) transistor_20 (.in(1'b0), .out(transistor_2_out), .gate(transistor_3_out));
  Transistor #(.\type ("n")) transistor_21 (.in(1'b0), .out(transistor_3_out), .gate(c_out));
  Transistor #(.\type ("n")) transistor_22 (.in(transistor_23_out), .out(transistor_4_out), .gate(transistor_7_out));
  Transistor #(.\type ("n")) transistor_23 (.in(1'b0), .out(transistor_23_out), .gate(nres));
  Transistor #(.\type ("n")) transistor_24 (.in(1'b0), .out(transistor_24_out), .gate(transistor_4_out));
  Transistor #(.\type ("n")) transistor_25 (.in(transistor_24_out), .out(transistor_7_out), .gate(transistor_3_out));
  Transistor #(.\type ("n")) transistor_26 (.in(transistor_9_out), .out(transistor_7_out), .gate(transistor_2_out));
  Transistor #(.\type ("n")) transistor_27 (.in(1'b0), .out(transistor_9_out), .gate(transistor_12_out));
  Transistor #(.\type ("n")) transistor_28 (.in(1'b0), .out(transistor_28_out), .gate(nres));
  Transistor #(.\type ("n")) transistor_29 (.in(transistor_28_out), .out(transistor_29_out), .gate(transistor_9_out));
  Transistor #(.\type ("n")) transistor_30 (.in(transistor_29_out), .out(transistor_12_out), .gate(transistor_2_out));
  Transistor #(.\type ("n")) transistor_31 (.in(transistor_14_out), .out(transistor_12_out), .gate(transistor_3_out));
  Transistor #(.\type ("n")) transistor_32 (.in(transistor_33_out), .out(transistor_14_out), .gate(mux_0));
  Transistor #(.\type ("n")) transistor_33 (.in(1'b0), .out(transistor_33_out), .gate(transistor_18_out));
  Transistor #(.\type ("n")) transistor_34 (.in(transistor_35_out), .out(transistor_14_out), .gate(mux_1));
  Transistor #(.\type ("n")) transistor_35 (.in(1'b0), .out(transistor_35_out), .gate(sel));
  Transistor #(.\type ("n")) transistor_36 (.in(1'b0), .out(transistor_18_out), .gate(sel));

  // Notes on the sheet:
  //   IMUX /out
  //   NOT
  //   DEMUX
  //   NAND
  //   NOT
  //   MUX
  //   NOT
  //   NAND
  //   MUX
  //   IMUX
endmodule

module \logic  (
  input  nres,
  input  sel,
  input  mux_0,
  input  mux_1,
  output out
);

  wire CLK_out, multiplexer_1_out, multiplexer_2_out, multiplexer_3_out, nand_1_out, nand_2_out, not_1_out,
       not_2_out, not_3_out, not_4_out;

  Clock #(.highDuration(2), .lowDuration(2)) CLK (.out(CLK_out));
  not not_1 (not_1_out, multiplexer_1_out);
  Multiplexer multiplexer_1 (.in0(mux_0), .in1(mux_1), .out(multiplexer_1_out), .sel(sel));  // open: en
  nand nand_1 (nand_1_out, nres, not_3_out);
  not not_2 (not_2_out, CLK_out);
  Multiplexer multiplexer_2 (.in0(nand_1_out), .in1(not_1_out), .out(multiplexer_2_out), .sel(not_2_out));  // open: en
  not not_3 (not_3_out, multiplexer_2_out);
  nand nand_2 (nand_2_out, nres, multiplexer_3_out);
  not not_4 (not_4_out, nand_2_out);
  not not_5 (out, nand_2_out);
  Multiplexer multiplexer_3 (.in0(not_4_out), .in1(not_3_out), .out(multiplexer_3_out), .sel(CLK_out));  // open: en
endmodule

module bot_part (
  input  mux_0,
  input  mux_1,
  input  sel,
  output nout
);

  wire transistor_2_out, transistor_5_out, transistor_7_out, transistor_9_out;

  Transistor #(.gate("br")) transistor_1 (.in(transistor_2_out), .out(nout), .gate(mux_0));
  Transistor #(.gate("br")) transistor_2 (.in(1'b1), .out(transistor_2_out), .gate(mux_1));
  Transistor #(.gate("br")) transistor_3 (.in(transistor_2_out), .out(nout), .gate(transistor_5_out));
  Transistor #(.gate("br")) transistor_4 (.in(1'b1), .out(transistor_2_out), .gate(sel));
  Transistor #(.gate("br")) transistor_5 (.in(1'b1), .out(transistor_5_out), .gate(sel));
  Transistor #(.\type ("n")) transistor_6 (.in(transistor_7_out), .out(nout), .gate(mux_0));
  Transistor #(.\type ("n")) transistor_7 (.in(1'b0), .out(transistor_7_out), .gate(transistor_5_out));
  Transistor #(.\type ("n")) transistor_8 (.in(transistor_9_out), .out(nout), .gate(mux_1));
  Transistor #(.\type ("n")) transistor_9 (.in(1'b0), .out(transistor_9_out), .gate(sel));
  Transistor #(.\type ("n")) transistor_10 (.in(1'b0), .out(transistor_5_out), .gate(sel));

  // Notes on the sheet:
  //   IMUX
endmodule

module bot_part2 (
  input  mux_0,
  input  mux_1,
  input  sel,
  output nout
);

  wire and_1_out, and_2_out, not_1_out, not_2_out, not_3_out;

  not not_1 (not_1_out, mux_0);
  and and_1 (and_1_out, not_1_out, not_2_out);
  not not_2 (not_2_out, sel);
  not not_3 (not_3_out, mux_1);
  and and_2 (and_2_out, not_3_out, sel);
  or or_1 (nout, and_1_out, and_2_out);

  // Notes on the sheet:
  //   IMUX
endmodule
