// Logisim project Dcache_control.circ as structural Verilog
module main (
  input  nRES,
  input  RW__unk3,
  input  nWORD,
  input  nBS0,
  input  nBS1,
  input  BYTESEL,
  input  nBS2,
  input  nRWC__unk2,
  input  nBS3,
  input  nRES_2,
  input  nBS0_2,
  input  nBS1_2,
  input  RW__unk3_2,
  input  nRWC__unk2_2,
  input  nBS2_2,
  input  nBS3_2,
  input  nBS4,
  input  nWORD_2,
  input  nBS5,
  input  BYTESEL__unk1,
  input  BS0,
  input  nRWC__unk2_3,
  input  RW__unk3_3,
  output BS0_2,
  output BS1,
  output RW__1,
  output BS2,
  output nRW__2,
  output RW__unk3_4,
  output BS3,
  output nRWC__unk2_4,
  output RW,
  output BYTESEL__unk1_2,
  output nRW,
  output DO_RW__Y2,
  output BYTE_EN
);

  wire and_1_out, and_2_out, controlled_buffer_1_out, controlled_buffer_3_out, controlled_buffer_4_out,
       CS_2_out, CS_out, nand_1_out, nand_2_out, nand_3_out, nand_4_out, nand_5_out, nand_6_out, nor_1_out,
       nor_2_out, nor_3_out, not_1_out, not_2_out, not_3_out, not_4_out, not_5_out, not_6_out, not_7_out,
       not_8_out, not_9_out, not_10_out, not_11_out, not_12_out, not_13_out, not_14_out, not_15_out,
       not_16_out, not_17_out, not_18_out, not_23_out, not_25_out, not_26_out, not_27_out, not_29_out,
       or_1_out, or_2_out, undriven;

  Clock #(.highDuration(4), .lowDuration(4)) CS (.out(CS_out));
  Clock #(.highDuration(4), .lowDuration(4)) CS_2 (.out(CS_2_out));
  not not_1 (not_1_out, nRES);
  not not_2 (not_2_out, nWORD);
  not not_3 (not_3_out, CS_out);
  not not_4 (not_4_out, nRES_2);
  or or_1 (or_1_out, not_4_out, not_5_out);
  not not_5 (not_5_out, nRWC__unk2_2);
  not not_6 (not_6_out, nWORD_2);
  or or_2 (or_2_out, not_6_out, BYTESEL__unk1);
  not not_7 (not_7_out, not_8_out);
  not not_8 (not_8_out, RW__unk3_3);
  not not_9 (not_9_out, not_1_out);
  not not_10 (not_10_out, not_11_out);
  not not_11 (not_11_out, not_3_out);
  not not_12 (not_12_out, not_7_out);
  not not_13 (not_13_out, not_12_out);
  not not_14 (not_14_out, not_9_out);
  assign controlled_buffer_1_out = not_14_out ? 1'b1 : 1'bz;  // Controlled_Buffer controlled_buffer_1
  not not_15 (not_15_out, not_16_out);
  not not_16 (not_16_out, not_17_out);
  not not_17 (not_17_out, not_10_out);
  not not_18 (not_18_out, nRWC__unk2);
  assign controlled_buffer_1_out = not_18_out ? 1'b1 : 1'bz;  // Controlled_Buffer controlled_buffer_2
  S_R_Flip_Flop s_r_ff_1 (.S(or_2_out), .clk(CS_2_out), .Q(RW), .Qn(nRW), .reset(or_1_out));  // open: R, preset, en
  nand nand_1 (nand_1_out, RW__unk3_3, nand_2_out);
  nand nand_2 (nand_2_out, nand_1_out, nand_3_out);
  assign controlled_buffer_3_out = not_3_out ? controlled_buffer_4_out : 1'bz;  // Controlled_Buffer controlled_buffer_3
  assign controlled_buffer_4_out = not_15_out ? 1'b0 : 1'bz;  // Controlled_Buffer controlled_buffer_4
  nand nand_3 (nand_3_out, and_2_out, and_1_out);
  assign controlled_buffer_1_out = not_2_out ? controlled_buffer_3_out : 1'bz;  // Controlled_Buffer controlled_buffer_5
  assign controlled_buffer_1_out = BYTESEL ? controlled_buffer_3_out : 1'bz;  // Controlled_Buffer controlled_buffer_6
  nand nand_4 (nand_4_out, nBS0_2, nBS1_2, nBS2_2);
  nor nor_1 (nor_1_out, nand_4_out, nand_5_out);
  nand nand_5 (nand_5_out, nBS3_2, nBS4, nBS5);
  not not_19 (BYTESEL__unk1_2, nor_1_out);
  and and_1 (and_1_out, undriven, nand_6_out);
  not not_20 (RW__unk3_4, controlled_buffer_1_out);
  not not_21 (controlled_buffer_1_out, RW__unk3_4);
  not not_22 (nRW__2, RW__unk3_4);
  not not_23 (not_23_out, and_1_out);
  nand nand_6 (nand_6_out, not_23_out, and_2_out);
  not not_24 (RW__1, nRW__2);
  not not_25 (not_25_out, RW__unk3_2);
  and and_2 (and_2_out, nRWC__unk2_3, RW__unk3_3);
  nor nor_2 (nor_2_out, not_25_out, nor_3_out);
  nor nor_3 (nor_3_out, nor_2_out, 1'b0);
  not not_26 (not_26_out, and_2_out);
  not not_27 (not_27_out, RW__unk3);
  not not_28 (nRWC__unk2_4, not_29_out);
  not not_29 (not_29_out, nor_3_out);
  and and_3 (BYTE_EN, BS0, and_2_out);
  D_Flip_Flop #(.trigger("high")) d_ff_1 (.clk(not_27_out), .D(nBS0), .Qn(BS0_2));  // open: Q, preset, en, reset
  D_Flip_Flop #(.trigger("high")) d_ff_2 (.clk(not_27_out), .D(nBS1), .Qn(BS1));  // open: Q, preset, en, reset
  D_Flip_Flop #(.trigger("high")) d_ff_3 (.clk(not_27_out), .D(nBS2), .Qn(BS2));  // open: Q, preset, en, reset
  D_Flip_Flop #(.trigger("high")) d_ff_4 (.clk(not_27_out), .D(nBS3), .Qn(BS3));  // open: Q, preset, en, reset
  or or_3 (DO_RW__Y2, not_13_out, and_2_out);
  // NOT_Gate not_30 is placed but not wired

  // Notes on the sheet:
  //   Read/Write Control
  //   falling edge (negedge) detect
  //   negedge
  //   RW_DELAY (unk3P)
  //   I
  //   Read/Write Control
  //   II
  //   Byte Select
  //   out
  //   III
  //   else out = Z;
  //   Bi-latch
  //   "Memory" part of RS
  //   if (#RES == 0 || ONE == 0) out = 1;
  //   Sorry for coloring but Logisim doesn't support bi-latches
  //   IV
  //   else if ((#WORD == 0 || BYTESEL) && negedge #CS) out = 0; 
  //   Read/Write Clear (Disabled)
  //   V
  //   RW_DELAY (unk3P)
endmodule

module _2_to_4_Switch (
  input  R0,
  input  R1,
  input  RW,
  output _00,
  output _01,
  output _10,
  output _11
);

  wire controlled_buffer_1_out, controlled_buffer_2_out, controlled_buffer_3_out, controlled_buffer_8_out,
       controlled_buffer_9_out, controlled_buffer_10_out, controlled_buffer_11_out, not_1_out, not_2_out,
       not_3_out, not_4_out, not_5_out, not_6_out, not_7_out;

  not not_1 (not_1_out, R0);
  not not_2 (not_2_out, R1);
  assign controlled_buffer_1_out = R0 ? controlled_buffer_3_out : 1'bz;  // Controlled_Buffer controlled_buffer_1
  assign controlled_buffer_2_out = not_1_out ? controlled_buffer_3_out : 1'bz;  // Controlled_Buffer controlled_buffer_2
  assign controlled_buffer_3_out = RW ? 1'b0 : 1'bz;  // Controlled_Buffer controlled_buffer_3
  not not_3 (not_3_out, RW);
  assign _11 = not_3_out ? 1'b1 : 1'bz;  // Controlled_Buffer controlled_buffer_4
  assign _10 = not_3_out ? 1'b1 : 1'bz;  // Controlled_Buffer controlled_buffer_5
  assign _01 = not_3_out ? 1'b1 : 1'bz;  // Controlled_Buffer controlled_buffer_6
  assign _00 = not_3_out ? 1'b1 : 1'bz;  // Controlled_Buffer controlled_buffer_7
  assign controlled_buffer_8_out = R1 ? controlled_buffer_1_out : 1'bz;  // Controlled_Buffer controlled_buffer_8
  not not_4 (not_4_out, controlled_buffer_8_out);
  assign controlled_buffer_9_out = not_2_out ? controlled_buffer_1_out : 1'bz;  // Controlled_Buffer controlled_buffer_9
  not not_5 (not_5_out, controlled_buffer_9_out);
  assign controlled_buffer_10_out = R1 ? controlled_buffer_2_out : 1'bz;  // Controlled_Buffer controlled_buffer_10
  not not_6 (not_6_out, controlled_buffer_10_out);
  not not_7 (not_7_out, controlled_buffer_11_out);
  assign controlled_buffer_11_out = not_2_out ? controlled_buffer_2_out : 1'bz;  // Controlled_Buffer controlled_buffer_11
  assign _11 = RW ? not_4_out : 1'bz;  // Controlled_Buffer controlled_buffer_12
  assign _10 = RW ? not_5_out : 1'bz;  // Controlled_Buffer controlled_buffer_13
  assign _01 = RW ? not_6_out : 1'bz;  // Controlled_Buffer controlled_buffer_14
  assign _00 = RW ? not_7_out : 1'bz;  // Controlled_Buffer controlled_buffer_15
endmodule
