// Logisim project MDEC.circ as structural Verilog: 30 circuits, main circuit IDCT_pass1
module IDCT_pass1 (
  input  AND_FLAG,
  input  D11,
  input  D10,
  input  D9,
  input  D8,
  input  D7,
  input  D6,
  input  D5,
  input  D4,
  input  D3,
  input  D2,
  input  D1,
  input  D0,
  input  S12,
  input  S11,
  input  S10,
  input  S09,
  input  S08,
  input  S07,
  input  S06,
  input  S05,
  input  S04,
  input  S03,
  input  S02,
  input  S01,
  input  S00,
  output RES16,
  output RES15,
  output RES14,
  output RES13,
  output RES12,
  output RES11,
  output RES10,
  output RES09,
  output RES08,
  output RES07,
  output RES06,
  output RES05,
  output RES04,
  output RES03,
  output RES02,
  output RES01,
  output RES00
);

  wire clock_1_out, d_ff_1_q, d_ff_2_q, d_ff_3_q, d_ff_4_q, d_ff_5_q, d_ff_6_q, d_ff_7_q, d_ff_8_q, d_ff_9_q,
       d_ff_10_q, d_ff_11_q, d_ff_12_q, d_ff_13_q, mux_control_1_l0_d1, mux_control_1_l0_d2,
       mux_control_1_l1_d1, mux_control_1_l1_d2, mux_control_1_l2_d1, mux_control_1_l2_d2,
       mux_control_1_l3_d1, mux_control_1_l3_d2, mux_control_1_l4_d1, mux_control_1_l4_d2,
       mux_control_1_l5_d1, mux_control_1_l5_d2, muxs_1_l0_00, muxs_1_l0_01, muxs_1_l0_02, muxs_1_l0_03,
       muxs_1_l0_04, muxs_1_l0_05, muxs_1_l0_06, muxs_1_l0_07, muxs_1_l0_08, muxs_1_l0_09, muxs_1_l0_10,
       muxs_1_l0_11, muxs_1_l0_12, muxs_1_l0_13, muxs_1_l1_00, muxs_1_l1_01, muxs_1_l1_02, muxs_1_l1_03,
       muxs_1_l1_04, muxs_1_l1_05, muxs_1_l1_06, muxs_1_l1_07, muxs_1_l1_08, muxs_1_l1_09, muxs_1_l1_10,
       muxs_1_l1_11, muxs_1_l1_12, muxs_1_l1_13, muxs_1_l2_00, muxs_1_l2_01, muxs_1_l2_02, muxs_1_l2_03,
       muxs_1_l2_04, muxs_1_l2_05, muxs_1_l2_06, muxs_1_l2_07, muxs_1_l2_08, muxs_1_l2_09, muxs_1_l2_10,
       muxs_1_l2_11, muxs_1_l2_12, muxs_1_l2_13, muxs_1_l3_00, muxs_1_l3_01, muxs_1_l3_02, muxs_1_l3_03,
       muxs_1_l3_04, muxs_1_l3_05, muxs_1_l3_06, muxs_1_l3_07, muxs_1_l3_08, muxs_1_l3_09, muxs_1_l3_10,
       muxs_1_l3_11, muxs_1_l3_12, muxs_1_l3_13, muxs_1_l4_00, muxs_1_l4_01, muxs_1_l4_02, muxs_1_l4_03,
       muxs_1_l4_04, muxs_1_l4_05, muxs_1_l4_06, muxs_1_l4_07, muxs_1_l4_08, muxs_1_l4_09, muxs_1_l4_10,
       muxs_1_l4_11, muxs_1_l4_12, muxs_1_l4_13, muxs_1_l5_00, muxs_1_l5_01, muxs_1_l5_02, muxs_1_l5_03,
       muxs_1_l5_04, muxs_1_l5_05, muxs_1_l5_06, muxs_1_l5_07, muxs_1_l5_08, muxs_1_l5_09, muxs_1_l5_10,
       muxs_1_l5_11, muxs_1_l5_12, muxs_1_l5_13, not_1_out, not_2_out, not_3_out, not_4_out, not_5_out,
       not_6_out;

  MUX_CONTROL mux_control_1 (
    ._11(D11), ._10(D10), ._09(D9), ._08(D8), ._07(D7), ._06(D6), ._05(D5), ._04(D4), ._03(D3), ._02(D2),
    ._01(D1), ._00(D0), .L5_D2(mux_control_1_l5_d2), .L5_D1(mux_control_1_l5_d1),
    .L4_D2(mux_control_1_l4_d2), .L4_D1(mux_control_1_l4_d1), .L3_D2(mux_control_1_l3_d2),
    .L3_D1(mux_control_1_l3_d1), .L2_D2(mux_control_1_l2_d2), .L2_D1(mux_control_1_l2_d1),
    .L1_D2(mux_control_1_l1_d2), .L1_D1(mux_control_1_l1_d1), .L0_D2(mux_control_1_l0_d2),
    .L0_D1(mux_control_1_l0_d1));
  Clock #(.highDuration(4), .lowDuration(4)) clock_1 (.out(clock_1_out));
  TREE tree_1 (
    .RES00(RES00), .RES01(RES01), .RES02(RES02), .RES03(RES03), .RES04(RES04), .RES05(RES05), .RES06(RES06),
    .RES07(RES07), .RES08(RES08), .RES09(RES09), .RES10(RES10), .RES11(RES11), .RES12(RES12), .RES13(RES13),
    .RES14(RES14), .RES15(RES15), .RES16(RES16), .IDCT_CLK(clock_1_out), .AND_FLAG(AND_FLAG), .MUL00(D0),
    .MUL01(D1), .MUL02(D2), .MUL03(D3), .MUL04(D4), .MUL05(D5), .MUL06(D6), .MUL07(D7), .MUL08(D8),
    .MUL09(D9), .MUL10(D10), .MUL11(D11), .L0_00(muxs_1_l0_00), .L0_01(muxs_1_l0_01), .L0_02(muxs_1_l0_02),
    .L0_03(muxs_1_l0_03), .L0_04(muxs_1_l0_04), .L0_05(muxs_1_l0_05), .L0_06(muxs_1_l0_06),
    .L0_07(muxs_1_l0_07), .L0_08(muxs_1_l0_08), .L0_09(muxs_1_l0_09), .L0_10(muxs_1_l0_10),
    .L0_11(muxs_1_l0_11), .L0_12(muxs_1_l0_12), .L0_13(muxs_1_l0_13), .L1_00(muxs_1_l1_00),
    .L1_01(muxs_1_l1_01), .L1_02(muxs_1_l1_02), .L1_03(muxs_1_l1_03), .L1_04(muxs_1_l1_04),
    .L1_05(muxs_1_l1_05), .L1_06(muxs_1_l1_06), .L1_07(muxs_1_l1_07), .L1_08(muxs_1_l1_08),
    .L1_09(muxs_1_l1_09), .L1_10(muxs_1_l1_10), .L1_11(muxs_1_l1_11), .L1_12(muxs_1_l1_12),
    .L2_00(muxs_1_l2_00), .L2_01(muxs_1_l2_01), .L2_02(muxs_1_l2_02), .L2_03(muxs_1_l2_03),
    .L2_04(muxs_1_l2_04), .L2_05(muxs_1_l2_05), .L2_06(muxs_1_l2_06), .L2_07(muxs_1_l2_07),
    .L2_08(muxs_1_l2_08), .L2_09(muxs_1_l2_09), .L2_10(muxs_1_l2_10), .L2_11(muxs_1_l2_11),
    .L2_12(muxs_1_l2_12), .L2_13(muxs_1_l2_13), .L3_00(muxs_1_l3_00), .L3_01(muxs_1_l3_01),
    .L3_02(muxs_1_l3_02), .L3_03(muxs_1_l3_03), .L3_05(muxs_1_l3_05), .L3_06(muxs_1_l3_06),
    .L3_07(muxs_1_l3_07), .L3_08(muxs_1_l3_08), .L3_09(muxs_1_l3_09), .L3_10(muxs_1_l3_10),
    .L3_11(muxs_1_l3_11), .L3_12(muxs_1_l3_12), .L3_13(muxs_1_l3_13), .L4_00(muxs_1_l4_00),
    .L4_01(muxs_1_l4_01), .L4_02(muxs_1_l4_02), .L4_03(muxs_1_l4_04), .L4_04(muxs_1_l4_05),
    .L4_05(muxs_1_l4_03), .L4_06(muxs_1_l4_06), .L4_07(muxs_1_l4_07), .L4_08(muxs_1_l4_08),
    .L4_09(muxs_1_l4_09), .L4_10(muxs_1_l4_10), .L4_11(muxs_1_l4_11), .L4_12(muxs_1_l4_12),
    .L4_13(muxs_1_l4_13), .L5_00(muxs_1_l5_00), .L5_01(muxs_1_l5_01), .L5_02(muxs_1_l5_02),
    .L5_03(muxs_1_l5_03), .L5_04(muxs_1_l5_04), .L5_05(muxs_1_l5_05), .L5_06(muxs_1_l5_06),
    .L5_07(muxs_1_l5_07), .L5_08(muxs_1_l5_08), .L5_09(muxs_1_l5_09), .L5_10(muxs_1_l5_10),
    .L5_11(muxs_1_l5_11), .L5_12(muxs_1_l5_12), .L5_13(muxs_1_l5_13), .L3_04(muxs_1_l3_04),
    .L1_13(muxs_1_l1_13));
  MUXs muxs_1 (
    .L5_C1(D11), .L5_C2(not_1_out), .L5_D1(mux_control_1_l5_d1), .L5_D2(mux_control_1_l5_d2), .L4_C1(D9),
    .L4_C2(not_2_out), .L4_D1(mux_control_1_l4_d1), .L4_D2(mux_control_1_l4_d2), .L3_C1(D7),
    .L3_C2(not_3_out), .L3_D1(mux_control_1_l3_d1), .L3_D2(mux_control_1_l3_d2), .L2_C1(D5),
    .L2_C2(not_4_out), .L2_D1(mux_control_1_l2_d1), .L2_D2(mux_control_1_l2_d2), .L1_C1(D3),
    .L1_C2(not_5_out), .L1_D1(mux_control_1_l1_d1), .L1_D2(mux_control_1_l1_d2), .L0_C1(D1),
    .L0_C2(not_6_out), .L0_D1(mux_control_1_l0_d1), .L0_D2(mux_control_1_l0_d2), .S2(d_ff_11_q),
    .S3(d_ff_10_q), .S4(d_ff_9_q), .S5(d_ff_8_q), .S6(d_ff_7_q), .S7(d_ff_6_q), .S8(d_ff_5_q), .S9(d_ff_4_q),
    .S10(d_ff_3_q), .S11(d_ff_2_q), .S12(d_ff_1_q), .L4_00(muxs_1_l4_00), .L4_01(muxs_1_l4_01),
    .L4_02(muxs_1_l4_02), .L4_04(muxs_1_l4_04), .L4_05(muxs_1_l4_05), .L4_03(muxs_1_l4_03),
    .L4_06(muxs_1_l4_06), .L4_07(muxs_1_l4_07), .L4_08(muxs_1_l4_08), .L4_09(muxs_1_l4_09),
    .L4_10(muxs_1_l4_10), .L4_11(muxs_1_l4_11), .L4_12(muxs_1_l4_12), .L4_13(muxs_1_l4_13),
    .L3_00(muxs_1_l3_00), .L3_01(muxs_1_l3_01), .L3_02(muxs_1_l3_02), .L3_03(muxs_1_l3_03),
    .L3_04(muxs_1_l3_04), .L3_05(muxs_1_l3_05), .L3_06(muxs_1_l3_06), .L3_07(muxs_1_l3_07),
    .L3_08(muxs_1_l3_08), .L3_09(muxs_1_l3_09), .L3_10(muxs_1_l3_10), .L3_11(muxs_1_l3_11),
    .L3_12(muxs_1_l3_12), .L3_13(muxs_1_l3_13), .L5_00(muxs_1_l5_00), .L5_01(muxs_1_l5_01),
    .L5_02(muxs_1_l5_02), .L5_03(muxs_1_l5_03), .L5_04(muxs_1_l5_04), .L5_05(muxs_1_l5_05),
    .L5_06(muxs_1_l5_06), .L5_07(muxs_1_l5_07), .L5_08(muxs_1_l5_08), .L5_09(muxs_1_l5_09),
    .L5_10(muxs_1_l5_10), .L5_11(muxs_1_l5_11), .L5_12(muxs_1_l5_12), .L5_13(muxs_1_l5_13),
    .L2_00(muxs_1_l2_00), .L2_01(muxs_1_l2_01), .L2_02(muxs_1_l2_02), .L2_03(muxs_1_l2_03),
    .L2_04(muxs_1_l2_04), .L2_05(muxs_1_l2_05), .L2_06(muxs_1_l2_06), .L2_07(muxs_1_l2_07),
    .L2_08(muxs_1_l2_08), .L2_09(muxs_1_l2_09), .L2_10(muxs_1_l2_10), .L2_11(muxs_1_l2_11),
    .L2_12(muxs_1_l2_12), .L2_13(muxs_1_l2_13), .L1_00(muxs_1_l1_00), .L1_01(muxs_1_l1_01),
    .L1_02(muxs_1_l1_02), .L1_03(muxs_1_l1_03), .L1_04(muxs_1_l1_04), .L1_05(muxs_1_l1_05),
    .L1_06(muxs_1_l1_06), .L1_07(muxs_1_l1_07), .L1_08(muxs_1_l1_08), .L1_09(muxs_1_l1_09),
    .L1_10(muxs_1_l1_10), .L1_11(muxs_1_l1_11), .L1_12(muxs_1_l1_12), .L1_13(muxs_1_l1_13),
    .L0_00(muxs_1_l0_00), .L0_01(muxs_1_l0_01), .L0_02(muxs_1_l0_02), .L0_03(muxs_1_l0_03),
    .L0_04(muxs_1_l0_04), .L0_05(muxs_1_l0_05), .L0_06(muxs_1_l0_06), .L0_07(muxs_1_l0_07),
    .L0_08(muxs_1_l0_08), .L0_09(muxs_1_l0_09), .L0_10(muxs_1_l0_10), .L0_11(muxs_1_l0_11),
    .L0_12(muxs_1_l0_12), .L0_13(muxs_1_l0_13), .S1(d_ff_12_q), .S0(d_ff_13_q));
  not not_1 (not_1_out, D11);
  not not_2 (not_2_out, D9);
  not not_3 (not_3_out, D7);
  not not_4 (not_4_out, D5);
  not not_5 (not_5_out, D3);
  not not_6 (not_6_out, D1);
  D_Flip_Flop d_ff_1 (.clk(clock_1_out), .D(S12), .Q(d_ff_1_q));  // open: Qn, preset, en, reset
  D_Flip_Flop d_ff_2 (.clk(clock_1_out), .D(S11), .Q(d_ff_2_q));  // open: Qn, preset, en, reset
  D_Flip_Flop d_ff_3 (.clk(clock_1_out), .D(S10), .Q(d_ff_3_q));  // open: Qn, preset, en, reset
  D_Flip_Flop d_ff_4 (.clk(clock_1_out), .D(S09), .Q(d_ff_4_q));  // open: Qn, preset, en, reset
  D_Flip_Flop d_ff_5 (.clk(clock_1_out), .D(S08), .Q(d_ff_5_q));  // open: Qn, preset, en, reset
  D_Flip_Flop d_ff_6 (.clk(clock_1_out), .D(S07), .Q(d_ff_6_q));  // open: Qn, preset, en, reset
  D_Flip_Flop d_ff_7 (.clk(clock_1_out), .D(S06), .Q(d_ff_7_q));  // open: Qn, preset, en, reset
  D_Flip_Flop d_ff_8 (.clk(clock_1_out), .D(S05), .Q(d_ff_8_q));  // open: Qn, preset, en, reset
  D_Flip_Flop d_ff_9 (.clk(clock_1_out), .D(S04), .Q(d_ff_9_q));  // open: Qn, preset, en, reset
  D_Flip_Flop d_ff_10 (.clk(clock_1_out), .D(S03), .Q(d_ff_10_q));  // open: Qn, preset, en, reset
  D_Flip_Flop d_ff_11 (.clk(clock_1_out), .D(S02), .Q(d_ff_11_q));  // open: Qn, preset, en, reset
  D_Flip_Flop d_ff_12 (.clk(clock_1_out), .D(S01), .Q(d_ff_12_q));  // open: Qn, preset, en, reset
  D_Flip_Flop d_ff_13 (.clk(clock_1_out), .D(S00), .Q(d_ff_13_q));  // open: Qn, preset, en, reset
endmodule

module MUX_ARRAY (
  input  C1,
  input  C2,
  input  in,
  input  _01,
  input  _00,
  input  _11,
  input  _10,
  input  _21,
  input  _20,
  input  _31,
  input  _30,
  input  D1,
  input  D2,
  output _02,
  output _12,
  output _22,
  output _32,
  output out
);

  wire transistor_2_out, transistor_4_out, transistor_8_out, transistor_9_out, transistor_13_out,
       transistor_14_out, transistor_18_out, transistor_21_out, transistor_26_out, transistor_28_out,
       transistor_32_out, transistor_33_out, transistor_37_out, transistor_38_out, transistor_42_out,
       transistor_45_out, transistor_49_out;

  Transistor #(.gate("br")) transistor_1 (.in(transistor_2_out), .out(_02), .gate(D1));
  Transistor #(.gate("br")) transistor_2 (.in(1'b1), .out(transistor_2_out), .gate(in));
  Transistor #(.gate("br")) transistor_3 (.in(transistor_2_out), .out(_02), .gate(transistor_9_out));
  Transistor #(.\type ("n")) transistor_4 (.in(1'b0), .out(transistor_4_out), .gate(in));
  Transistor #(.\type ("n")) transistor_5 (.in(transistor_4_out), .out(_02), .gate(D2));
  Transistor #(.\type ("n")) transistor_6 (.in(transistor_8_out), .out(_02), .gate(D1));
  Transistor #(.gate("br")) transistor_7 (.in(1'b1), .out(transistor_2_out), .gate(D2));
  Transistor #(.\type ("n")) transistor_8 (.in(1'b0), .out(transistor_8_out), .gate(transistor_9_out));
  Transistor #(.gate("br")) transistor_9 (.in(_00), .out(transistor_9_out), .gate(C2));
  Transistor #(.gate("br")) transistor_10 (.in(_01), .out(transistor_9_out), .gate(C1));
  Transistor #(.\type ("n")) transistor_11 (.in(_00), .out(transistor_9_out), .gate(C1));
  Transistor #(.\type ("n")) transistor_12 (.in(_01), .out(transistor_9_out), .gate(C2));
  Transistor #(.gate("br")) transistor_13 (.in(1'b1), .out(transistor_13_out), .gate(transistor_9_out));
  Transistor #(.\type ("n")) transistor_14 (.in(1'b0), .out(transistor_14_out), .gate(transistor_9_out));
  Transistor #(.gate("br")) transistor_15 (.in(1'b1), .out(transistor_13_out), .gate(D2));
  Transistor #(.gate("br")) transistor_16 (.in(transistor_13_out), .out(_12), .gate(D1));
  Transistor #(.gate("br")) transistor_17 (.in(transistor_13_out), .out(_12), .gate(transistor_21_out));
  Transistor #(.\type ("n")) transistor_18 (.in(1'b0), .out(transistor_18_out), .gate(transistor_21_out));
  Transistor #(.\type ("n")) transistor_19 (.in(transistor_14_out), .out(_12), .gate(D2));
  Transistor #(.\type ("n")) transistor_20 (.in(transistor_18_out), .out(_12), .gate(D1));
  Transistor #(.gate("br")) transistor_21 (.in(_10), .out(transistor_21_out), .gate(C2));
  Transistor #(.gate("br")) transistor_22 (.in(_11), .out(transistor_21_out), .gate(C1));
  Transistor #(.\type ("n")) transistor_23 (.in(_11), .out(transistor_21_out), .gate(C2));
  Transistor #(.\type ("n")) transistor_24 (.in(_10), .out(transistor_21_out), .gate(C1));
  Transistor #(.gate("br")) transistor_25 (.in(transistor_26_out), .out(_22), .gate(transistor_33_out));
  Transistor #(.gate("br")) transistor_26 (.in(1'b1), .out(transistor_26_out), .gate(transistor_21_out));
  Transistor #(.gate("br")) transistor_27 (.in(transistor_26_out), .out(_22), .gate(D1));
  Transistor #(.\type ("n")) transistor_28 (.in(1'b0), .out(transistor_28_out), .gate(transistor_21_out));
  Transistor #(.\type ("n")) transistor_29 (.in(transistor_32_out), .out(_22), .gate(D1));
  Transistor #(.\type ("n")) transistor_30 (.in(transistor_28_out), .out(_22), .gate(D2));
  Transistor #(.gate("br")) transistor_31 (.in(1'b1), .out(transistor_26_out), .gate(D2));
  Transistor #(.\type ("n")) transistor_32 (.in(1'b0), .out(transistor_32_out), .gate(transistor_33_out));
  Transistor #(.gate("br")) transistor_33 (.in(_21), .out(transistor_33_out), .gate(C1));
  Transistor #(.gate("br")) transistor_34 (.in(_20), .out(transistor_33_out), .gate(C2));
  Transistor #(.\type ("n")) transistor_35 (.in(_21), .out(transistor_33_out), .gate(C2));
  Transistor #(.\type ("n")) transistor_36 (.in(_20), .out(transistor_33_out), .gate(C1));
  Transistor #(.gate("br")) transistor_37 (.in(1'b1), .out(transistor_37_out), .gate(transistor_33_out));
  Transistor #(.\type ("n")) transistor_38 (.in(1'b0), .out(transistor_38_out), .gate(transistor_33_out));
  Transistor #(.gate("br")) transistor_39 (.in(transistor_37_out), .out(_32), .gate(D1));
  Transistor #(.gate("br")) transistor_40 (.in(transistor_37_out), .out(_32), .gate(transistor_45_out));
  Transistor #(.gate("br")) transistor_41 (.in(1'b1), .out(transistor_37_out), .gate(D2));
  Transistor #(.\type ("n")) transistor_42 (.in(1'b0), .out(transistor_42_out), .gate(transistor_45_out));
  Transistor #(.\type ("n")) transistor_43 (.in(transistor_38_out), .out(_32), .gate(D2));
  Transistor #(.\type ("n")) transistor_44 (.in(transistor_42_out), .out(_32), .gate(D1));
  Transistor #(.gate("br")) transistor_45 (.in(_31), .out(transistor_45_out), .gate(C1));
  Transistor #(.gate("br")) transistor_46 (.in(_30), .out(transistor_45_out), .gate(C2));
  Transistor #(.\type ("n")) transistor_47 (.in(_30), .out(transistor_45_out), .gate(C1));
  Transistor #(.\type ("n")) transistor_48 (.in(_31), .out(transistor_45_out), .gate(C2));
  Transistor #(.gate("br")) transistor_49 (.in(1'b1), .out(transistor_49_out), .gate(transistor_45_out));
  Transistor #(.\type ("n")) transistor_50 (.in(1'b0), .out(transistor_49_out), .gate(transistor_45_out));
  Transistor #(.gate("br")) transistor_51 (.in(1'b1), .out(out), .gate(transistor_49_out));
  Transistor #(.\type ("n")) transistor_52 (.in(1'b0), .out(out), .gate(transistor_49_out));

  // Notes on the sheet:
  //   MUX ARRAY
endmodule

module IMUX (
  input  sel,
  input  b___in0,
  input  c___in1,
  output out
);

  wire transistor_2_out, transistor_3_out;

  Transistor #(.gate("br")) transistor_1 (.in(1'b1), .out(out), .gate(transistor_3_out));
  Transistor #(.gate("br")) transistor_2 (.in(1'b1), .out(transistor_2_out), .gate(sel));
  Transistor #(.gate("br")) transistor_3 (.in(b___in0), .out(transistor_3_out), .gate(sel));
  Transistor #(.gate("br")) transistor_4 (.in(c___in1), .out(transistor_3_out), .gate(transistor_2_out));
  Transistor #(.\type ("n")) transistor_5 (.in(1'b0), .out(out), .gate(transistor_3_out));
  Transistor #(.\type ("n")) transistor_6 (.in(1'b0), .out(transistor_2_out), .gate(sel));
  Transistor #(.\type ("n")) transistor_7 (.in(b___in0), .out(transistor_3_out), .gate(transistor_2_out));
  Transistor #(.\type ("n")) transistor_8 (.in(c___in1), .out(transistor_3_out), .gate(sel));

  // Notes on the sheet:
  //   INVERTING MUX
endmodule

module _12_OAI (
  input  a,
  input  b,
  input  c,
  output out
);

  wire transistor_3_out, transistor_5_out;

  Transistor #(.gate("br")) transistor_1 (.in(1'b1), .out(out), .gate(a));
  Transistor #(.gate("br")) transistor_2 (.in(transistor_3_out), .out(out), .gate(b));
  Transistor #(.gate("br")) transistor_3 (.in(1'b1), .out(transistor_3_out), .gate(c));
  Transistor #(.\type ("n")) transistor_4 (.in(transistor_5_out), .out(out), .gate(a));
  Transistor #(.\type ("n")) transistor_5 (.in(1'b0), .out(transistor_5_out), .gate(b));
  Transistor #(.\type ("n")) transistor_6 (.in(1'b0), .out(transistor_5_out), .gate(c));

  // Notes on the sheet:
  //   12-OAI
  //   out = ~ (a & (b|c))
endmodule

module MUX_CONTROL (
  input  _11,
  input  _10,
  input  _09,
  input  _08,
  input  _07,
  input  _06,
  input  _05,
  input  _04,
  input  _03,
  input  _02,
  input  _01,
  input  _00,
  output L5_D2,
  output L5_D1,
  output L4_D2,
  output L4_D1,
  output L3_D2,
  output L3_D1,
  output L2_D2,
  output L2_D1,
  output L1_D2,
  output L1_D1,
  output L0_D2,
  output L0_D1
);

  wire nand_1_out, nand_2_out, nand_3_out, nand_4_out, nand_5_out, nand_6_out, xnor_1_out, xnor_2_out,
       xnor_3_out, xnor_4_out, xnor_5_out, xnor_6_out, xor_1_out, xor_2_out, xor_3_out, xor_4_out, xor_5_out,
       xor_6_out;

  xor xor_1 (xor_1_out, _11, _10);
  xnor xnor_1 (xnor_1_out, _10, _09);
  xor xor_2 (xor_2_out, _09, _08);
  xnor xnor_2 (xnor_2_out, _08, _07);
  xor xor_3 (xor_3_out, _07, _06);
  xnor xnor_3 (xnor_3_out, _06, _05);
  xor xor_4 (xor_4_out, _05, _04);
  xnor xnor_4 (xnor_4_out, _04, _03);
  xor xor_5 (xor_5_out, _03, _02);
  xnor xnor_5 (xnor_5_out, _02, _01);
  xor xor_6 (xor_6_out, _01, _00);
  xnor xnor_6 (xnor_6_out, _00, 1'b0);
  nand nand_1 (nand_1_out, xor_1_out, xnor_1_out);
  nand nand_2 (nand_2_out, xor_2_out, xnor_2_out);
  nand nand_3 (nand_3_out, xor_3_out, xnor_3_out);
  nand nand_4 (nand_4_out, xor_4_out, xnor_4_out);
  nand nand_5 (nand_5_out, xor_5_out, xnor_5_out);
  nand nand_6 (nand_6_out, xor_6_out, xnor_6_out);
  not not_1 (L5_D2, nand_1_out);
  not not_2 (L5_D1, xnor_1_out);
  not not_3 (L4_D2, nand_2_out);
  not not_4 (L4_D1, xnor_2_out);
  not not_5 (L3_D2, nand_3_out);
  not not_6 (L3_D1, xnor_3_out);
  not not_7 (L2_D2, nand_4_out);
  not not_8 (L2_D1, xnor_4_out);
  not not_9 (L1_D2, nand_5_out);
  not not_10 (L1_D1, xnor_5_out);
  not not_11 (L0_D2, nand_6_out);
  not not_12 (L0_D1, xnor_6_out);
endmodule

module MUXs (
  input  L5_C1,
  input  L5_C2,
  input  L5_D1,
  input  L5_D2,
  input  L4_C1,
  input  L4_C2,
  input  L4_D1,
  input  L4_D2,
  input  L3_C1,
  input  L3_C2,
  input  L3_D1,
  input  L3_D2,
  input  L2_C1,
  input  L2_C2,
  input  L2_D1,
  input  L2_D2,
  input  L1_C1,
  input  L1_C2,
  input  L1_D1,
  input  L1_D2,
  input  L0_C1,
  input  L0_C2,
  input  L0_D1,
  input  L0_D2,
  input  S0,
  input  S1,
  input  S2,
  input  S3,
  input  S4,
  input  S5,
  input  S6,
  input  S7,
  input  S8,
  input  S9,
  input  S10,
  input  S11,
  input  S12,
  output L5_00,
  output L5_01,
  output L5_02,
  output L5_03,
  output L5_04,
  output L5_05,
  output L5_06,
  output L5_07,
  output L5_08,
  output L5_09,
  output L5_10,
  output L5_11,
  output L5_12,
  output L5_13,
  output L4_00,
  output L4_01,
  output L4_02,
  output L4_03,
  output L4_04,
  output L4_05,
  output L4_06,
  output L4_07,
  output L4_08,
  output L4_09,
  output L4_10,
  output L4_11,
  output L4_12,
  output L4_13,
  output L3_00,
  output L3_01,
  output L3_02,
  output L3_03,
  output L3_04,
  output L3_05,
  output L3_06,
  output L3_07,
  output L3_08,
  output L3_09,
  output L3_10,
  output L3_11,
  output L3_12,
  output L3_13,
  output L2_00,
  output L2_01,
  output L2_02,
  output L2_03,
  output L2_04,
  output L2_05,
  output L2_06,
  output L2_07,
  output L2_08,
  output L2_09,
  output L2_10,
  output L2_11,
  output L2_12,
  output L2_13,
  output L1_00,
  output L1_01,
  output L1_02,
  output L1_03,
  output L1_04,
  output L1_05,
  output L1_06,
  output L1_07,
  output L1_08,
  output L1_09,
  output L1_10,
  output L1_11,
  output L1_12,
  output L1_13,
  output L0_00,
  output L0_01,
  output L0_02,
  output L0_03,
  output L0_04,
  output L0_05,
  output L0_06,
  output L0_07,
  output L0_08,
  output L0_09,
  output L0_10,
  output L0_11,
  output L0_12,
  output L0_13
);

  wire mux_array_1_out, mux_array_2_out, mux_array_3_out, mux_array_4_out, mux_array_5_out, mux_array_6_out,
       mux_array_7_out, mux_array_8_out, mux_array_9_out, mux_array_10_out, mux_array_11_out,
       mux_array_12_out, mux_array_13_out, mux_array_14_out, mux_array_15_out, mux_array_16_out,
       mux_array_17_out, mux_array_18_out, not_1_out, not_2_out, not_3_out, not_4_out, not_5_out, not_6_out,
       not_7_out, not_8_out, not_9_out, not_10_out, not_11_out, not_12_out, not_13_out, not_14_out;

  not not_1 (not_1_out, S0);
  MUX_ARRAY mux_array_1 (
    .C1(L5_C1), .C2(L5_C2), .in(1'b1), .D1(L5_D1), .D2(L5_D2), .out(mux_array_1_out), ._22(L5_00),
    ._32(L5_01), ._01(1'b0), ._00(1'b0), ._11(L5_C2), ._10(L5_C2), ._21(not_1_out), ._20(S0),
    ._31(not_2_out), ._30(S1));  // open: _02, _12
  MUX_ARRAY mux_array_2 (
    .C1(L4_C1), .C2(L4_C2), .in(1'b1), .D1(L4_D1), .D2(L4_D2), .out(mux_array_2_out), ._22(L4_00),
    ._32(L4_01), ._01(1'b0), ._00(1'b0), ._11(L4_C2), ._10(L4_C2), ._21(not_1_out), ._20(S0),
    ._31(not_2_out), ._30(S1));  // open: _02, _12
  MUX_ARRAY mux_array_3 (
    .C1(L3_C1), .C2(L3_C2), .in(1'b1), .D1(L3_D1), .D2(L3_D2), .out(mux_array_3_out), ._22(L3_00),
    ._32(L3_01), ._01(1'b0), ._00(1'b0), ._11(L3_C2), ._10(L3_C2), ._21(not_1_out), ._20(S0),
    ._31(not_2_out), ._30(S1));  // open: _02, _12
  MUX_ARRAY mux_array_4 (
    .C1(L2_C1), .C2(L2_C2), .in(1'b1), .D1(L2_D1), .D2(L2_D2), .out(mux_array_4_out), ._22(L2_00),
    ._32(L2_01), ._01(1'b0), ._00(1'b0), ._11(L2_C2), ._10(L2_C2), ._21(not_1_out), ._20(S0),
    ._31(not_2_out), ._30(S1));  // open: _02, _12
  MUX_ARRAY mux_array_5 (
    .C1(L1_C1), .C2(L1_C2), .in(1'b1), .D1(L1_D1), .D2(L1_D2), .out(mux_array_5_out), ._22(L1_00),
    ._32(L1_01), ._01(1'b0), ._00(1'b0), ._11(L1_C2), ._10(L1_C2), ._21(not_1_out), ._20(S0),
    ._31(not_2_out), ._30(S1));  // open: _02, _12
  MUX_ARRAY mux_array_6 (
    .C1(L0_C1), .C2(L0_C2), .in(1'b1), .D1(L0_D1), .D2(L0_D2), .out(mux_array_6_out), ._22(L0_00),
    ._32(L0_01), ._01(1'b0), ._00(1'b0), ._11(L0_C2), ._10(L0_C2), ._21(not_1_out), ._20(S0),
    ._31(not_2_out), ._30(S1));  // open: _02, _12
  not not_2 (not_2_out, S1);
  not not_3 (not_3_out, S2);
  not not_4 (not_4_out, S3);
  not not_5 (not_5_out, S4);
  not not_6 (not_6_out, S5);
  MUX_ARRAY mux_array_7 (
    .C1(L5_C1), .C2(L5_C2), .in(mux_array_1_out), .D1(L5_D1), .D2(L5_D2), .out(mux_array_7_out), ._02(L5_02),
    ._12(L5_03), ._22(L5_04), ._32(L5_05), ._01(not_3_out), ._00(S2), ._11(not_4_out), ._10(S3),
    ._21(not_5_out), ._20(S4), ._31(not_6_out), ._30(S5));
  MUX_ARRAY mux_array_8 (
    .C1(L4_C1), .C2(L4_C2), .in(mux_array_2_out), .D1(L4_D1), .D2(L4_D2), .out(mux_array_8_out), ._02(L4_02),
    ._12(L4_03), ._22(L4_04), ._32(L4_05), ._01(not_3_out), ._00(S2), ._11(not_4_out), ._10(S3),
    ._21(not_5_out), ._20(S4), ._31(not_6_out), ._30(S5));
  MUX_ARRAY mux_array_9 (
    .C1(L3_C1), .C2(L3_C2), .in(mux_array_3_out), .D1(L3_D1), .D2(L3_D2), .out(mux_array_9_out), ._02(L3_02),
    ._12(L3_03), ._22(L3_04), ._32(L3_05), ._01(not_3_out), ._00(S2), ._11(not_4_out), ._10(S3),
    ._21(not_5_out), ._20(S4), ._31(not_6_out), ._30(S5));
  MUX_ARRAY mux_array_10 (
    .C1(L2_C1), .C2(L2_C2), .in(mux_array_4_out), .D1(L2_D1), .D2(L2_D2), .out(mux_array_10_out),
    ._02(L2_02), ._12(L2_03), ._22(L2_04), ._32(L2_05), ._01(not_3_out), ._00(S2), ._11(not_4_out), ._10(S3),
    ._21(not_5_out), ._20(S4), ._31(not_6_out), ._30(S5));
  MUX_ARRAY mux_array_11 (
    .C1(L1_C1), .C2(L1_C2), .in(mux_array_5_out), .D1(L1_D1), .D2(L1_D2), .out(mux_array_11_out),
    ._02(L1_02), ._12(L1_03), ._22(L1_04), ._32(L1_05), ._01(not_3_out), ._00(S2), ._11(not_4_out), ._10(S3),
    ._21(not_5_out), ._20(S4), ._31(not_6_out), ._30(S5));
  MUX_ARRAY mux_array_12 (
    .C1(L0_C1), .C2(L0_C2), .in(mux_array_6_out), .D1(L0_D1), .D2(L0_D2), .out(mux_array_12_out),
    ._02(L0_02), ._12(L0_03), ._22(L0_04), ._32(L0_05), ._01(not_3_out), ._00(S2), ._11(not_4_out), ._10(S3),
    ._21(not_5_out), ._20(S4), ._31(not_6_out), ._30(S5));
  not not_7 (not_7_out, S6);
  not not_8 (not_8_out, S7);
  not not_9 (not_9_out, S8);
  MUX_ARRAY mux_array_13 (
    .C1(L5_C1), .C2(L5_C2), .in(mux_array_7_out), .D1(L5_D1), .D2(L5_D2), .out(mux_array_13_out),
    ._02(L5_06), ._12(L5_07), ._22(L5_08), ._32(L5_09), ._01(not_7_out), ._00(S6), ._11(not_8_out), ._10(S7),
    ._21(not_9_out), ._20(S8), ._31(not_10_out), ._30(S9));
  MUX_ARRAY mux_array_14 (
    .C1(L4_C1), .C2(L4_C2), .in(mux_array_8_out), .D1(L4_D1), .D2(L4_D2), .out(mux_array_14_out),
    ._02(L4_06), ._12(L4_07), ._22(L4_08), ._32(L4_09), ._01(not_7_out), ._00(S6), ._11(not_8_out), ._10(S7),
    ._21(not_9_out), ._20(S8), ._31(not_10_out), ._30(S9));
  MUX_ARRAY mux_array_15 (
    .C1(L3_C1), .C2(L3_C2), .in(mux_array_9_out), .D1(L3_D1), .D2(L3_D2), .out(mux_array_15_out),
    ._02(L3_06), ._12(L3_07), ._22(L3_08), ._32(L3_09), ._01(not_7_out), ._00(S6), ._11(not_8_out), ._10(S7),
    ._21(not_9_out), ._20(S8), ._31(not_10_out), ._30(S9));
  MUX_ARRAY mux_array_16 (
    .C1(L2_C1), .C2(L2_C2), .in(mux_array_10_out), .D1(L2_D1), .D2(L2_D2), .out(mux_array_16_out),
    ._02(L2_06), ._12(L2_07), ._22(L2_08), ._32(L2_09), ._01(not_7_out), ._00(S6), ._11(not_8_out), ._10(S7),
    ._21(not_9_out), ._20(S8), ._31(not_10_out), ._30(S9));
  MUX_ARRAY mux_array_17 (
    .C1(L1_C1), .C2(L1_C2), .in(mux_array_11_out), .D1(L1_D1), .D2(L1_D2), .out(mux_array_17_out),
    ._02(L1_06), ._12(L1_07), ._22(L1_08), ._32(L1_09), ._01(not_7_out), ._00(S6), ._11(not_8_out), ._10(S7),
    ._21(not_9_out), ._20(S8), ._31(not_10_out), ._30(S9));
  MUX_ARRAY mux_array_18 (
    .C1(L0_C1), .C2(L0_C2), .in(mux_array_12_out), .D1(L0_D1), .D2(L0_D2), .out(mux_array_18_out),
    ._02(L0_06), ._12(L0_07), ._22(L0_08), ._32(L0_09), ._01(not_7_out), ._00(S6), ._11(not_8_out), ._10(S7),
    ._21(not_9_out), ._20(S8), ._31(not_10_out), ._30(S9));
  not not_10 (not_10_out, S9);
  not not_11 (not_11_out, S10);
  not not_12 (not_12_out, S11);
  not not_13 (not_13_out, S12);
  MUX_ARRAY mux_array_19 (
    .C1(L5_C1), .C2(L5_C2), .in(mux_array_13_out), .D1(L5_D1), .D2(L5_D2), ._02(L5_10), ._12(L5_11),
    ._22(L5_12), ._32(L5_13), ._01(not_11_out), ._00(S10), ._11(not_12_out), ._10(S11), ._21(not_13_out),
    ._20(S12), ._31(not_14_out), ._30(S12));  // open: out
  MUX_ARRAY mux_array_20 (
    .C1(L4_C1), .C2(L4_C2), .in(mux_array_14_out), .D1(L4_D1), .D2(L4_D2), ._02(L4_10), ._12(L4_11),
    ._22(L4_12), ._32(L4_13), ._01(not_11_out), ._00(S10), ._11(not_12_out), ._10(S11), ._21(not_13_out),
    ._20(S12), ._31(not_14_out), ._30(S12));  // open: out
  MUX_ARRAY mux_array_21 (
    .C1(L3_C1), .C2(L3_C2), .in(mux_array_15_out), .D1(L3_D1), .D2(L3_D2), ._02(L3_10), ._12(L3_11),
    ._22(L3_12), ._32(L3_13), ._01(not_11_out), ._00(S10), ._11(not_12_out), ._10(S11), ._21(not_13_out),
    ._20(S12), ._31(not_14_out), ._30(S12));  // open: out
  MUX_ARRAY mux_array_22 (
    .C1(L2_C1), .C2(L2_C2), .in(mux_array_16_out), .D1(L2_D1), .D2(L2_D2), ._02(L2_10), ._12(L2_11),
    ._22(L2_12), ._32(L2_13), ._01(not_11_out), ._00(S10), ._11(not_12_out), ._10(S11), ._21(not_13_out),
    ._20(S12), ._31(not_14_out), ._30(S12));  // open: out
  MUX_ARRAY mux_array_23 (
    .C1(L1_C1), .C2(L1_C2), .in(mux_array_17_out), .D1(L1_D1), .D2(L1_D2), ._02(L1_10), ._12(L1_11),
    ._22(L1_12), ._32(L1_13), ._01(not_11_out), ._00(S10), ._11(not_12_out), ._10(S11), ._21(not_13_out),
    ._20(S12), ._31(not_14_out), ._30(S12));  // open: out
  MUX_ARRAY mux_array_24 (
    .C1(L0_C1), .C2(L0_C2), .in(mux_array_18_out), .D1(L0_D1), .D2(L0_D2), ._02(L0_10), ._12(L0_11),
    ._22(L0_12), ._32(L0_13), ._01(not_11_out), ._00(S10), ._11(not_12_out), ._10(S11), ._21(not_13_out),
    ._20(S12), ._31(not_14_out), ._30(S12));  // open: out
  not not_14 (not_14_out, S12);
endmodule

module TREE (
  input  IDCT_CLK,
  input  AND_FLAG,
  input  MUL00,
  input  MUL01,
  input  MUL02,
  input  MUL03,
  input  MUL04,
  input  MUL05,
  input  MUL06,
  input  MUL07,
  input  MUL08,
  input  MUL09,
  input  MUL10,
  input  MUL11,
  input  L0_00,
  input  L0_01,
  input  L0_02,
  input  L0_03,
  input  L0_04,
  input  L0_05,
  input  L0_06,
  input  L0_07,
  input  L0_08,
  input  L0_09,
  input  L0_10,
  input  L0_11,
  input  L0_12,
  input  L0_13,
  input  L1_00,
  input  L1_01,
  input  L1_02,
  input  L1_03,
  input  L1_04,
  input  L1_05,
  input  L1_06,
  input  L1_07,
  input  L1_08,
  input  L1_09,
  input  L1_10,
  input  L1_11,
  input  L1_12,
  input  L1_13,
  input  L2_00,
  input  L2_01,
  input  L2_02,
  input  L2_03,
  input  L2_04,
  input  L2_05,
  input  L2_06,
  input  L2_07,
  input  L2_08,
  input  L2_09,
  input  L2_10,
  input  L2_11,
  input  L2_12,
  input  L2_13,
  input  L3_00,
  input  L3_01,
  input  L3_02,
  input  L3_03,
  input  L3_04,
  input  L3_05,
  input  L3_06,
  input  L3_07,
  input  L3_08,
  input  L3_09,
  input  L3_10,
  input  L3_11,
  input  L3_12,
  input  L3_13,
  input  L4_00,
  input  L4_01,
  input  L4_02,
  input  L4_03,
  input  L4_04,
  input  L4_05,
  input  L4_06,
  input  L4_07,
  input  L4_08,
  input  L4_09,
  input  L4_10,
  input  L4_11,
  input  L4_12,
  input  L4_13,
  input  L5_00,
  input  L5_01,
  input  L5_02,
  input  L5_03,
  input  L5_04,
  input  L5_05,
  input  L5_06,
  input  L5_07,
  input  L5_08,
  input  L5_09,
  input  L5_10,
  input  L5_11,
  input  L5_12,
  input  L5_13,
  output RES00,
  output RES01,
  output RES02,
  output RES03,
  output RES04,
  output RES05,
  output RES06,
  output RES07,
  output RES08,
  output RES09,
  output RES10,
  output RES11,
  output RES12,
  output RES13,
  output RES14,
  output RES15,
  output RES16
);

  wire _0001_out1___cout, _0001_out2___sum, _0002_out1___sum, _0002_out2___cout, _0003_out1___cout,
       _0003_out2___sum, _0004_out1___cout, _0004_out2___sum, _0006_out1___cout, _0006_out2___sum,
       _0007_out1___cout, _027_out1___cout, _027_out2___sum, _028_out1___cout, _028_out2___sum,
       _029_out1___cout, _029_out2___sum, _030_out1___cout, _030_out2___sum, _031_out1___cout,
       _031_out2___sum, _032_out1___cout, _032_out2___sum, _033_out1___cout, _033_out2___sum,
       _035_out1___cout, _035_out2___sum, _039_out1___cout, _039_out2___sum, _048_out1___cout,
       _048_out2___sum, _049_out1___cout, _049_out2___sum, _051_out1___cout, _051_out2___sum,
       _056_out1___cout, _056_out2___sum, _059_out1___cout, _059_out2___sum, _063_out2___sum,
       _064_out1___cout, _064_out2___sum, _065_out1___cout, _065_out2___sum, _066_out1___cout,
       _066_out2___sum, _067_out1___cout, _067_out2___sum, _068_out1___cout, _068_out2___sum,
       _069_out1___cout, _069_out2___sum, _070_out1___cout, _070_out2___sum, _071_out1___cout,
       _071_out2___sum, _072_out1___cout, _072_out2___sum, _073_out1___cout, _073_out2___sum,
       _074_out1___cout, _074_out2___sum, _075_out1___cout, _075_out2___sum, _076_out1___cout,
       _076_out2___sum, _077_out1___cout, _077_out2___sum, _078_out1___cout, _078_out2___sum,
       _080_out1___cout, _080_out2___sum, _085_out1___cout, _085_out2___sum, _086_out1___cout,
       _086_out2___sum, _087_out1___cout, _087_out2___sum, _089_out1___cout, _089_out2___sum,
       _0102_out1___cout, _0102_out2___sum, _0103_out1___cout, _0103_out2___sum, _0105_out1___cout,
       _0105_out2___sum, _108_out1___cout, _108_out2___sum, _0109_out1___cout, _115_out1___cout,
       _115_out2___sum, _187_out1___cout, _187_out2___sum, _195_out1___sum, _195_out2___cout,
       _198_out1___sum, _198_out2___cout, _0201_out1___cout, _201_out1___sum, _201_out2___cout,
       _0201_out2___sum, _0202_out1___cout, _0202_out2___sum, _0204_out1___cout, _0204_out2___sum,
       _229_out1___cout, _229_out2___sum, _230_out1___cout, _230_out2___sum, _237_out1___cout,
       _237_out2___sum, _0301_out1___cout, _0301_out2___sum, _0302_out1___cout, _0302_out2___sum,
       _0304_out1___cout, _0304_out2___sum, _0307_out1___cout, _0308_out1___cout, _371_out, _372_out,
       _373_out, _374_out2, _374_out3, _375_out2, _375_out3, _376_out2, _376_out3, _0401_out1___cout,
       _0401_out2___sum, _0402_out1___cout, _0402_out2___sum, _0403_out1___cout, _0403_out2___sum,
       _0502_out1___cout, _0502_out2___sum, _0503_out1___cout, _0503_out2___sum, _0602_out1___cout,
       _0602_out2___sum, _603_out1___cout, _603_out2___sum, _0606_out1___cout, _0606_out2___sum,
       _0607_out1___cout, _0607_out2___sum, _0703_out1___sum, _0703_out2___cout, _0704_out1___sum,
       _0704_out2___cout, _0706_out1___cout, _0706_out2___sum, _0801_out1___cout, _0801_out2___sum,
       _0803_out1___cout, _0803_out2___sum, _0903_out1___cout, _0903_out2___sum, _0904_out1___cout,
       _0904_out2___sum, _1006_out1___cout, _1006_out2___sum, _1011_out1___cout, _1011_out2___sum, and_1_out,
       and_2_out, and_3_out, and_4_out, and_5_out, and_6_out, and_7_out, and_8_out, and_9_out, and_10_out,
       and_11_out, and_12_out, and_13_out, and_14_out, and_15_out, and_16_out, and_17_out, clock_1_out,
       d_ff_1_q, d_ff_3_q, d_ff_4_q, d_ff_5_q, d_ff_7_q, d_ff_8_q, d_ff_10_q, d_ff_11_q, d_ff_13_q,
       d_ff_14_q, d_ff_16_q, d_ff_17_q, d_ff_19_q, d_ff_20_q, d_ff_22_q, d_ff_23_q, d_ff_25_q, d_ff_26_q,
       d_ff_28_q, d_ff_29_q, d_ff_31_q, d_ff_32_q, d_ff_34_q, d_ff_35_q, d_ff_37_q, d_ff_38_q, d_ff_40_q,
       d_ff_41_q, d_ff_43_q, d_ff_44_q, d_ff_46_q, d_ff_47_q, d_ff_49_q, d_ff_50_q, d_ff_52_q,
       fa_1_out1___cout, fa_1_out2___sum, fa_2_out1___cout, fa_2_out2___sum, fa_3_out1___cout,
       fa_3_out2___sum, multiplexer_1_out, n12_oai_1_out, n12_oai_2_out, n12_oai_3_out, n12_oai_4_out,
       n12_oai_5_out, n12_oai_6_out, not_1_out, not_2_out, not_3_out, not_4_out, not_5_out, not_6_out,
       not_7_out, not_8_out, not_9_out, not_10_out, not_11_out, not_12_out, not_13_out, ws1_1_out1,
       ws1_1_out2, ws1_1_out3, ws1_2_out1, ws1_2_out2, ws1_2_out3, ws1_3_out1, ws1_3_out2, ws1_3_out3,
       ws1_4_out1, ws1_4_out2, ws1_4_out3, ws1_5_out1, ws1_5_out2, ws1_5_out3, ws1_6_out1, ws1_6_out2,
       ws1_6_out3, ws1_7_out1, ws1_7_out2, ws1_7_out3, ws2_1_out1, ws2_1_out2, ws2_1_out3, ws2_2_out1,
       ws2_2_out2, ws2_2_out3, ws2_3_out1, ws2_3_out2, ws2_3_out3, ws2_4_out1, ws2_4_out2, ws2_4_out3,
       ws2_5_out1, ws2_5_out2, ws2_5_out3, ws2_6_out1, ws2_6_out2, ws2_6_out3, ws2_7_out1;

  Clock clock_1 (.out(clock_1_out));
  not not_1 (not_1_out, clock_1_out);
  ha _0007 (.out1___cout(_0007_out1___cout), .in2___b(_0308_out1___cout), .in1___a(L0_01));  // open: out2___sum
  ha _0308 (.out1___cout(_0308_out1___cout), .in2___b(n12_oai_1_out), .in1___a(L0_00));  // open: out2___sum
  not not_2 (not_2_out, MUL01);
  IMUX _373 (.b___in0(_376_out3), .c___in1(_376_out2), .out(_373_out), .sel(_372_out));
  IMUX _372 (.b___in0(_375_out3), .c___in1(_375_out2), .out(_372_out), .sel(_371_out));
  IMUX _371 (.b___in0(_374_out3), .c___in1(_374_out2), .out(_371_out), .sel(_0307_out1___cout));
  fa _0307 (
    .out1___cout(_0307_out1___cout), .in3___cin(_0607_out2___sum), .in2___b(_0006_out1___cout),
    .in1___a(_0109_out1___cout));  // open: out2___sum
  fa _0109 (
    .out1___cout(_0109_out1___cout), .in3___cin(_0006_out2___sum), .in2___b(_0007_out1___cout),
    .in1___a(L0_02));  // open: out2___sum
  _12_OAI u_12_oai_1 (.out(n12_oai_1_out), .a(not_2_out), .b(1'b0), .c(MUL00));
  not not_3 (not_3_out, MUL03);
  ws1 _376 (
    .in5(_035_out2___sum), .in4(_229_out1___cout), .in3(1'b1), .in2(1'b0), .in1(_372_out), .out3(_376_out3),
    .out2(_376_out2));  // open: out1
  ws1 _375 (
    .in5(_229_out2___sum), .in4(_237_out1___cout), .in3(1'b1), .in2(1'b0), .in1(_371_out), .out3(_375_out3),
    .out2(_375_out2));  // open: out1
  ws1 _374 (
    .in5(_237_out2___sum), .in4(_230_out2___sum), .in3(1'b1), .in2(1'b0), .in1(_0307_out1___cout),
    .out3(_374_out3), .out2(_374_out2));  // open: out1
  ha _237 (.out2___sum(_237_out2___sum), .out1___cout(_237_out1___cout), .in2___b(L0_04), .in1___a(_0607_out1___cout));
  ha _0607 (.out2___sum(_0607_out2___sum), .out1___cout(_0607_out1___cout), .in2___b(L1_01), .in1___a(L0_03));
  ha _0006 (.out2___sum(_0006_out2___sum), .out1___cout(_0006_out1___cout), .in2___b(n12_oai_2_out), .in1___a(L1_00));
  _12_OAI u_12_oai_2 (.out(n12_oai_2_out), .a(not_3_out), .b(MUL01), .c(MUL02));
  ha _229 (
    .out2___sum(_229_out2___sum), .out1___cout(_229_out1___cout), .in2___b(_187_out2___sum),
    .in1___a(_230_out1___cout));
  fa _230 (
    .out2___sum(_230_out2___sum), .out1___cout(_230_out1___cout), .in3___cin(L2_00), .in2___b(n12_oai_3_out),
    .in1___a(L1_02));
  not not_4 (not_4_out, MUL05);
  _12_OAI u_12_oai_3 (.out(n12_oai_3_out), .a(not_4_out), .b(MUL03), .c(MUL04));
  D_Flip_Flop d_ff_1 (.clk(not_1_out), .D(_373_out), .Q(d_ff_1_q));  // open: Qn, preset, en, reset
  ha _035 (
    .out2___sum(_035_out2___sum), .out1___cout(_035_out1___cout), .in2___b(_1011_out2___sum),
    .in1___a(_080_out2___sum));
  not not_5 (not_5_out, MUL07);
  D_Flip_Flop d_ff_2 (.clk(clock_1_out), .D(fa_1_out2___sum), .Q(RES00));  // open: Qn, preset, en, reset
  fa fa_1 (
    .out2___sum(fa_1_out2___sum), .out1___cout(fa_1_out1___cout), .in3___cin(d_ff_4_q), .in2___b(d_ff_3_q),
    .in1___a(d_ff_1_q));
  D_Flip_Flop d_ff_3 (.clk(not_1_out), .D(_035_out1___cout), .Q(d_ff_3_q));  // open: Qn, preset, en, reset
  fa _080 (
    .out2___sum(_080_out2___sum), .out1___cout(_080_out1___cout), .in3___cin(L3_00), .in2___b(n12_oai_4_out),
    .in1___a(L2_02));
  _12_OAI u_12_oai_4 (.out(n12_oai_4_out), .a(not_5_out), .b(MUL04), .c(MUL06));
  D_Flip_Flop d_ff_4 (.clk(not_1_out), .D(_059_out2___sum), .Q(d_ff_4_q));  // open: Qn, preset, en, reset
  D_Flip_Flop d_ff_5 (.clk(not_1_out), .D(_059_out1___cout), .Q(d_ff_5_q));  // open: Qn, preset, en, reset
  fa _059 (
    .out2___sum(_059_out2___sum), .out1___cout(_059_out1___cout), .in3___cin(_076_out2___sum),
    .in2___b(_077_out2___sum), .in1___a(_1011_out1___cout));
  fa _1011 (
    .out2___sum(_1011_out2___sum), .out1___cout(_1011_out1___cout), .in3___cin(L1_04),
    .in2___b(_187_out1___cout), .in1___a(L0_06));
  fa _187 (
    .out2___sum(_187_out2___sum), .out1___cout(_187_out1___cout), .in3___cin(L2_01), .in2___b(L1_03),
    .in1___a(L0_05));
  D_Flip_Flop d_ff_6 (.clk(clock_1_out), .D(fa_2_out2___sum), .Q(RES01));  // open: Qn, preset, en, reset
  fa fa_2 (
    .out2___sum(fa_2_out2___sum), .out1___cout(fa_2_out1___cout), .in3___cin(d_ff_7_q), .in2___b(d_ff_5_q),
    .in1___a(fa_1_out1___cout));
  fa _076 (
    .out2___sum(_076_out2___sum), .out1___cout(_076_out1___cout), .in3___cin(L1_05), .in2___b(L0_07),
    .in1___a(_080_out1___cout));
  fa _077 (
    .out2___sum(_077_out2___sum), .out1___cout(_077_out1___cout), .in3___cin(and_1_out), .in2___b(L3_01),
    .in1___a(L2_03));
  D_Flip_Flop d_ff_7 (.clk(not_1_out), .D(_056_out2___sum), .Q(d_ff_7_q));  // open: Qn, preset, en, reset
  fa _056 (
    .out2___sum(_056_out2___sum), .out1___cout(_056_out1___cout), .in3___cin(_071_out2___sum),
    .in2___b(_075_out2___sum), .in1___a(_076_out1___cout));
  fa _075 (
    .out2___sum(_075_out2___sum), .out1___cout(_075_out1___cout), .in3___cin(L3_02), .in2___b(L2_04),
    .in1___a(L1_06));
  D_Flip_Flop d_ff_8 (.clk(not_1_out), .D(_056_out1___cout), .Q(d_ff_8_q));  // open: Qn, preset, en, reset
  not not_6 (not_6_out, MUL09);
  D_Flip_Flop d_ff_9 (.clk(clock_1_out), .D(fa_3_out2___sum), .Q(RES02));  // open: Qn, preset, en, reset
  fa fa_3 (
    .out2___sum(fa_3_out2___sum), .out1___cout(fa_3_out1___cout), .in3___cin(d_ff_10_q), .in2___b(d_ff_8_q),
    .in1___a(fa_2_out1___cout));
  fa _071 (
    .out2___sum(_071_out2___sum), .out1___cout(_071_out1___cout), .in3___cin(L0_08),
    .in2___b(_087_out2___sum), .in1___a(_077_out1___cout));
  fa _087 (
    .out2___sum(_087_out2___sum), .out1___cout(_087_out1___cout), .in3___cin(and_2_out),
    .in2___b(n12_oai_5_out), .in1___a(L4_00));
  _12_OAI u_12_oai_5 (.out(n12_oai_5_out), .a(not_6_out), .b(MUL07), .c(MUL08));
  D_Flip_Flop d_ff_10 (.clk(not_1_out), .D(_039_out2___sum), .Q(d_ff_10_q));  // open: Qn, preset, en, reset
  fa _039 (
    .out2___sum(_039_out2___sum), .out1___cout(_039_out1___cout), .in3___cin(_069_out2___sum),
    .in2___b(_070_out2___sum), .in1___a(_071_out1___cout));
  fa _070 (
    .out2___sum(_070_out2___sum), .out1___cout(_070_out1___cout), .in3___cin(L2_05), .in2___b(L1_07),
    .in1___a(L0_09));
  D_Flip_Flop d_ff_11 (.clk(not_1_out), .D(_039_out1___cout), .Q(d_ff_11_q));  // open: Qn, preset, en, reset
  D_Flip_Flop d_ff_12 (.clk(clock_1_out), .D(ws1_1_out1), .Q(RES03));  // open: Qn, preset, en, reset
  ws1 ws1_1 (
    .in5(d_ff_13_q), .in4(d_ff_11_q), .in3(1'b1), .in2(1'b0), .in1(fa_3_out1___cout), .out3(ws1_1_out3),
    .out2(ws1_1_out2), .out1(ws1_1_out1));
  fa _069 (
    .out2___sum(_069_out2___sum), .out1___cout(_069_out1___cout), .in3___cin(_085_out2___sum),
    .in2___b(_087_out1___cout), .in1___a(_075_out1___cout));
  fa _085 (
    .out2___sum(_085_out2___sum), .out1___cout(_085_out1___cout), .in3___cin(and_3_out), .in2___b(L4_01),
    .in1___a(L3_03));
  D_Flip_Flop d_ff_13 (.clk(not_1_out), .D(_033_out2___sum), .Q(d_ff_13_q));  // open: Qn, preset, en, reset
  D_Flip_Flop d_ff_14 (.clk(not_1_out), .D(_033_out1___cout), .Q(d_ff_14_q));  // open: Qn, preset, en, reset
  fa _033 (
    .out2___sum(_033_out2___sum), .out1___cout(_033_out1___cout), .in3___cin(_072_out2___sum),
    .in2___b(_073_out2___sum), .in1___a(_069_out1___cout));
  fa _073 (
    .out2___sum(_073_out2___sum), .out1___cout(_073_out1___cout), .in3___cin(L1_08), .in2___b(L0_10),
    .in1___a(_085_out1___cout));
  D_Flip_Flop d_ff_15 (.clk(clock_1_out), .D(ws2_1_out1), .Q(RES04));  // open: Qn, preset, en, reset
  ws2 ws2_1 (
    .in5(d_ff_16_q), .in4(d_ff_14_q), .in3(ws1_1_out2), .in2(ws1_1_out3), .in1(fa_3_out1___cout),
    .out3(ws2_1_out3), .out2(ws2_1_out2), .out1(ws2_1_out1));
  fa _072 (
    .out2___sum(_072_out2___sum), .out1___cout(_072_out1___cout), .in3___cin(_086_out2___sum),
    .in2___b(_0606_out2___sum), .in1___a(_070_out1___cout));
  fa _0606 (
    .out2___sum(_0606_out2___sum), .out1___cout(_0606_out1___cout), .in3___cin(L4_02), .in2___b(L3_04),
    .in1___a(L2_06));
  not not_7 (not_7_out, MUL11);
  fa _086 (
    .out2___sum(_086_out2___sum), .out1___cout(_086_out1___cout), .in3___cin(and_4_out),
    .in2___b(n12_oai_6_out), .in1___a(L5_00));
  _12_OAI u_12_oai_6 (.out(n12_oai_6_out), .a(not_7_out), .b(MUL09), .c(MUL10));
  D_Flip_Flop d_ff_16 (.clk(not_1_out), .D(_029_out2___sum), .Q(d_ff_16_q));  // open: Qn, preset, en, reset
  fa _029 (
    .out2___sum(_029_out2___sum), .out1___cout(_029_out1___cout), .in3___cin(_074_out2___sum),
    .in2___b(_078_out2___sum), .in1___a(_072_out1___cout));
  fa _078 (
    .out2___sum(_078_out2___sum), .out1___cout(_078_out1___cout), .in3___cin(L0_11),
    .in2___b(_086_out1___cout), .in1___a(_0606_out1___cout));
  D_Flip_Flop d_ff_17 (.clk(not_1_out), .D(_029_out1___cout), .Q(d_ff_17_q));  // open: Qn, preset, en, reset
  ws1 ws1_2 (
    .in5(d_ff_19_q), .in4(d_ff_17_q), .in3(ws2_1_out2), .in2(ws2_1_out3), .in1(fa_3_out1___cout),
    .out3(ws1_2_out3), .out2(ws1_2_out2), .out1(ws1_2_out1));
  fa _074 (
    .out2___sum(_074_out2___sum), .out1___cout(_074_out1___cout), .in3___cin(_0204_out2___sum),
    .in2___b(_115_out2___sum), .in1___a(_073_out1___cout));
  fa _115 (
    .out2___sum(_115_out2___sum), .out1___cout(_115_out1___cout), .in3___cin(and_5_out), .in2___b(L4_03),
    .in1___a(L5_01));
  D_Flip_Flop d_ff_18 (.clk(clock_1_out), .D(ws1_2_out1), .Q(RES05));  // open: Qn, preset, en, reset
  fa _0204 (
    .out2___sum(_0204_out2___sum), .out1___cout(_0204_out1___cout), .in3___cin(L3_05), .in2___b(L2_07),
    .in1___a(L1_09));
  D_Flip_Flop d_ff_19 (.clk(not_1_out), .D(_028_out2___sum), .Q(d_ff_19_q));  // open: Qn, preset, en, reset
  fa _028 (
    .out2___sum(_028_out2___sum), .out1___cout(_028_out1___cout), .in3___cin(_066_out2___sum),
    .in2___b(_0503_out2___sum), .in1___a(_074_out1___cout));
  fa _0503 (
    .out2___sum(_0503_out2___sum), .out1___cout(_0503_out1___cout), .in3___cin(L0_12),
    .in2___b(_0204_out1___cout), .in1___a(_115_out1___cout));
  D_Flip_Flop d_ff_20 (.clk(not_1_out), .D(_028_out1___cout), .Q(d_ff_20_q));  // open: Qn, preset, en, reset
  D_Flip_Flop d_ff_21 (.clk(clock_1_out), .D(ws2_2_out1), .Q(RES06));  // open: Qn, preset, en, reset
  ws2 ws2_2 (
    .in5(d_ff_22_q), .in4(d_ff_20_q), .in3(ws1_2_out2), .in2(ws1_2_out3), .in1(fa_3_out1___cout),
    .out3(ws2_2_out3), .out2(ws2_2_out2), .out1(ws2_2_out1));
  fa _066 (
    .out2___sum(_066_out2___sum), .out1___cout(_066_out1___cout), .in3___cin(_089_out2___sum),
    .in2___b(_0304_out2___sum), .in1___a(_078_out1___cout));
  fa _0304 (
    .out2___sum(_0304_out2___sum), .out1___cout(_0304_out1___cout), .in3___cin(L3_06), .in2___b(L2_08),
    .in1___a(L1_10));
  ha _027 (
    .out2___sum(_027_out2___sum), .out1___cout(_027_out1___cout), .in2___b(_0502_out2___sum),
    .in1___a(_066_out1___cout));
  fa _089 (
    .out2___sum(_089_out2___sum), .out1___cout(_089_out1___cout), .in3___cin(and_6_out), .in2___b(L5_02),
    .in1___a(L4_04));
  D_Flip_Flop d_ff_22 (.clk(not_1_out), .D(_027_out2___sum), .Q(d_ff_22_q));  // open: Qn, preset, en, reset
  ws1 ws1_3 (
    .in5(d_ff_25_q), .in4(d_ff_23_q), .in3(ws2_2_out2), .in2(ws2_2_out3), .in1(fa_3_out1___cout),
    .out3(ws1_3_out3), .out2(ws1_3_out2), .out1(ws1_3_out1));
  D_Flip_Flop d_ff_23 (.clk(not_1_out), .D(_027_out1___cout), .Q(d_ff_23_q));  // open: Qn, preset, en, reset
  D_Flip_Flop d_ff_24 (.clk(clock_1_out), .D(ws1_3_out1), .Q(RES07));  // open: Qn, preset, en, reset
  fa _0502 (
    .out2___sum(_0502_out2___sum), .out1___cout(_0502_out1___cout), .in3___cin(_0403_out2___sum),
    .in2___b(_0202_out2___sum), .in1___a(_0503_out1___cout));
  fa _0202 (
    .out2___sum(_0202_out2___sum), .out1___cout(_0202_out1___cout), .in3___cin(_0105_out2___sum),
    .in2___b(_089_out1___cout), .in1___a(_0304_out1___cout));
  fa _0105 (
    .out2___sum(_0105_out2___sum), .out1___cout(_0105_out1___cout), .in3___cin(L4_05), .in2___b(L3_07),
    .in1___a(L2_09));
  D_Flip_Flop d_ff_25 (.clk(not_1_out), .D(_0903_out2___sum), .Q(d_ff_25_q));  // open: Qn, preset, en, reset
  ha _0903 (
    .out2___sum(_0903_out2___sum), .out1___cout(_0903_out1___cout), .in2___b(_0201_out2___sum),
    .in1___a(_0502_out1___cout));
  fa _0403 (
    .out2___sum(_0403_out2___sum), .out1___cout(_0403_out1___cout), .in3___cin(_0703_out1___sum),
    .in2___b(L1_11), .in1___a(not_8_out));
  not not_8 (not_8_out, L0_13);
  ca _0703 (.out1___sum(_0703_out1___sum), .out2___cout(_0703_out2___cout), .a(L5_03), .b(and_7_out));
  D_Flip_Flop d_ff_26 (.clk(not_1_out), .D(_0903_out1___cout), .Q(d_ff_26_q));  // open: Qn, preset, en, reset
  D_Flip_Flop d_ff_27 (.clk(clock_1_out), .D(ws2_3_out1), .Q(RES08));  // open: Qn, preset, en, reset
  ws2 ws2_3 (
    .in5(d_ff_28_q), .in4(d_ff_26_q), .in3(ws1_3_out2), .in2(ws1_3_out3), .in1(fa_3_out1___cout),
    .out3(ws2_3_out3), .out2(ws2_3_out2), .out1(ws2_3_out1));
  fa _0201 (
    .out2___sum(_0201_out2___sum), .out1___cout(_0201_out1___cout), .in3___cin(_0103_out2___sum),
    .in2___b(_0402_out2___sum), .in1___a(_0202_out1___cout));
  fa _0402 (
    .out2___sum(_0402_out2___sum), .out1___cout(_0402_out1___cout), .in3___cin(_0704_out1___sum),
    .in2___b(L1_12), .in1___a(_0703_out2___cout));
  ca _0704 (.out1___sum(_0704_out1___sum), .out2___cout(_0704_out2___cout), .a(L5_04), .b(and_8_out));
  D_Flip_Flop d_ff_28 (.clk(not_1_out), .D(_0001_out2___sum), .Q(d_ff_28_q));  // open: Qn, preset, en, reset
  D_Flip_Flop d_ff_29 (.clk(not_1_out), .D(_0001_out1___cout), .Q(d_ff_29_q));  // open: Qn, preset, en, reset
  fa _0001 (
    .out2___sum(_0001_out2___sum), .out1___cout(_0001_out1___cout), .in3___cin(_0102_out2___sum),
    .in2___b(_0103_out1___cout), .in1___a(_0201_out1___cout));
  fa _0103 (
    .out2___sum(_0103_out2___sum), .out1___cout(_0103_out1___cout), .in3___cin(_0003_out2___sum),
    .in2___b(_0403_out1___cout), .in1___a(_0105_out1___cout));
  D_Flip_Flop d_ff_30 (.clk(clock_1_out), .D(ws1_4_out1), .Q(RES09));  // open: Qn, preset, en, reset
  ws1 ws1_4 (
    .in5(d_ff_29_q), .in4(d_ff_31_q), .in3(ws2_3_out2), .in2(ws2_3_out3), .in1(fa_3_out1___cout),
    .out3(ws1_4_out3), .out2(ws1_4_out2), .out1(ws1_4_out1));
  fa _0102 (
    .out2___sum(_0102_out2___sum), .out1___cout(_0102_out1___cout), .in3___cin(_0302_out2___sum),
    .in2___b(_0004_out2___sum), .in1___a(_0402_out1___cout));
  fa _0004 (
    .out2___sum(_0004_out2___sum), .out1___cout(_0004_out1___cout), .in3___cin(L3_09), .in2___b(L2_11),
    .in1___a(not_9_out));
  not not_9 (not_9_out, L1_13);
  D_Flip_Flop d_ff_31 (.clk(not_1_out), .D(_0401_out2___sum), .Q(d_ff_31_q));  // open: Qn, preset, en, reset
  ha _0401 (
    .out2___sum(_0401_out2___sum), .out1___cout(_0401_out1___cout), .in2___b(_0301_out2___sum),
    .in1___a(_0102_out1___cout));
  fa _0302 (
    .out2___sum(_0302_out2___sum), .out1___cout(_0302_out1___cout), .in3___cin(_0803_out2___sum),
    .in2___b(_0003_out1___cout), .in1___a(_0704_out2___cout));
  fa _0003 (
    .out2___sum(_0003_out2___sum), .out1___cout(_0003_out1___cout), .in3___cin(L4_06), .in2___b(L3_08),
    .in1___a(L2_10));
  ws2 ws2_4 (
    .in5(d_ff_32_q), .in4(d_ff_34_q), .in3(ws1_4_out2), .in2(ws1_4_out3), .in1(fa_3_out1___cout),
    .out3(ws2_4_out3), .out2(ws2_4_out2), .out1(ws2_4_out1));
  D_Flip_Flop d_ff_32 (.clk(not_1_out), .D(_0401_out1___cout), .Q(d_ff_32_q));  // open: Qn, preset, en, reset
  and and_1 (and_1_out, RES00, AND_FLAG);
  D_Flip_Flop d_ff_33 (.clk(clock_1_out), .D(ws2_4_out1), .Q(RES10));  // open: Qn, preset, en, reset
  fa _0301 (
    .out2___sum(_0301_out2___sum), .out1___cout(_0301_out1___cout), .in3___cin(_0602_out2___sum),
    .in2___b(_0706_out2___sum), .in1___a(_0302_out1___cout));
  fa _0706 (
    .out2___sum(_0706_out2___sum), .out1___cout(_0706_out1___cout), .in3___cin(L4_08), .in2___b(L3_10),
    .in1___a(L2_12));
  fa _0803 (
    .out2___sum(_0803_out2___sum), .out1___cout(_0803_out1___cout), .in3___cin(and_9_out), .in2___b(L5_05),
    .in1___a(L4_07));
  and and_2 (and_2_out, RES01, AND_FLAG);
  Multiplexer #(.enable("false")) multiplexer_1 (
    .in0(ws2_4_out3), .in1(ws2_4_out2), .out(multiplexer_1_out), .sel(fa_3_out1___cout));
  D_Flip_Flop d_ff_34 (.clk(not_1_out), .D(_0801_out2___sum), .Q(d_ff_34_q));  // open: Qn, preset, en, reset
  and and_3 (and_3_out, RES02, AND_FLAG);
  D_Flip_Flop d_ff_35 (.clk(not_1_out), .D(_0801_out1___cout), .Q(d_ff_35_q));  // open: Qn, preset, en, reset
  fa _0801 (
    .out2___sum(_0801_out2___sum), .out1___cout(_0801_out1___cout), .in3___cin(_0904_out2___sum),
    .in2___b(_0602_out1___cout), .in1___a(_0301_out1___cout));
  fa _0602 (
    .out2___sum(_0602_out2___sum), .out1___cout(_0602_out1___cout), .in3___cin(_0002_out1___sum),
    .in2___b(_0803_out1___cout), .in1___a(_0004_out1___cout));
  and and_4 (and_4_out, RES03, AND_FLAG);
  D_Flip_Flop d_ff_36 (.clk(clock_1_out), .D(ws1_5_out1), .Q(RES11));  // open: Qn, preset, en, reset
  ws1 ws1_5 (
    .in5(d_ff_35_q), .in4(d_ff_37_q), .in3(1'b1), .in2(1'b0), .in1(multiplexer_1_out), .out3(ws1_5_out3),
    .out2(ws1_5_out2), .out1(ws1_5_out1));
  fa _0904 (
    .out2___sum(_0904_out2___sum), .out1___cout(_0904_out1___cout), .in3___cin(_1006_out2___sum),
    .in2___b(_603_out2___sum), .in1___a(_0706_out1___cout));
  ca _0002 (.out1___sum(_0002_out1___sum), .out2___cout(_0002_out2___cout), .a(L5_06), .b(and_10_out));
  and and_5 (and_5_out, RES04, AND_FLAG);
  and and_6 (and_6_out, RES05, AND_FLAG);
  D_Flip_Flop d_ff_37 (.clk(not_1_out), .D(_030_out2___sum), .Q(d_ff_37_q));  // open: Qn, preset, en, reset
  ha _030 (
    .out2___sum(_030_out2___sum), .out1___cout(_030_out1___cout), .in2___b(_048_out2___sum),
    .in1___a(_0904_out1___cout));
  fa _603 (
    .out2___sum(_603_out2___sum), .out1___cout(_603_out1___cout), .in3___cin(L3_11), .in2___b(not_10_out),
    .in1___a(_0002_out2___cout));
  not not_10 (not_10_out, L2_13);
  and and_7 (and_7_out, RES06, AND_FLAG);
  ws2 ws2_5 (
    .in5(d_ff_38_q), .in4(d_ff_40_q), .in3(ws1_5_out2), .in2(ws1_5_out3), .in1(multiplexer_1_out),
    .out3(ws2_5_out3), .out2(ws2_5_out2), .out1(ws2_5_out1));
  D_Flip_Flop d_ff_38 (.clk(not_1_out), .D(_030_out1___cout), .Q(d_ff_38_q));  // open: Qn, preset, en, reset
  and and_8 (and_8_out, RES07, AND_FLAG);
  D_Flip_Flop d_ff_39 (.clk(clock_1_out), .D(ws2_5_out1), .Q(RES12));  // open: Qn, preset, en, reset
  fa _048 (
    .out2___sum(_048_out2___sum), .out1___cout(_048_out1___cout), .in3___cin(_065_out2___sum),
    .in2___b(_1006_out1___cout), .in1___a(_603_out1___cout));
  fa _1006 (
    .out2___sum(_1006_out2___sum), .out1___cout(_1006_out1___cout), .in3___cin(and_11_out), .in2___b(L5_07),
    .in1___a(L4_09));
  and and_9 (and_9_out, RES08, AND_FLAG);
  D_Flip_Flop d_ff_40 (.clk(not_1_out), .D(_031_out2___sum), .Q(d_ff_40_q));  // open: Qn, preset, en, reset
  fa _031 (
    .out2___sum(_031_out2___sum), .out1___cout(_031_out1___cout), .in3___cin(_049_out2___sum),
    .in2___b(_065_out1___cout), .in1___a(_048_out1___cout));
  fa _065 (
    .out2___sum(_065_out2___sum), .out1___cout(_065_out1___cout), .in3___cin(_201_out1___sum),
    .in2___b(L4_10), .in1___a(L3_12));
  and and_10 (and_10_out, RES09, AND_FLAG);
  D_Flip_Flop d_ff_41 (.clk(not_1_out), .D(_031_out1___cout), .Q(d_ff_41_q));  // open: Qn, preset, en, reset
  and and_11 (and_11_out, RES10, AND_FLAG);
  D_Flip_Flop d_ff_42 (.clk(clock_1_out), .D(ws1_6_out1), .Q(RES13));  // open: Qn, preset, en, reset
  ws1 ws1_6 (
    .in5(d_ff_41_q), .in4(d_ff_43_q), .in3(ws2_5_out2), .in2(ws2_5_out3), .in1(multiplexer_1_out),
    .out3(ws1_6_out3), .out2(ws1_6_out2), .out1(ws1_6_out1));
  fa _049 (
    .out2___sum(_049_out2___sum), .out1___cout(_049_out1___cout), .in3___cin(_108_out2___sum),
    .in2___b(_201_out2___cout), .in1___a(not_11_out));
  not not_11 (not_11_out, L3_13);
  ca _201 (.out1___sum(_201_out1___sum), .out2___cout(_201_out2___cout), .a(L5_08), .b(and_12_out));
  and and_12 (and_12_out, RES11, AND_FLAG);
  ha _064 (
    .out2___sum(_064_out2___sum), .out1___cout(_064_out1___cout), .in2___b(_067_out2___sum),
    .in1___a(_049_out1___cout));
  and and_13 (and_13_out, RES12, AND_FLAG);
  D_Flip_Flop d_ff_43 (.clk(not_1_out), .D(_064_out2___sum), .Q(d_ff_43_q));  // open: Qn, preset, en, reset
  fa _108 (
    .out2___sum(_108_out2___sum), .out1___cout(_108_out1___cout), .in3___cin(and_13_out), .in2___b(L5_09),
    .in1___a(L4_11));
  and and_14 (and_14_out, RES13, AND_FLAG);
  ws2 ws2_6 (
    .in5(d_ff_44_q), .in4(d_ff_46_q), .in3(ws1_6_out2), .in2(ws1_6_out3), .in1(multiplexer_1_out),
    .out3(ws2_6_out3), .out2(ws2_6_out2), .out1(ws2_6_out1));
  D_Flip_Flop d_ff_44 (.clk(not_1_out), .D(_064_out1___cout), .Q(d_ff_44_q));  // open: Qn, preset, en, reset
  and and_15 (and_15_out, RES14, AND_FLAG);
  D_Flip_Flop d_ff_45 (.clk(clock_1_out), .D(ws2_6_out1), .Q(RES14));  // open: Qn, preset, en, reset
  fa _067 (
    .out2___sum(_067_out2___sum), .out1___cout(_067_out1___cout), .in3___cin(_198_out1___sum),
    .in2___b(L4_12), .in1___a(_108_out1___cout));
  and and_16 (and_16_out, RES15, AND_FLAG);
  D_Flip_Flop d_ff_46 (.clk(not_1_out), .D(_032_out2___sum), .Q(d_ff_46_q));  // open: Qn, preset, en, reset
  fa _032 (
    .out2___sum(_032_out2___sum), .out1___cout(_032_out1___cout), .in3___cin(_068_out2___sum),
    .in2___b(_198_out2___cout), .in1___a(_067_out1___cout));
  ca _198 (.out1___sum(_198_out1___sum), .out2___cout(_198_out2___cout), .a(L5_10), .b(and_14_out));
  and and_17 (and_17_out, RES16, AND_FLAG);
  D_Flip_Flop d_ff_47 (.clk(not_1_out), .D(_032_out1___cout), .Q(d_ff_47_q));  // open: Qn, preset, en, reset
  D_Flip_Flop d_ff_48 (.clk(clock_1_out), .D(ws1_7_out1), .Q(RES15));  // open: Qn, preset, en, reset
  ws1 ws1_7 (
    .in5(d_ff_47_q), .in4(d_ff_49_q), .in3(ws2_6_out2), .in2(ws2_6_out3), .in1(multiplexer_1_out),
    .out3(ws1_7_out3), .out2(ws1_7_out2), .out1(ws1_7_out1));
  fa _068 (
    .out2___sum(_068_out2___sum), .out1___cout(_068_out1___cout), .in3___cin(and_15_out), .in2___b(L5_11),
    .in1___a(not_12_out));
  not not_12 (not_12_out, L4_13);
  D_Flip_Flop d_ff_49 (.clk(not_1_out), .D(_051_out2___sum), .Q(d_ff_49_q));  // open: Qn, preset, en, reset
  ha _051 (
    .out2___sum(_051_out2___sum), .out1___cout(_051_out1___cout), .in2___b(_195_out1___sum),
    .in1___a(_068_out1___cout));
  D_Flip_Flop d_ff_50 (.clk(not_1_out), .D(_051_out1___cout), .Q(d_ff_50_q));  // open: Qn, preset, en, reset
  D_Flip_Flop d_ff_51 (.clk(clock_1_out), .D(ws2_7_out1), .Q(RES16));  // open: Qn, preset, en, reset
  ws2 ws2_7 (
    .in5(d_ff_50_q), .in4(d_ff_52_q), .in3(ws1_7_out2), .in2(ws1_7_out3), .in1(multiplexer_1_out),
    .out1(ws2_7_out1));  // open: out3, out2
  ca _195 (.out1___sum(_195_out1___sum), .out2___cout(_195_out2___cout), .a(L5_12), .b(and_16_out));
  D_Flip_Flop d_ff_52 (.clk(not_1_out), .D(_063_out2___sum), .Q(d_ff_52_q));  // open: Qn, preset, en, reset
  fa _063 (
    .out2___sum(_063_out2___sum), .in3___cin(and_17_out), .in2___b(not_13_out), .in1___a(_195_out2___cout));  // open: out1___cout
  not not_13 (not_13_out, L5_13);
  D_Flip_Flop d_ff_53 ();  // open: clk, D, Q, Qn, preset, en, reset

  // Notes on the sheet:
  //   ARES00
  //   01
  //   02
  //   03
  //   04
  //   05
  //   06
  //   07
  //   08
  //   09
  //   10
  //   11
  //   12
  //   13
  //   14
  //   15
  //   ARES16
endmodule

module SIGNED_ADDER_TREE (
  input  ARES16,
  input  ARES15,
  input  ARES14,
  input  L4_00,
  input  L4_01,
  input  L4_02,
  input  L4_03,
  input  L4_04,
  input  L4_05,
  input  L4_06,
  input  L4_07,
  input  L4_08,
  input  L4_09,
  input  L4_10,
  input  L4_11,
  input  L4_12,
  input  L4_13,
  input  L5_00,
  input  L5_01,
  input  L5_02,
  input  L5_03,
  input  L5_04,
  input  L5_05,
  input  L5_06,
  input  L5_07,
  input  L5_08,
  input  L5_09,
  input  L5_10,
  input  L5_11,
  input  L5_12,
  input  L5_13,
  output out_32,
  output out_33
);

  wire ca_1_out1___sum, ca_1_out2___cout, clock_1_out, clock_2_out, d_ff_2_q, d_ff_4_q, d_ff_5_q,
       fa_1_out1___cout, fa_1_out2___sum, fa_2_out2___sum, ha_1_out1___cout, ha_1_out2___sum, not_1_out,
       not_2_out, ws1_1_out1, ws1_1_out2, ws1_1_out3, ws2_1_out1;

  Clock clock_1 (.out(clock_1_out));
  ws1 ws1_1 (
    .in5(1'b0), .in4(d_ff_2_q), .in3(1'b1), .in2(1'b0), .in1(1'b1), .out3(ws1_1_out3), .out2(ws1_1_out2),
    .out1(ws1_1_out1));
  D_Flip_Flop d_ff_1 (.clk(clock_1_out), .D(ws1_1_out1), .Q(out_32));  // open: Qn, preset, en, reset
  Clock clock_2 (.out(clock_2_out));
  ws2 ws2_1 (
    .in5(d_ff_4_q), .in4(d_ff_5_q), .in3(ws1_1_out2), .in2(ws1_1_out3), .in1(1'b1), .out1(ws2_1_out1));  // open: out3, out2
  D_Flip_Flop d_ff_2 (.clk(clock_2_out), .D(ha_1_out2___sum), .Q(d_ff_2_q));  // open: Qn, preset, en, reset
  ha ha_1 (
    .out2___sum(ha_1_out2___sum), .out1___cout(ha_1_out1___cout), .in2___b(ca_1_out1___sum),
    .in1___a(fa_1_out1___cout));
  fa fa_1 (
    .out2___sum(fa_1_out2___sum), .out1___cout(fa_1_out1___cout), .in3___cin(ARES14), .in2___b(L5_11),
    .in1___a(not_1_out));
  not not_1 (not_1_out, L4_13);
  D_Flip_Flop d_ff_3 (.clk(clock_1_out), .D(ws2_1_out1), .Q(out_33));  // open: Qn, preset, en, reset
  D_Flip_Flop d_ff_4 (.clk(clock_2_out), .D(ha_1_out1___cout), .Q(d_ff_4_q));  // open: Qn, preset, en, reset
  not not_2 (not_2_out, L5_13);
  ca ca_1 (.out1___sum(ca_1_out1___sum), .out2___cout(ca_1_out2___cout), .a(L5_12), .b(ARES15));
  D_Flip_Flop d_ff_5 (.clk(clock_2_out), .D(fa_2_out2___sum), .Q(d_ff_5_q));  // open: Qn, preset, en, reset
  fa fa_2 (
    .out2___sum(fa_2_out2___sum), .in3___cin(ARES16), .in2___b(not_2_out), .in1___a(ca_1_out2___cout));  // open: out1___cout
endmodule

module DFFR_logic (
  input  clk,
  input  in,
  input  nres,
  output out_4
);

  wire multiplexer_1_out, multiplexer_2_out, nand_1_out, nand_2_out, not_1_out, not_2_out, not_3_out,
       not_4_out;

  not not_1 (not_1_out, clk);
  not not_2 (not_2_out, in);
  Multiplexer multiplexer_1 (.in0(nand_1_out), .in1(not_2_out), .out(multiplexer_1_out), .sel(not_1_out));  // open: en
  nand nand_1 (nand_1_out, not_3_out, nres);
  not not_3 (not_3_out, multiplexer_1_out);
  not not_4 (not_4_out, nand_2_out);
  Multiplexer multiplexer_2 (.in0(not_4_out), .in1(not_3_out), .out(multiplexer_2_out), .sel(clk));  // open: en
  nand nand_2 (nand_2_out, multiplexer_2_out, nres);
  not not_5 (out_4, nand_2_out);
endmodule

module NOR_AND (
  input  a,
  input  b,
  input  c,
  input  d,
  output out
);

  wire and_1_out, nor_1_out;

  and and_1 (and_1_out, c, d);
  nor nor_1 (nor_1_out, a, b);
  or or_1 (out, nor_1_out, and_1_out);
endmodule

module ca (
  input  a,
  input  b,
  output out1___sum,
  output out2___cout
);

  wire transistor_3_out, transistor_5_out, transistor_6_out, transistor_7_out;

  Transistor #(.gate("br")) transistor_1 (.in(1'b1), .out(out1___sum), .gate(transistor_3_out));
  Transistor #(.gate("br")) transistor_2 (.in(1'b1), .out(out2___cout), .gate(transistor_7_out));
  Transistor #(.gate("br")) transistor_3 (.in(a), .out(transistor_3_out), .gate(b));
  Transistor #(.gate("br")) transistor_4 (.in(b), .out(transistor_3_out), .gate(a));
  Transistor #(.gate("br")) transistor_5 (.in(1'b1), .out(transistor_5_out), .gate(b));
  Transistor #(.gate("br")) transistor_6 (.in(1'b1), .out(transistor_6_out), .gate(a));
  Transistor #(.gate("br")) transistor_7 (.in(transistor_6_out), .out(transistor_7_out), .gate(b));
  Transistor #(.\type ("n")) transistor_8 (.in(1'b0), .out(out1___sum), .gate(transistor_3_out));
  Transistor #(.\type ("n")) transistor_9 (.in(1'b0), .out(out2___cout), .gate(transistor_7_out));
  Transistor #(.\type ("n")) transistor_10 (.in(a), .out(transistor_3_out), .gate(transistor_5_out));
  Transistor #(.\type ("n")) transistor_11 (.in(transistor_5_out), .out(transistor_3_out), .gate(a));
  Transistor #(.\type ("n")) transistor_12 (.in(1'b0), .out(transistor_5_out), .gate(b));
  Transistor #(.\type ("n")) transistor_13 (.in(1'b0), .out(transistor_7_out), .gate(a));
  Transistor #(.\type ("n")) transistor_14 (.in(1'b0), .out(transistor_7_out), .gate(b));

  // Notes on the sheet:
  //   CARRY ADDER
  //   (full adder with cin = 1)
  //   out1 = XNOR(a,b)
  //   out2 = OR(a,b)
endmodule

module fa (
  input  in3___cin,
  input  in2___b,
  input  in1___a,
  output out2___sum,
  output out1___cout
);

  wire transistor_1_out, transistor_3_out, transistor_6_out, transistor_8_out, transistor_9_out,
       transistor_11_out;

  Transistor #(.gate("br")) transistor_1 (.in(in3___cin), .out(transistor_1_out), .gate(transistor_9_out));
  Transistor #(.gate("br")) transistor_2 (.in(transistor_3_out), .out(transistor_1_out), .gate(transistor_11_out));
  Transistor #(.gate("br")) transistor_3 (.in(1'b1), .out(transistor_3_out), .gate(in3___cin));
  Transistor #(.gate("br")) transistor_4 (.in(1'b1), .out(out2___sum), .gate(transistor_1_out));
  Transistor #(.gate("br")) transistor_5 (.in(1'b1), .out(out1___cout), .gate(transistor_6_out));
  Transistor #(.gate("br")) transistor_6 (.in(transistor_3_out), .out(transistor_6_out), .gate(transistor_9_out));
  Transistor #(.gate("br")) transistor_7 (.in(transistor_8_out), .out(transistor_6_out), .gate(transistor_11_out));
  Transistor #(.gate("br")) transistor_8 (.in(1'b1), .out(transistor_8_out), .gate(in2___b));
  Transistor #(.gate("br")) transistor_9 (.in(transistor_8_out), .out(transistor_9_out), .gate(in1___a));
  Transistor #(.gate("br")) transistor_10 (.in(in1___a), .out(transistor_9_out), .gate(transistor_8_out));
  Transistor #(.gate("br")) transistor_11 (.in(in1___a), .out(transistor_11_out), .gate(in2___b));
  Transistor #(.gate("br")) transistor_12 (.in(in2___b), .out(transistor_11_out), .gate(in1___a));
  Transistor #(.\type ("n")) transistor_13 (.in(in3___cin), .out(transistor_1_out), .gate(transistor_11_out));
  Transistor #(.\type ("n")) transistor_14 (.in(transistor_3_out), .out(transistor_1_out), .gate(transistor_9_out));
  Transistor #(.\type ("n")) transistor_15 (.in(1'b0), .out(transistor_3_out), .gate(in3___cin));
  Transistor #(.\type ("n")) transistor_16 (.in(1'b0), .out(out2___sum), .gate(transistor_1_out));
  Transistor #(.\type ("n")) transistor_17 (.in(1'b0), .out(out1___cout), .gate(transistor_6_out));
  Transistor #(.\type ("n")) transistor_18 (.in(transistor_3_out), .out(transistor_6_out), .gate(transistor_11_out));
  Transistor #(.\type ("n")) transistor_19 (.in(transistor_8_out), .out(transistor_6_out), .gate(transistor_9_out));
  Transistor #(.\type ("n")) transistor_20 (.in(1'b0), .out(transistor_8_out), .gate(in2___b));
  Transistor #(.\type ("n")) transistor_21 (.in(transistor_8_out), .out(transistor_11_out), .gate(in1___a));
  Transistor #(.\type ("n")) transistor_22 (.in(in1___a), .out(transistor_11_out), .gate(transistor_8_out));
  Transistor #(.\type ("n")) transistor_23 (.in(in1___a), .out(transistor_9_out), .gate(in2___b));
  Transistor #(.\type ("n")) transistor_24 (.in(in2___b), .out(transistor_9_out), .gate(in1___a));

  // Notes on the sheet:
  //   FULL ADDER
  //   xor
  //   xnor
endmodule

module ha (
  input  in2___b,
  input  in1___a,
  output out2___sum,
  output out1___cout
);

  wire transistor_3_out, transistor_5_out, transistor_6_out, transistor_13_out;

  Transistor #(.gate("br")) transistor_1 (.in(1'b1), .out(out2___sum), .gate(transistor_3_out));
  Transistor #(.gate("br")) transistor_2 (.in(1'b1), .out(out1___cout), .gate(transistor_6_out));
  Transistor #(.gate("br")) transistor_3 (.in(in2___b), .out(transistor_3_out), .gate(transistor_5_out));
  Transistor #(.gate("br")) transistor_4 (.in(transistor_5_out), .out(transistor_3_out), .gate(in2___b));
  Transistor #(.gate("br")) transistor_5 (.in(1'b1), .out(transistor_5_out), .gate(in1___a));
  Transistor #(.gate("br")) transistor_6 (.in(1'b1), .out(transistor_6_out), .gate(in2___b));
  Transistor #(.gate("br")) transistor_7 (.in(1'b1), .out(transistor_6_out), .gate(in1___a));
  Transistor #(.\type ("n")) transistor_8 (.in(1'b0), .out(out2___sum), .gate(transistor_3_out));
  Transistor #(.\type ("n")) transistor_9 (.in(1'b0), .out(out1___cout), .gate(transistor_6_out));
  Transistor #(.\type ("n")) transistor_10 (.in(in2___b), .out(transistor_3_out), .gate(in1___a));
  Transistor #(.\type ("n")) transistor_11 (.in(in1___a), .out(transistor_3_out), .gate(in2___b));
  Transistor #(.\type ("n")) transistor_12 (.in(1'b0), .out(transistor_5_out), .gate(in1___a));
  Transistor #(.\type ("n")) transistor_13 (.in(1'b0), .out(transistor_13_out), .gate(in2___b));
  Transistor #(.\type ("n")) transistor_14 (.in(transistor_13_out), .out(transistor_6_out), .gate(in1___a));

  // Notes on the sheet:
  //   HALF ADDER
endmodule

module ws1 (
  input  in5,
  input  in4,
  input  in3,
  input  in2,
  input  in1,
  output out3,
  output out2,
  output out1
);

  wire transistor_1_out, transistor_3_out, transistor_5_out, transistor_6_out, transistor_10_out,
       transistor_11_out, transistor_13_out, transistor_15_out, transistor_19_out, transistor_23_out,
       transistor_27_out, transistor_39_out, transistor_43_out;

  Transistor #(.gate("br")) transistor_1 (.in(1'b1), .out(transistor_1_out), .gate(transistor_3_out));
  Transistor #(.\type ("n")) transistor_2 (.in(1'b0), .out(transistor_1_out), .gate(transistor_3_out));
  Transistor #(.gate("br")) transistor_3 (.in(1'b1), .out(transistor_3_out), .gate(in5));
  Transistor #(.\type ("n")) transistor_4 (.in(1'b0), .out(transistor_3_out), .gate(in5));
  Transistor #(.gate("br")) transistor_5 (.in(1'b1), .out(transistor_5_out), .gate(in4));
  Transistor #(.gate("br")) transistor_6 (.in(in4), .out(transistor_6_out), .gate(transistor_3_out));
  Transistor #(.gate("br")) transistor_7 (.in(transistor_5_out), .out(transistor_6_out), .gate(in5));
  Transistor #(.\type ("n")) transistor_8 (.in(transistor_10_out), .out(transistor_6_out), .gate(transistor_3_out));
  Transistor #(.\type ("n")) transistor_9 (.in(in4), .out(transistor_6_out), .gate(in5));
  Transistor #(.\type ("n")) transistor_10 (.in(1'b0), .out(transistor_10_out), .gate(in4));
  Transistor #(.gate("br")) transistor_11 (.in(1'b1), .out(transistor_11_out), .gate(transistor_6_out));
  Transistor #(.\type ("n")) transistor_12 (.in(1'b0), .out(transistor_11_out), .gate(transistor_6_out));
  Transistor #(.gate("br")) transistor_13 (.in(1'b1), .out(transistor_13_out), .gate(transistor_11_out));
  Transistor #(.\type ("n")) transistor_14 (.in(1'b0), .out(transistor_13_out), .gate(transistor_11_out));
  Transistor #(.gate("br")) transistor_15 (.in(transistor_13_out), .out(transistor_15_out), .gate(in3));
  Transistor transistor_16 (.in(in3), .out(transistor_15_out), .gate(transistor_13_out));
  Transistor #(.\type ("n"), .gate("br")) transistor_17 (.in(in3), .out(transistor_15_out), .gate(transistor_11_out));
  Transistor #(.\type ("n")) transistor_18 (.in(transistor_11_out), .out(transistor_15_out), .gate(in3));
  Transistor #(.gate("br")) transistor_19 (.in(transistor_1_out), .out(transistor_19_out), .gate(transistor_11_out));
  Transistor #(.gate("br")) transistor_20 (.in(in3), .out(transistor_19_out), .gate(transistor_6_out));
  Transistor #(.\type ("n")) transistor_21 (.in(transistor_1_out), .out(transistor_19_out), .gate(transistor_6_out));
  Transistor #(.\type ("n")) transistor_22 (.in(in3), .out(transistor_19_out), .gate(transistor_11_out));
  Transistor #(.gate("br")) transistor_23 (.in(transistor_1_out), .out(transistor_23_out), .gate(transistor_11_out));
  Transistor #(.gate("br")) transistor_24 (.in(in2), .out(transistor_23_out), .gate(transistor_6_out));
  Transistor #(.\type ("n")) transistor_25 (.in(transistor_1_out), .out(transistor_23_out), .gate(transistor_6_out));
  Transistor #(.\type ("n")) transistor_26 (.in(in2), .out(transistor_23_out), .gate(transistor_11_out));
  Transistor #(.gate("br")) transistor_27 (.in(transistor_13_out), .out(transistor_27_out), .gate(in2));
  Transistor transistor_28 (.in(in2), .out(transistor_27_out), .gate(transistor_13_out));
  Transistor #(.\type ("n")) transistor_29 (.in(transistor_11_out), .out(transistor_27_out), .gate(in2));
  Transistor #(.\type ("n"), .gate("br")) transistor_30 (.in(in2), .out(transistor_27_out), .gate(transistor_11_out));
  Transistor #(.gate("br")) transistor_31 (.in(1'b1), .out(out3), .gate(transistor_23_out));
  Transistor #(.gate("br")) transistor_32 (.in(1'b1), .out(out3), .gate(transistor_23_out));
  Transistor #(.\type ("n")) transistor_33 (.in(1'b0), .out(out3), .gate(transistor_23_out));
  Transistor #(.\type ("n")) transistor_34 (.in(1'b0), .out(out3), .gate(transistor_23_out));
  Transistor #(.gate("br")) transistor_35 (.in(1'b1), .out(out2), .gate(transistor_19_out));
  Transistor #(.gate("br")) transistor_36 (.in(1'b1), .out(out2), .gate(transistor_19_out));
  Transistor #(.\type ("n")) transistor_37 (.in(1'b0), .out(out2), .gate(transistor_19_out));
  Transistor #(.\type ("n")) transistor_38 (.in(1'b0), .out(out2), .gate(transistor_19_out));
  Transistor #(.gate("br")) transistor_39 (.in(transistor_27_out), .out(transistor_39_out), .gate(in1));
  Transistor #(.gate("br")) transistor_40 (.in(transistor_15_out), .out(transistor_39_out), .gate(transistor_43_out));
  Transistor #(.\type ("n")) transistor_41 (.in(transistor_27_out), .out(transistor_39_out), .gate(transistor_43_out));
  Transistor #(.\type ("n")) transistor_42 (.in(transistor_15_out), .out(transistor_39_out), .gate(in1));
  Transistor #(.gate("br")) transistor_43 (.in(1'b1), .out(transistor_43_out), .gate(in1));
  Transistor #(.\type ("n")) transistor_44 (.in(1'b0), .out(transistor_43_out), .gate(in1));
  Transistor #(.gate("br")) transistor_45 (.in(1'b1), .out(out1), .gate(transistor_39_out));
  Transistor #(.gate("br")) transistor_46 (.in(1'b1), .out(out1), .gate(transistor_39_out));
  Transistor #(.\type ("n")) transistor_47 (.in(1'b0), .out(out1), .gate(transistor_39_out));
  Transistor #(.\type ("n")) transistor_48 (.in(1'b0), .out(out1), .gate(transistor_39_out));

  // Notes on the sheet:
  //   in5'
  //   XNOR
  //   x
  //   !x
  //   x2
  //   s1
  //   s0
endmodule

module ws2 (
  input  in5,
  input  in4,
  input  in3,
  input  in2,
  input  in1,
  output out3,
  output out2,
  output out1
);

  wire transistor_1_out, transistor_3_out, transistor_5_out, transistor_6_out, transistor_7_out,
       transistor_11_out, transistor_13_out, transistor_15_out, transistor_19_out, transistor_23_out,
       transistor_27_out, transistor_39_out, transistor_43_out;

  Transistor #(.gate("br")) transistor_1 (.in(1'b1), .out(transistor_1_out), .gate(in5));
  Transistor #(.\type ("n")) transistor_2 (.in(1'b0), .out(transistor_1_out), .gate(in5));
  Transistor #(.gate("br")) transistor_3 (.in(1'b1), .out(transistor_3_out), .gate(in5));
  Transistor #(.\type ("n")) transistor_4 (.in(1'b0), .out(transistor_3_out), .gate(in5));
  Transistor #(.gate("br")) transistor_5 (.in(1'b1), .out(transistor_5_out), .gate(in4));
  Transistor #(.\type ("n")) transistor_6 (.in(1'b0), .out(transistor_6_out), .gate(in4));
  Transistor #(.gate("br")) transistor_7 (.in(transistor_5_out), .out(transistor_7_out), .gate(in5));
  Transistor #(.gate("br")) transistor_8 (.in(in4), .out(transistor_7_out), .gate(transistor_3_out));
  Transistor #(.\type ("n")) transistor_9 (.in(in4), .out(transistor_7_out), .gate(in5));
  Transistor #(.\type ("n")) transistor_10 (.in(transistor_6_out), .out(transistor_7_out), .gate(transistor_3_out));
  Transistor #(.gate("br")) transistor_11 (.in(1'b1), .out(transistor_11_out), .gate(transistor_7_out));
  Transistor #(.\type ("n")) transistor_12 (.in(1'b0), .out(transistor_11_out), .gate(transistor_7_out));
  Transistor #(.gate("br")) transistor_13 (.in(1'b1), .out(transistor_13_out), .gate(transistor_11_out));
  Transistor #(.\type ("n")) transistor_14 (.in(1'b0), .out(transistor_13_out), .gate(transistor_11_out));
  Transistor #(.gate("br")) transistor_15 (.in(transistor_11_out), .out(transistor_15_out), .gate(in3));
  Transistor #(.\type ("n")) transistor_16 (.in(transistor_13_out), .out(transistor_15_out), .gate(in3));
  Transistor #(.gate("br")) transistor_17 (.in(in3), .out(transistor_15_out), .gate(transistor_11_out));
  Transistor #(.\type ("n")) transistor_18 (.in(in3), .out(transistor_15_out), .gate(transistor_13_out));
  Transistor #(.gate("br")) transistor_19 (.in(transistor_1_out), .out(transistor_19_out), .gate(transistor_11_out));
  Transistor #(.gate("br")) transistor_20 (.in(in3), .out(transistor_19_out), .gate(transistor_7_out));
  Transistor #(.\type ("n")) transistor_21 (.in(transistor_1_out), .out(transistor_19_out), .gate(transistor_7_out));
  Transistor #(.\type ("n")) transistor_22 (.in(in3), .out(transistor_19_out), .gate(transistor_11_out));
  Transistor #(.gate("br")) transistor_23 (.in(in2), .out(transistor_23_out), .gate(transistor_7_out));
  Transistor #(.gate("br")) transistor_24 (.in(transistor_1_out), .out(transistor_23_out), .gate(transistor_11_out));
  Transistor #(.\type ("n")) transistor_25 (.in(transistor_1_out), .out(transistor_23_out), .gate(transistor_7_out));
  Transistor #(.\type ("n")) transistor_26 (.in(in2), .out(transistor_23_out), .gate(transistor_11_out));
  Transistor #(.gate("br")) transistor_27 (.in(transistor_11_out), .out(transistor_27_out), .gate(in2));
  Transistor #(.gate("br")) transistor_28 (.in(in2), .out(transistor_27_out), .gate(transistor_11_out));
  Transistor #(.\type ("n")) transistor_29 (.in(transistor_13_out), .out(transistor_27_out), .gate(in2));
  Transistor #(.\type ("n")) transistor_30 (.in(in2), .out(transistor_27_out), .gate(transistor_13_out));
  Transistor #(.gate("br")) transistor_31 (.in(1'b1), .out(out3), .gate(transistor_23_out));
  Transistor #(.gate("br")) transistor_32 (.in(1'b1), .out(out3), .gate(transistor_23_out));
  Transistor #(.\type ("n")) transistor_33 (.in(1'b0), .out(out3), .gate(transistor_23_out));
  Transistor #(.\type ("n")) transistor_34 (.in(1'b0), .out(out3), .gate(transistor_23_out));
  Transistor #(.gate("br")) transistor_35 (.in(1'b1), .out(out2), .gate(transistor_19_out));
  Transistor #(.gate("br")) transistor_36 (.in(1'b1), .out(out2), .gate(transistor_19_out));
  Transistor #(.\type ("n")) transistor_37 (.in(1'b0), .out(out2), .gate(transistor_19_out));
  Transistor #(.\type ("n")) transistor_38 (.in(1'b0), .out(out2), .gate(transistor_19_out));
  Transistor #(.gate("br")) transistor_39 (.in(transistor_15_out), .out(transistor_39_out), .gate(transistor_43_out));
  Transistor #(.gate("br")) transistor_40 (.in(transistor_27_out), .out(transistor_39_out), .gate(in1));
  Transistor #(.\type ("n")) transistor_41 (.in(transistor_27_out), .out(transistor_39_out), .gate(transistor_43_out));
  Transistor #(.\type ("n")) transistor_42 (.in(transistor_15_out), .out(transistor_39_out), .gate(in1));
  Transistor #(.gate("br")) transistor_43 (.in(1'b1), .out(transistor_43_out), .gate(in1));
  Transistor #(.\type ("n")) transistor_44 (.in(1'b0), .out(transistor_43_out), .gate(in1));
  Transistor #(.gate("br")) transistor_45 (.in(1'b1), .out(out1), .gate(transistor_39_out));
  Transistor #(.gate("br")) transistor_46 (.in(1'b1), .out(out1), .gate(transistor_39_out));
  Transistor #(.\type ("n")) transistor_47 (.in(1'b0), .out(out1), .gate(transistor_39_out));
  Transistor #(.\type ("n")) transistor_48 (.in(1'b0), .out(out1), .gate(transistor_39_out));

  // Notes on the sheet:
  //   !in5'
  //   XNOR
  //   x
  //   !x
  //   x2
  //   s1
  //   s0
endmodule

module _4_mux (
  input  s1,
  input  _3,
  input  _2,
  input  _1,
  input  _0,
  input  s0,
  output out
);

  wire transistor_2_out, transistor_3_out, transistor_5_out, transistor_6_out, transistor_8_out,
       transistor_9_out, transistor_10_out, transistor_12_out, transistor_13_out, transistor_18_out,
       transistor_21_out, transistor_22_out, transistor_25_out;

  Transistor #(.gate("br")) transistor_1 (.in(1'b1), .out(out), .gate(transistor_3_out));
  Transistor #(.gate("br")) transistor_2 (.in(1'b1), .out(transistor_2_out), .gate(s1));
  Transistor #(.gate("br")) transistor_3 (.in(transistor_6_out), .out(transistor_3_out), .gate(transistor_2_out));
  Transistor #(.gate("br")) transistor_4 (.in(transistor_10_out), .out(transistor_3_out), .gate(s1));
  Transistor #(.gate("br")) transistor_5 (.in(1'b1), .out(transistor_5_out), .gate(_3));
  Transistor #(.gate("br")) transistor_6 (.in(transistor_5_out), .out(transistor_6_out), .gate(transistor_13_out));
  Transistor #(.gate("br")) transistor_7 (.in(transistor_8_out), .out(transistor_6_out), .gate(s0));
  Transistor #(.gate("br")) transistor_8 (.in(1'b1), .out(transistor_8_out), .gate(_2));
  Transistor #(.gate("br")) transistor_9 (.in(1'b1), .out(transistor_9_out), .gate(_1));
  Transistor #(.gate("br")) transistor_10 (.in(transistor_9_out), .out(transistor_10_out), .gate(transistor_13_out));
  Transistor #(.gate("br")) transistor_11 (.in(transistor_12_out), .out(transistor_10_out), .gate(s0));
  Transistor #(.gate("br")) transistor_12 (.in(1'b1), .out(transistor_12_out), .gate(_0));
  Transistor #(.gate("br")) transistor_13 (.in(1'b1), .out(transistor_13_out), .gate(s0));
  Transistor #(.\type ("n")) transistor_14 (.in(1'b0), .out(out), .gate(transistor_3_out));
  Transistor #(.\type ("n")) transistor_15 (.in(1'b0), .out(transistor_2_out), .gate(s1));
  Transistor #(.\type ("n")) transistor_16 (.in(transistor_6_out), .out(transistor_3_out), .gate(s1));
  Transistor #(.\type ("n")) transistor_17 (.in(transistor_10_out), .out(transistor_3_out), .gate(transistor_2_out));
  Transistor #(.\type ("n")) transistor_18 (.in(1'b0), .out(transistor_18_out), .gate(_3));
  Transistor #(.\type ("n")) transistor_19 (.in(transistor_18_out), .out(transistor_6_out), .gate(s0));
  Transistor #(.\type ("n")) transistor_20 (.in(transistor_21_out), .out(transistor_6_out), .gate(transistor_13_out));
  Transistor #(.\type ("n")) transistor_21 (.in(1'b0), .out(transistor_21_out), .gate(_2));
  Transistor #(.\type ("n")) transistor_22 (.in(1'b0), .out(transistor_22_out), .gate(_1));
  Transistor #(.\type ("n")) transistor_23 (.in(transistor_22_out), .out(transistor_10_out), .gate(s0));
  Transistor #(.\type ("n")) transistor_24 (.in(transistor_25_out), .out(transistor_10_out), .gate(transistor_13_out));
  Transistor #(.\type ("n")) transistor_25 (.in(1'b0), .out(transistor_25_out), .gate(_0));
  Transistor #(.\type ("n")) transistor_26 (.in(1'b0), .out(transistor_13_out), .gate(s0));
endmodule
module RLE (
  input  [15:0] RLE_input,
  input  in_2,
  input  nc8__kill,
  input  ac4_q_nfull,
  input  nFE00,
  input  ch0_0,
  input  ch1_3,
  input  lc_n0,
  input  ac4_d_nfull,
  input  lum_col,
  input  nres,
  input  mclk,
  input  c8,
  output ie1,
  output ie2,
  output [5:0] Address_for_decoded_data,
  output [11:0] Decoded_data,
  output rle_finished,
  output oe1,
  output oe2,
  output [5:0] Address_for_RLE_input,
  output rle_data_ended
);

  wire _3387_out, _3390_out, _3491_out, _3492_out, _3493_out, _3495_out, _3496_out, _3497_out, _3786_out_4,
       _3789_out_4, _3790_q, _3791_out, _3792_q, _3793_out, _3794_out, _3795_out, _3796_out, _3797_q,
       _3799_out, _3893_out, _3898_out_4, _3899_out, _3993_out, _3994_out, _3995_out, _4073_out, _4074_out,
       _4075_out, _4077_out, _4078_out, _4079_out, _4080_out, _4081_out, _4083_out, _4095_out_4, _4096_out,
       _4097_out, _4098_out, _4099_out, _4195_out, _4196_out, _4197_out, _4293_out, _4294_out, _4295_out,
       _4296_out, _4298_out, _4310_out_4, _4398_out, _4399_out, _34102_out, _34103_out, _34110_out,
       _34112_out, _34114_2_out, _34114_out, _35103_out, _35104_q, _35105_out, _35106_out, _35107_out,
       _35108_q, _35111_out, _35114_out, _35115_out, _35116_out, _35117_out, _35119_out, _35120_out,
       _35121_out, _35122_out, _35123_out, _35124_out, _36104_q, _36105_q, _36106_out, _36107_q,
       _36108_2_out, _36108_out, _36109_2_out, _36109_out, _36110_q, _36111_out, _36112_out, _36113_out,
       _36114_out, _36115_out, _36116_out, _36117_out, _36118_out, _36119_out, _37100_out, _37101_out,
       _37102_out, _37104_out, _37105_out, _37106_out, _37110_out, _37111_out, _37112_out, _37113_out,
       _38102_out, _38103_out, _38106_out_4, _38107_out, _38108_out, _38109_q, _38110_out, _38111_out,
       _38112_out, _38113_q, _38114_out, _38115_out, _38116_q, _38118_out, _38119_out, _38120_out,
       _38121_out, _38122_out, _38123_out, _38124_out, _38125_out, _38127_out, _38128_out, _38129_out,
       _38130_out, _38131_out, _39100_out, _39112_out, _39113_out, _39114_out, _39116_out, _39117_out,
       _39120_out, _39121_out, _39122_out, _39123_out, _39124_out, _39125_out, _39126_q, _39127_out,
       _39128_q, _39129_out, _39130_q, _39131_out, _39132_q, _39133_out, _39135_out, _39137_out, _39139_out,
       _39140_out, _39145_out, _39150_out, _39152_out, _39153_out, _40100_2_out, _40100_out, _40101_out,
       _40102_out, _40105_q, _40106_out, _40111_out, _40114_out, _40120_out, _40125_out, _41100_out,
       _41101_out, _41102_out, _41104_out, _41105_out, _41106_out, _41107_out, _41108_out, _41109_out,
       _41110_out, _41121_out, _41122_out, _41123_out_4, _41124_out, _41125_out, _41127_out, _41137_out,
       _41138_out, _41139_out, _41140_out, _41145_out, _41149_out, _41153_out, _41154_out, _42101_out,
       _42102_out, _42103_out_4, _42104_out, _42105_out, _42106_out, _42113_out_4, _42114_out, _42115_out_4,
       _42116_out_4, _42117_2_out, _42117_out, _42118_out, _42133_out, _42138_out, _43101_out, _43102_out_4,
       _43103_out_4, _43104_out, _43106_out, _43107_out_4, _43112_2_out, _43112_out, _43115_out, _43116_out,
       _43119_out, _43122_out, _43123_out_4, _43124_out, _43130_out, _43132_out, _44109_out, _44110_out_4,
       _44130_out, _44131_out, _44132_out, _44138_out, _44140_out, _45122_out, _45123_out, _45128_out_4,
       _45129_out, _45130_out, _45131_out, _45132_out, _45134_out, _45136_out, _45137_out, _45178_out,
       _46134_out, _46135_out, _46136_out, _46137_out, _46139_out, _46140_out_4, _46141_out, _46142_out,
       _46143_out, _46144_out, _46145_out, _46147_out, _46149_out, _46152_out, _46154_out, _46155_out,
       _46201_out, _47109_out, _47111_out, _47112_out_4, _47114_out, and_1_out, and_2_out, and_3_out,
       and_4_out, and_5_out, and_6_out, and_7_out, and_8_out, and_9_out, and_10_out, and_11_out, and_12_out,
       and_13_out, and_14_out, and_15_out, and_16_out, and_17_out, and_18_out, and_19_out, and_20_out,
       and_21_out, and_22_out, and_23_out, and_24_out, and_25_out, and_26_out, and_27_out, and_28_out,
       and_29_out, and_30_out, and_31_out, and_32_out, and_33_out, and_34_out, and_35_out, and_36_out,
       and_37_out, and_38_out, and_39_out, and_40_out, and_41_out, and_42_out, and_43_out, and_44_out,
       and_45_out, and_46_out, and_47_out, and_48_out, and_49_out, and_50_out, and_51_out, and_52_out,
       and_53_out, and_54_out, and_55_out, and_56_out, and_57_out, and_58_out, and_59_out, and_60_out,
       and_61_out, and_62_out, and_63_out, and_64_out, and_65_out, and_66_out, and_67_out, and_68_out,
       clock_1_out, d_ff_1_q, d_ff_2_q, d_ff_3_q, d_ff_4_q, d_ff_5_q, d_ff_6_q, d_ff_7_q, d_ff_8_q, d_ff_9_q,
       d_ff_10_q, d_ff_11_q, d_ff_12_q, d_ff_13_q, d_ff_14_q, d_ff_15_q, d_ff_16_q, d_ff_17_q, d_ff_18_q,
       d_ff_19_q, d_ff_20_q, d_ff_21_q, d_ff_22_q, d_ff_23_q, d_ff_24_q, d_ff_25_q, d_ff_26_q, d_ff_27_q,
       d_ff_28_q, d_ff_29_q, d_ff_30_q, d_ff_31_q, d_ff_32_q, d_ff_33_q, d_ff_34_q, d_ff_35_q, d_ff_36_q,
       d_ff_37_q, d_ff_38_q, d_ff_39_q, d_ff_40_q, d_ff_41_q, d_ff_42_q, d_ff_43_q, d_ff_44_q, d_ff_45_q,
       d_ff_46_q, d_ff_47_q, d_ff_48_q, d_ff_49_q, d_ff_50_q, d_ff_51_q, d_ff_52_q, d_ff_53_q, d_ff_54_q,
       d_ff_55_q, d_ff_56_q, d_ff_57_q, d_ff_58_q, d_ff_59_q, d_ff_60_q, d_ff_61_q, d_ff_62_q, d_ff_63_q,
       d_ff_67_q, d_ff_68_q, d_ff_69_q, d_ff_71_q, d_ff_72_q, d_ff_73_q, d_ff_75_q, d_ff_76_q, d_ff_77_q,
       d_ff_79_q, d_ff_80_q, d_ff_81_q, d_ff_83_q, d_ff_84_q, d_ff_85_q, d_ff_87_q, d_ff_88_q, d_ff_89_q,
       d_ff_91_q, d_ff_92_q, d_ff_93_q, d_ff_96_q, d_ff_97_q, d_ff_98_q, d_ff_99_q, d_ff_100_q, d_ff_101_q,
       d_ff_103_q, d_ff_104_q, d_ff_105_q, dffr_logic_1_out_4, dffr_logic_2_out_4, dffr_logic_3_out_4,
       dffr_logic_4_out_4, dffr_logic_5_out_4, dffr_logic_6_out_4, dffr_logic_7_out_4, dffr_logic_8_out_4,
       dffr_logic_9_out_4, dffr_logic_10_out_4, dffr_logic_11_out_4, dffr_logic_12_out_4,
       dffr_logic_13_out_4, dffr_logic_14_out_4, dffr_logic_15_out_4, dffr_logic_16_out_4,
       dffr_logic_17_out_4, dffr_logic_18_out_4, dffr_logic_19_out_4, dffr_logic_20_out_4,
       dffr_logic_21_out_4, dffr_logic_22_out_4, dffr_logic_23_out_4, dffr_logic_24_out_4,
       dffr_logic_25_out_4, dffr_logic_26_out_4, dffr_logic_27_out_4, dffr_logic_28_out_4,
       dffr_logic_29_out_4, dffr_logic_30_out_4, imux_1_out, imux_2_out, imux_3_out, imux_4_out, imux_5_out,
       imux_6_out, imux_7_out, imux_8_out, imux_9_out, imux_10_out, imux_11_out, imux_12_out, imux_13_out,
       imux_14_out, imux_15_out, imux_16_out, imux_17_out, imux_18_out, imux_19_out, imux_20_out,
       imux_21_out, imux_22_out, imux_23_out, imux_24_out, imux_25_out, imux_26_out, imux_27_out,
       imux_28_out, imux_29_out, minus_234_minus_out, minus_241_minus_out, minus_242_minus_out,
       minus_243_minus_out, minus_246_minus_out, minus_248_minus_out, minus_249_minus_out,
       minus_250_minus_out, minus_252_minus_out, minus_253_minus_out, minus_254_minus_out,
       minus_256_minus_out, minus_257_minus_out, minus_258_minus_out, minus_259_minus_out,
       minus_260_minus_out, minus_261_minus_out, minus_262_minus_out, minus_268_minus_out,
       minus_270_minus_out, minus_271_minus_out, minus_272_minus_out, minus_273_minus_out,
       minus_274_minus_out, minus_275_minus_out, minus_276_minus_out, minus_277_minus_out,
       minus_278_minus_out, minus_279_minus_out, minus_280_minus_out, minus_299_minus_out,
       minus_300_minus_out, minus_310_minus_out, minus_355_minus_out, minus_356_minus_out,
       minus_357_minus_out, minus_358_minus_out, minus_359_minus_out, minus_360_minus_out,
       minus_361_minus_out, minus_362_minus_out, minus_363_minus_out, minus_364_minus_out,
       minus_410_minus_out, minus_411_minus_out, minus_412_minus_out, minus_413_minus_out,
       minus_414_minus_out, minus_415_minus_out, minus_416_minus_out, minus_417_minus_out,
       minus_419_minus_out, minus_420_minus_out, minus_421_minus_2_out, minus_421_minus_out,
       minus_422_minus_out, minus_423_minus_out, minus_424_minus_out, minus_425_minus_out,
       minus_426_minus_out, minus_427_minus_out, minus_428_minus_out, minus_429_minus_out,
       minus_432_minus_out, minus_433_minus_out, minus_434_minus_out, minus_436_minus_out,
       minus_437_minus_out, minus_438_minus_out, minus_439_minus_out, minus_440_minus_out,
       minus_441_minus_out, minus_444_minus_out, minus_445_minus_out, minus_447_minus_out,
       minus_448_minus_out, minus_449_minus_out, minus_450_minus_out, minus_451_minus_out,
       minus_453_minus_out, minus_454_minus_out, minus_455_minus_2_out, minus_455_minus_out,
       minus_456_minus_out, minus_457_minus_out, minus_459_minus_out, minus_460_minus_out,
       minus_462_minus_out, minus_463_minus_out, minus_464_minus_out, minus_467_minus_out,
       minus_469_minus_out, minus_470_minus_out, minus_471_minus_out, minus_472_minus_out,
       minus_474_minus_out, minus_475_minus_out, minus_476_minus_out, minus_477_minus_out,
       minus_478_minus_out, minus_480_minus_out, minus_481_minus_out, minus_482_minus_out,
       minus_484_minus_out, minus_485_minus_out, minus_486_minus_out, minus_487_minus_out,
       minus_488_minus_out, minus_489_minus_out, minus_490_minus_out, minus_491_minus_out,
       minus_492_minus_out, minus_494_minus_out, minus_495_minus_out, minus_496_minus_out,
       minus_499_minus_out, minus_500_minus_out, minus_501_minus_out, minus_502_minus_out,
       minus_504_minus_out, minus_505_minus_out, minus_506_minus_out, minus_507_minus_out,
       minus_509_minus_out, minus_510_minus_out, minus_511_minus_out, minus_513_minus_out,
       minus_515_minus_out, minus_516_minus_out, minus_519_minus_out, minus_520_minus_out,
       minus_521_minus_out, minus_522_minus_out, minus_523_minus_out, minus_524_minus_out,
       minus_525_minus_out, minus_526_minus_out, minus_527_minus_out, minus_528_minus_out,
       minus_529_minus_out, minus_530_minus_out, minus_531_minus_out, minus_532_minus_out,
       minus_536_minus_out, minus_537_minus_out, minus_538_minus_out, minus_540_minus_out,
       minus_541_minus_out, minus_542_minus_out, minus_543_minus_out, minus_544_minus_out,
       minus_545_minus_out, minus_546_minus_out, minus_552_minus_out, minus_554_minus_out,
       minus_556_minus_out, minus_558_minus_out, minus_560_minus_out, minus_562_minus_out,
       minus_574_minus_out, minus_576_minus_out, minus_578_minus_out, minus_579_minus_out,
       minus_581_minus_out, minus_582_minus_out, minus_584_minus_out, minus_586_minus_out,
       minus_588_minus_out, minus_589_minus_out, minus_590_minus_out, minus_591_minus_out,
       minus_592_minus_out, minus_593_minus_out, minus_594_minus_out, minus_595_minus_out,
       minus_597_minus_out, minus_598_minus_out, minus_599_minus_out, minus_600_minus_out,
       minus_601_minus_out, minus_602_minus_out, minus_603_minus_out, minus_604_minus_out,
       minus_605_minus_out, minus_606_minus_out, minus_607_minus_out, minus_608_minus_out,
       minus_609_minus_out, minus_610_minus_out, minus_611_minus_out, minus_612_minus_out,
       minus_613_minus_out, minus_614_minus_out, minus_615_minus_out, minus_616_minus_out,
       minus_617_minus_out, minus_618_minus_out, minus_619_minus_out, minus_620_minus_out,
       minus_621_minus_out, minus_622_minus_out, minus_623_minus_out, minus_624_minus_out,
       minus_625_minus_out, minus_626_minus_out, minus_627_minus_out, minus_628_minus_out,
       minus_629_minus_out, minus_630_minus_out, minus_631_minus_out, minus_632_minus_out,
       minus_650_minus_out, minus_673_minus_out, minus_678_minus_out_4, minus_679_minus_out_4,
       minus_680_minus_out, minus_706_minus_out, minus_712_minus_out, minus_725_minus_out,
       minus_726_minus_out, minus_728_minus_out, minus_733_minus_out, minus_734_minus_out,
       minus_738_minus_out, minus_745_minus_out, minus_756_minus_out, minus_769_minus_out,
       minus_771_minus_out, n4_mux_1_out, n4_mux_2_out, n4_mux_3_out, n4_mux_4_out, n4_mux_5_out,
       n4_mux_6_out, n4_mux_7_out, n4_mux_8_out, n4_mux_9_out, n4_mux_10_out, n4_mux_11_out, n4_mux_12_out,
       n4_mux_13_out, n4_mux_14_out, nand_1_out, nand_2_out, nand_3_out, nand_4_out, nand_5_out, nand_6_out,
       nand_7_out, nand_8_out, nand_9_out, nand_10_out, nand_11_out, nand_12_out, nand_13_out, nand_14_out,
       nand_15_out, nand_16_out, nand_17_out, nand_18_out, nand_19_out, nand_20_out, nand_21_out,
       nand_22_out, nand_23_out, nand_24_out, nand_25_out, nand_26_out, nand_27_out, nand_28_out,
       nand_29_out, nand_30_out, nand_31_out, nand_32_out, nand_33_out, nand_34_out, nand_35_out,
       nand_36_out, nand_37_out, nand_38_out, nand_39_out, nand_40_out, nand_41_out, nand_42_out,
       nand_43_out, nand_44_out, nand_45_out, nand_46_out, nand_47_out, nand_48_out, nand_49_out,
       nand_50_out, nand_51_out, nand_52_out, nand_53_out, nand_54_out, nand_55_out, nand_56_out,
       nand_57_out, nand_58_out, nand_59_out, nand_60_out, nand_61_out, nand_62_out, nand_63_out,
       nand_64_out, nand_65_out, nand_66_out, nand_67_out, nand_68_out, nand_69_out, nand_70_out,
       nand_71_out, nand_72_out, nand_73_out, nand_74_out, nand_75_out, nand_76_out, nand_77_out,
       nand_78_out, nand_79_out, nand_80_out, nand_81_out, nand_82_out, nand_83_out, nand_84_out,
       nand_85_out, nor_1_out, nor_2_out, nor_3_out, nor_4_out, nor_5_out, nor_6_out, nor_7_out, nor_8_out,
       nor_9_out, nor_10_out, nor_11_out, not_1_out, not_2_out, not_3_out, not_4_out, not_5_out, not_6_out,
       not_7_out, not_8_out, not_9_out, not_10_out, not_11_out, not_12_out, not_13_out, not_14_out,
       not_15_out, not_16_out, not_17_out, not_18_out, not_19_out, not_20_out, not_21_out, not_28_out,
       not_29_out, not_30_out, not_31_out, not_32_out, not_33_out, not_34_out, not_35_out, not_36_out,
       not_37_out, not_38_out, not_39_out, not_40_out, not_41_out, not_48_out, not_49_out, not_50_out,
       not_51_out, not_52_out, not_53_out, not_54_out, not_55_out, not_56_out, not_57_out, not_58_out,
       not_59_out, not_60_out, not_61_out, not_62_out, not_63_out, not_64_out, not_65_out, not_66_out,
       not_67_out, not_68_out, not_69_out, not_70_out, not_71_out, not_72_out, not_73_out, not_74_out,
       not_75_out, not_76_out, not_77_out, not_78_out, not_79_out, or_1_out, or_2_out, or_3_out, or_4_out,
       or_5_out, or_6_out, or_7_out, or_8_out, or_9_out, or_10_out, or_11_out, or_12_out, or_13_out,
       or_14_out, or_15_out, or_16_out, or_17_out, or_18_out, or_19_out, or_20_out, or_21_out, or_22_out,
       or_23_out, or_24_out, or_25_out, or_26_out, or_27_out, or_28_out, or_29_out, or_30_out, or_31_out,
       or_32_out, or_33_out, or_34_out, or_35_out, or_36_out, or_37_out, or_38_out, or_39_out, or_40_out,
       or_41_out, or_42_out, or_43_out, or_44_out, or_45_out, undriven, xor_1_out, xor_2_out, xor_3_out,
       xor_4_out, xor_5_out, xor_6_out, xor_7_out, xor_8_out, xor_9_out, xor_10_out, xor_11_out, xor_12_out,
       xor_13_out, xor_14_out, xor_15_out, xor_16_out, xor_17_out, xor_18_out, xor_19_out, xor_20_out,
       xor_21_out, xor_22_out;

  DFFR_logic _3898 (.clk(_42117_2_out), .in(_39112_out), .nres(_43112_out), .out_4(_3898_out_4));
  IMUX _39112 (.b___in0(_39123_out), .c___in1(_3898_out_4), .out(_39112_out), .sel(_38103_out));
  not _39123 (_39123_out, RLE_input[10]);
  IMUX _38102 (.b___in0(_39117_out), .c___in1(_3899_out), .out(_38102_out), .sel(_38103_out));
  and _3899 (_3899_out, nand_1_out, xor_1_out);
  xor xor_1 (xor_1_out, _3786_out_4, _3898_out_4);
  nand nand_1 (nand_1_out, _3898_out_4, _3786_out_4);
  not _39117 (_39117_out, RLE_input[11]);
  DFFR_logic _3786 (.clk(_42117_2_out), .in(_38102_out), .nres(_43112_out), .out_4(_3786_out_4));
  and _39114 (_39114_out, nand_2_out, xor_2_out);
  nand nand_2 (nand_2_out, _39113_out, _4095_out_4);
  or _39113 (_39113_out, _3898_out_4, _3786_out_4);
  IMUX _4096 (.b___in0(_40100_out), .c___in1(_39114_out), .out(_4096_out), .sel(_38103_out));
  xor xor_2 (xor_2_out, _4095_out_4, _39113_out);
  not _40100 (_40100_out, RLE_input[12]);
  nor _4074 (_4074_out, and_2_out, and_1_out);
  and and_1 (and_1_out, _4195_out, _4075_out);
  and and_2 (and_2_out, _44110_out_4, dffr_logic_3_out_4);
  or or_1 (or_1_out, not_15_out, not_8_out);
  DFFR_logic _4095 (.clk(_42117_2_out), .in(_4096_out), .nres(_43112_out), .out_4(_4095_out_4));
  and _39121 (_39121_out, nand_3_out, xor_3_out);
  nand nand_3 (nand_3_out, _39116_out, _38106_out_4);
  or _39116 (_39116_out, _39113_out, _4095_out_4);
  xor _4073 (_4073_out, _4075_out, _4195_out);
  nand _4075 (_4075_out, or_1_out, or_2_out);
  xor _4195 (_4195_out, not_17_out, not_9_out);
  or or_2 (or_2_out, _3995_out, _3994_out);
  DFFR_logic _38106 (.clk(_42117_2_out), .in(_39120_out), .nres(_43112_out), .out_4(_38106_out_4));
  IMUX _39120 (.b___in0(_40100_2_out), .c___in1(_39121_out), .out(_39120_out), .sel(_38103_out));
  xor xor_3 (xor_3_out, _38106_out_4, _39116_out);
  or _39122 (_39122_out, _39116_out, _38106_out_4);
  not _40100_2 (_40100_2_out, RLE_input[13]);
  nand _4078 (_4078_out, _4074_out, _4077_out);
  nand _4077 (_4077_out, _4073_out, _3993_out, _4298_out);
  xor _3993 (_3993_out, _3994_out, _3995_out);
  nand _3995 (_3995_out, _43102_out_4, _43103_out_4);
  xnor _3994 (_3994_out, _4310_out_4, _42103_out_4);
  and _41127 (_41127_out, nand_4_out, xor_4_out);
  nand nand_4 (nand_4_out, _39122_out, _41123_out_4);
  xor xor_4 (xor_4_out, _41123_out_4, _39122_out);
  or or_3 (or_3_out, mclk, _46139_out);
  or _41108 (_41108_out, mclk, _46139_out, _41105_out);
  IMUX _41105 (.b___in0(_41102_out), .c___in1(_4197_out), .out(_41105_out), .sel(_4078_out));
  nand _41102 (_41102_out, _41101_out, _4298_out);
  nand _4197 (_4197_out, _4196_out, or_4_out);
  or or_4 (or_4_out, not_15_out, not_17_out);
  and _41101 (_41101_out, not_8_out, not_9_out, not_1_out);
  DFFR_logic _41123 (.clk(_42117_2_out), .in(_41125_out), .nres(_43112_out), .out_4(_41123_out_4));
  IMUX _41125 (.b___in0(_41124_out), .c___in1(_41127_out), .out(_41125_out), .sel(_38103_out));
  or _40102 (_40102_out, _39122_out, _41123_out_4);
  not _41124 (_41124_out, RLE_input[14]);
  or _41107 (_41107_out, mclk, _46139_out, _41106_out);
  IMUX _41106 (.b___in0(_4081_out), .c___in1(_42101_out), .out(_41106_out), .sel(_4078_out));
  or _4081 (_4081_out, _4080_out, _4298_out);
  or _4080 (_4080_out, _44110_out_4, _4310_out_4, _43102_out_4);
  // Probe on _47114_out
  not _47114 (_47114_out, dffr_logic_1_out_4);
  DFFR_logic dffr_logic_1 (.clk(minus_706_minus_out), .in(dffr_logic_2_out_4), .nres(nres), .out_4(dffr_logic_1_out_4));
  DFFR_logic dffr_logic_2 (.clk(or_34_out), .in(_47112_out_4), .nres(nres), .out_4(dffr_logic_2_out_4));
  DFFR_logic _47112 (.clk(_36109_out), .in(_38103_out), .nres(nres), .out_4(_47112_out_4));
  IMUX _4099 (.b___in0(_4098_out), .c___in1(_40101_out), .out(_4099_out), .sel(_38103_out));
  and _40101 (_40101_out, nand_5_out, xor_5_out);
  nand nand_5 (nand_5_out, _40102_out, _3789_out_4);
  xor xor_5 (xor_5_out, _3789_out_4, _40102_out);
  not _4098 (_4098_out, RLE_input[15]);
  DFFR_logic _43103 (.clk(_41108_out), .in(_43104_out), .nres(nres), .out_4(_43103_out_4));
  not _43104 (_43104_out, _43103_out_4);
  not not_1 (not_1_out, _43103_out_4);
  DFFR_logic _3789 (.clk(_42117_2_out), .in(_4099_out), .nres(_43112_out), .out_4(_3789_out_4));
  not not_2 (not_2_out, _3786_out_4);
  not not_3 (not_3_out, _3898_out_4);
  xor _42104 (_42104_out, _42106_out, _42102_out);
  xnor _42102 (_42102_out, _42101_out, _4298_out);
  xor _42106 (_42106_out, _43103_out_4, _42103_out_4);
  nand _42101 (_42101_out, _4079_out, _4298_out);
  and _4079 (_4079_out, _43102_out_4, _4310_out_4, _44110_out_4);
  DFFR_logic _45128 (.clk(_45129_out), .in(_4097_out), .nres(nres), .out_4(_45128_out_4));
  nand _38103 (_38103_out, not_3_out, not_2_out, not_7_out, not_5_out, not_6_out, not_4_out);
  not not_4 (not_4_out, _3789_out_4);
  not not_5 (not_5_out, _38106_out_4);
  not not_6 (not_6_out, _41123_out_4);
  not not_7 (not_7_out, _4095_out_4);
  and and_3 (and_3_out, dffr_logic_6_out_4, dffr_logic_7_out_4);
  and and_4 (and_4_out, and_3_out, dffr_logic_8_out_4);
  and and_5 (and_5_out, and_4_out, dffr_logic_9_out_4);
  and and_6 (and_6_out, and_5_out, dffr_logic_10_out_4);
  DFFR_logic _42103 (.clk(_41108_out), .in(_42104_out), .nres(nres), .out_4(_42103_out_4));
  xor _4083 (_4083_out, _41109_out, dffr_logic_3_out_4);
  IMUX _41109 (.b___in0(_41110_out), .c___in1(_41104_out), .out(_41109_out), .sel(_42102_out));
  nand _41110 (_41110_out, _42103_out_4, _43103_out_4);
  xor _4298 (_4298_out, not_1_out, not_11_out);
  not not_8 (not_8_out, _42103_out_4);
  D_Flip_Flop d_ff_1 (.clk(_45131_out), .D(and_7_out), .Q(d_ff_1_q));  // open: Qn, preset, en, reset
  and and_7 (and_7_out, d_ff_3_q, _44131_out);
  nand _4097 (_4097_out, _39123_out, _39117_out, _40100_out, _40100_2_out, _41124_out, _4098_out);
  nand nand_6 (nand_6_out, dffr_logic_6_out_4, dffr_logic_7_out_4);
  xor xor_6 (xor_6_out, dffr_logic_6_out_4, dffr_logic_7_out_4);
  nand nand_7 (nand_7_out, and_3_out, dffr_logic_8_out_4);
  xor xor_7 (xor_7_out, and_3_out, dffr_logic_8_out_4);
  nand nand_8 (nand_8_out, and_4_out, dffr_logic_9_out_4);
  xor xor_8 (xor_8_out, and_4_out, dffr_logic_9_out_4);
  nand nand_9 (nand_9_out, and_5_out, dffr_logic_10_out_4);
  xor xor_9 (xor_9_out, and_5_out, dffr_logic_10_out_4);
  nand nand_10 (nand_10_out, and_6_out, dffr_logic_11_out_4);
  xor xor_10 (xor_10_out, and_6_out, dffr_logic_11_out_4);
  DFFR_logic dffr_logic_3 (.clk(_41108_out), .in(_4083_out), .nres(nres), .out_4(dffr_logic_3_out_4));
  not _43101 (_43101_out, _43102_out_4);
  nand _41104 (_41104_out, not_8_out, not_1_out);
  not not_9 (not_9_out, dffr_logic_3_out_4);
  nand nand_11 (nand_11_out, or_5_out, _45134_out);
  or or_5 (or_5_out, minus_712_minus_out, dffr_logic_15_out_4);
  nand _45134 (_45134_out, dffr_logic_15_out_4, d_ff_2_q);
  D_Flip_Flop d_ff_2 (.clk(_45131_out), .D(and_8_out), .Q(d_ff_2_q));  // open: Qn, preset, en, reset
  and and_8 (and_8_out, d_ff_4_q, _44131_out);
  // Probe on dffr_logic_4_out_4
  DFFR_logic dffr_logic_4 (.clk(minus_706_minus_out), .in(dffr_logic_5_out_4), .nres(nres), .out_4(dffr_logic_4_out_4));
  DFFR_logic dffr_logic_5 (.clk(or_34_out), .in(_46140_out_4), .nres(nres), .out_4(dffr_logic_5_out_4));
  DFFR_logic _46140 (.clk(_36109_out), .in(_46141_out), .nres(nres), .out_4(_46140_out_4));
  nor _46141 (_46141_out, _46142_out, _38103_out);
  not _46142 (_46142_out, _45128_out_4);
  not not_10 (not_10_out, dffr_logic_6_out_4);
  and and_9 (and_9_out, nand_6_out, xor_6_out);
  and and_10 (and_10_out, nand_7_out, xor_7_out);
  and and_11 (and_11_out, nand_8_out, xor_8_out);
  and and_12 (and_12_out, nand_9_out, xor_9_out);
  and and_13 (and_13_out, nand_10_out, xor_10_out);
  IMUX _41120 (.b___in0(_42113_out_4), .c___in1(dffr_logic_6_out_4), .out(oe1), .sel(_45130_out));
  DFFR_logic _43102 (.clk(_41107_out), .in(_43101_out), .nres(nres), .out_4(_43102_out_4));
  xor _4399 (_4399_out, _43102_out_4, _4310_out_4);
  not not_11 (not_11_out, _43102_out_4);
  not not_12 (not_12_out, nand_12_out);
  nand nand_12 (nand_12_out, nand_13_out, nand_14_out);
  nand nand_13 (nand_13_out, nand_11_out, and_14_out, nand_14_out);
  and and_14 (and_14_out, dffr_logic_15_out_4, d_ff_3_q);
  D_Flip_Flop d_ff_3 (.clk(_45131_out), .D(not_13_out), .Q(d_ff_3_q));  // open: Qn, preset, en, reset
  not not_13 (not_13_out, imux_1_out);
  IMUX imux_1 (.b___in0(RLE_input[10]), .c___in1(d_ff_5_q), .out(imux_1_out), .sel(_44131_out));
  DFFR_logic dffr_logic_6 (.clk(_45122_out), .in(not_10_out), .nres(nres), .out_4(dffr_logic_6_out_4));
  DFFR_logic dffr_logic_7 (.clk(_45122_out), .in(and_9_out), .nres(nres), .out_4(dffr_logic_7_out_4));
  DFFR_logic dffr_logic_8 (.clk(_45122_out), .in(and_10_out), .nres(nres), .out_4(dffr_logic_8_out_4));
  DFFR_logic dffr_logic_9 (.clk(_45122_out), .in(and_11_out), .nres(nres), .out_4(dffr_logic_9_out_4));
  DFFR_logic dffr_logic_10 (.clk(_45122_out), .in(and_12_out), .nres(nres), .out_4(dffr_logic_10_out_4));
  DFFR_logic dffr_logic_11 (.clk(_45122_out), .in(and_13_out), .nres(nres), .out_4(dffr_logic_11_out_4));
  IMUX imux_2 (.b___in0(minus_679_minus_out_4), .c___in1(dffr_logic_7_out_4), .out(imux_2_out), .sel(_45130_out));
  DFFR_logic _4310 (.clk(_41107_out), .in(_4398_out), .nres(nres), .out_4(_4310_out_4));
  xor _4398 (_4398_out, _4399_out, _4293_out);
  xnor _4293 (_4293_out, _4196_out, _4298_out);
  nor _4196 (_4196_out, _41100_out, _4298_out);
  or _41100 (_41100_out, not_1_out, not_8_out, not_9_out);
  nor minus_488_minus (minus_488_minus_out, minus_457_minus_out, minus_456_minus_out, minus_562_minus_out);
  and minus_456_minus (minus_456_minus_out, not_12_out, imux_13_out);
  and minus_457_minus (minus_457_minus_out, imux_13_out, and_33_out);
  or or_6 (or_6_out, xor_11_out, nor_1_out);
  xor xor_11 (xor_11_out, nand_11_out, xor_12_out);
  nor nor_1 (nor_1_out, nand_11_out, and_14_out, nand_14_out);
  xor xor_12 (xor_12_out, and_14_out, nand_14_out);
  nand nand_14 (nand_14_out, or_7_out, _45132_out);
  or or_7 (or_7_out, minus_734_minus_out, dffr_logic_15_out_4);
  nand _45132 (_45132_out, dffr_logic_15_out_4, d_ff_4_q);
  D_Flip_Flop d_ff_4 (.clk(_45131_out), .D(not_14_out), .Q(d_ff_4_q));  // open: Qn, preset, en, reset
  not not_14 (not_14_out, imux_3_out);
  IMUX imux_3 (.b___in0(RLE_input[11]), .c___in1(d_ff_6_q), .out(imux_3_out), .sel(_44131_out));
  nand nand_15 (nand_15_out, dffr_logic_6_out_4, dffr_logic_7_out_4, dffr_logic_8_out_4, dffr_logic_9_out_4, dffr_logic_10_out_4, dffr_logic_11_out_4);
  xor _44109 (_44109_out, _4294_out, _44110_out_4);
  IMUX _4294 (.b___in0(_4295_out), .c___in1(_4296_out), .out(_4294_out), .sel(_4293_out));
  nand _4296 (_4296_out, not_11_out, not_15_out);
  nand _4295 (_4295_out, _4310_out_4, _43102_out_4);
  not not_15 (not_15_out, _4310_out_4);
  xor minus_492_minus (minus_492_minus_out, not_12_out, minus_455_minus_out);
  xor minus_455_minus (minus_455_minus_out, and_33_out, imux_13_out);
  and minus_562_minus (minus_562_minus_out, not_12_out, and_33_out);
  nand nand_16 (nand_16_out, nand_13_out, xor_11_out);
  D_Flip_Flop d_ff_5 (.clk(_45131_out), .D(not_16_out), .Q(d_ff_5_q));  // open: Qn, preset, en, reset
  not not_16 (not_16_out, imux_4_out);
  IMUX imux_4 (.b___in0(RLE_input[12]), .c___in1(d_ff_7_q), .out(imux_4_out), .sel(_44131_out));
  IMUX imux_5 (.b___in0(_42115_out_4), .c___in1(dffr_logic_8_out_4), .out(imux_5_out), .sel(_45130_out));
  DFFR_logic _44110 (.clk(_41107_out), .in(_44109_out), .nres(nres), .out_4(_44110_out_4));
  not not_17 (not_17_out, _44110_out_4);
  xnor minus_490_minus (minus_490_minus_out, minus_488_minus_out, minus_455_minus_2_out);
  xor minus_455_minus_2 (minus_455_minus_2_out, and_37_out, not_28_out);
  or or_8 (or_8_out, nor_1_out, nand_14_out);
  D_Flip_Flop d_ff_6 (.clk(_45131_out), .D(not_18_out), .Q(d_ff_6_q));  // open: Qn, preset, en, reset
  not not_18 (not_18_out, imux_6_out);
  IMUX imux_6 (.b___in0(RLE_input[13]), .c___in1(d_ff_8_q), .out(imux_6_out), .sel(_44131_out));
  and _43115 (_43115_out, _43123_out_4, _42113_out_4);
  and _43116 (_43116_out, _43115_out, minus_679_minus_out_4);
  and _43119 (_43119_out, _43116_out, _42115_out_4);
  and _41121 (_41121_out, _43119_out, minus_678_minus_out_4);
  IMUX imux_7 (.b___in0(minus_678_minus_out_4), .c___in1(dffr_logic_9_out_4), .out(imux_7_out), .sel(_45130_out));
  or _3492 (_3492_out, _44132_out, _3491_out);
  not not_19 (not_19_out, dffr_logic_12_out_4);
  xor minus_496_minus (minus_496_minus_out, minus_489_minus_out, minus_447_minus_out);
  xor minus_447_minus (minus_447_minus_out, and_39_out, not_29_out);
  D_Flip_Flop d_ff_7 (.clk(_45131_out), .D(not_20_out), .Q(d_ff_7_q));  // open: Qn, preset, en, reset
  not not_20 (not_20_out, imux_8_out);
  IMUX imux_8 (.b___in0(RLE_input[14]), .c___in1(d_ff_1_q), .out(imux_8_out), .sel(_44131_out));
  buf _36108 (_36108_out, _35108_q);
  not _34103 (_34103_out, _34102_out);
  IMUX _34102 (.b___in0(RLE_input[0]), .c___in1(RLE_input[8]), .out(_34102_out), .sel(_43123_out_4));
  nand nand_17 (nand_17_out, _43123_out_4, _42113_out_4);
  xor xor_13 (xor_13_out, _43123_out_4, _42113_out_4);
  nand nand_18 (nand_18_out, _43115_out, minus_679_minus_out_4);
  xor xor_14 (xor_14_out, _43115_out, minus_679_minus_out_4);
  nand nand_19 (nand_19_out, _43116_out, _42115_out_4);
  xor xor_15 (xor_15_out, _43116_out, _42115_out_4);
  nand nand_20 (nand_20_out, _43119_out, minus_678_minus_out_4);
  xor xor_16 (xor_16_out, _43119_out, minus_678_minus_out_4);
  nand nand_21 (nand_21_out, _41121_out, _42116_out_4);
  xor xor_17 (xor_17_out, _41121_out, _42116_out_4);
  IMUX imux_9 (.b___in0(_42116_out_4), .c___in1(dffr_logic_10_out_4), .out(imux_9_out), .sel(_45130_out));
  nor _34106 (ie2, _3493_out, mclk);
  nor _34104 (ie1, _3492_out, mclk);
  or _3493 (_3493_out, _3893_out, _44132_out);
  not _3491 (_3491_out, _3893_out);
  IMUX _3893 (.b___in0(dffr_logic_12_out_4), .c___in1(_43103_out_4), .out(_3893_out), .sel(_45128_out_4));
  DFFR_logic dffr_logic_12 (.clk(or_3_out), .in(not_19_out), .nres(nres), .out_4(dffr_logic_12_out_4));
  and and_15 (and_15_out, nand_22_out, xor_18_out);
  nand nand_22 (nand_22_out, dffr_logic_12_out_4, dffr_logic_13_out_4);
  and and_16 (and_16_out, dffr_logic_12_out_4, dffr_logic_13_out_4);
  IMUX minus_494_minus (
    .b___in0(minus_597_minus_out), .c___in1(minus_495_minus_out), .out(minus_494_minus_out),
    .sel(minus_489_minus_out));
  nand minus_489_minus (minus_489_minus_out, or_9_out, minus_453_minus_out);
  or or_9 (or_9_out, minus_454_minus_out, minus_488_minus_out);
  nand minus_450_minus (minus_450_minus_out, not_29_out, and_39_out);
  nor minus_454_minus (minus_454_minus_out, and_37_out, not_28_out);
  nand minus_453_minus (minus_453_minus_out, and_37_out, not_28_out);
  D_Flip_Flop d_ff_8 (.clk(_45131_out), .D(not_21_out), .Q(d_ff_8_q));  // open: Qn, preset, en, reset
  not not_21 (not_21_out, imux_10_out);
  IMUX imux_10 (.b___in0(RLE_input[15]), .c___in1(d_ff_2_q), .out(imux_10_out), .sel(_44131_out));
  D_Flip_Flop _36110 (.clk(_43130_out), .D(_36108_out), .Q(_36110_q));  // open: Qn, preset, en, reset
  and _39131 (_39131_out, minus_310_minus_out, _39130_q);
  D_Flip_Flop _35108 (.clk(_39124_out), .D(_34103_out), .Q(_35108_q));  // open: Qn, preset, en, reset
  not _43124 (_43124_out, _43123_out_4);
  and _42114 (_42114_out, nand_17_out, xor_13_out);
  and minus_680_minus (minus_680_minus_out, nand_18_out, xor_14_out);
  and _42117 (_42117_out, nand_19_out, xor_15_out);
  and _43122 (_43122_out, nand_20_out, xor_16_out);
  and _41122 (_41122_out, nand_21_out, xor_17_out);
  IMUX imux_11 (.b___in0(lum_col), .c___in1(dffr_logic_11_out_4), .out(imux_11_out), .sel(_45130_out));
  IMUX imux_12 (.b___in0(dffr_logic_13_out_4), .c___in1(_42103_out_4), .out(imux_12_out), .sel(_45128_out_4));
  DFFR_logic dffr_logic_13 (.clk(or_3_out), .in(and_15_out), .nres(nres), .out_4(dffr_logic_13_out_4));
  nand nand_23 (nand_23_out, and_16_out, dffr_logic_14_out_4);
  xor xor_18 (xor_18_out, dffr_logic_12_out_4, dffr_logic_13_out_4);
  xnor minus_597_minus (minus_597_minus_out, minus_450_minus_out, minus_444_minus_out);
  xor minus_495_minus (minus_495_minus_out, minus_451_minus_out, minus_444_minus_out);
  or minus_451_minus (minus_451_minus_out, and_39_out, not_29_out);
  xnor minus_444_minus (minus_444_minus_out, not_35_out, and_42_out);
  IMUX imux_13 (.b___in0(nand_12_out), .c___in1(nand_16_out), .out(imux_13_out), .sel(d_ff_9_q));
  D_Flip_Flop _39132 (.clk(_43130_out), .D(_39131_out), .Q(_39132_q), .preset(undriven));  // open: Qn, en, reset
  not _38115 (_38115_out, _38114_out);
  IMUX _38114 (.b___in0(_38113_q), .c___in1(_3797_q), .out(_38114_out), .sel(minus_310_minus_out));
  D_Flip_Flop _38113 (.clk(_39124_out), .D(_38112_out), .Q(_38113_q));  // open: Qn, preset, en, reset
  not _38112 (_38112_out, _3390_out);
  IMUX _3390 (.b___in0(RLE_input[1]), .c___in1(RLE_input[9]), .out(_3390_out), .sel(_43123_out_4));
  DFFR_logic _43123 (.clk(_36109_out), .in(_43124_out), .nres(nres), .out_4(_43123_out_4));
  DFFR_logic _42113 (.clk(_36109_out), .in(_42114_out), .nres(nres), .out_4(_42113_out_4));
  DFFR_logic minus_679_minus (.clk(_36109_out), .in(minus_680_minus_out), .nres(nres), .out_4(minus_679_minus_out_4));
  DFFR_logic _42115 (.clk(_36109_out), .in(_42117_out), .nres(nres), .out_4(_42115_out_4));
  DFFR_logic minus_678_minus (.clk(_36109_out), .in(_43122_out), .nres(nres), .out_4(minus_678_minus_out_4));
  DFFR_logic _42116 (.clk(_36109_out), .in(_41122_out), .nres(nres), .out_4(_42116_out_4));
  not not_22 (Address_for_RLE_input[0], imux_2_out);
  not not_23 (Address_for_RLE_input[1], imux_5_out);
  not not_24 (Address_for_RLE_input[2], imux_7_out);
  not not_25 (Address_for_RLE_input[3], imux_9_out);
  not not_26 (Address_for_RLE_input[4], imux_11_out);
  not not_27 (Address_for_RLE_input[5], _45130_out);
  IMUX imux_14 (.b___in0(dffr_logic_14_out_4), .c___in1(dffr_logic_3_out_4), .out(imux_14_out), .sel(_45128_out_4));
  DFFR_logic dffr_logic_14 (.clk(or_3_out), .in(and_17_out), .nres(nres), .out_4(dffr_logic_14_out_4));
  and and_17 (and_17_out, nand_23_out, xor_19_out);
  xor xor_19 (xor_19_out, and_16_out, dffr_logic_14_out_4);
  and and_18 (and_18_out, and_16_out, dffr_logic_14_out_4);
  IMUX minus_502_minus (
    .b___in0(minus_546_minus_out), .c___in1(minus_436_minus_out), .out(minus_502_minus_out),
    .sel(minus_594_minus_out));
  not minus_546_minus (minus_546_minus_out, minus_436_minus_out);
  xnor minus_436_minus (minus_436_minus_out, and_45_out, not_37_out);
  nand minus_449_minus (minus_449_minus_out, or_10_out, or_12_out);
  or or_10 (or_10_out, not_28_out, and_37_out);
  not not_28 (not_28_out, n4_mux_1_out);
  _4_mux u_4_mux_1 (
    .out(n4_mux_1_out), .s1(d_ff_11_q), ._3(or_8_out), ._2(nand_16_out), ._1(or_6_out), ._0(nand_12_out),
    .s0(d_ff_9_q));
  D_Flip_Flop _38116 (.clk(_43130_out), .D(_38115_out), .Q(_38116_q));  // open: Qn, preset, en, reset
  not _39127 (_39127_out, _39125_out);
  IMUX _39125 (.b___in0(_39126_q), .c___in1(_40105_q), .out(_39125_out), .sel(minus_310_minus_out));
  D_Flip_Flop _39126 (.clk(_39124_out), .D(_38111_out), .Q(_39126_q));  // open: Qn, preset, en, reset
  not _38111 (_38111_out, _3794_out);
  IMUX _3794 (.b___in0(RLE_input[2]), .c___in1(RLE_input[10]), .out(_3794_out), .sel(_43123_out_4));
  // Probe on _34114_out
  nand _34114 (_34114_out, _43123_out_4, _42113_out_4, minus_679_minus_out_4, _42115_out_4, minus_678_minus_out_4, _42116_out_4);
  and and_19 (and_19_out, nand_24_out, xor_20_out);
  nand nand_24 (nand_24_out, and_18_out, dffr_logic_17_out_4);
  xor xor_20 (xor_20_out, and_18_out, dffr_logic_17_out_4);
  and and_20 (and_20_out, and_18_out, dffr_logic_17_out_4);
  IMUX minus_594_minus (
    .b___in0(minus_491_minus_out), .c___in1(minus_445_minus_out), .out(minus_594_minus_out),
    .sel(minus_444_minus_out));
  nand minus_491_minus (minus_491_minus_out, or_11_out, and_21_out);
  or or_11 (or_11_out, minus_488_minus_out, minus_449_minus_out);
  and and_21 (and_21_out, minus_448_minus_out, minus_450_minus_out);
  or minus_448_minus (minus_448_minus_out, nand_25_out, nor_2_out);
  nand nand_25 (nand_25_out, not_28_out, and_37_out);
  or or_12 (or_12_out, not_29_out, and_39_out);
  not not_29 (not_29_out, n4_mux_2_out);
  _4_mux u_4_mux_2 (
    .out(n4_mux_2_out), .s1(d_ff_13_q), ._3(or_8_out), ._2(nand_16_out), ._1(or_6_out), ._0(nand_12_out),
    .s0(d_ff_11_q));
  D_Flip_Flop _39130 (.clk(_43130_out), .D(_39127_out), .Q(_39130_q));  // open: Qn, preset, en, reset
  not _3796 (_3796_out, _3795_out);
  IMUX _3795 (.b___in0(_36107_q), .c___in1(_3792_q), .out(_3795_out), .sel(minus_310_minus_out));
  D_Flip_Flop _36107 (.clk(_39124_out), .D(_35106_out), .Q(_36107_q));  // open: Qn, preset, en, reset
  not _35106 (_35106_out, _35105_out);
  IMUX _35105 (.b___in0(RLE_input[3]), .c___in1(RLE_input[11]), .out(_35105_out), .sel(_43123_out_4));
  // Probe on dffr_logic_15_out_4
  DFFR_logic dffr_logic_15 (.clk(or_34_out), .in(dffr_logic_16_out_4), .nres(nres), .out_4(dffr_logic_15_out_4));
  DFFR_logic dffr_logic_16 (.clk(_36109_out), .in(_34114_2_out), .nres(nres), .out_4(dffr_logic_16_out_4));
  nand _34114_2 (_34114_2_out, not_34_out, not_31_out, not_33_out, not_32_out, not_30_out, not_36_out);
  not not_30 (not_30_out, minus_678_minus_out_4);
  not not_31 (not_31_out, _42113_out_4);
  not not_32 (not_32_out, _42115_out_4);
  not not_33 (not_33_out, minus_679_minus_out_4);
  not not_34 (not_34_out, _43123_out_4);
  IMUX imux_15 (.b___in0(dffr_logic_17_out_4), .c___in1(_43102_out_4), .out(imux_15_out), .sel(_45128_out_4));
  DFFR_logic dffr_logic_17 (.clk(or_3_out), .in(and_19_out), .nres(nres), .out_4(dffr_logic_17_out_4));
  and and_22 (and_22_out, nand_26_out, xor_21_out);
  nand nand_26 (nand_26_out, and_20_out, dffr_logic_18_out_4);
  xor xor_21 (xor_21_out, and_20_out, dffr_logic_18_out_4);
  and and_23 (and_23_out, and_20_out, dffr_logic_18_out_4);
  IMUX minus_441_minus (
    .b___in0(minus_440_minus_out), .c___in1(minus_438_minus_out), .out(minus_441_minus_out),
    .sel(minus_594_minus_out));
  xor minus_440_minus (minus_440_minus_out, minus_432_minus_out, minus_478_minus_out);
  nor minus_478_minus (minus_478_minus_out, and_45_out, not_37_out);
  xor minus_432_minus (minus_432_minus_out, and_47_out, not_38_out);
  or minus_445_minus (minus_445_minus_out, not_35_out, and_42_out);
  nor nor_2 (nor_2_out, not_29_out, and_39_out);
  not not_35 (not_35_out, n4_mux_3_out);
  _4_mux u_4_mux_3 (
    .out(n4_mux_3_out), .s1(d_ff_15_q), ._3(or_8_out), ._2(nand_16_out), ._1(or_6_out), ._0(nand_12_out),
    .s0(d_ff_13_q));
  D_Flip_Flop _3797 (.clk(_43130_out), .D(_3796_out), .Q(_3797_q));  // open: Qn, preset, en, reset
  not _40106 (_40106_out, _38110_out);
  IMUX _38110 (.b___in0(_39128_q), .c___in1(_38109_q), .out(_38110_out), .sel(minus_310_minus_out));
  D_Flip_Flop _39128 (.clk(_39124_out), .D(_39129_out), .Q(_39128_q));  // open: Qn, preset, en, reset
  not _39129 (_39129_out, _35107_out);
  IMUX _35107 (.b___in0(RLE_input[4]), .c___in1(RLE_input[12]), .out(_35107_out), .sel(_43123_out_4));
  not not_36 (not_36_out, _42116_out_4);
  IMUX imux_16 (.b___in0(dffr_logic_18_out_4), .c___in1(_4310_out_4), .out(imux_16_out), .sel(_45128_out_4));
  DFFR_logic dffr_logic_18 (.clk(or_3_out), .in(and_22_out), .nres(nres), .out_4(dffr_logic_18_out_4));
  and and_24 (and_24_out, nand_27_out, xor_22_out);
  nand nand_27 (nand_27_out, and_23_out, dffr_logic_19_out_4);
  xor minus_438_minus (minus_438_minus_out, minus_432_minus_out, minus_437_minus_out);
  nand minus_437_minus (minus_437_minus_out, and_45_out, not_37_out);
  not not_37 (not_37_out, n4_mux_4_out);
  _4_mux u_4_mux_4 (
    .out(n4_mux_4_out), .s1(d_ff_18_q), ._3(or_8_out), ._2(nand_16_out), ._1(or_6_out), ._0(nand_12_out),
    .s0(d_ff_15_q));
  D_Flip_Flop d_ff_9 (.clk(or_34_out), .D(nand_28_out), .Q(d_ff_9_q));  // open: Qn, preset, en, reset
  nand nand_28 (nand_28_out, _41149_out, nand_29_out);
  nand nand_29 (nand_29_out, _42138_out, d_ff_10_q);
  D_Flip_Flop d_ff_10 (.clk(_46155_out), .D(d_ff_14_q), .Q(d_ff_10_q));  // open: Qn, preset, en, reset
  not _39139 (_39139_out, _38118_out);
  nand _38118 (_38118_out, _37100_out, _39130_q);
  nand _37100 (_37100_out, _39132_q, _38116_q, _39130_q);
  D_Flip_Flop _40105 (.clk(_43130_out), .D(_40106_out), .Q(_40105_q));  // open: Qn, preset, en, reset
  not _3793 (_3793_out, _36106_out);
  IMUX _36106 (.b___in0(_36105_q), .c___in1(_36104_q), .out(_36106_out), .sel(minus_310_minus_out));
  D_Flip_Flop _36105 (.clk(_39124_out), .D(_3495_out), .Q(_36105_q));  // open: Qn, preset, en, reset
  not _3495 (_3495_out, _3387_out);
  IMUX _3387 (.b___in0(RLE_input[5]), .c___in1(RLE_input[13]), .out(_3387_out), .sel(_43123_out_4));
  IMUX imux_17 (.b___in0(dffr_logic_19_out_4), .c___in1(_44110_out_4), .out(imux_17_out), .sel(_45128_out_4));
  DFFR_logic dffr_logic_19 (.clk(or_3_out), .in(and_24_out), .nres(nres), .out_4(dffr_logic_19_out_4));
  xor xor_22 (xor_22_out, and_23_out, dffr_logic_19_out_4);
  IMUX minus_429_minus (
    .b___in0(minus_427_minus_out), .c___in1(minus_428_minus_out), .out(minus_429_minus_out),
    .sel(minus_594_minus_out));
  xnor minus_427_minus (minus_427_minus_out, minus_421_minus_out, minus_501_minus_out);
  xnor minus_428_minus (minus_428_minus_out, minus_421_minus_out, minus_439_minus_out);
  xor minus_421_minus (minus_421_minus_out, and_46_out, not_39_out);
  or or_13 (or_13_out, minus_478_minus_out, minus_434_minus_out);
  not not_38 (not_38_out, n4_mux_5_out);
  _4_mux u_4_mux_5 (
    .out(n4_mux_5_out), .s1(d_ff_22_q), ._3(or_8_out), ._2(nand_16_out), ._1(or_6_out), ._0(nand_12_out),
    .s0(d_ff_18_q));
  D_Flip_Flop d_ff_11 (.clk(or_34_out), .D(nand_30_out), .Q(d_ff_11_q));  // open: Qn, preset, en, reset
  nand nand_30 (nand_30_out, _41149_out, nand_31_out);
  nand nand_31 (nand_31_out, _42138_out, d_ff_12_q);
  D_Flip_Flop d_ff_12 (.clk(_46155_out), .D(d_ff_16_q), .Q(d_ff_12_q));  // open: Qn, preset, en, reset
  not _39133 (_39133_out, _37102_out);
  IMUX _39137 (.b___in0(_38118_out), .c___in1(_36112_out), .out(_39137_out), .sel(d_ff_69_q));
  or _35111 (_35111_out, _36111_out, _37101_out);
  xor _36111 (_36111_out, _39132_q, _3799_out);
  nor _37101 (_37101_out, _39132_q, _38116_q, _39130_q);
  xor _3799 (_3799_out, _38116_q, _39130_q);
  D_Flip_Flop _3792 (.clk(_43130_out), .D(_3793_out), .Q(_3792_q));  // open: Qn, preset, en, reset
  and _38107 (_38107_out, _38108_out, _3790_q);
  not _38108 (_38108_out, minus_310_minus_out);
  D_Flip_Flop _3790 (.clk(_39124_out), .D(_3791_out), .Q(_3790_q));  // open: Qn, preset, en, reset
  not _3791 (_3791_out, _35103_out);
  IMUX _35103 (.b___in0(RLE_input[6]), .c___in1(RLE_input[14]), .out(_35103_out), .sel(_43123_out_4));
  nand minus_501_minus (minus_501_minus_out, or_13_out, minus_433_minus_out);
  nor minus_434_minus (minus_434_minus_out, and_47_out, not_38_out);
  nand minus_433_minus (minus_433_minus_out, and_47_out, not_38_out);
  not not_39 (not_39_out, n4_mux_6_out);
  _4_mux u_4_mux_6 (
    .out(n4_mux_6_out), .s1(d_ff_21_q), ._3(or_8_out), ._2(nand_16_out), ._1(or_6_out), ._0(nand_12_out),
    .s0(d_ff_22_q));
  D_Flip_Flop d_ff_13 (.clk(or_34_out), .D(nand_32_out), .Q(d_ff_13_q));  // open: Qn, preset, en, reset
  nand nand_32 (nand_32_out, _41149_out, nand_33_out);
  nand nand_33 (nand_33_out, _42138_out, d_ff_14_q);
  D_Flip_Flop d_ff_14 (.clk(_46155_out), .D(d_ff_19_q), .Q(d_ff_14_q));  // open: Qn, preset, en, reset
  _4_mux _37102 (
    .out(_37102_out), .s1(d_ff_73_q), ._3(_36113_out), ._2(_36112_out), ._1(_35111_out), ._0(_38118_out),
    .s0(d_ff_69_q));
  nand _36112 (_36112_out, _37100_out, _36111_out);
  D_Flip_Flop _38109 (.clk(_43130_out), .D(_38107_out), .Q(_38109_q));  // open: Qn, preset, en, reset
  buf _36108_2 (_36108_2_out, _35104_q);
  D_Flip_Flop _35104 (.clk(_39124_out), .D(_3497_out), .Q(_35104_q));  // open: Qn, preset, en, reset
  not _3497 (_3497_out, _3496_out);
  IMUX _3496 (.b___in0(RLE_input[7]), .c___in1(RLE_input[15]), .out(_3496_out), .sel(_43123_out_4));
  nand _39100 (_39100_out, dffr_logic_12_out_4, dffr_logic_13_out_4, dffr_logic_14_out_4, dffr_logic_17_out_4, dffr_logic_18_out_4, dffr_logic_19_out_4);
  // Probe on _39100_out
  IMUX minus_416_minus (
    .b___in0(minus_414_minus_out), .c___in1(minus_415_minus_out), .out(minus_416_minus_out),
    .sel(minus_594_minus_out));
  IMUX minus_414_minus (
    .b___in0(minus_413_minus_out), .c___in1(minus_424_minus_out), .out(minus_414_minus_out),
    .sel(minus_501_minus_out));
  xnor minus_424_minus (minus_424_minus_out, minus_423_minus_out, minus_410_minus_out);
  nand minus_439_minus (minus_439_minus_out, or_14_out, minus_433_minus_out);
  or or_14 (or_14_out, minus_434_minus_out, minus_437_minus_out);
  xnor minus_410_minus (minus_410_minus_out, and_50_out, not_40_out);
  or minus_423_minus (minus_423_minus_out, and_46_out, not_39_out);
  not not_40 (not_40_out, n4_mux_7_out);
  _4_mux u_4_mux_7 (
    .out(n4_mux_7_out), .s1(d_ff_26_q), ._3(or_8_out), ._2(nand_16_out), ._1(or_6_out), ._0(nand_12_out),
    .s0(d_ff_21_q));
  D_Flip_Flop d_ff_15 (.clk(or_34_out), .D(nand_34_out), .Q(d_ff_15_q));  // open: Qn, preset, en, reset
  nand nand_34 (nand_34_out, _41149_out, nand_35_out);
  nand nand_35 (nand_35_out, _42138_out, d_ff_16_q);
  D_Flip_Flop d_ff_16 (.clk(_46155_out), .D(d_ff_23_q), .Q(d_ff_16_q));  // open: Qn, preset, en, reset
  nor minus_299_minus (minus_299_minus_out, minus_243_minus_out, minus_246_minus_out, minus_242_minus_out);
  and minus_243_minus (minus_243_minus_out, _39139_out, _40114_out);
  and minus_246_minus (minus_246_minus_out, _39139_out, _39137_out);
  not _39135 (_39135_out, _38119_out);
  _4_mux _38119 (
    .out(_38119_out), .s1(d_ff_77_q), ._3(_36113_out), ._2(_36112_out), ._1(_35111_out), ._0(_38118_out),
    .s0(d_ff_73_q));
  or _36113 (_36113_out, _37101_out, _39130_q);
  D_Flip_Flop _36104 (.clk(_43130_out), .D(_36108_2_out), .Q(_36104_q));  // open: Qn, preset, en, reset
  not _42105 (_42105_out, _43107_out_4);
  DFFR_logic _43107 (.clk(not_76_out), .in(_43106_out), .nres(nres), .out_4(_43107_out_4));
  not _43106 (_43106_out, _43107_out_4);
  D_Flip_Flop d_ff_17 (.clk(minus_552_minus_out), .D(d_ff_25_q), .Q(d_ff_17_q));  // open: Qn, preset, en, reset
  IMUX minus_415_minus (
    .b___in0(minus_413_minus_out), .c___in1(minus_424_minus_out), .out(minus_415_minus_out),
    .sel(minus_439_minus_out));
  xor minus_413_minus (minus_413_minus_out, minus_410_minus_out, minus_422_minus_out);
  nand minus_422_minus (minus_422_minus_out, and_46_out, not_39_out);
  or or_15 (or_15_out, minus_478_minus_out, minus_419_minus_out);
  nand nand_36 (nand_36_out, not_38_out, and_47_out);
  not not_41 (not_41_out, n4_mux_8_out);
  D_Flip_Flop d_ff_18 (.clk(or_34_out), .D(nand_38_out), .Q(d_ff_18_q));  // open: Qn, preset, en, reset
  nand nand_37 (nand_37_out, _41149_out, nand_41_out);
  nand nand_38 (nand_38_out, _41149_out, nand_39_out);
  nand nand_39 (nand_39_out, _42138_out, d_ff_19_q);
  D_Flip_Flop d_ff_19 (.clk(_46155_out), .D(d_ff_24_q), .Q(d_ff_19_q));  // open: Qn, preset, en, reset
  nand minus_300_minus (minus_300_minus_out, minus_249_minus_out, or_16_out);
  or or_16 (or_16_out, minus_250_minus_out, minus_299_minus_out);
  nand minus_249_minus (minus_249_minus_out, _39133_out, _40111_out);
  nor minus_250_minus (minus_250_minus_out, _40111_out, _39133_out);
  and minus_242_minus (minus_242_minus_out, _39137_out, _40114_out);
  not _40120 (_40120_out, _38120_out);
  _4_mux _38120 (
    .out(_38120_out), .s1(d_ff_81_q), ._3(_36113_out), ._2(_36112_out), ._1(_35111_out), ._0(_38118_out),
    .s0(d_ff_77_q));
  nor nor_3 (nor_3_out, RLE_input[3], RLE_input[4], RLE_input[5]);
  nor nor_4 (nor_4_out, RLE_input[0], RLE_input[1], RLE_input[2]);
  not not_42 (Address_for_decoded_data[0], imux_12_out);
  not not_43 (Address_for_decoded_data[1], imux_14_out);
  not not_44 (Address_for_decoded_data[2], imux_15_out);
  not not_45 (Address_for_decoded_data[3], imux_16_out);
  not not_46 (Address_for_decoded_data[4], imux_17_out);
  not not_47 (Address_for_decoded_data[5], _42105_out);
  and minus_608_minus (minus_608_minus_out, minus_606_minus_out, minus_625_minus_out);
  and minus_606_minus (minus_606_minus_out, minus_600_minus_out, minus_623_minus_out, minus_624_minus_out);
  and minus_623_minus (minus_623_minus_out, minus_576_minus_out, minus_588_minus_out, minus_574_minus_out);
  and minus_600_minus (minus_600_minus_out, minus_586_minus_out, minus_578_minus_out, minus_631_minus_out);
  D_Flip_Flop d_ff_20 (.clk(minus_552_minus_out), .D(d_ff_29_q), .Q(d_ff_20_q));  // open: Qn, preset, en, reset
  IMUX minus_593_minus (
    .b___in0(minus_411_minus_out), .c___in1(minus_412_minus_out), .out(minus_593_minus_out),
    .sel(minus_594_minus_out));
  IMUX minus_411_minus (
    .b___in0(minus_426_minus_out), .c___in1(minus_545_minus_out), .out(minus_411_minus_out),
    .sel(minus_410_minus_out));
  or minus_545_minus (minus_545_minus_out, and_50_out, not_40_out);
  nand minus_426_minus (minus_426_minus_out, or_15_out, and_25_out);
  or or_17 (or_17_out, minus_437_minus_out, minus_419_minus_out);
  and and_25 (and_25_out, minus_422_minus_out, minus_420_minus_out);
  or minus_420_minus (minus_420_minus_out, nand_36_out, nor_5_out);
  nor nor_5 (nor_5_out, not_39_out, and_46_out);
  or or_18 (or_18_out, not_38_out, and_47_out);
  _4_mux u_4_mux_8 (
    .out(n4_mux_8_out), .s1(d_ff_30_q), ._3(or_8_out), ._2(nand_16_out), ._1(or_6_out), ._0(nand_12_out),
    .s0(d_ff_26_q));
  D_Flip_Flop d_ff_21 (.clk(or_34_out), .D(nand_40_out), .Q(d_ff_21_q));  // open: Qn, preset, en, reset
  D_Flip_Flop d_ff_22 (.clk(or_34_out), .D(nand_37_out), .Q(d_ff_22_q));  // open: Qn, preset, en, reset
  nand nand_40 (nand_40_out, _41149_out, nand_42_out);
  nand nand_41 (nand_41_out, _42138_out, d_ff_23_q);
  nand nand_42 (nand_42_out, _42138_out, d_ff_24_q);
  D_Flip_Flop d_ff_23 (.clk(_46155_out), .D(d_ff_27_q), .Q(d_ff_23_q));  // open: Qn, preset, en, reset
  D_Flip_Flop d_ff_24 (.clk(_46155_out), .D(minus_234_minus_out), .Q(d_ff_24_q));  // open: Qn, preset, en, reset
  not _36115 (_36115_out, _36114_out);
  _4_mux _36114 (
    .out(_36114_out), .s1(d_ff_85_q), ._3(_36113_out), ._2(_36112_out), ._1(_35111_out), ._0(_38118_out),
    .s0(d_ff_81_q));
  // Probe on _45128_out_4
  // Probe on dffr_logic_20_out_4
  DFFR_logic dffr_logic_20 (.clk(_45129_out), .in(not_48_out), .nres(nres), .out_4(dffr_logic_20_out_4));
  not not_48 (not_48_out, nand_43_out);
  nand nand_43 (nand_43_out, nor_4_out, nor_3_out, nor_6_out, and_26_out, and_28_out, RLE_input[15]);
  nor nor_6 (nor_6_out, RLE_input[6], RLE_input[7], RLE_input[8]);
  and and_26 (and_26_out, RLE_input[9], RLE_input[10], RLE_input[11]);
  and minus_625_minus (minus_625_minus_out, minus_589_minus_out, minus_591_minus_out, minus_626_minus_out);
  and minus_624_minus (minus_624_minus_out, minus_560_minus_out, minus_579_minus_out, minus_590_minus_out);
  D_Flip_Flop d_ff_25 (.clk(minus_552_minus_out), .D(d_ff_28_q), .Q(d_ff_25_q));  // open: Qn, preset, en, reset
  IMUX minus_417_minus (
    .b___in0(minus_460_minus_out), .c___in1(minus_516_minus_out), .out(minus_417_minus_out),
    .sel(minus_593_minus_out));
  not minus_516_minus (minus_516_minus_out, minus_460_minus_out);
  xnor minus_460_minus (minus_460_minus_out, and_53_out, not_41_out);
  IMUX minus_412_minus (
    .b___in0(minus_425_minus_out), .c___in1(minus_545_minus_out), .out(minus_412_minus_out),
    .sel(minus_410_minus_out));
  nand minus_425_minus (minus_425_minus_out, or_17_out, and_27_out);
  and and_27 (and_27_out, minus_422_minus_out, minus_420_minus_out);
  nand minus_419_minus (minus_419_minus_out, or_18_out, or_19_out);
  or or_19 (or_19_out, not_39_out, and_46_out);
  not not_49 (not_49_out, n4_mux_9_out);
  _4_mux u_4_mux_9 (
    .out(n4_mux_9_out), .s1(d_ff_33_q), ._3(or_8_out), ._2(nand_16_out), ._1(or_6_out), ._0(nand_12_out),
    .s0(d_ff_30_q));
  D_Flip_Flop d_ff_26 (.clk(or_34_out), .D(nand_44_out), .Q(d_ff_26_q));  // open: Qn, preset, en, reset
  nand nand_44 (nand_44_out, _41149_out, nand_45_out);
  nand nand_45 (nand_45_out, _42138_out, d_ff_27_q);
  D_Flip_Flop d_ff_27 (.clk(_46155_out), .D(_41140_out), .Q(d_ff_27_q));  // open: Qn, preset, en, reset
  xnor minus_277_minus (minus_277_minus_out, minus_299_minus_out, minus_248_minus_out);
  xor _41140 (_41140_out, _39139_out, minus_241_minus_out);
  xor minus_241_minus (minus_241_minus_out, _39137_out, _40114_out);
  xor minus_248_minus (minus_248_minus_out, _39133_out, _40111_out);
  not _38124 (_38124_out, _38123_out);
  _4_mux _38123 (
    .out(_38123_out), .s1(d_ff_89_q), ._3(_36113_out), ._2(_36112_out), ._1(_35111_out), ._0(_38118_out),
    .s0(d_ff_85_q));
  // Probe on _34114_2_out
  and and_28 (and_28_out, RLE_input[12], RLE_input[13], RLE_input[14]);
  nor minus_364_minus (minus_364_minus_out, minus_610_minus_out, minus_609_minus_out);
  nor minus_610_minus (minus_610_minus_out, minus_601_minus_out, minus_578_minus_out);
  nor minus_601_minus (minus_601_minus_out, minus_608_minus_out, minus_599_minus_out);
  nand minus_599_minus (minus_599_minus_out, minus_626_minus_out, minus_586_minus_out);
  nor minus_586_minus (minus_586_minus_out, minus_630_minus_out, and_29_out);
  and and_29 (and_29_out, d_ff_17_q, minus_558_minus_out);
  D_Flip_Flop d_ff_28 (
    .clk(minus_552_minus_out), .D(minus_492_minus_out), .Q(d_ff_28_q));  // open: Qn, preset, en, reset
  D_Flip_Flop d_ff_29 (.clk(minus_552_minus_out), .D(d_ff_32_q), .Q(d_ff_29_q));  // open: Qn, preset, en, reset
  IMUX minus_507_minus (
    .b___in0(minus_504_minus_out), .c___in1(minus_521_minus_out), .out(minus_507_minus_out),
    .sel(minus_593_minus_out));
  xor minus_504_minus (minus_504_minus_out, minus_459_minus_out, minus_421_minus_2_out);
  nand minus_459_minus (minus_459_minus_out, and_53_out, not_41_out);
  not not_50 (not_50_out, n4_mux_10_out);
  _4_mux u_4_mux_10 (
    .out(n4_mux_10_out), .s1(d_ff_36_q), ._3(or_8_out), ._2(nand_16_out), ._1(or_6_out), ._0(nand_12_out),
    .s0(d_ff_33_q));
  D_Flip_Flop d_ff_30 (.clk(or_34_out), .D(nand_46_out), .Q(d_ff_30_q));  // open: Qn, preset, en, reset
  nand nand_46 (nand_46_out, _41149_out, nand_47_out);
  nand nand_47 (nand_47_out, _42138_out, d_ff_31_q);
  D_Flip_Flop d_ff_31 (.clk(_46155_out), .D(minus_277_minus_out), .Q(d_ff_31_q));  // open: Qn, preset, en, reset
  IMUX minus_276_minus (
    .b___in0(minus_271_minus_out), .c___in1(minus_270_minus_out), .out(minus_276_minus_out),
    .sel(minus_300_minus_out));
  xor minus_273_minus (minus_273_minus_out, minus_300_minus_out, minus_254_minus_out);
  xnor minus_271_minus (minus_271_minus_out, minus_252_minus_out, minus_257_minus_out);
  xor minus_254_minus (minus_254_minus_out, _39135_out, _42133_out);
  nand minus_252_minus (minus_252_minus_out, _39135_out, _42133_out);
  not _38122 (_38122_out, _38121_out);
  _4_mux _38121 (
    .out(_38121_out), .s1(d_ff_93_q), ._3(_36113_out), ._2(_36112_out), ._1(_35111_out), ._0(_38118_out),
    .s0(d_ff_89_q));
  // Probe on or_20_out
  or or_20 (or_20_out, dffr_logic_20_out_4, not_51_out, mclk);
  not not_51 (not_51_out, dffr_logic_21_out_4);
  DFFR_logic dffr_logic_21 (.clk(or_36_out), .in(dffr_logic_22_out_4), .nres(nres), .out_4(dffr_logic_21_out_4));
  nor minus_363_minus (minus_363_minus_out, minus_622_minus_out, minus_607_minus_out);
  nor minus_622_minus (minus_622_minus_out, minus_609_minus_out, minus_631_minus_out);
  and minus_609_minus (minus_609_minus_out, minus_601_minus_out, minus_578_minus_out);
  nor minus_578_minus (minus_578_minus_out, minus_630_minus_out, and_31_out);
  nor minus_631_minus (minus_631_minus_out, minus_630_minus_out, and_30_out);
  and and_30 (and_30_out, d_ff_25_q, minus_558_minus_out);
  and and_31 (and_31_out, d_ff_20_q, minus_558_minus_out);
  D_Flip_Flop d_ff_32 (
    .clk(minus_552_minus_out), .D(minus_490_minus_out), .Q(d_ff_32_q));  // open: Qn, preset, en, reset
  xor minus_521_minus (minus_521_minus_out, minus_421_minus_2_out, minus_477_minus_out);
  xor minus_421_minus_2 (minus_421_minus_2_out, and_57_out, not_49_out);
  nor minus_477_minus (minus_477_minus_out, and_53_out, not_41_out);
  not not_52 (not_52_out, n4_mux_11_out);
  _4_mux u_4_mux_11 (
    .out(n4_mux_11_out), .s1(d_ff_39_q), ._3(or_8_out), ._2(nand_16_out), ._1(or_6_out), ._0(nand_12_out),
    .s0(d_ff_36_q));
  D_Flip_Flop d_ff_33 (.clk(or_34_out), .D(nand_48_out), .Q(d_ff_33_q));  // open: Qn, preset, en, reset
  nand nand_48 (nand_48_out, _41149_out, nand_49_out);
  nand nand_49 (nand_49_out, _42138_out, d_ff_34_q);
  D_Flip_Flop d_ff_34 (.clk(_46155_out), .D(minus_273_minus_out), .Q(d_ff_34_q));  // open: Qn, preset, en, reset
  xor minus_270_minus (minus_270_minus_out, minus_257_minus_out, minus_253_minus_out);
  xnor minus_257_minus (minus_257_minus_out, _40120_out, _41145_out);
  or or_21 (or_21_out, minus_299_minus_out, _41137_out);
  or minus_253_minus (minus_253_minus_out, _39135_out, _42133_out);
  nand _41137 (_41137_out, or_22_out, or_23_out);
  or or_22 (or_22_out, _39133_out, _40111_out);
  not _37111 (_37111_out, _37105_out);
  _4_mux _37105 (
    .out(_37105_out), .s1(d_ff_100_q), ._3(_36113_out), ._2(_36112_out), ._1(_35111_out), ._0(_38118_out),
    .s0(d_ff_93_q));
  nand _44132 (_44132_out, dffr_logic_23_out_4, dffr_logic_25_out_4);
  DFFR_logic dffr_logic_22 (.clk(or_36_out), .in(dffr_logic_23_out_4), .nres(nres), .out_4(dffr_logic_22_out_4));
  nor minus_362_minus (minus_362_minus_out, minus_611_minus_out, minus_612_minus_out);
  nor minus_611_minus (minus_611_minus_out, minus_607_minus_out, minus_576_minus_out);
  and minus_607_minus (minus_607_minus_out, minus_601_minus_out, minus_600_minus_out);
  nor minus_576_minus (minus_576_minus_out, minus_630_minus_out, and_32_out);
  and and_32 (and_32_out, d_ff_29_q, minus_558_minus_out);
  and and_33 (and_33_out, minus_598_minus_out, d_ff_35_q);
  D_Flip_Flop d_ff_35 (
    .clk(minus_552_minus_out), .D(minus_496_minus_out), .Q(d_ff_35_q));  // open: Qn, preset, en, reset
  IMUX minus_511_minus (
    .b___in0(minus_509_minus_out), .c___in1(minus_522_minus_out), .out(minus_511_minus_out),
    .sel(minus_593_minus_out));
  xnor minus_509_minus (minus_509_minus_out, minus_467_minus_out, minus_505_minus_out);
  xor minus_467_minus (minus_467_minus_out, and_58_out, not_50_out);
  not not_53 (not_53_out, n4_mux_12_out);
  _4_mux u_4_mux_12 (
    .out(n4_mux_12_out), .s1(d_ff_42_q), ._3(or_8_out), ._2(nand_16_out), ._1(or_6_out), ._0(nand_12_out),
    .s0(d_ff_39_q));
  D_Flip_Flop d_ff_36 (.clk(or_34_out), .D(nand_50_out), .Q(d_ff_36_q));  // open: Qn, preset, en, reset
  nand nand_50 (nand_50_out, _41149_out, nand_51_out);
  nand nand_51 (nand_51_out, _42138_out, d_ff_37_q);
  D_Flip_Flop d_ff_37 (.clk(_46155_out), .D(minus_276_minus_out), .Q(d_ff_37_q));  // open: Qn, preset, en, reset
  xnor minus_275_minus (minus_275_minus_out, minus_272_minus_out, minus_258_minus_out);
  IMUX minus_272_minus (
    .b___in0(_41138_out), .c___in1(minus_256_minus_out), .out(minus_272_minus_out), .sel(minus_257_minus_out));
  xor minus_258_minus (minus_258_minus_out, _36115_out, _40125_out);
  or minus_256_minus (minus_256_minus_out, _40120_out, _41145_out);
  nand _41138 (_41138_out, or_21_out, and_34_out);
  and and_34 (and_34_out, minus_252_minus_out, _41139_out);
  or _41139 (_41139_out, nand_52_out, nor_7_out);
  nand nand_52 (nand_52_out, _39133_out, _40111_out);
  or or_23 (or_23_out, _39135_out, _42133_out);
  not _35120 (_35120_out, _36119_out);
  _4_mux _36119 (
    .out(_36119_out), .s1(d_ff_101_q), ._3(_36113_out), ._2(_36112_out), ._1(_35111_out), ._0(_38118_out),
    .s0(d_ff_100_q));
  // Probe on _43130_out
  or _43130 (_43130_out, mclk, _44138_out);
  and _44138 (_44138_out, _46152_out, minus_310_minus_out);
  nand _46139 (_46139_out, dffr_logic_21_out_4, dffr_logic_25_out_4);
  DFFR_logic dffr_logic_23 (.clk(or_36_out), .in(not_56_out), .nres(nres), .out_4(dffr_logic_23_out_4));
  nor minus_361_minus (minus_361_minus_out, minus_615_minus_out, minus_614_minus_out);
  nor minus_615_minus (minus_615_minus_out, minus_612_minus_out, minus_588_minus_out);
  and minus_612_minus (minus_612_minus_out, minus_607_minus_out, minus_576_minus_out);
  nor minus_574_minus (minus_574_minus_out, minus_630_minus_out, and_35_out);
  nor minus_588_minus (minus_588_minus_out, minus_630_minus_out, and_36_out);
  and and_35 (and_35_out, d_ff_32_q, minus_558_minus_out);
  and and_36 (and_36_out, d_ff_28_q, minus_558_minus_out);
  and and_37 (and_37_out, minus_598_minus_out, d_ff_38_q);
  D_Flip_Flop d_ff_38 (
    .clk(minus_552_minus_out), .D(minus_494_minus_out), .Q(d_ff_38_q));  // open: Qn, preset, en, reset
  xnor minus_522_minus (minus_522_minus_out, minus_467_minus_out, minus_519_minus_out);
  nand minus_505_minus (minus_505_minus_out, or_24_out, minus_544_minus_out);
  or or_24 (or_24_out, minus_459_minus_out, minus_464_minus_out);
  nor minus_464_minus (minus_464_minus_out, and_57_out, not_49_out);
  not not_54 (not_54_out, n4_mux_13_out);
  _4_mux u_4_mux_13 (
    .out(n4_mux_13_out), .s1(d_ff_45_q), ._3(or_8_out), ._2(nand_16_out), ._1(or_6_out), ._0(nand_12_out),
    .s0(d_ff_42_q));
  D_Flip_Flop d_ff_39 (.clk(or_34_out), .D(nand_53_out), .Q(d_ff_39_q));  // open: Qn, preset, en, reset
  nand nand_53 (nand_53_out, _41149_out, nand_54_out);
  nand nand_54 (nand_54_out, _42138_out, d_ff_40_q);
  D_Flip_Flop d_ff_40 (.clk(_46155_out), .D(minus_275_minus_out), .Q(d_ff_40_q));  // open: Qn, preset, en, reset
  xnor minus_278_minus (minus_278_minus_out, minus_274_minus_out, minus_261_minus_out);
  IMUX minus_274_minus (
    .b___in0(minus_259_minus_out), .c___in1(minus_260_minus_out), .out(minus_274_minus_out),
    .sel(minus_272_minus_out));
  and minus_260_minus (minus_260_minus_out, _36115_out, _40125_out);
  or minus_259_minus (minus_259_minus_out, _36115_out, _40125_out);
  nor nor_7 (nor_7_out, _39135_out, _42133_out);
  not _36117 (_36117_out, _37104_out);
  // Probe on _39124_out
  or _39124 (_39124_out, mclk, _45130_out);
  nand _45130 (_45130_out, dffr_logic_23_out_4, dffr_logic_28_out_4);
  not not_55 (not_55_out, dffr_logic_24_out_4);
  DFFR_logic dffr_logic_24 (.clk(or_36_out), .in(not_58_out), .nres(nres), .out_4(dffr_logic_24_out_4));
  not not_56 (not_56_out, dffr_logic_24_out_4);
  nor minus_616_minus (minus_616_minus_out, minus_614_minus_out, minus_574_minus_out);
  and minus_614_minus (minus_614_minus_out, minus_612_minus_out, minus_588_minus_out);
  nor minus_579_minus (minus_579_minus_out, minus_630_minus_out, and_41_out);
  nor minus_560_minus (minus_560_minus_out, minus_630_minus_out, and_38_out);
  and and_38 (and_38_out, d_ff_35_q, minus_558_minus_out);
  and and_39 (and_39_out, minus_598_minus_out, d_ff_41_q);
  D_Flip_Flop d_ff_41 (
    .clk(minus_552_minus_out), .D(minus_502_minus_out), .Q(d_ff_41_q));  // open: Qn, preset, en, reset
  IMUX minus_513_minus (
    .b___in0(minus_510_minus_out), .c___in1(minus_523_minus_out), .out(minus_513_minus_out),
    .sel(minus_593_minus_out));
  IMUX minus_510_minus (
    .b___in0(minus_537_minus_out), .c___in1(minus_536_minus_out), .out(minus_510_minus_out),
    .sel(minus_505_minus_out));
  nand minus_519_minus (minus_519_minus_out, or_25_out, minus_544_minus_out);
  or or_25 (or_25_out, minus_464_minus_out, minus_477_minus_out);
  nand minus_544_minus (minus_544_minus_out, and_57_out, not_49_out);
  not not_57 (not_57_out, n4_mux_14_out);
  _4_mux u_4_mux_14 (
    .out(n4_mux_14_out), .s1(d_ff_46_q), ._3(or_8_out), ._2(nand_16_out), ._1(or_6_out), ._0(nand_12_out),
    .s0(d_ff_45_q));
  D_Flip_Flop d_ff_42 (.clk(or_34_out), .D(nand_56_out), .Q(d_ff_42_q));  // open: Qn, preset, en, reset
  nand nand_55 (nand_55_out, _41149_out, nand_58_out);
  nand nand_56 (nand_56_out, _41149_out, nand_57_out);
  nand nand_57 (nand_57_out, _42138_out, d_ff_43_q);
  D_Flip_Flop d_ff_43 (.clk(_46155_out), .D(minus_278_minus_out), .Q(d_ff_43_q));  // open: Qn, preset, en, reset
  xor minus_261_minus (minus_261_minus_out, _38124_out, _38125_out);
  nand minus_262_minus (minus_262_minus_out, _38124_out, _38125_out);
  _4_mux _37104 (
    .out(_37104_out), .s1(d_ff_105_q), ._3(_36113_out), ._2(_36112_out), ._1(_35111_out), ._0(_38118_out),
    .s0(d_ff_101_q));
  // Probe on _36109_2_out
  // Probe on _36109_out
  or _36109 (_36109_out, mclk, _46145_out);
  or _36109_2 (_36109_2_out, mclk, minus_310_minus_out);
  nand minus_310_minus (minus_310_minus_out, dffr_logic_28_out_4, dffr_logic_22_out_4);
  not not_58 (not_58_out, dffr_logic_21_out_4);
  nor minus_360_minus (minus_360_minus_out, minus_616_minus_out, minus_613_minus_out);
  and minus_613_minus (minus_613_minus_out, minus_607_minus_out, minus_623_minus_out);
  nor minus_590_minus (minus_590_minus_out, minus_630_minus_out, and_40_out);
  and and_40 (and_40_out, d_ff_41_q, minus_558_minus_out);
  and and_41 (and_41_out, d_ff_38_q, minus_558_minus_out);
  and and_42 (and_42_out, minus_598_minus_out, d_ff_44_q);
  D_Flip_Flop d_ff_44 (
    .clk(minus_552_minus_out), .D(minus_441_minus_out), .Q(d_ff_44_q));  // open: Qn, preset, en, reset
  IMUX minus_523_minus (
    .b___in0(minus_537_minus_out), .c___in1(minus_536_minus_out), .out(minus_523_minus_out),
    .sel(minus_519_minus_out));
  xnor minus_536_minus (minus_536_minus_out, minus_472_minus_out, minus_470_minus_out);
  xor minus_537_minus (minus_537_minus_out, minus_469_minus_out, minus_472_minus_out);
  xnor minus_472_minus (minus_472_minus_out, and_60_out, not_52_out);
  or minus_470_minus (minus_470_minus_out, and_58_out, not_50_out);
  D_Flip_Flop d_ff_45 (.clk(or_34_out), .D(nand_55_out), .Q(d_ff_45_q));  // open: Qn, preset, en, reset
  D_Flip_Flop d_ff_46 (.clk(or_34_out), .D(d_ff_55_q), .Q(d_ff_46_q));  // open: Qn, preset, en, reset
  nand nand_58 (nand_58_out, _42138_out, d_ff_48_q);
  D_Flip_Flop d_ff_47 (.clk(_46155_out), .D(minus_280_minus_out), .Q(d_ff_47_q));  // open: Qn, preset, en, reset
  D_Flip_Flop d_ff_48 (.clk(_46155_out), .D(minus_279_minus_out), .Q(d_ff_48_q));  // open: Qn, preset, en, reset
  xor minus_279_minus (minus_279_minus_out, _39150_out, minus_268_minus_out);
  nand _39150 (_39150_out, minus_262_minus_out, or_26_out);
  or or_26 (or_26_out, minus_274_minus_out, nor_8_out);
  xor minus_268_minus (minus_268_minus_out, _38122_out, _37106_out);
  nor nor_8 (nor_8_out, _38124_out, _38125_out);
  IMUX _36116 (.b___in0(_38118_out), .c___in1(_36113_out), .out(_36116_out), .sel(d_ff_105_q));
  // Probe on _46145_out
  nand _46145 (_46145_out, dffr_logic_28_out_4, _46144_out, dffr_logic_21_out_4);
  not _46144 (_46144_out, dffr_logic_20_out_4);
  nand minus_733_minus (minus_733_minus_out, dffr_logic_27_out_4, dffr_logic_23_out_4);
  nor minus_359_minus (minus_359_minus_out, minus_618_minus_out, minus_617_minus_out);
  nor minus_618_minus (minus_618_minus_out, minus_613_minus_out, minus_560_minus_out);
  and minus_617_minus (minus_617_minus_out, minus_613_minus_out, minus_560_minus_out);
  nor minus_591_minus (minus_591_minus_out, minus_630_minus_out, and_44_out);
  nor minus_589_minus (minus_589_minus_out, minus_630_minus_out, and_43_out);
  and and_43 (and_43_out, d_ff_44_q, minus_558_minus_out);
  and and_44 (and_44_out, d_ff_49_q, minus_558_minus_out);
  and and_45 (and_45_out, minus_598_minus_out, d_ff_49_q);
  D_Flip_Flop d_ff_49 (
    .clk(minus_552_minus_out), .D(minus_429_minus_out), .Q(d_ff_49_q));  // open: Qn, preset, en, reset
  or or_27 (or_27_out, minus_459_minus_out, minus_463_minus_out);
  or minus_462_minus (minus_462_minus_out, nand_59_out, nor_9_out);
  nand nand_59 (nand_59_out, and_57_out, not_49_out);
  nand minus_469_minus (minus_469_minus_out, and_58_out, not_50_out);
  IMUX imux_18 (.b___in0(nand_12_out), .c___in1(or_8_out), .out(imux_18_out), .sel(d_ff_46_q));
  nand _42138 (_42138_out, _41154_out, d_ff_55_q);
  nand _41154 (_41154_out, d_ff_47_q, d_ff_53_q, d_ff_50_q);
  D_Flip_Flop d_ff_50 (.clk(_46155_out), .D(_35124_out), .Q(d_ff_50_q));  // open: Qn, preset, en, reset
  IMUX minus_280_minus (.b___in0(_38130_out), .c___in1(_38128_out), .out(minus_280_minus_out), .sel(_39150_out));
  xnor _38130 (_38130_out, _39153_out, _37112_out);
  xor _38128 (_38128_out, _37112_out, _38127_out);
  or _38127 (_38127_out, _38122_out, _37106_out);
  nand _39153 (_39153_out, _38122_out, _37106_out);
  xnor _37112 (_37112_out, _37111_out, _37110_out);
  // Probe on _46155_out
  // Probe on _45122_out
  or _46155 (_46155_out, mclk, _46154_out);
  and _46154 (_46154_out, _46152_out, nand_60_out);
  nand nand_60 (nand_60_out, dffr_logic_22_out_4, dffr_logic_27_out_4);
  and _46152 (_46152_out, _46145_out, minus_733_minus_out, _46149_out);
  nor minus_355_minus (minus_355_minus_out, minus_619_minus_out, minus_620_minus_out);
  nor minus_619_minus (minus_619_minus_out, minus_617_minus_out, minus_579_minus_out);
  and minus_620_minus (minus_620_minus_out, minus_617_minus_out, minus_579_minus_out);
  not minus_626_minus (minus_626_minus_out, d_ff_61_q);
  and minus_630_minus (minus_630_minus_out, minus_629_minus_out, minus_628_minus_out);
  not minus_628_minus (minus_628_minus_out, d_ff_61_q);
  or minus_629_minus (minus_629_minus_out, minus_592_minus_out, minus_584_minus_out, minus_581_minus_out);
  or minus_584_minus (minus_584_minus_out, d_ff_54_q, d_ff_56_q);
  or minus_592_minus (minus_592_minus_out, d_ff_52_q, d_ff_51_q);
  and and_46 (and_46_out, minus_598_minus_out, d_ff_51_q);
  and and_47 (and_47_out, minus_598_minus_out, d_ff_52_q);
  D_Flip_Flop d_ff_51 (
    .clk(minus_552_minus_out), .D(minus_417_minus_out), .Q(d_ff_51_q));  // open: Qn, preset, en, reset
  D_Flip_Flop d_ff_52 (
    .clk(minus_552_minus_out), .D(minus_416_minus_out), .Q(d_ff_52_q));  // open: Qn, preset, en, reset
  IMUX minus_595_minus (
    .b___in0(minus_515_minus_out), .c___in1(minus_524_minus_out), .out(minus_595_minus_out),
    .sel(minus_593_minus_out));
  IMUX minus_515_minus (
    .b___in0(minus_506_minus_out), .c___in1(minus_471_minus_out), .out(minus_515_minus_out),
    .sel(minus_472_minus_out));
  or minus_471_minus (minus_471_minus_out, and_60_out, not_52_out);
  nand minus_506_minus (minus_506_minus_out, or_27_out, and_48_out);
  or or_28 (or_28_out, minus_477_minus_out, minus_463_minus_out);
  and and_48 (and_48_out, minus_469_minus_out, minus_462_minus_out);
  nand minus_463_minus (minus_463_minus_out, or_29_out, or_32_out);
  nor nor_9 (nor_9_out, and_58_out, not_50_out);
  or or_29 (or_29_out, and_57_out, not_49_out);
  nand nand_61 (nand_61_out, d_ff_46_q, not_12_out);
  or _41149 (_41149_out, d_ff_55_q, _41153_out);
  nor _41153 (_41153_out, d_ff_47_q, d_ff_50_q, d_ff_53_q);
  D_Flip_Flop d_ff_53 (.clk(_46155_out), .D(_34112_out), .Q(d_ff_53_q));  // open: Qn, preset, en, reset
  xor _35124 (_35124_out, _35122_out, _38131_out);
  nand _39145 (_39145_out, or_30_out, and_52_out);
  or or_30 (or_30_out, minus_274_minus_out, _38129_out);
  xnor _35122 (_35122_out, _35120_out, _35119_out);
  nand _38129 (_38129_out, or_31_out, or_33_out);
  or or_31 (or_31_out, _38124_out, _38125_out);
  IMUX minus_234_minus (.b___in0(nand_62_out), .c___in1(not_59_out), .out(minus_234_minus_out), .sel(_46145_out));
  not not_59 (not_59_out, d_ff_31_q);
  nand nand_62 (nand_62_out, _36110_q, d_ff_69_q);
  // Probe on _45129_out
  or _45129 (_45129_out, mclk, _44131_out);
  or _44131 (_44131_out, minus_310_minus_out, _34114_2_out);
  nand _46149 (_46149_out, dffr_logic_27_out_4, not_55_out);
  nand minus_725_minus (minus_725_minus_out, dffr_logic_27_out_4, dffr_logic_21_out_4);
  and and_49 (and_49_out, not_60_out, not_63_out);
  not not_60 (not_60_out, dffr_logic_25_out_4);
  DFFR_logic dffr_logic_25 (.clk(or_20_out), .in(dffr_logic_26_out_4), .nres(nres), .out_4(dffr_logic_25_out_4));
  nor minus_356_minus (minus_356_minus_out, minus_621_minus_out, minus_602_minus_out);
  nor minus_621_minus (minus_621_minus_out, minus_620_minus_out, minus_590_minus_out);
  and minus_602_minus (minus_602_minus_out, minus_601_minus_out, minus_606_minus_out);
  and minus_556_minus (minus_556_minus_out, d_ff_52_q, d_ff_51_q);
  or minus_581_minus (minus_581_minus_out, d_ff_58_q, d_ff_59_q, d_ff_60_q);
  and and_50 (and_50_out, minus_598_minus_out, d_ff_54_q);
  D_Flip_Flop d_ff_54 (
    .clk(minus_552_minus_out), .D(minus_507_minus_out), .Q(d_ff_54_q));  // open: Qn, preset, en, reset
  IMUX minus_526_minus (
    .b___in0(minus_475_minus_out), .c___in1(minus_538_minus_out), .out(minus_526_minus_out),
    .sel(minus_595_minus_out));
  not minus_538_minus (minus_538_minus_out, minus_475_minus_out);
  xnor minus_475_minus (minus_475_minus_out, and_62_out, not_53_out);
  IMUX minus_524_minus (
    .b___in0(minus_520_minus_out), .c___in1(minus_471_minus_out), .out(minus_524_minus_out),
    .sel(minus_472_minus_out));
  nand minus_520_minus (minus_520_minus_out, or_28_out, and_51_out);
  and and_51 (and_51_out, minus_469_minus_out, minus_462_minus_out);
  or or_32 (or_32_out, and_58_out, not_50_out);
  D_Flip_Flop d_ff_55 (.clk(_46155_out), .D(_34110_out), .Q(d_ff_55_q));  // open: Qn, preset, en, reset
  xor _34112 (_34112_out, _35123_out, _35116_out);
  IMUX _38131 (.b___in0(_39145_out), .c___in1(_37113_out), .out(_38131_out), .sel(_37112_out));
  and and_52 (and_52_out, _39153_out, _39152_out);
  or _37113 (_37113_out, _37110_out, _37111_out);
  or _39152 (_39152_out, nand_63_out, nor_10_out);
  nand nand_63 (nand_63_out, _38124_out, _38125_out);
  or or_33 (or_33_out, _38122_out, _37106_out);
  IMUX _40114 (.b___in0(nand_64_out), .c___in1(not_61_out), .out(_40114_out), .sel(_46145_out));
  not not_61 (not_61_out, d_ff_34_q);
  nand nand_64 (nand_64_out, _36110_q, d_ff_73_q);
  // Probe on or_34_out
  or or_34 (or_34_out, minus_725_minus_out, mclk);
  or minus_706_minus (minus_706_minus_out, minus_726_minus_out, mclk);
  nand minus_726_minus (minus_726_minus_out, dffr_logic_26_out_4, dffr_logic_21_out_4);
  not not_62 (not_62_out, nand_65_out);
  nand nand_65 (nand_65_out, and_49_out, and_56_out);
  not not_63 (not_63_out, dffr_logic_26_out_4);
  DFFR_logic dffr_logic_26 (.clk(or_20_out), .in(dffr_logic_27_out_4), .nres(nres), .out_4(dffr_logic_26_out_4));
  // Probe on nand_15_out
  // Probe on _38103_out
  nor minus_357_minus (minus_357_minus_out, minus_604_minus_out, minus_603_minus_out);
  nor minus_604_minus (minus_604_minus_out, minus_602_minus_out, minus_589_minus_out);
  nand minus_558_minus (minus_558_minus_out, minus_632_minus_out, d_ff_61_q);
  nand minus_632_minus (minus_632_minus_out, minus_556_minus_out, minus_554_minus_out, minus_582_minus_out);
  and minus_582_minus (minus_582_minus_out, d_ff_58_q, d_ff_59_q, d_ff_60_q);
  and minus_554_minus (minus_554_minus_out, d_ff_54_q, d_ff_56_q);
  and and_53 (and_53_out, minus_598_minus_out, d_ff_56_q);
  D_Flip_Flop d_ff_56 (
    .clk(minus_552_minus_out), .D(minus_511_minus_out), .Q(d_ff_56_q));  // open: Qn, preset, en, reset
  IMUX minus_525_minus (
    .b___in0(minus_530_minus_out), .c___in1(minus_499_minus_out), .out(minus_525_minus_out),
    .sel(minus_595_minus_out));
  xor minus_530_minus (minus_530_minus_out, minus_474_minus_out, minus_482_minus_out);
  xor minus_482_minus (minus_482_minus_out, and_64_out, not_54_out);
  nand minus_474_minus (minus_474_minus_out, and_62_out, not_53_out);
  D_Flip_Flop d_ff_57 (.clk(_46155_out), .D(_39140_out), .Q(d_ff_57_q));  // open: Qn, preset, en, reset
  xor _34110 (_34110_out, _35115_out, _35114_out);
  nor _35115 (_35115_out, and_55_out, and_54_out);
  and and_54 (and_54_out, _35123_out, _35116_out);
  and and_55 (and_55_out, _36117_out, _35117_out);
  xor _35116 (_35116_out, _36117_out, _35117_out);
  nand _35123 (_35123_out, _35121_out, or_35_out);
  or or_35 (or_35_out, _38131_out, _35122_out);
  nand _35121 (_35121_out, _35120_out, _35119_out);
  nor nor_10 (nor_10_out, _38122_out, _37106_out);
  IMUX _40111 (.b___in0(nand_66_out), .c___in1(not_64_out), .out(_40111_out), .sel(_46145_out));
  not not_64 (not_64_out, d_ff_37_q);
  nand nand_66 (nand_66_out, _36110_q, d_ff_77_q);
  // Probe on _42117_2_out
  // Probe on minus_706_minus_out
  or _42117_2 (_42117_2_out, _42118_out, mclk);
  or _42118 (_42118_out, minus_310_minus_out, _44130_out);
  not _44130 (_44130_out, _34114_2_out);
  // Probe on or_36_out
  or or_36 (or_36_out, not_62_out, mclk);
  and and_56 (and_56_out, not_65_out, not_67_out);
  not not_65 (not_65_out, dffr_logic_27_out_4);
  DFFR_logic dffr_logic_27 (.clk(or_20_out), .in(dffr_logic_28_out_4), .nres(nres), .out_4(dffr_logic_27_out_4));
  nor minus_358_minus (minus_358_minus_out, minus_627_minus_out, minus_605_minus_out);
  nor minus_627_minus (minus_627_minus_out, minus_603_minus_out, minus_591_minus_out);
  and minus_603_minus (minus_603_minus_out, minus_602_minus_out, minus_589_minus_out);
  and and_57 (and_57_out, minus_598_minus_out, d_ff_58_q);
  D_Flip_Flop d_ff_58 (
    .clk(minus_552_minus_out), .D(minus_513_minus_out), .Q(d_ff_58_q));  // open: Qn, preset, en, reset
  xor minus_499_minus (minus_499_minus_out, minus_482_minus_out, minus_476_minus_out);
  nor minus_476_minus (minus_476_minus_out, and_62_out, not_53_out);
  nand _36118 (_36118_out, d_ff_55_q, d_ff_57_q);
  nand _39140 (_39140_out, _39139_out, d_ff_105_q);
  xnor _35114 (_35114_out, _36116_out, _35117_out);
  IMUX _42133 (.b___in0(nand_67_out), .c___in1(not_66_out), .out(_42133_out), .sel(_46145_out));
  not not_66 (not_66_out, d_ff_40_q);
  nand nand_67 (nand_67_out, _36110_q, d_ff_81_q);
  // Probe on _43132_out
  or _43132 (_43132_out, _44140_out, mclk);
  or _45136 (_45136_out, minus_598_minus_out, _45128_out_4);
  or _44140 (_44140_out, minus_733_minus_out, _45128_out_4);
  nand minus_598_minus (minus_598_minus_out, dffr_logic_26_out_4, not_55_out);
  not not_67 (not_67_out, dffr_logic_28_out_4);
  DFFR_logic dffr_logic_28 (.clk(mclk), .in(or_37_out), .nres(nres), .out_4(dffr_logic_28_out_4));
  or or_37 (or_37_out, minus_738_minus_out, minus_745_minus_out);
  and minus_738_minus (minus_738_minus_out, dffr_logic_28_out_4, not_69_out);
  and minus_745_minus (minus_745_minus_out, not_68_out, minus_771_minus_out);
  not not_68 (not_68_out, dffr_logic_28_out_4);
  not not_69 (not_69_out, nand_68_out);
  nand nand_68 (nand_68_out, _46134_out, or_38_out);
  or _46134 (_46134_out, _38103_out, _46136_out);
  or or_38 (or_38_out, _34114_out, minus_673_minus_out);
  or _46136 (_46136_out, nand_15_out, minus_673_minus_out);
  nand minus_673_minus (minus_673_minus_out, dffr_logic_21_out_4, dffr_logic_28_out_4);
  and minus_605_minus (minus_605_minus_out, minus_603_minus_out, minus_591_minus_out);
  and and_58 (and_58_out, minus_598_minus_out, d_ff_59_q);
  D_Flip_Flop d_ff_59 (
    .clk(minus_552_minus_out), .D(minus_526_minus_out), .Q(d_ff_59_q));  // open: Qn, preset, en, reset
  IMUX minus_527_minus (
    .b___in0(minus_532_minus_out), .c___in1(minus_540_minus_out), .out(minus_527_minus_out),
    .sel(minus_595_minus_out));
  xnor minus_540_minus (minus_540_minus_out, minus_484_minus_out, minus_500_minus_out);
  xnor minus_532_minus (minus_532_minus_out, minus_484_minus_out, minus_529_minus_out);
  xor minus_484_minus (minus_484_minus_out, and_63_out, not_57_out);
  or or_39 (or_39_out, minus_474_minus_out, minus_481_minus_out);
  IMUX _41145 (.b___in0(nand_69_out), .c___in1(not_70_out), .out(_41145_out), .sel(_46145_out));
  not not_70 (not_70_out, d_ff_43_q);
  nand nand_69 (nand_69_out, _36110_q, d_ff_85_q);
  // Probe on _45178_out
  or _45178 (_45178_out, _45136_out, mclk);
  or _45131 (_45131_out, mclk, minus_650_minus_out);
  and minus_650_minus (minus_650_minus_out, _44131_out, and_59_out, and_61_out);
  and and_59 (and_59_out, minus_598_minus_out, minus_734_minus_out);
  nand minus_734_minus (minus_734_minus_out, dffr_logic_26_out_4, dffr_logic_23_out_4);
  and and_60 (and_60_out, minus_598_minus_out, d_ff_60_q);
  D_Flip_Flop d_ff_60 (
    .clk(minus_552_minus_out), .D(minus_525_minus_out), .Q(d_ff_60_q));  // open: Qn, preset, en, reset
  nand minus_529_minus (minus_529_minus_out, or_39_out, minus_480_minus_out);
  nor minus_481_minus (minus_481_minus_out, and_64_out, not_54_out);
  nand minus_480_minus (minus_480_minus_out, and_64_out, not_54_out);
  IMUX _40125 (.b___in0(nand_70_out), .c___in1(not_71_out), .out(_40125_out), .sel(_46145_out));
  not not_71 (not_71_out, d_ff_48_q);
  nand nand_70 (nand_70_out, _36110_q, d_ff_89_q);
  // Probe on _45131_out
  // Probe on minus_552_minus_out
  or minus_552_minus (minus_552_minus_out, mclk, minus_728_minus_out);
  and minus_728_minus (minus_728_minus_out, and_59_out, and_61_out);
  and and_61 (and_61_out, minus_726_minus_out, minus_712_minus_out);
  nand minus_712_minus (minus_712_minus_out, dffr_logic_22_out_4, dffr_logic_26_out_4);
  and and_62 (and_62_out, minus_598_minus_out, d_ff_61_q);
  D_Flip_Flop d_ff_61 (
    .clk(minus_552_minus_out), .D(minus_527_minus_out), .Q(d_ff_61_q));  // open: Qn, preset, en, reset
  IMUX minus_528_minus (
    .b___in0(minus_531_minus_out), .c___in1(minus_542_minus_out), .out(minus_528_minus_out),
    .sel(minus_595_minus_out));
  IMUX minus_531_minus (
    .b___in0(minus_541_minus_out), .c___in1(minus_543_minus_out), .out(minus_531_minus_out),
    .sel(minus_529_minus_out));
  nand minus_500_minus (minus_500_minus_out, or_40_out, minus_480_minus_out);
  xor minus_541_minus (minus_541_minus_out, minus_485_minus_out, minus_487_minus_out);
  or or_40 (or_40_out, minus_481_minus_out, minus_476_minus_out);
  xnor minus_487_minus (minus_487_minus_out, and_63_out, imux_18_out);
  nand minus_485_minus (minus_485_minus_out, not_57_out, and_63_out);
  IMUX _38125 (.b___in0(nand_71_out), .c___in1(not_72_out), .out(_38125_out), .sel(_46145_out));
  not not_72 (not_72_out, d_ff_47_q);
  nand nand_71 (nand_71_out, _36110_q, d_ff_93_q);
  or _45137 (_45137_out, mclk, _46147_out);
  nand _46147 (_46147_out, not_55_out, dffr_logic_25_out_4);
  or _45122 (_45122_out, mclk, _46137_out);
  or _46137 (_46137_out, _46143_out, minus_673_minus_out, dffr_logic_29_out_4);
  and and_63 (and_63_out, minus_598_minus_out, d_ff_63_q, d_ff_62_q);
  and and_64 (and_64_out, minus_598_minus_out, d_ff_63_q);
  D_Flip_Flop d_ff_62 (.clk(minus_552_minus_out), .D(nand_61_out), .Q(d_ff_62_q));  // open: Qn, preset, en, reset
  D_Flip_Flop d_ff_63 (
    .clk(minus_552_minus_out), .D(minus_528_minus_out), .Q(d_ff_63_q));  // open: Qn, preset, en, reset
  IMUX minus_542_minus (
    .b___in0(minus_541_minus_out), .c___in1(minus_543_minus_out), .out(minus_542_minus_out),
    .sel(minus_500_minus_out));
  xnor minus_543_minus (minus_543_minus_out, minus_487_minus_out, minus_486_minus_out);
  or minus_486_minus (minus_486_minus_out, and_63_out, not_57_out);
  IMUX _37106 (.b___in0(nand_72_out), .c___in1(not_73_out), .out(_37106_out), .sel(_46145_out));
  not not_73 (not_73_out, d_ff_50_q);
  nand nand_72 (nand_72_out, _36110_q, d_ff_100_q);
  // Probe on _45137_out
  not _47111 (_47111_out, dffr_logic_29_out_4);
  DFFR_logic dffr_logic_29 (.clk(mclk), .in(minus_769_minus_out), .nres(nres), .out_4(dffr_logic_29_out_4));
  or minus_769_minus (minus_769_minus_out, minus_756_minus_out, _47109_out);
  and minus_756_minus (minus_756_minus_out, dffr_logic_29_out_4, not_74_out);
  and _47109 (_47109_out, _46135_out, _47111_out);
  not not_74 (not_74_out, minus_771_minus_out);
  nor _46135 (_46135_out, _46143_out, _46136_out);
  and _46143 (_46143_out, _38103_out, nand_43_out);
  IMUX _37110 (.b___in0(nand_73_out), .c___in1(not_75_out), .out(_37110_out), .sel(_46145_out));
  not not_75 (not_75_out, d_ff_53_q);
  nand nand_73 (nand_73_out, _36110_q, d_ff_101_q);
  not _43112 (_43112_out, _43112_2_out);
  nand _43112_2 (_43112_2_out, nres, not_76_out);
  // Probe on not_76_out
  not not_76 (not_76_out, rle_finished);
  DFFR_logic _49107 (.clk(mclk), .in(_45123_out), .nres(c8), .out_4(rle_finished));
  nor _45123 (_45123_out, _39100_out, _46147_out);
  not minus_771_minus (minus_771_minus_out, c8);
  IMUX _35119 (.b___in0(nand_74_out), .c___in1(not_77_out), .out(_35119_out), .sel(_46145_out));
  not not_77 (not_77_out, d_ff_55_q);
  nand nand_74 (nand_74_out, _36110_q, d_ff_105_q);
  IMUX _35117 (.b___in0(nand_74_out), .c___in1(_36118_out), .out(_35117_out), .sel(_46145_out));
  not _3392 (oe2, oe1);
  IMUX _46201 (.b___in0(1'b1), .c___in1(minus_608_minus_out), .out(_46201_out), .sel(dffr_logic_4_out_4));
  D_Flip_Flop d_ff_64 (.clk(_45137_out), .D(_46201_out), .Q(Decoded_data[0]));  // open: Qn, preset, en, reset
  IMUX imux_19 (.b___in0(1'b1), .c___in1(minus_364_minus_out), .out(imux_19_out), .sel(dffr_logic_4_out_4));
  D_Flip_Flop d_ff_65 (.clk(_45137_out), .D(imux_19_out), .Q(Decoded_data[1]));  // open: Qn, preset, en, reset
  D_Flip_Flop d_ff_66 (.clk(_45137_out), .D(imux_20_out), .Q(Decoded_data[2]));  // open: Qn, preset, en, reset
  IMUX imux_20 (.b___in0(nand_75_out), .c___in1(minus_363_minus_out), .out(imux_20_out), .sel(dffr_logic_4_out_4));
  nand nand_75 (nand_75_out, _47114_out, d_ff_67_q);
  D_Flip_Flop d_ff_67 (.clk(_45178_out), .D(d_ff_68_q), .Q(d_ff_67_q));  // open: Qn, preset, en, reset
  D_Flip_Flop d_ff_68 (.clk(_43132_out), .D(d_ff_69_q), .Q(d_ff_68_q));  // open: Qn, preset, en, reset
  D_Flip_Flop d_ff_69 (.clk(_36109_2_out), .D(RLE_input[0]), .Q(d_ff_69_q));  // open: Qn, preset, en, reset
  D_Flip_Flop d_ff_70 (.clk(_45137_out), .D(imux_21_out), .Q(Decoded_data[3]));  // open: Qn, preset, en, reset
  IMUX imux_21 (.b___in0(nand_76_out), .c___in1(minus_362_minus_out), .out(imux_21_out), .sel(dffr_logic_4_out_4));
  nand nand_76 (nand_76_out, _47114_out, d_ff_71_q);
  D_Flip_Flop d_ff_71 (.clk(_45178_out), .D(d_ff_72_q), .Q(d_ff_71_q));  // open: Qn, preset, en, reset
  D_Flip_Flop d_ff_72 (.clk(_43132_out), .D(d_ff_73_q), .Q(d_ff_72_q));  // open: Qn, preset, en, reset
  D_Flip_Flop d_ff_73 (.clk(_36109_2_out), .D(RLE_input[1]), .Q(d_ff_73_q));  // open: Qn, preset, en, reset
  not not_78 (not_78_out, dffr_logic_30_out_4);
  DFFR_logic dffr_logic_30 (.clk(clock_1_out), .in(or_41_out), .nres(in_2), .out_4(dffr_logic_30_out_4));
  Clock clock_1 (.out(clock_1_out));
  and and_65 (and_65_out, dffr_logic_30_out_4, not_79_out);
  D_Flip_Flop d_ff_74 (.clk(_45137_out), .D(imux_22_out), .Q(Decoded_data[4]));  // open: Qn, preset, en, reset
  IMUX imux_22 (.b___in0(nand_77_out), .c___in1(minus_361_minus_out), .out(imux_22_out), .sel(dffr_logic_4_out_4));
  nand nand_77 (nand_77_out, _47114_out, d_ff_75_q);
  D_Flip_Flop d_ff_75 (.clk(_45178_out), .D(d_ff_76_q), .Q(d_ff_75_q));  // open: Qn, preset, en, reset
  D_Flip_Flop d_ff_76 (.clk(_43132_out), .D(d_ff_77_q), .Q(d_ff_76_q));  // open: Qn, preset, en, reset
  D_Flip_Flop d_ff_77 (.clk(_36109_2_out), .D(RLE_input[2]), .Q(d_ff_77_q));  // open: Qn, preset, en, reset
  or or_41 (or_41_out, and_65_out, and_66_out);
  and and_66 (and_66_out, nor_11_out, not_78_out);
  nor nor_11 (nor_11_out, and_68_out, or_45_out);
  not not_79 (not_79_out, nc8__kill);
  D_Flip_Flop d_ff_78 (.clk(_45137_out), .D(imux_23_out), .Q(Decoded_data[5]));  // open: Qn, preset, en, reset
  IMUX imux_23 (.b___in0(nand_78_out), .c___in1(minus_360_minus_out), .out(imux_23_out), .sel(dffr_logic_4_out_4));
  nand nand_78 (nand_78_out, _47114_out, d_ff_79_q);
  D_Flip_Flop d_ff_79 (.clk(_45178_out), .D(d_ff_80_q), .Q(d_ff_79_q));  // open: Qn, preset, en, reset
  D_Flip_Flop d_ff_80 (.clk(_43132_out), .D(d_ff_81_q), .Q(d_ff_80_q));  // open: Qn, preset, en, reset
  D_Flip_Flop d_ff_81 (.clk(_36109_2_out), .D(RLE_input[3]), .Q(d_ff_81_q));  // open: Qn, preset, en, reset
  D_Flip_Flop d_ff_82 (.clk(_45137_out), .D(imux_24_out), .Q(Decoded_data[6]));  // open: Qn, preset, en, reset
  IMUX imux_24 (.b___in0(nand_79_out), .c___in1(minus_359_minus_out), .out(imux_24_out), .sel(dffr_logic_4_out_4));
  nand nand_79 (nand_79_out, _47114_out, d_ff_83_q);
  D_Flip_Flop d_ff_83 (.clk(_45178_out), .D(d_ff_84_q), .Q(d_ff_83_q));  // open: Qn, preset, en, reset
  D_Flip_Flop d_ff_84 (.clk(_43132_out), .D(d_ff_85_q), .Q(d_ff_84_q));  // open: Qn, preset, en, reset
  D_Flip_Flop d_ff_85 (.clk(_36109_2_out), .D(RLE_input[4]), .Q(d_ff_85_q));  // open: Qn, preset, en, reset
  not not_80 (rle_data_ended, and_67_out);
  and and_67 (and_67_out, or_42_out, or_43_out, or_44_out);
  or or_42 (or_42_out, or_45_out, lc_n0);
  or or_43 (or_43_out, ac4_q_nfull, and_68_out, or_45_out);
  and and_68 (and_68_out, lc_n0, nFE00);
  D_Flip_Flop d_ff_86 (.clk(_45137_out), .D(imux_25_out), .Q(Decoded_data[7]));  // open: Qn, preset, en, reset
  IMUX imux_25 (.b___in0(nand_80_out), .c___in1(minus_355_minus_out), .out(imux_25_out), .sel(dffr_logic_4_out_4));
  nand nand_80 (nand_80_out, _47114_out, d_ff_87_q);
  D_Flip_Flop d_ff_87 (.clk(_45178_out), .D(d_ff_88_q), .Q(d_ff_87_q));  // open: Qn, preset, en, reset
  D_Flip_Flop d_ff_88 (.clk(_43132_out), .D(d_ff_89_q), .Q(d_ff_88_q));  // open: Qn, preset, en, reset
  D_Flip_Flop d_ff_89 (.clk(_36109_2_out), .D(RLE_input[5]), .Q(d_ff_89_q));  // open: Qn, preset, en, reset
  or or_44 (or_44_out, ac4_q_nfull, not_78_out, nand_82_out);
  or or_45 (or_45_out, ac4_d_nfull, nand_82_out);
  D_Flip_Flop d_ff_90 (.clk(_45137_out), .D(imux_26_out), .Q(Decoded_data[8]));  // open: Qn, preset, en, reset
  IMUX imux_26 (.b___in0(nand_81_out), .c___in1(minus_356_minus_out), .out(imux_26_out), .sel(dffr_logic_4_out_4));
  nand nand_81 (nand_81_out, _47114_out, d_ff_91_q);
  D_Flip_Flop d_ff_91 (.clk(_45178_out), .D(d_ff_92_q), .Q(d_ff_91_q));  // open: Qn, preset, en, reset
  D_Flip_Flop d_ff_92 (.clk(_43132_out), .D(d_ff_93_q), .Q(d_ff_92_q));  // open: Qn, preset, en, reset
  D_Flip_Flop d_ff_93 (.clk(_36109_2_out), .D(RLE_input[6]), .Q(d_ff_93_q));  // open: Qn, preset, en, reset
  nand nand_82 (nand_82_out, ch0_0, ch1_3);
  D_Flip_Flop d_ff_94 (.clk(_45137_out), .D(imux_28_out), .Q(Decoded_data[10]));  // open: Qn, preset, en, reset
  D_Flip_Flop d_ff_95 (.clk(_45137_out), .D(imux_27_out), .Q(Decoded_data[9]));  // open: Qn, preset, en, reset
  IMUX imux_27 (.b___in0(nand_83_out), .c___in1(minus_357_minus_out), .out(imux_27_out), .sel(dffr_logic_4_out_4));
  nand nand_83 (nand_83_out, _47114_out, d_ff_97_q);
  nand nand_84 (nand_84_out, _47114_out, d_ff_96_q);
  D_Flip_Flop d_ff_96 (.clk(_45178_out), .D(d_ff_99_q), .Q(d_ff_96_q));  // open: Qn, preset, en, reset
  D_Flip_Flop d_ff_97 (.clk(_45178_out), .D(d_ff_98_q), .Q(d_ff_97_q));  // open: Qn, preset, en, reset
  D_Flip_Flop d_ff_98 (.clk(_43132_out), .D(d_ff_100_q), .Q(d_ff_98_q));  // open: Qn, preset, en, reset
  D_Flip_Flop d_ff_99 (.clk(_43132_out), .D(d_ff_101_q), .Q(d_ff_99_q));  // open: Qn, preset, en, reset
  D_Flip_Flop d_ff_100 (.clk(_36109_2_out), .D(RLE_input[7]), .Q(d_ff_100_q));  // open: Qn, preset, en, reset
  D_Flip_Flop d_ff_101 (.clk(_36109_2_out), .D(RLE_input[8]), .Q(d_ff_101_q));  // open: Qn, preset, en, reset
  D_Flip_Flop d_ff_102 (.clk(_45137_out), .D(imux_29_out), .Q(Decoded_data[11]));  // open: Qn, preset, en, reset
  IMUX imux_28 (.b___in0(nand_84_out), .c___in1(minus_358_minus_out), .out(imux_28_out), .sel(dffr_logic_4_out_4));
  nand nand_85 (nand_85_out, _47114_out, d_ff_103_q);
  D_Flip_Flop d_ff_103 (.clk(_45178_out), .D(d_ff_104_q), .Q(d_ff_103_q));  // open: Qn, preset, en, reset
  D_Flip_Flop d_ff_104 (.clk(_43132_out), .D(d_ff_105_q), .Q(d_ff_104_q));  // open: Qn, preset, en, reset
  D_Flip_Flop d_ff_105 (.clk(_36109_2_out), .D(RLE_input[9]), .Q(d_ff_105_q));  // open: Qn, preset, en, reset
  IMUX imux_29 (.b___in0(nand_85_out), .c___in1(minus_626_minus_out), .out(imux_29_out), .sel(dffr_logic_4_out_4));

  // Notes on the sheet:
  //   in_2: pull=up
  //   nc8__kill: pull=up
  //   c8: pull=up
  //   AC - address counter for reading data from unit04
  //   AC4_Q - quant counter for reading quant data from unit04
  //   1 - stop address counter increment
  //   len counter don't work or data == 0xFE00 - increment data address counter
  //   0x1XXX_XXX1
endmodule
module IDCT (
  input  cnt2_ovfl,
  input  ncnt1_1,
  input  ncnt1_2,
  input  ncnt1_3,
  input  cnt1_0,
  input  ncnt2_ovfl,
  input  ncnt2_ovfl_2,
  input  ncnt2_ovfl_3,
  input  CTRL4,
  input  ncnt2_run,
  input  nres,
  input  nRES_2,
  input  CTRL4_2,
  input  cnt2_0,
  input  cnt2_1,
  input  cnt2_2,
  input  cnt2_3,
  input  ncnt2_ovfl_s,
  input  ncnt2_ovfl_4,
  input  ncnt2_run_2,
  input  cnt0_ovfl,
  input  ncnt3_0,
  input  ncnt3_1,
  input  ncnt3_2,
  input  ncnt3_3,
  input  cnt3_0,
  input  ncnt0_ovfl,
  input  nRES_3,
  input  ctrl4_s,
  input  ncnt0_run,
  input  nRES_4,
  input  ctrl4_s_2,
  input  ncnt0_full,
  input  cnt0_0,
  input  cnt0_1,
  input  cnt0_2,
  input  cnt0_3,
  input  ncnt0_ovfl_s,
  input  ncnt0_ovfl_2,
  input  ncnt0_run_2,
  output result1__use_previous_result_in_summation,
  output stm_sel1,
  output [5:0] Address_for_STM_data,
  output clk1,
  output clk3,
  output rle_sel,
  output [5:0] Address_for_RLE_data,
  output u9__XXXX111111,
  output ctrl3__X111111110,
  output [3:0] Address_for_store_row_multiplication,
  output result2,
  output clk6,
  output clk7,
  output clk8,
  output stm_sel2,
  output [5:0] Address_for_STM_data_2,
  output [3:0] Address_for_read_row_multiplication_result,
  output clk9,
  output ncnt0_ovfl_3,
  output [5:0] Address_for_store_row_multiplication_2
);

  wire _3131_out, _3132_out, _3229_out, _3337_out, _3340_out, _3428_out, _3432_out, _3440_out_4, _3524_out,
       _3529_out, _3530_out, _3531_out, _3532_out, _3533_out, _3534_out, _3535_out, _3536_out, _3537_out,
       _3538_out, _3539_out, _3540_out, _3541_out, _3542_out, _3543_out, _3544_out, _3545_out, _3546_out,
       _3547_2_out, _3547_out, _3548_out, _3549_out, _3552_out, _3553_out, _3555_out, _3620_out, _3622_out,
       _3623_out, _3632_2_out, _3634_2_out, _3636_out, _3637_out, _3638_out, _3639_out, _3640_out, _3641_out,
       _3642_2_out, _3643_out, _3644_out, _3645_out, _3647_out, _3648_out, _3726_out, _3730_out, _3731_out,
       _3733_2_out, _3734_out, _3737_out, _3738_2_out, _3738_out, _3846_out, _3847_out, _3848_out, _3849_out,
       _3850_out, _3851_out, _3852_out, _3853_out, _3943_out, _3944_out, _3945_out, _4155_out, _4156_out,
       _4157_out, and_1_out, and_2_out, and_3_out, and_4_out, and_5_out, and_6_out, and_7_out, and_8_out,
       and_9_out, and_10_out, and_11_out, and_12_out, and_13_out, and_14_out, and_15_out, and_16_out,
       and_17_out, and_18_out, and_19_out, and_20_out, and_21_out, and_22_out, and_23_out, and_24_out,
       and_25_out, and_26_out, and_27_out, and_28_out, clock_1_out, clock_2_out, clock_3_out, clock_4_out,
       d_ff_1_q, d_ff_2_q, dffr_logic_1_out_4, dffr_logic_2_out_4, dffr_logic_3_out_4, dffr_logic_4_out_4,
       dffr_logic_5_out_4, dffr_logic_6_out_4, dffr_logic_7_out_4, dffr_logic_8_out_4, dffr_logic_9_out_4,
       dffr_logic_10_out_4, dffr_logic_11_out_4, dffr_logic_12_out_4, dffr_logic_13_out_4,
       dffr_logic_14_out_4, dffr_logic_15_out_4, dffr_logic_16_out_4, dffr_logic_17_out_4,
       dffr_logic_18_out_4, dffr_logic_19_out_4, dffr_logic_20_out_4, dffr_logic_21_out_4,
       dffr_logic_22_out_4, dffr_logic_23_out_4, dffr_logic_24_out_4, dffr_logic_25_out_4,
       dffr_logic_26_out_4, idct_1st_mul_counter_1__0, imux_1_out, imux_2_out, imux_3_out, nand_1_out,
       nand_2_out, nand_3_out, nand_4_out, nand_5_out, nand_6_out, nand_7_out, nand_8_out, nand_9_out,
       nand_10_out, nand_11_out, nand_12_out, nor_1_out, nor_2_out, nor_3_out, nor_4_out, nor_5_out,
       nor_6_out, nor_7_out, nor_8_out, nor_9_out, nor_10_out, nor_11_out, nor_12_out, nor_13_out,
       nor_14_out, nor_15_out, nor_16_out, nor_17_out, nor_18_out, nor_19_out, nor_20_out, nor_21_out,
       nor_22_out, nor_23_out, nor_24_out, not_1_out, not_2_out, not_3_out, not_4_out, not_5_out, not_7_out,
       not_8_out, not_12_out, not_15_out, not_16_out, not_17_out, or_1_out, or_2_out, or_3_out, or_4_out,
       or_5_out, or_6_out, or_7_out, or_8_out, or_9_out, or_10_out, or_11_out, or_12_out, or_13_out,
       or_14_out, or_15_out, or_16_out, or_17_out, or_18_out, or_19_out, or_20_out, or_21_out, or_22_out,
       or_23_out, or_24_out, or_25_out, or_26_out, or_27_out, or_28_out, or_29_out, or_30_out, or_31_out,
       or_32_out, or_33_out, or_34_out, or_35_out, or_36_out, or_37_out, or_38_out, or_39_out, or_40_out,
       or_41_out, or_42_out, or_47_out, or_48_out, or_49_out, or_50_out, or_51_out, or_52_out, or_53_out,
       xnor_1_out, xnor_2_out, xor_1_out, xor_2_out, xor_3_out, xor_4_out;

  IDCT_1st_mul_counter idct_1st_mul_counter_1 (
    .clk11(_3738_2_out), .nres(nres), ._0(idct_1st_mul_counter_1__0), ._1(Address_for_RLE_data[2]),
    ._2(Address_for_RLE_data[3]), ._3(Address_for_RLE_data[4]), ._4(Address_for_RLE_data[0]),
    ._5(Address_for_RLE_data[1]), ._6(stm_sel1), ._7(Address_for_STM_data[0]), ._8(Address_for_STM_data[1]),
    ._9(Address_for_RLE_data[5]));
  IDCT_2nd_mul_counter idct_2nd_mul_counter_1 (.clk9(nres));  // open: nres, _0, _1, _2, _3, _4, _5, _6, _7, _8
  or or_1 (or_1_out, dffr_logic_1_out_4, dffr_logic_2_out_4);
  or or_2 (or_2_out, or_1_out, dffr_logic_3_out_4);
  or or_3 (or_3_out, or_2_out, dffr_logic_4_out_4);
  or or_4 (or_4_out, or_3_out, dffr_logic_5_out_4);
  or or_5 (or_5_out, or_4_out, dffr_logic_6_out_4);
  or or_6 (or_6_out, dffr_logic_8_out_4, dffr_logic_9_out_4);
  or or_7 (or_7_out, or_6_out, dffr_logic_10_out_4);
  or or_8 (or_8_out, or_7_out, dffr_logic_11_out_4);
  or or_9 (or_9_out, or_8_out, dffr_logic_12_out_4);
  or or_10 (or_10_out, or_9_out, dffr_logic_13_out_4);
  or or_11 (or_11_out, or_10_out, dffr_logic_14_out_4);
  or or_12 (or_12_out, or_11_out, dffr_logic_15_out_4);
  or or_13 (or_13_out, dffr_logic_17_out_4, dffr_logic_18_out_4);
  or or_14 (or_14_out, or_13_out, dffr_logic_19_out_4);
  or or_15 (or_15_out, or_14_out, dffr_logic_20_out_4);
  or or_16 (or_16_out, or_15_out, dffr_logic_21_out_4);
  or or_17 (or_17_out, or_16_out, dffr_logic_22_out_4);
  or or_18 (or_18_out, or_17_out, dffr_logic_23_out_4);
  or or_19 (or_19_out, or_18_out, dffr_logic_24_out_4);
  not not_1 (not_1_out, dffr_logic_1_out_4);
  nor nor_1 (nor_1_out, dffr_logic_2_out_4, dffr_logic_1_out_4);
  or or_20 (or_20_out, nor_1_out, and_1_out);
  and and_1 (and_1_out, dffr_logic_1_out_4, dffr_logic_2_out_4);
  nor nor_2 (nor_2_out, dffr_logic_3_out_4, or_1_out);
  or or_21 (or_21_out, nor_2_out, and_2_out);
  and and_2 (and_2_out, or_1_out, dffr_logic_3_out_4);
  nor nor_3 (nor_3_out, dffr_logic_4_out_4, or_2_out);
  or or_22 (or_22_out, nor_3_out, and_3_out);
  and and_3 (and_3_out, or_2_out, dffr_logic_4_out_4);
  nor nor_4 (nor_4_out, dffr_logic_5_out_4, or_3_out);
  or or_23 (or_23_out, nor_4_out, and_4_out);
  and and_4 (and_4_out, or_3_out, dffr_logic_5_out_4);
  nor nor_5 (nor_5_out, dffr_logic_6_out_4, or_4_out);
  or or_24 (or_24_out, nor_5_out, and_5_out);
  and and_5 (and_5_out, or_4_out, dffr_logic_6_out_4);
  nor nor_6 (nor_6_out, dffr_logic_7_out_4, or_5_out);
  or or_25 (or_25_out, nor_6_out, and_6_out);
  and and_6 (and_6_out, or_5_out, dffr_logic_7_out_4);
  not not_2 (not_2_out, dffr_logic_8_out_4);
  nor nor_7 (nor_7_out, dffr_logic_9_out_4, dffr_logic_8_out_4);
  or or_26 (or_26_out, nor_7_out, and_7_out);
  and and_7 (and_7_out, dffr_logic_8_out_4, dffr_logic_9_out_4);
  nor nor_8 (nor_8_out, dffr_logic_10_out_4, or_6_out);
  or or_27 (or_27_out, nor_8_out, and_8_out);
  and and_8 (and_8_out, or_6_out, dffr_logic_10_out_4);
  nor nor_9 (nor_9_out, dffr_logic_11_out_4, or_7_out);
  or or_28 (or_28_out, nor_9_out, and_9_out);
  and and_9 (and_9_out, or_7_out, dffr_logic_11_out_4);
  nor nor_10 (nor_10_out, dffr_logic_12_out_4, or_8_out);
  or or_29 (or_29_out, nor_10_out, and_10_out);
  and and_10 (and_10_out, or_8_out, dffr_logic_12_out_4);
  nor nor_11 (nor_11_out, dffr_logic_13_out_4, or_9_out);
  or or_30 (or_30_out, nor_11_out, and_11_out);
  and and_11 (and_11_out, or_9_out, dffr_logic_13_out_4);
  nor nor_12 (nor_12_out, dffr_logic_14_out_4, or_10_out);
  or or_31 (or_31_out, nor_12_out, and_12_out);
  and and_12 (and_12_out, or_10_out, dffr_logic_14_out_4);
  nor nor_13 (nor_13_out, dffr_logic_15_out_4, or_11_out);
  or or_32 (or_32_out, nor_13_out, and_13_out);
  and and_13 (and_13_out, or_11_out, dffr_logic_15_out_4);
  nor nor_14 (nor_14_out, dffr_logic_16_out_4, or_12_out);
  or or_33 (or_33_out, nor_14_out, and_14_out);
  and and_14 (and_14_out, or_12_out, dffr_logic_16_out_4);
  not not_3 (not_3_out, dffr_logic_17_out_4);
  nor nor_15 (nor_15_out, dffr_logic_18_out_4, dffr_logic_17_out_4);
  or or_34 (or_34_out, nor_15_out, and_15_out);
  and and_15 (and_15_out, dffr_logic_17_out_4, dffr_logic_18_out_4);
  nor nor_16 (nor_16_out, dffr_logic_19_out_4, or_13_out);
  or or_35 (or_35_out, nor_16_out, and_16_out);
  and and_16 (and_16_out, or_13_out, dffr_logic_19_out_4);
  nor nor_17 (nor_17_out, dffr_logic_20_out_4, or_14_out);
  or or_36 (or_36_out, nor_17_out, and_17_out);
  and and_17 (and_17_out, or_14_out, dffr_logic_20_out_4);
  nor nor_18 (nor_18_out, dffr_logic_21_out_4, or_15_out);
  or or_37 (or_37_out, nor_18_out, and_18_out);
  and and_18 (and_18_out, or_15_out, dffr_logic_21_out_4);
  nor nor_19 (nor_19_out, dffr_logic_22_out_4, or_16_out);
  or or_38 (or_38_out, nor_19_out, and_19_out);
  and and_19 (and_19_out, or_16_out, dffr_logic_22_out_4);
  nor nor_20 (nor_20_out, dffr_logic_23_out_4, or_17_out);
  or or_39 (or_39_out, nor_20_out, and_20_out);
  and and_20 (and_20_out, or_17_out, dffr_logic_23_out_4);
  nor nor_21 (nor_21_out, dffr_logic_24_out_4, or_18_out);
  or or_40 (or_40_out, nor_21_out, and_21_out);
  and and_21 (and_21_out, or_18_out, dffr_logic_24_out_4);
  nor nor_22 (nor_22_out, dffr_logic_25_out_4, or_19_out);
  or or_41 (or_41_out, nor_22_out, and_22_out);
  and and_22 (and_22_out, or_19_out, dffr_logic_25_out_4);
  DFFR_logic dffr_logic_1 (.clk(_3432_out), .in(not_1_out), .nres(nRES_2), .out_4(dffr_logic_1_out_4));
  DFFR_logic dffr_logic_2 (.clk(_3432_out), .in(or_20_out), .nres(nRES_2), .out_4(dffr_logic_2_out_4));
  DFFR_logic dffr_logic_3 (.clk(_3432_out), .in(or_21_out), .nres(nRES_2), .out_4(dffr_logic_3_out_4));
  DFFR_logic dffr_logic_4 (.clk(_3432_out), .in(or_22_out), .nres(nRES_2), .out_4(dffr_logic_4_out_4));
  DFFR_logic dffr_logic_5 (.clk(_3432_out), .in(or_23_out), .nres(nRES_2), .out_4(dffr_logic_5_out_4));
  DFFR_logic dffr_logic_6 (.clk(_3432_out), .in(or_24_out), .nres(nRES_2), .out_4(dffr_logic_6_out_4));
  DFFR_logic dffr_logic_7 (.clk(_3432_out), .in(or_25_out), .nres(nRES_2), .out_4(dffr_logic_7_out_4));
  DFFR_logic dffr_logic_8 (.clk(clk9), .in(not_2_out), .nres(nRES_3), .out_4(dffr_logic_8_out_4));
  DFFR_logic dffr_logic_9 (.clk(clk9), .in(or_26_out), .nres(nRES_3), .out_4(dffr_logic_9_out_4));
  DFFR_logic dffr_logic_10 (.clk(clk9), .in(or_27_out), .nres(nRES_3), .out_4(dffr_logic_10_out_4));
  DFFR_logic dffr_logic_11 (.clk(clk9), .in(or_28_out), .nres(nRES_3), .out_4(dffr_logic_11_out_4));
  DFFR_logic dffr_logic_12 (.clk(clk9), .in(or_29_out), .nres(nRES_3), .out_4(dffr_logic_12_out_4));
  DFFR_logic dffr_logic_13 (.clk(clk9), .in(or_30_out), .nres(nRES_3), .out_4(dffr_logic_13_out_4));
  DFFR_logic dffr_logic_14 (.clk(clk9), .in(or_31_out), .nres(nRES_3), .out_4(dffr_logic_14_out_4));
  DFFR_logic dffr_logic_15 (.clk(clk9), .in(or_32_out), .nres(nRES_3), .out_4(dffr_logic_15_out_4));
  DFFR_logic dffr_logic_16 (.clk(clk9), .in(or_33_out), .nres(nRES_3), .out_4(dffr_logic_16_out_4));
  DFFR_logic dffr_logic_17 (.clk(or_53_out), .in(not_3_out), .nres(nRES_4), .out_4(dffr_logic_17_out_4));
  DFFR_logic dffr_logic_18 (.clk(or_53_out), .in(or_34_out), .nres(nRES_4), .out_4(dffr_logic_18_out_4));
  DFFR_logic dffr_logic_19 (.clk(or_53_out), .in(or_35_out), .nres(nRES_4), .out_4(dffr_logic_19_out_4));
  DFFR_logic dffr_logic_20 (.clk(or_53_out), .in(or_36_out), .nres(nRES_4), .out_4(dffr_logic_20_out_4));
  DFFR_logic dffr_logic_21 (.clk(or_53_out), .in(or_37_out), .nres(nRES_4), .out_4(dffr_logic_21_out_4));
  DFFR_logic dffr_logic_22 (.clk(or_53_out), .in(or_38_out), .nres(nRES_4), .out_4(dffr_logic_22_out_4));
  DFFR_logic dffr_logic_23 (.clk(or_53_out), .in(or_39_out), .nres(nRES_4), .out_4(dffr_logic_23_out_4));
  DFFR_logic dffr_logic_24 (.clk(or_53_out), .in(or_40_out), .nres(nRES_4), .out_4(dffr_logic_24_out_4));
  DFFR_logic dffr_logic_25 (.clk(or_53_out), .in(or_41_out), .nres(nRES_4), .out_4(dffr_logic_25_out_4));
  not _3648 (_3648_out, not_4_out);
  not not_4 (not_4_out, idct_1st_mul_counter_1__0);
  not not_5 (not_5_out, dffr_logic_1_out_4);
  not not_6 (Address_for_store_row_multiplication[0], dffr_logic_2_out_4);
  not not_7 (not_7_out, dffr_logic_3_out_4);
  not not_8 (not_8_out, dffr_logic_4_out_4);
  not not_9 (Address_for_store_row_multiplication[1], dffr_logic_5_out_4);
  not not_10 (Address_for_store_row_multiplication[2], dffr_logic_6_out_4);
  not not_11 (Address_for_store_row_multiplication[3], dffr_logic_7_out_4);
  not not_12 (not_12_out, dffr_logic_8_out_4);
  not _3632 (Address_for_read_row_multiplication_result[0], dffr_logic_9_out_4);
  not _3733 (Address_for_read_row_multiplication_result[1], dffr_logic_10_out_4);
  not _3634 (Address_for_read_row_multiplication_result[2], dffr_logic_11_out_4);
  not _3635 (Address_for_STM_data_2[0], dffr_logic_12_out_4);
  not _3328 (Address_for_STM_data_2[1], dffr_logic_13_out_4);
  not _3621 (Address_for_read_row_multiplication_result[3], dffr_logic_14_out_4);
  not _3620 (_3620_out, dffr_logic_15_out_4);
  not _3623 (_3623_out, dffr_logic_16_out_4);
  not not_13 (Address_for_store_row_multiplication_2[0], dffr_logic_17_out_4);
  not _3632_2 (_3632_2_out, dffr_logic_18_out_4);
  not _3733_2 (_3733_2_out, dffr_logic_19_out_4);
  not _3634_2 (_3634_2_out, dffr_logic_20_out_4);
  not _3635_2 (Address_for_store_row_multiplication_2[1], dffr_logic_21_out_4);
  not _3328_2 (Address_for_store_row_multiplication_2[2], dffr_logic_22_out_4);
  not _3621_2 (Address_for_store_row_multiplication_2[3], dffr_logic_23_out_4);
  not _3620_2 (Address_for_store_row_multiplication_2[4], dffr_logic_24_out_4);
  not _3623_2 (Address_for_store_row_multiplication_2[5], dffr_logic_25_out_4);
  or _3545 (_3545_out, Address_for_RLE_data[3], Address_for_RLE_data[4], cnt2_ovfl);
  Clock #(.highDuration(4), .lowDuration(4)) clock_1 (.out(clock_1_out));
  and _3532 (_3532_out, not_5_out, Address_for_store_row_multiplication[0]);
  or _3530 (_3530_out, Address_for_store_row_multiplication[0], not_7_out, not_8_out);
  and _3529 (_3529_out, not_7_out, not_8_out);
  and _3524 (_3524_out, Address_for_store_row_multiplication[1], Address_for_store_row_multiplication[2], Address_for_store_row_multiplication[3]);
  or or_42 (or_42_out, Address_for_read_row_multiplication_result[1], Address_for_read_row_multiplication_result[2], cnt0_ovfl);
  Clock #(.highDuration(4), .lowDuration(4)) clock_2 (.out(clock_2_out));
  and and_23 (and_23_out, Address_for_store_row_multiplication_2[0], _3632_2_out);
  and and_24 (and_24_out, _3733_2_out, _3634_2_out);
  and and_25 (and_25_out, Address_for_store_row_multiplication_2[1], Address_for_store_row_multiplication_2[2], Address_for_store_row_multiplication_2[3]);
  xnor _3229 (_3229_out, _3648_out, Address_for_RLE_data[2]);
  or _3228 (result1__use_previous_result_in_summation, _3229_out, _3545_out);
  D_Flip_Flop d_ff_1 (.clk(clock_1_out), .D(cnt1_0), .Q(d_ff_1_q));  // open: Qn, preset, en, reset
  D_Flip_Flop _3226 (.clk(clock_1_out), .D(_3648_out), .Q(rle_sel));  // open: Qn, preset, en, reset
  and _3547 (_3547_out, _3648_out, Address_for_RLE_data[2], Address_for_RLE_data[3]);
  or _3645 (_3645_out, Address_for_RLE_data[2], Address_for_RLE_data[3], Address_for_RLE_data[4]);
  and _3555 (_3555_out, Address_for_RLE_data[4], Address_for_RLE_data[0], Address_for_RLE_data[1]);
  and _3340 (_3340_out, stm_sel1, Address_for_STM_data[0], Address_for_STM_data[1]);
  nand nand_1 (nand_1_out, dffr_logic_2_out_4, dffr_logic_3_out_4, dffr_logic_4_out_4);
  nand _3531 (_3531_out, _3532_out, _3529_out, _3524_out);
  xnor xnor_1 (xnor_1_out, not_12_out, Address_for_read_row_multiplication_result[0]);
  or or_43 (result2, xnor_1_out, or_42_out);
  nand nand_2 (nand_2_out, ncnt3_1, ncnt3_2, ncnt3_3);
  nand nand_3 (nand_3_out, ncnt3_0, ncnt3_2, ncnt3_3);
  D_Flip_Flop d_ff_2 (.clk(clock_2_out), .D(cnt3_0), .Q(d_ff_2_q));  // open: Qn, preset, en, reset
  D_Flip_Flop d_ff_3 (.clk(clock_2_out), .D(not_12_out), .Q(stm_sel2));  // open: Qn, preset, en, reset
  and _3730 (_3730_out, not_12_out, Address_for_read_row_multiplication_result[0], Address_for_read_row_multiplication_result[1]);
  and _3636 (_3636_out, Address_for_read_row_multiplication_result[2], Address_for_STM_data_2[0], Address_for_STM_data_2[1]);
  and _3622 (_3622_out, Address_for_read_row_multiplication_result[3], _3620_out, _3623_out);
  xnor xnor_2 (xnor_2_out, Address_for_store_row_multiplication_2[0], _3632_2_out);
  nand nand_4 (nand_4_out, and_23_out, and_24_out, and_25_out);
  xor xor_1 (xor_1_out, _3648_out, rle_sel);
  nand _3428 (_3428_out, ncnt1_1, ncnt1_2, ncnt1_3);
  xor xor_2 (xor_2_out, cnt1_0, d_ff_1_q);
  and _3549 (_3549_out, not_4_out, ncnt2_ovfl_2);
  and _3548 (_3548_out, _3549_out, _3647_out);
  and _3647 (_3647_out, Address_for_RLE_data[2], Address_for_RLE_data[3]);
  nand _3552 (_3552_out, _3547_out, _3555_out, _3340_out);
  xor xor_3 (xor_3_out, not_12_out, stm_sel2);
  nand nand_5 (nand_5_out, nand_2_out, nand_3_out);
  xor xor_4 (xor_4_out, cnt3_0, d_ff_2_q);
  xnor _3726 (_3726_out, not_12_out, Address_for_read_row_multiplication_result[0]);
  nand _3734 (_3734_out, _3730_out, _3636_out, _3622_out);
  and and_26 (and_26_out, xnor_2_out, _3733_2_out, _3634_2_out);
  IMUX _3132 (.b___in0(xor_2_out), .c___in1(xor_1_out), .out(_3132_out), .sel(_3428_out));
  IMUX _3131 (.b___in0(xor_2_out), .c___in1(xor_1_out), .out(_3131_out), .sel(_3428_out));
  nand _3337 (_3337_out, not_4_out, rle_sel, ncnt2_ovfl);
  IMUX imux_1 (.b___in0(xor_4_out), .c___in1(xor_3_out), .out(imux_1_out), .sel(nand_2_out));
  IMUX imux_2 (.b___in0(xor_4_out), .c___in1(xor_3_out), .out(imux_2_out), .sel(nand_2_out));
  IMUX imux_3 (.b___in0(xor_3_out), .c___in1(xor_4_out), .out(imux_3_out), .sel(nand_5_out));
  nand nand_6 (nand_6_out, dffr_logic_8_out_4, stm_sel2, ncnt0_ovfl);
  or _3731 (_3731_out, _3726_out, Address_for_read_row_multiplication_result[1], Address_for_read_row_multiplication_result[2]);
  or or_44 (clk6, clock_2_out, imux_1_out);
  or or_45 (clk7, clock_2_out, imux_2_out);
  or or_46 (clk8, clock_2_out, imux_3_out);
  or or_47 (or_47_out, nand_6_out, clock_2_out);
  or _2930 (clk1, clock_1_out, _3132_out);
  or _3029 (clk3, clock_1_out, _3131_out);
  // Probe on _3738_out
  or _3738 (_3738_out, _3337_out, clock_1_out);
  nand _3642 (u9__XXXX111111, ncnt2_ovfl_3, _3547_out, _3555_out);
  nand _3553 (_3553_out, _3548_out, _3555_out, _3340_out);
  not not_14 (ctrl3__X111111110, _3553_out);
  // Probe on or_47_out
  or _3644 (_3644_out, CTRL4, _3645_out);
  not _3637 (_3637_out, _3552_out);
  not _3640 (_3640_out, ncnt2_run);
  nand _3536 (_3536_out, not_5_out, ncnt2_run_2);
  not not_15 (not_15_out, ncnt2_ovfl_4);
  nand nand_7 (nand_7_out, Address_for_store_row_multiplication_2[0], ncnt0_run_2);
  not not_16 (not_16_out, ncnt0_ovfl_2);
  nand _3643 (_3643_out, _3648_out, ncnt2_run);
  or or_48 (or_48_out, CTRL4_2, _3530_out);
  or or_49 (or_49_out, CTRL4_2, _3530_out);
  and _3547_2 (_3547_2_out, cnt2_0, cnt2_1, cnt2_2);
  not _3851 (_3851_out, _3734_out);
  not _3853 (_3853_out, ncnt0_run);
  or or_50 (or_50_out, ctrl4_s_2, and_26_out);
  or or_51 (or_51_out, ctrl4_s_2, and_26_out);
  and and_27 (and_27_out, cnt0_0, cnt0_1, cnt0_2);
  nand _3642_2 (_3642_2_out, _3643_out, _3644_out, _3440_out_4);
  // Probe on _3641_out
  not _3641 (_3641_out, _3639_out);
  nand _3639 (_3639_out, _3637_out, _3640_out);
  // Probe on _3638_out
  nor _3638 (_3638_out, _3552_out, _3640_out);
  nand _3538 (_3538_out, _3536_out, or_48_out);
  nand _3539 (_3539_out, not_15_out, or_49_out);
  nand _3848 (_3848_out, not_12_out, ncnt0_run);
  or _3849 (_3849_out, ctrl4_s, _3731_out);
  nand _3850 (_3850_out, _3851_out, _3853_out);
  nor _3852 (_3852_out, _3734_out, _3853_out);
  nand nand_8 (nand_8_out, nand_7_out, or_50_out);
  nand nand_9 (nand_9_out, not_16_out, or_51_out);
  not _3544 (_3544_out, _3440_out_4);
  not _3540 (_3540_out, _3638_out);
  nand _3537 (_3537_out, _3538_out, _3539_out, ncnt2_ovfl_4);
  nand _3546 (_3546_out, ncnt2_ovfl_4, _3547_2_out, cnt2_3);
  // Probe on _3943_out
  not _3943 (_3943_out, _3850_out);
  // Probe on _3852_out
  not _4157 (_4157_out, _3852_out);
  nand nand_10 (nand_10_out, nand_8_out, nand_9_out, ncnt0_full);
  nand nand_11 (nand_11_out, ncnt0_ovfl_2, and_27_out, cnt0_3);
  and _3737 (_3737_out, _3642_2_out, _3639_out);
  and _3541 (_3541_out, _3641_out, _3544_out);
  and _3543 (_3543_out, _3540_out, _3440_out_4);
  DFFR_logic dffr_logic_26 (.clk(clock_3_out), .in(nor_23_out), .nres(nRES_2), .out_4(dffr_logic_26_out_4));
  nor nor_23 (nor_23_out, nand_1_out, _3534_out);
  nand _3533 (_3533_out, _3537_out, _3531_out, ncnt2_ovfl_s);
  or _3535 (_3535_out, _3546_out, ncnt2_run_2);
  not _3945 (_3945_out, ncnt0_ovfl_3);
  nand nand_12 (nand_12_out, nand_10_out, nand_4_out, ncnt0_ovfl_s);
  or or_52 (or_52_out, nand_11_out, ncnt0_run_2);
  or _3542 (_3542_out, _3541_out, _3543_out);
  Clock #(.highDuration(4), .lowDuration(4)) clock_3 (.out(clock_3_out));
  not not_17 (not_17_out, dffr_logic_26_out_4);
  and _3534 (_3534_out, _3533_out, _3535_out);
  nand _3847 (_3847_out, _3848_out, _3849_out, ncnt0_ovfl_3);
  and _3944 (_3944_out, _3943_out, _3945_out);
  and _4156 (_4156_out, _4157_out, ncnt0_ovfl_3);
  Clock #(.highDuration(4), .lowDuration(4)) clock_4 (.out(clock_4_out));
  and and_28 (and_28_out, nand_12_out, or_52_out);
  or _3738_2 (_3738_2_out, _3737_out, clock_1_out);
  // Probe on _3738_2_out
  // Probe on _3440_out_4
  DFFR_logic _3440 (.clk(clock_1_out), .in(_3542_out), .nres(nres), .out_4(_3440_out_4));
  nor nor_24 (nor_24_out, not_17_out, clock_3_out);
  // Probe on nor_24_out
  // Probe on _3432_out
  or _3432 (_3432_out, clock_3_out, _3534_out);
  and _3846 (_3846_out, _3847_out, _3850_out);
  or _3845 (clk9, _3846_out, clock_2_out);
  or _4155 (_4155_out, _3944_out, _4156_out);
  // Probe on or_53_out
  or or_53 (or_53_out, clock_4_out, and_28_out);
  DFFR_logic _4158 (.clk(clock_2_out), .in(_4155_out), .nres(nRES_3), .out_4(ncnt0_ovfl_3));

  assign Address_for_STM_data[5:2] = {1'b0, Address_for_RLE_data[4:2]};
  assign Address_for_STM_data_2[5:2] = {1'b0, Address_for_read_row_multiplication_result[2:0]};

  // Notes on the sheet:
  //   2nd MULTIPLICATION COUNTER (cnt0)
  //   1st MULTIPLICATION STORE (cnt1)
  //   2nd MULTIPLICATION STORE (cnt3)
endmodule

module IDCT_1st_mul_control (
  input  cnt2_ovfl,
  input  ncnt1_1,
  input  ncnt1_2,
  input  ncnt1_3,
  input  cnt1_0,
  input  ncnt2_ovfl,
  input  ncnt2_ovfl_2,
  input  ncnt2_ovfl_3,
  input  ctrl4,
  input  ncnt2_run,
  input  _0,
  input  _1,
  input  _2,
  input  _3,
  input  _4,
  input  _5,
  input  _6,
  input  _7,
  input  _8,
  input  _9,
  input  nres,
  output result1__use_previous_result_in_summation,
  output stm_sel1,
  output [5:0] Address_for_STM_data,
  output clk1,
  output clk3,
  output rle_sel,
  output u9__XXXX111111,
  output ctrl3__X111111110,
  output rle_sel_2,
  output _0_2,
  output _1_2,
  output _2_2,
  output _3_2,
  output _4_2,
  output _5_2
);

  wire _3131_out, _3132_out, _3229_out, _3337_out, _3340_out, _3428_out, _3440_out_4, _3541_out, _3542_out,
       _3543_out, _3545_out, _3547_out, _3548_out, _3549_out, _3553_out, _3555_out, _3638_out, _3639_out,
       _3641_out, _3642_out, _3643_out, _3644_out, _3645_out, _3647_out, _3648_out, _3737_out, _3738_2_out,
       _3738_out, and_1_out, and_2_out, and_3_out, clock_1_out, clock_2_out, d_ff_1_q, nand_1_out, not_1_out,
       not_2_out, not_3_out, not_4_out, not_5_out, undriven, undriven_2, undriven_3, xor_1_out, xor_2_out;

  Clock clock_1 (.out(clock_1_out));
  nand _3643 (_3643_out, _0, ncnt2_run);
  // Probe on _3738_out
  or _3738 (_3738_out, _3737_out, clock_1_out);
  and _3737 (_3737_out, _3642_out, _3639_out);
  nand _3642 (_3642_out, _3643_out, _3644_out, _3440_out_4);
  or _3644 (_3644_out, _3645_out, ctrl4);
  or _3645 (_3645_out, _1, _2, _3);
  // Probe on _3440_out_4
  DFFR_logic _3440 (.clk(clock_1_out), .in(_3542_out), .nres(nres), .out_4(_3440_out_4));
  and _3541 (_3541_out, _3641_out, not_1_out);
  not not_1 (not_1_out, _3440_out_4);
  // Probe on _3641_out
  not _3641 (_3641_out, _3639_out);
  nand _3639 (_3639_out, not_2_out, not_4_out);
  not not_2 (not_2_out, nand_1_out);
  nand nand_1 (nand_1_out, and_2_out, and_1_out, and_3_out);
  and and_1 (and_1_out, _3, _4, _5);
  and and_2 (and_2_out, _0, _1, _2);
  or _3542 (_3542_out, _3541_out, _3543_out);
  and _3543 (_3543_out, not_3_out, _3440_out_4);
  not not_3 (not_3_out, _3638_out);
  // Probe on _3638_out
  nor _3638 (_3638_out, nand_1_out, not_4_out);
  not not_4 (not_4_out, ncnt2_run);
  and and_3 (and_3_out, _6, _7, _8);
  D_Flip_Flop _3226 (.clk(clock_1_out), .D(_0), .Q(rle_sel_2));  // open: Qn, preset, en, reset
  not _3648 (_3648_out, not_5_out);
  not not_5 (not_5_out, undriven);
  or _3545 (_3545_out, Address_for_STM_data[3], Address_for_STM_data[4], cnt2_ovfl);
  Clock #(.highDuration(4), .lowDuration(4)) clock_2 (.out(clock_2_out));
  xnor _3229 (_3229_out, _3648_out, Address_for_STM_data[2]);
  or _3228 (result1__use_previous_result_in_summation, _3229_out, _3545_out);
  D_Flip_Flop d_ff_1 (.clk(clock_2_out), .D(cnt1_0), .Q(d_ff_1_q));  // open: Qn, preset, en, reset
  D_Flip_Flop _3226_2 (.clk(clock_2_out), .D(_3648_out), .Q(rle_sel));  // open: Qn, preset, en, reset
  and _3547 (_3547_out, _3648_out, Address_for_STM_data[2], Address_for_STM_data[3]);
  and _3555 (_3555_out, Address_for_STM_data[4], undriven_2, undriven_3);
  and _3340 (_3340_out, stm_sel1, Address_for_STM_data[0], Address_for_STM_data[1]);
  xor xor_1 (xor_1_out, _3648_out, rle_sel);
  nand _3428 (_3428_out, ncnt1_1, ncnt1_2, ncnt1_3);
  xor xor_2 (xor_2_out, cnt1_0, d_ff_1_q);
  and _3549 (_3549_out, not_5_out, ncnt2_ovfl_2);
  and _3548 (_3548_out, _3549_out, _3647_out);
  and _3647 (_3647_out, Address_for_STM_data[2], Address_for_STM_data[3]);
  IMUX _3132 (.b___in0(xor_2_out), .c___in1(xor_1_out), .out(_3132_out), .sel(_3428_out));
  IMUX _3131 (.b___in0(xor_2_out), .c___in1(xor_1_out), .out(_3131_out), .sel(_3428_out));
  nand _3337 (_3337_out, not_5_out, rle_sel, ncnt2_ovfl);
  or _2930 (clk1, clock_2_out, _3132_out);
  or _3029 (clk3, clock_2_out, _3131_out);
  or _3738_2 (_3738_2_out, _3337_out, clock_2_out);
  // Probe on _3738_2_out
  nand _3642_2 (u9__XXXX111111, ncnt2_ovfl_3, _3547_out, _3555_out);
  nand _3553 (_3553_out, _3548_out, _3555_out, _3340_out);
  not not_6 (ctrl3__X111111110, _3553_out);

  assign _0_2 = _4;
  assign _1_2 = _5;
  assign _2_2 = _1;
  assign _3_2 = _2;
  assign _4_2 = _3;
  assign _5_2 = _8;
  assign Address_for_STM_data[5] = 1'b0;

  // Notes on the sheet:
  //   1st Multiplication Counter (cnt2)
  //   Unit05 OA (rle data)
endmodule

module IDCT_1st_mul_counter (
  input  clk11,
  input  nres,
  output _0,
  output _1,
  output _2,
  output _3,
  output _4,
  output _5,
  output _6,
  output _7,
  output _8,
  output _9
);

  wire and_1_out, and_2_out, and_3_out, and_4_out, and_5_out, and_6_out, and_7_out, and_8_out, and_9_out,
       dffr_logic_1_out_4, dffr_logic_2_out_4, dffr_logic_3_out_4, dffr_logic_4_out_4, dffr_logic_5_out_4,
       dffr_logic_6_out_4, dffr_logic_7_out_4, dffr_logic_8_out_4, dffr_logic_9_out_4, dffr_logic_10_out_4,
       nor_1_out, nor_2_out, nor_3_out, nor_4_out, nor_5_out, nor_6_out, nor_7_out, nor_8_out, nor_9_out,
       not_1_out, or_1_out, or_2_out, or_3_out, or_4_out, or_5_out, or_6_out, or_7_out, or_8_out, or_9_out,
       or_10_out, or_11_out, or_12_out, or_13_out, or_14_out, or_15_out, or_16_out, or_17_out;

  not not_1 (not_1_out, dffr_logic_1_out_4);
  or or_1 (or_1_out, dffr_logic_1_out_4, dffr_logic_2_out_4);
  or or_2 (or_2_out, or_1_out, dffr_logic_3_out_4);
  or or_3 (or_3_out, or_2_out, dffr_logic_4_out_4);
  or or_4 (or_4_out, or_3_out, dffr_logic_5_out_4);
  or or_5 (or_5_out, or_4_out, dffr_logic_6_out_4);
  or or_6 (or_6_out, or_5_out, dffr_logic_7_out_4);
  or or_7 (or_7_out, or_6_out, dffr_logic_8_out_4);
  or or_8 (or_8_out, or_7_out, dffr_logic_9_out_4);
  nor nor_1 (nor_1_out, dffr_logic_2_out_4, dffr_logic_1_out_4);
  or or_9 (or_9_out, nor_1_out, and_1_out);
  and and_1 (and_1_out, dffr_logic_1_out_4, dffr_logic_2_out_4);
  nor nor_2 (nor_2_out, dffr_logic_3_out_4, or_1_out);
  or or_10 (or_10_out, nor_2_out, and_2_out);
  and and_2 (and_2_out, or_1_out, dffr_logic_3_out_4);
  nor nor_3 (nor_3_out, dffr_logic_4_out_4, or_2_out);
  or or_11 (or_11_out, nor_3_out, and_3_out);
  and and_3 (and_3_out, or_2_out, dffr_logic_4_out_4);
  nor nor_4 (nor_4_out, dffr_logic_5_out_4, or_3_out);
  or or_12 (or_12_out, nor_4_out, and_4_out);
  and and_4 (and_4_out, or_3_out, dffr_logic_5_out_4);
  nor nor_5 (nor_5_out, dffr_logic_6_out_4, or_4_out);
  or or_13 (or_13_out, nor_5_out, and_5_out);
  and and_5 (and_5_out, or_4_out, dffr_logic_6_out_4);
  nor nor_6 (nor_6_out, dffr_logic_7_out_4, or_5_out);
  or or_14 (or_14_out, nor_6_out, and_6_out);
  and and_6 (and_6_out, or_5_out, dffr_logic_7_out_4);
  nor nor_7 (nor_7_out, dffr_logic_8_out_4, or_6_out);
  or or_15 (or_15_out, nor_7_out, and_7_out);
  and and_7 (and_7_out, or_6_out, dffr_logic_8_out_4);
  nor nor_8 (nor_8_out, dffr_logic_9_out_4, or_7_out);
  or or_16 (or_16_out, nor_8_out, and_8_out);
  and and_8 (and_8_out, or_7_out, dffr_logic_9_out_4);
  nor nor_9 (nor_9_out, dffr_logic_10_out_4, or_8_out);
  or or_17 (or_17_out, nor_9_out, and_9_out);
  and and_9 (and_9_out, or_8_out, dffr_logic_10_out_4);
  DFFR_logic dffr_logic_1 (.clk(clk11), .in(not_1_out), .nres(nres), .out_4(dffr_logic_1_out_4));
  DFFR_logic dffr_logic_2 (.clk(clk11), .in(or_9_out), .nres(nres), .out_4(dffr_logic_2_out_4));
  DFFR_logic dffr_logic_3 (.clk(clk11), .in(or_10_out), .nres(nres), .out_4(dffr_logic_3_out_4));
  DFFR_logic dffr_logic_4 (.clk(clk11), .in(or_11_out), .nres(nres), .out_4(dffr_logic_4_out_4));
  DFFR_logic dffr_logic_5 (.clk(clk11), .in(or_12_out), .nres(nres), .out_4(dffr_logic_5_out_4));
  DFFR_logic dffr_logic_6 (.clk(clk11), .in(or_13_out), .nres(nres), .out_4(dffr_logic_6_out_4));
  DFFR_logic dffr_logic_7 (.clk(clk11), .in(or_14_out), .nres(nres), .out_4(dffr_logic_7_out_4));
  DFFR_logic dffr_logic_8 (.clk(clk11), .in(or_15_out), .nres(nres), .out_4(dffr_logic_8_out_4));
  DFFR_logic dffr_logic_9 (.clk(clk11), .in(or_16_out), .nres(nres), .out_4(dffr_logic_9_out_4));
  DFFR_logic dffr_logic_10 (.clk(clk11), .in(or_17_out), .nres(nres), .out_4(dffr_logic_10_out_4));
  not not_2 (_0, dffr_logic_1_out_4);
  not not_3 (_1, dffr_logic_2_out_4);
  not not_4 (_2, dffr_logic_3_out_4);
  not not_5 (_3, dffr_logic_4_out_4);
  not not_6 (_4, dffr_logic_5_out_4);
  not not_7 (_5, dffr_logic_6_out_4);
  not not_8 (_6, dffr_logic_7_out_4);
  not not_9 (_7, dffr_logic_8_out_4);
  not not_10 (_8, dffr_logic_9_out_4);
  not not_11 (_9, dffr_logic_10_out_4);

  // Notes on the sheet:
  //   1st MULTIPLICATION COUNTER (cnt2)
endmodule

module IDCT_2nd_mul_counter (
  input  clk9,
  input  nres,
  output _0,
  output _1,
  output _2,
  output _3,
  output _4,
  output _5,
  output _6,
  output _7,
  output _8
);

  wire and_1_out, and_2_out, and_3_out, and_4_out, and_5_out, and_6_out, and_7_out, and_8_out,
       dffr_logic_1_out_4, dffr_logic_2_out_4, dffr_logic_3_out_4, dffr_logic_4_out_4, dffr_logic_5_out_4,
       dffr_logic_6_out_4, dffr_logic_7_out_4, dffr_logic_8_out_4, dffr_logic_9_out_4, nor_1_out, nor_2_out,
       nor_3_out, nor_4_out, nor_5_out, nor_6_out, nor_7_out, nor_8_out, not_1_out, or_1_out, or_2_out,
       or_3_out, or_4_out, or_5_out, or_6_out, or_7_out, or_8_out, or_9_out, or_10_out, or_11_out, or_12_out,
       or_13_out, or_14_out, or_15_out;

  not not_1 (not_1_out, dffr_logic_1_out_4);
  or or_1 (or_1_out, dffr_logic_1_out_4, dffr_logic_2_out_4);
  or or_2 (or_2_out, or_1_out, dffr_logic_3_out_4);
  or or_3 (or_3_out, or_2_out, dffr_logic_4_out_4);
  or or_4 (or_4_out, or_3_out, dffr_logic_5_out_4);
  or or_5 (or_5_out, or_4_out, dffr_logic_6_out_4);
  or or_6 (or_6_out, or_5_out, dffr_logic_7_out_4);
  or or_7 (or_7_out, or_6_out, dffr_logic_8_out_4);
  nor nor_1 (nor_1_out, dffr_logic_2_out_4, dffr_logic_1_out_4);
  or or_8 (or_8_out, nor_1_out, and_1_out);
  and and_1 (and_1_out, dffr_logic_1_out_4, dffr_logic_2_out_4);
  nor nor_2 (nor_2_out, dffr_logic_3_out_4, or_1_out);
  or or_9 (or_9_out, nor_2_out, and_2_out);
  and and_2 (and_2_out, or_1_out, dffr_logic_3_out_4);
  nor nor_3 (nor_3_out, dffr_logic_4_out_4, or_2_out);
  or or_10 (or_10_out, nor_3_out, and_3_out);
  and and_3 (and_3_out, or_2_out, dffr_logic_4_out_4);
  nor nor_4 (nor_4_out, dffr_logic_5_out_4, or_3_out);
  or or_11 (or_11_out, nor_4_out, and_4_out);
  and and_4 (and_4_out, or_3_out, dffr_logic_5_out_4);
  nor nor_5 (nor_5_out, dffr_logic_6_out_4, or_4_out);
  or or_12 (or_12_out, nor_5_out, and_5_out);
  and and_5 (and_5_out, or_4_out, dffr_logic_6_out_4);
  nor nor_6 (nor_6_out, dffr_logic_7_out_4, or_5_out);
  or or_13 (or_13_out, nor_6_out, and_6_out);
  and and_6 (and_6_out, or_5_out, dffr_logic_7_out_4);
  nor nor_7 (nor_7_out, dffr_logic_8_out_4, or_6_out);
  or or_14 (or_14_out, nor_7_out, and_7_out);
  and and_7 (and_7_out, or_6_out, dffr_logic_8_out_4);
  nor nor_8 (nor_8_out, dffr_logic_9_out_4, or_7_out);
  or or_15 (or_15_out, nor_8_out, and_8_out);
  and and_8 (and_8_out, or_7_out, dffr_logic_9_out_4);
  DFFR_logic dffr_logic_1 (.clk(clk9), .in(not_1_out), .nres(nres), .out_4(dffr_logic_1_out_4));
  DFFR_logic dffr_logic_2 (.clk(clk9), .in(or_8_out), .nres(nres), .out_4(dffr_logic_2_out_4));
  DFFR_logic dffr_logic_3 (.clk(clk9), .in(or_9_out), .nres(nres), .out_4(dffr_logic_3_out_4));
  DFFR_logic dffr_logic_4 (.clk(clk9), .in(or_10_out), .nres(nres), .out_4(dffr_logic_4_out_4));
  DFFR_logic dffr_logic_5 (.clk(clk9), .in(or_11_out), .nres(nres), .out_4(dffr_logic_5_out_4));
  DFFR_logic dffr_logic_6 (.clk(clk9), .in(or_12_out), .nres(nres), .out_4(dffr_logic_6_out_4));
  DFFR_logic dffr_logic_7 (.clk(clk9), .in(or_13_out), .nres(nres), .out_4(dffr_logic_7_out_4));
  DFFR_logic dffr_logic_8 (.clk(clk9), .in(or_14_out), .nres(nres), .out_4(dffr_logic_8_out_4));
  DFFR_logic dffr_logic_9 (.clk(clk9), .in(or_15_out), .nres(nres), .out_4(dffr_logic_9_out_4));
  not not_2 (_0, dffr_logic_1_out_4);
  not not_3 (_1, dffr_logic_2_out_4);
  not not_4 (_2, dffr_logic_3_out_4);
  not not_5 (_3, dffr_logic_4_out_4);
  not not_6 (_4, dffr_logic_5_out_4);
  not not_7 (_5, dffr_logic_6_out_4);
  not not_8 (_6, dffr_logic_7_out_4);
  not not_9 (_7, dffr_logic_8_out_4);
  not not_10 (_8, dffr_logic_9_out_4);

  // Notes on the sheet:
  //   2nd MULTIPLICATION COUNTER (cnt0)
endmodule

module YUV (
  input  mclk,
  input  nres,
  input  ctrl4_s,
  input  do0,
  input  do1,
  input  dos,
  input  dob15,
  input  pack_enable,
  input  _0,
  input  _1,
  input  _2,
  input  _3,
  input  _4,
  input  _5,
  input  _6,
  input  _7,
  input  _2_2,
  input  _3_2,
  input  _4_2,
  input  _5_2,
  input  _6_2,
  input  _7_2,
  input  _8,
  input  _9,
  input  _10,
  input  _11,
  input  f05,
  input  f06,
  input  f11,
  input  f12,
  input  f14,
  input  f15,
  input  ctrl4_s_2,
  input  do1_2,
  output ia0,
  output ia1,
  output ia2,
  output ia3,
  output ia4,
  output ia5,
  output nout_res_8,
  output ia0_2,
  output ia1_2,
  output ia2_2,
  output ia3_2,
  output ia4_2,
  output ia5_2,
  output yuv_res_8,
  output ie1,
  output ie2,
  output _00,
  output _01,
  output _02,
  output _03,
  output _04,
  output _05,
  output _06,
  output _07,
  output _08,
  output _09,
  output _10_2,
  output _11_2,
  output _12,
  output _13,
  output _14,
  output _15,
  output _16,
  output _17,
  output _18,
  output _19,
  output _20,
  output _21,
  output _22,
  output _23,
  output _24,
  output _25,
  output _26,
  output _27,
  output _28,
  output _29,
  output _30,
  output _31,
  output pack_enable_2
);

  wire and_1_out, nand_1_out, nand_2_out, nand_3_out, nand_4_out, not_1_out, not_2_out, not_4_out, undriven,
       yuv_pack_counter_1__0, yuv_pack_counter_1__1, yuv_pack_counter_1__2, yuv_pack_counter_1__3,
       yuv_pack_logic_1_clk14_1, yuv_pack_logic_1_clk14_2, yuv_pack_logic_1_clk14_3,
       yuv_pack_logic_1_clk14_4, yuv_pack_logic_1_clk14_5, yuv_pack_logic_1_clk14_6,
       yuv_pack_logic_1_clk14_7, yuv_pack_logic_1_clk14_8, yuv_pack_logic_1_clk14_9,
       yuv_pack_logic_1_clk14_10, yuv_pack_logic_1_clk14_11, yuv_pack_logic_1_clk14_12,
       yuv_pack_logic_1_clk57, yuv_pack_logic_1_nbefore_clk, yuv_result_rounding_1__0_2,
       yuv_result_rounding_1__1_2, yuv_result_rounding_1__2_3, yuv_result_rounding_1__3_3,
       yuv_result_rounding_1__4_3, yuv_result_rounding_1__5_3, yuv_result_rounding_1__6_3,
       yuv_result_rounding_1__7_3;

  MDEC_bus_unit03_ac mdec_bus_unit03_ac_1 (
    .clk65(undriven), .nres(nres), .nout_res_8(nout_res_8), .unit03_oa0(ia0), .unit03_oa1(ia1),
    .unit03_oa2(ia2), .unit03_oa3(ia3), .unit03_oa4(ia4), .unit03_oa5(ia5));
  not not_1 (not_1_out, f05);
  not not_2 (not_2_out, f06);
  not not_3 (pack_enable_2, and_1_out);
  and and_1 (and_1_out, not_2_out, nand_2_out, nand_1_out);
  nand nand_1 (nand_1_out, ctrl4_s_2, f14);
  nand nand_2 (nand_2_out, ctrl4_s_2, nand_3_out, do1_2);
  nand nand_3 (nand_3_out, not_4_out, not_1_out, nand_4_out);
  nand nand_4 (nand_4_out, f15, f12);
  not not_4 (not_4_out, f11);
  YUV_pack_unit03_ac yuv_pack_unit03_ac_1 (
    .yuv_res_8(yuv_res_8), .unit03_ia0(ia0_2), .unit03_ia1(ia1_2), .unit03_ia2(ia2_2), .unit03_ia3(ia3_2),
    .unit03_ia4(ia4_2), .unit03_ia5(ia5_2), .nbefore_clk(yuv_pack_logic_1_nbefore_clk),
    .clk57(yuv_pack_logic_1_clk57), .nres(nres));
  YUV_pack_logic yuv_pack_logic_1 (
    .nres(nres), .mclk(mclk), .ctrl4_s(ctrl4_s), .pack_enable(pack_enable), .do0(do0), .do1(do1),
    .nbefore_clk(yuv_pack_logic_1_nbefore_clk), .unit03_ie1(ie1), .unit03_ie2(ie2),
    .clk57(yuv_pack_logic_1_clk57), ._0(yuv_pack_counter_1__0), ._1(yuv_pack_counter_1__1),
    ._2(yuv_pack_counter_1__2), ._3(yuv_pack_counter_1__3), .clk14_12(yuv_pack_logic_1_clk14_12),
    .clk14_11(yuv_pack_logic_1_clk14_11), .clk14_10(yuv_pack_logic_1_clk14_10),
    .clk14_9(yuv_pack_logic_1_clk14_9), .clk14_5(yuv_pack_logic_1_clk14_5),
    .clk14_4(yuv_pack_logic_1_clk14_4), .clk14_1(yuv_pack_logic_1_clk14_1),
    .clk14_6(yuv_pack_logic_1_clk14_6), .clk14_3(yuv_pack_logic_1_clk14_3),
    .clk14_7(yuv_pack_logic_1_clk14_7), .clk14_8(yuv_pack_logic_1_clk14_8), .clk14_2(yuv_pack_logic_1_clk14_2));
  YUV_pack_counter yuv_pack_counter_1 (
    .nres(nres), .mclk(mclk), .pack_enable(pack_enable), .do0(do0), .do1(do1), ._0(yuv_pack_counter_1__0),
    ._1(yuv_pack_counter_1__1), ._2(yuv_pack_counter_1__2), ._3(yuv_pack_counter_1__3));
  YUV_pack_data yuv_pack_data_1 (
    ._00(_00), ._01(_01), ._02(_02), ._03(_03), ._04(_04), ._05(_05), ._06(_06), ._07(_07), ._08(_08),
    ._09(_09), ._10(_10_2), ._11(_11_2), ._12(_12), ._13(_13), ._14(_14), ._15(_15), ._16(_16), ._17(_17),
    ._18(_18), ._19(_19), ._20(_20), ._21(_21), ._22(_22), ._23(_23), ._24(_24), ._25(_25), ._26(_26),
    ._27(_27), ._28(_28), ._29(_29), ._30(_30), ._31(_31), ._0(yuv_result_rounding_1__0_2),
    ._1(yuv_result_rounding_1__1_2), ._2(yuv_result_rounding_1__2_3), ._3(yuv_result_rounding_1__3_3),
    ._4(yuv_result_rounding_1__4_3), ._5(yuv_result_rounding_1__5_3), ._6(yuv_result_rounding_1__6_3),
    ._7(yuv_result_rounding_1__7_3), .dob15(dob15), .do1(do1), .do0(do0),
    .clk14_12(yuv_pack_logic_1_clk14_12), .clk14_11(yuv_pack_logic_1_clk14_11),
    .clk14_10(yuv_pack_logic_1_clk14_10), .clk14_9(yuv_pack_logic_1_clk14_9),
    .clk14_5(yuv_pack_logic_1_clk14_5), .clk14_4(yuv_pack_logic_1_clk14_4),
    .clk14_2(yuv_pack_logic_1_clk14_1), .clk14_1(yuv_pack_logic_1_clk14_6),
    .clk14_7(yuv_pack_logic_1_clk14_3), .clk14_6(yuv_pack_logic_1_clk14_7),
    .clk14_8(yuv_pack_logic_1_clk14_8), .clk14_3(yuv_pack_logic_1_clk14_2));
  YUV_result_rounding yuv_result_rounding_1 (
    ._0_2(yuv_result_rounding_1__0_2), ._1_2(yuv_result_rounding_1__1_2), ._2_3(yuv_result_rounding_1__2_3),
    ._3_3(yuv_result_rounding_1__3_3), ._4_3(yuv_result_rounding_1__4_3), ._5_3(yuv_result_rounding_1__5_3),
    ._6_3(yuv_result_rounding_1__6_3), ._7_3(yuv_result_rounding_1__7_3), .dos(dos), .do1(do1), .do0(do0),
    ._0(_0), ._1(_1), ._2(_2), ._3(_3), ._4(_4), ._5(_5), ._6(_6), ._7(_7), ._2_2(_2_2), ._3_2(_3_2),
    ._4_2(_4_2), ._5_2(_5_2), ._6_2(_6_2), ._7_2(_7_2), ._8(_8), ._9(_9), ._10(_10), ._11(_11));

  // Notes on the sheet:
  //   unit20_oe1 else 2
  //   4_
  //   YUV output to Unit03
  //   res2_
endmodule

module YUV_pack_data (
  input  clk14_12,
  input  clk14_11,
  input  clk14_10,
  input  clk14_9,
  input  clk14_5,
  input  clk14_4,
  input  clk14_2,
  input  clk14_1,
  input  clk14_7,
  input  clk14_6,
  input  clk14_8,
  input  clk14_3,
  input  do0,
  input  do1,
  input  _0,
  input  _1,
  input  _2,
  input  _3,
  input  _4,
  input  _5,
  input  _6,
  input  _7,
  input  dob15,
  output _00,
  output _01,
  output _02,
  output _03,
  output _04,
  output _05,
  output _06,
  output _07,
  output _08,
  output _09,
  output _10,
  output _11,
  output _12,
  output _13,
  output _14,
  output _15,
  output _16,
  output _17,
  output _18,
  output _19,
  output _20,
  output _21,
  output _22,
  output _23,
  output _24,
  output _25,
  output _26,
  output _27,
  output _28,
  output _29,
  output _30,
  output _31
);

  wire imux_1_out, imux_2_out, imux_3_out, imux_4_out, imux_5_out, imux_6_out, imux_7_out, imux_8_out,
       n4_mux_1_out, n4_mux_2_out, n4_mux_3_out, n4_mux_4_out, n4_mux_5_out, n4_mux_6_out, n4_mux_7_out,
       n4_mux_8_out, nand_1_out, not_1_out, not_2_out, not_3_out, not_4_out, not_5_out, not_6_out, not_7_out,
       not_8_out, not_9_out, not_10_out, not_11_out, not_12_out, not_13_out, not_14_out, not_15_out,
       not_16_out, not_17_out;

  D_Flip_Flop d_ff_1 (.clk(clk14_12), .D(not_1_out), .Q(_00));  // open: Qn, preset, en, reset
  D_Flip_Flop d_ff_2 (.clk(clk14_12), .D(not_2_out), .Q(_01));  // open: Qn, preset, en, reset
  D_Flip_Flop d_ff_3 (.clk(clk14_12), .D(not_3_out), .Q(_02));  // open: Qn, preset, en, reset
  D_Flip_Flop d_ff_4 (.clk(clk14_12), .D(not_4_out), .Q(_03));  // open: Qn, preset, en, reset
  D_Flip_Flop d_ff_5 (.clk(clk14_11), .D(imux_1_out), .Q(_04));  // open: Qn, preset, en, reset
  D_Flip_Flop d_ff_6 (.clk(clk14_10), .D(imux_2_out), .Q(_05));  // open: Qn, preset, en, reset
  D_Flip_Flop d_ff_7 (.clk(clk14_10), .D(imux_3_out), .Q(_06));  // open: Qn, preset, en, reset
  not not_1 (not_1_out, n4_mux_1_out);
  _4_mux u_4_mux_1 (
    .out(n4_mux_1_out), .s1(do1), ._3(not_8_out), ._2(not_9_out), ._1(not_9_out), ._0(not_12_out), .s0(do0));
  D_Flip_Flop d_ff_8 (.clk(clk14_10), .D(imux_4_out), .Q(_07));  // open: Qn, preset, en, reset
  not not_2 (not_2_out, n4_mux_2_out);
  _4_mux u_4_mux_2 (
    .out(n4_mux_2_out), .s1(do1), ._3(not_12_out), ._2(not_6_out), ._1(not_6_out), ._0(not_10_out), .s0(do0));
  D_Flip_Flop d_ff_9 (.clk(clk14_9), .D(not_5_out), .Q(_08));  // open: Qn, preset, en, reset
  not not_3 (not_3_out, n4_mux_3_out);
  _4_mux u_4_mux_3 (
    .out(n4_mux_3_out), .s1(do1), ._3(not_10_out), ._2(not_7_out), ._1(not_7_out), ._0(not_13_out), .s0(do0));
  D_Flip_Flop d_ff_10 (.clk(clk14_9), .D(not_14_out), .Q(_09));  // open: Qn, preset, en, reset
  not not_4 (not_4_out, n4_mux_4_out);
  _4_mux u_4_mux_4 (
    .out(n4_mux_4_out), .s1(do1), ._3(not_13_out), ._2(not_8_out), ._1(not_8_out), ._0(not_11_out), .s0(do0));
  D_Flip_Flop d_ff_11 (.clk(clk14_5), .D(not_15_out), .Q(_10));  // open: Qn, preset, en, reset
  D_Flip_Flop d_ff_12 (.clk(clk14_4), .D(imux_5_out), .Q(_12));  // open: Qn, preset, en, reset
  D_Flip_Flop d_ff_13 (.clk(clk14_5), .D(not_16_out), .Q(_11));  // open: Qn, preset, en, reset
  IMUX imux_1 (.b___in0(not_11_out), .c___in1(not_12_out), .out(imux_1_out), .sel(nand_1_out));
  D_Flip_Flop d_ff_14 (.clk(clk14_4), .D(imux_6_out), .Q(_13));  // open: Qn, preset, en, reset
  IMUX imux_2 (.b___in0(not_8_out), .c___in1(not_10_out), .out(imux_2_out), .sel(nand_1_out));
  D_Flip_Flop d_ff_15 (.clk(clk14_4), .D(imux_7_out), .Q(_14));  // open: Qn, preset, en, reset
  IMUX imux_3 (.b___in0(not_12_out), .c___in1(not_13_out), .out(imux_3_out), .sel(nand_1_out));
  D_Flip_Flop d_ff_16 (.clk(clk14_4), .D(imux_8_out), .Q(_15));  // open: Qn, preset, en, reset
  not not_5 (not_5_out, n4_mux_5_out);
  IMUX imux_4 (.b___in0(not_10_out), .c___in1(not_11_out), .out(imux_4_out), .sel(nand_1_out));
  not not_6 (not_6_out, _1);
  not not_7 (not_7_out, _2);
  not not_8 (not_8_out, _3);
  not not_9 (not_9_out, _0);
  D_Flip_Flop d_ff_17 (.clk(clk14_2), .D(not_1_out), .Q(_16));  // open: Qn, preset, en, reset
  _4_mux u_4_mux_5 (
    .out(n4_mux_5_out), .s1(do1), ._3(not_13_out), ._2(not_9_out), ._1(not_9_out), ._0(not_12_out), .s0(do0));
  not not_10 (not_10_out, _5);
  not not_11 (not_11_out, _7);
  not not_12 (not_12_out, _4);
  not not_13 (not_13_out, _6);
  D_Flip_Flop d_ff_18 (.clk(clk14_2), .D(not_2_out), .Q(_17));  // open: Qn, preset, en, reset
  not not_14 (not_14_out, n4_mux_6_out);
  _4_mux u_4_mux_6 (
    .out(n4_mux_6_out), .s1(do1), ._3(not_11_out), ._2(not_6_out), ._1(not_6_out), ._0(not_10_out), .s0(do0));
  D_Flip_Flop d_ff_19 (.clk(clk14_2), .D(not_3_out), .Q(_18));  // open: Qn, preset, en, reset
  not not_15 (not_15_out, n4_mux_7_out);
  _4_mux u_4_mux_7 (
    .out(n4_mux_7_out), .s1(do1), ._3(not_8_out), ._2(not_7_out), ._1(not_7_out), ._0(not_13_out), .s0(do0));
  D_Flip_Flop d_ff_20 (.clk(clk14_1), .D(imux_1_out), .Q(_20));  // open: Qn, preset, en, reset
  D_Flip_Flop d_ff_21 (.clk(clk14_2), .D(not_4_out), .Q(_19));  // open: Qn, preset, en, reset
  not not_16 (not_16_out, n4_mux_8_out);
  _4_mux u_4_mux_8 (
    .out(n4_mux_8_out), .s1(do1), ._3(not_12_out), ._2(not_8_out), ._1(not_8_out), ._0(not_11_out), .s0(do0));
  D_Flip_Flop d_ff_22 (.clk(clk14_7), .D(imux_2_out), .Q(_21));  // open: Qn, preset, en, reset
  IMUX imux_5 (.b___in0(not_10_out), .c___in1(not_12_out), .out(imux_5_out), .sel(nand_1_out));
  D_Flip_Flop d_ff_23 (.clk(clk14_7), .D(imux_3_out), .Q(_22));  // open: Qn, preset, en, reset
  IMUX imux_6 (.b___in0(not_13_out), .c___in1(not_10_out), .out(imux_6_out), .sel(nand_1_out));
  D_Flip_Flop d_ff_24 (.clk(clk14_7), .D(imux_4_out), .Q(_23));  // open: Qn, preset, en, reset
  IMUX imux_7 (.b___in0(not_11_out), .c___in1(not_13_out), .out(imux_7_out), .sel(nand_1_out));
  D_Flip_Flop d_ff_25 (.clk(clk14_6), .D(not_5_out), .Q(_24));  // open: Qn, preset, en, reset
  IMUX imux_8 (.b___in0(not_17_out), .c___in1(not_11_out), .out(imux_8_out), .sel(nand_1_out));
  D_Flip_Flop d_ff_26 (.clk(clk14_6), .D(not_14_out), .Q(_25));  // open: Qn, preset, en, reset
  not not_17 (not_17_out, dob15);
  D_Flip_Flop d_ff_27 (.clk(clk14_8), .D(not_15_out), .Q(_26));  // open: Qn, preset, en, reset
  D_Flip_Flop d_ff_28 (.clk(clk14_3), .D(imux_5_out), .Q(_28));  // open: Qn, preset, en, reset
  D_Flip_Flop d_ff_29 (.clk(clk14_8), .D(not_16_out), .Q(_27));  // open: Qn, preset, en, reset
  nand nand_1 (nand_1_out, do0, do1);
  D_Flip_Flop d_ff_30 (.clk(clk14_3), .D(imux_6_out), .Q(_29));  // open: Qn, preset, en, reset
  D_Flip_Flop d_ff_31 (.clk(clk14_3), .D(imux_7_out), .Q(_30));  // open: Qn, preset, en, reset
  D_Flip_Flop d_ff_32 (.clk(clk14_3), .D(imux_8_out), .Q(_31));  // open: Qn, preset, en, reset

  // Notes on the sheet:
  //   YUV output to Unit03
endmodule

module YUV_pack_counter (
  input  nres,
  input  mclk,
  input  pack_enable,
  input  do0,
  input  do1,
  output _0,
  output _1,
  output _2,
  output _3
);

  wire _43164_out, _44177_out, _44178_out, _44179_out, _44180_out, _44181_out, _45171_out, _45172_out,
       _45173_out, _45174_out, _45175_out, _45176_out, _45177_out, _46184_out, _46185_out, _46186_out,
       _46189_out, _46190_out, _47146_out, _47147_out, _47148_out, _47149_out, _47151_out, and_1_out,
       nand_1_out, nand_2_out, not_1_out, not_2_out, not_3_out, not_4_out, not_5_out, not_6_out, not_7_out,
       not_8_out, not_9_out, not_10_out, not_11_out, not_12_out, not_13_out, not_14_out, not_15_out,
       not_16_out, not_17_out, not_18_out, not_19_out, not_20_out, not_21_out, not_22_out, not_23_out,
       or_1_out;

  or or_1 (or_1_out, mclk, not_1_out);
  not not_1 (not_1_out, pack_enable);
  nand _44181 (_44181_out, _45176_out, _44180_out);
  nand _44180 (_44180_out, not_2_out, not_6_out);
  not not_2 (not_2_out, _2);
  nand _45176 (_45176_out, not_4_out, _2, not_3_out);
  not not_3 (not_3_out, _0);
  not not_4 (not_4_out, _3);
  DFFR_logic dffr_logic_1 (.clk(or_1_out), .in(_44181_out), .nres(nres), .out_4(_0));
  nand _46189 (_46189_out, _0, not_5_out, not_7_out);
  not not_5 (not_5_out, _2);
  not not_6 (not_6_out, _0);
  not not_7 (not_7_out, _1);
  nand nand_1 (nand_1_out, not_9_out, not_8_out, _1);
  not not_8 (not_8_out, _3);
  not not_9 (not_9_out, _0);
  DFFR_logic dffr_logic_2 (.clk(or_1_out), .in(_47151_out), .nres(nres), .out_4(_1));
  nand _47151 (_47151_out, _46189_out, and_1_out, _47148_out);
  and _47148 (_47148_out, _46186_out, _47147_out);
  and and_1 (and_1_out, nand_1_out, nand_2_out);
  nand _46186 (_46186_out, _0, _46185_out, _46184_out);
  nand nand_2 (nand_2_out, not_11_out, not_10_out, _1);
  not not_10 (not_10_out, _2);
  not not_11 (not_11_out, _0);
  and _46184 (_46184_out, not_13_out, _2);
  and _46185 (_46185_out, not_14_out, not_12_out);
  not not_12 (not_12_out, do0);
  not not_13 (not_13_out, _1);
  not not_14 (not_14_out, _3);
  or _46190 (_46190_out, _45177_out, _47149_out);
  nand _45177 (_45177_out, _45176_out, _45174_out);
  nand _47147 (_47147_out, _0, _46184_out, _47146_out);
  or _45174 (_45174_out, _45175_out, _45173_out);
  nand _45175 (_45175_out, not_17_out, not_19_out);
  and _47146 (_47146_out, not_16_out, not_15_out);
  not not_15 (not_15_out, do1);
  not not_16 (not_16_out, _3);
  not not_17 (not_17_out, _2);
  DFFR_logic dffr_logic_3 (.clk(or_1_out), .in(_46190_out), .nres(nres), .out_4(_2));
  nand _47149 (_47149_out, _46186_out, _47147_out);
  not not_18 (not_18_out, _1);
  nand _45173 (_45173_out, _0, _1);
  not not_19 (not_19_out, _3);
  nand _43164 (_43164_out, _44178_out, _44177_out, _44179_out);
  nand _44178 (_44178_out, not_18_out, not_20_out, _3);
  nand _44177 (_44177_out, _45172_out, _45171_out, _0);
  not not_20 (not_20_out, _2);
  not not_21 (not_21_out, _0);
  and _45171 (_45171_out, do1, not_22_out);
  and _45172 (_45172_out, _1, _2);
  not not_22 (not_22_out, _3);
  DFFR_logic dffr_logic_4 (.clk(or_1_out), .in(_43164_out), .nres(nres), .out_4(_3));
  nand _44179 (_44179_out, not_21_out, not_23_out, _3);
  not not_23 (not_23_out, _2);

  // Notes on the sheet:
  //   Counter for pack
  //   Depends on data output depth
  //   0 - 4bit (count 0-7)
  //   1 - 8bit (count 0-7)
  //   2 - 24bit (count 0-11)
  //   3 - 15bit (count 0-5)
  //   Data output depth
  //   0 - 4bit, 1 - 8bit, 2 - 24bit, 3 - 15bit
endmodule

module YUV_pack_unit03_ac (
  input  nbefore_clk,
  input  clk57,
  input  nres,
  output yuv_res_8,
  output unit03_ia0,
  output unit03_ia1,
  output unit03_ia2,
  output unit03_ia3,
  output unit03_ia4,
  output unit03_ia5
);

  wire and_1_out, and_2_out, and_3_out, and_4_out, and_5_out, and_6_out, and_7_out, and_8_out, and_9_out,
       and_10_out, and_11_out, and_12_out, and_13_out, and_14_out, and_15_out, and_16_out, and_17_out,
       and_18_out, and_19_out, and_20_out, nand_1_out, nand_2_out, nand_3_out, nand_4_out, nand_5_out,
       nand_6_out, nand_7_out, nand_8_out, nand_9_out, nand_10_out, nand_11_out, not_2_out, not_3_out,
       not_4_out, not_5_out, not_6_out, not_7_out, not_8_out, not_9_out, not_10_out, not_11_out, not_12_out,
       not_13_out, not_14_out, not_15_out, not_16_out, not_17_out, not_18_out, or_1_out, or_2_out, or_3_out,
       or_4_out, or_5_out, or_6_out, or_7_out;

  not not_1 (yuv_res_8, or_1_out);
  or or_1 (or_1_out, nand_2_out, nand_1_out);
  nand nand_1 (nand_1_out, unit03_ia1, unit03_ia2);
  nand nand_2 (nand_2_out, not_2_out, unit03_ia0);
  not not_2 (not_2_out, nbefore_clk);
  not not_3 (not_3_out, unit03_ia4);
  and and_1 (and_1_out, unit03_ia5, not_3_out);
  and and_2 (and_2_out, unit03_ia1, unit03_ia0);
  and and_3 (and_3_out, unit03_ia3, unit03_ia2);
  nand nand_3 (nand_3_out, and_1_out, and_3_out, and_2_out);
  or or_2 (or_2_out, and_4_out, and_6_out);
  and and_4 (and_4_out, nand_3_out, not_4_out);
  not not_4 (not_4_out, unit03_ia0);
  DFFR_logic dffr_logic_1 (.clk(clk57), .in(or_2_out), .nres(nres), .out_4(unit03_ia0));
  or or_3 (or_3_out, and_5_out, and_8_out);
  and and_5 (and_5_out, not_6_out, and_7_out);
  and and_6 (and_6_out, not_5_out, unit03_ia0);
  not not_5 (not_5_out, 1'b1);
  not not_6 (not_6_out, unit03_ia1);
  and and_7 (and_7_out, unit03_ia0, nand_3_out);
  DFFR_logic dffr_logic_2 (.clk(clk57), .in(or_3_out), .nres(nres), .out_4(unit03_ia1));
  or or_4 (or_4_out, and_9_out, and_12_out);
  and and_8 (and_8_out, not_8_out, unit03_ia1);
  and and_9 (and_9_out, not_7_out, and_10_out);
  not not_7 (not_7_out, unit03_ia2);
  not not_8 (not_8_out, unit03_ia0);
  and and_10 (and_10_out, and_7_out, unit03_ia1);
  DFFR_logic dffr_logic_3 (.clk(clk57), .in(or_4_out), .nres(nres), .out_4(unit03_ia2));
  or or_5 (or_5_out, and_11_out, and_14_out);
  and and_11 (and_11_out, not_10_out, and_13_out);
  and and_12 (and_12_out, not_9_out, unit03_ia2);
  not not_9 (not_9_out, nand_4_out);
  not not_10 (not_10_out, unit03_ia3);
  and and_13 (and_13_out, and_10_out, unit03_ia2);
  nand nand_4 (nand_4_out, nand_3_out, nand_5_out);
  nand nand_5 (nand_5_out, unit03_ia0, unit03_ia1);
  DFFR_logic dffr_logic_4 (.clk(clk57), .in(or_5_out), .nres(nres), .out_4(unit03_ia3));
  or or_6 (or_6_out, and_15_out, and_18_out);
  and and_14 (and_14_out, not_12_out, unit03_ia3);
  and and_15 (and_15_out, not_11_out, and_16_out);
  not not_11 (not_11_out, unit03_ia4);
  not not_12 (not_12_out, nand_6_out);
  and and_16 (and_16_out, and_13_out, unit03_ia3);
  nand nand_6 (nand_6_out, nand_3_out, nand_7_out);
  nand nand_7 (nand_7_out, not_13_out, unit03_ia2);
  not not_13 (not_13_out, nand_5_out);
  DFFR_logic dffr_logic_5 (.clk(clk57), .in(or_6_out), .nres(nres), .out_4(unit03_ia4));
  or or_7 (or_7_out, and_17_out, and_20_out);
  and and_17 (and_17_out, not_15_out, and_19_out);
  and and_18 (and_18_out, not_14_out, unit03_ia4);
  not not_14 (not_14_out, nand_8_out);
  not not_15 (not_15_out, unit03_ia5);
  and and_19 (and_19_out, and_16_out, unit03_ia4);
  nand nand_8 (nand_8_out, nand_3_out, nand_9_out);
  nand nand_9 (nand_9_out, not_16_out, unit03_ia3);
  not not_16 (not_16_out, nand_7_out);
  DFFR_logic dffr_logic_6 (.clk(clk57), .in(or_7_out), .nres(nres), .out_4(unit03_ia5));
  and and_20 (and_20_out, not_17_out, unit03_ia5);
  not not_17 (not_17_out, nand_10_out);
  nand nand_10 (nand_10_out, nand_3_out, nand_11_out);
  nand nand_11 (nand_11_out, not_18_out, unit03_ia4);
  not not_18 (not_18_out, nand_9_out);

  // Notes on the sheet:
  //   Unit03 Input Address Counter
  //   Counts from 0 to 0x2F (0-47). This is size of Unit03
  //   On each 8 (7, 15,23 ...) generates yuv_res_8 signal for MDEC control
endmodule

module YUV_pack_logic (
  input  nres,
  input  mclk,
  input  ctrl4_s,
  input  pack_enable,
  input  do0,
  input  do1,
  input  _0,
  input  _1,
  input  _2,
  input  _3,
  output nbefore_clk,
  output unit03_ie1,
  output unit03_ie2,
  output clk57,
  output clk14_12,
  output clk14_10,
  output clk14_5,
  output clk14_1,
  output clk14_6,
  output clk14_3,
  output clk14_11,
  output clk14_9,
  output clk14_4,
  output clk14_2,
  output clk14_7,
  output clk14_8
);

  wire _39134_out, _41151_out, _41152_out, _41155_out, _41156_out, _41158_out, _41174_out, _42140_out,
       _42141_out, _42142_out, _42143_out, _42144_out, _42146_out, _42147_out, _42148_out, _42149_out,
       _42150_out, _42151_out, _42152_out, _43141_out_4, _43145_out, _43146_out, _43147_out, _43148_out,
       _43149_out, _43150_out, _43151_out, _43152_out, _43153_out, _43154_out, _43155_out, _43156_out,
       _43157_out, _43158_2_out, _43158_out, _44148_out_4, _44150_out, _44151_out, _44154_out, _44155_out,
       _44157_out, _44158_out, _44159_out, _44160_out, _44161_out, _44162_out, _44163_out, _44164_out,
       _44165_out, _44167_out, _44168_out, _44169_2_out, _44169_out, _44171_out, _44172_out, _44173_out,
       _44174_out, _45144_out, _45145_out, _45146_out, _45147_out, _45150_out, _45152_out, _45155_out,
       _45156_out, _45158_out, _45159_out, _45160_out, _45161_out, _45162_out, _45163_out, _45165_out,
       _45166_out, _45167_out, _45168_out, _45169_out, _45170_out, _45171_out, _45172_out, _46170_out,
       _46171_out, _46172_out, _46173_out, _46174_out, _46175_out, _46176_out, _46177_out, _46178_out,
       _46179_out, _46180_out, _46182_out, _46184_out, _47135_out, _47136_out, _47137_out, _47138_out,
       _47139_out, _47140_out, _47141_out, _47142_out, _47143_out, _47145_out, and_1_out, and_2_out,
       nand_1_out, nand_2_out, nand_3_out, nand_4_out, nand_5_out, nand_6_out, nand_7_out, nand_8_out,
       nand_9_out, nand_10_out, nand_11_out, nand_12_out, nand_13_out, not_1_out, not_2_out, not_3_out,
       not_4_out, not_5_out, not_6_out, not_7_out, not_8_out, not_9_out, not_10_out, not_11_out, not_12_out,
       not_13_out, not_14_out, not_15_out, not_16_out, not_17_out, not_18_out, not_19_out, not_20_out,
       not_21_out, not_22_out, not_23_out, not_24_out, not_25_out, not_26_out, not_27_out, not_28_out,
       not_29_out, not_30_out, not_31_out, not_32_out, not_33_out, not_34_out, not_35_out, not_36_out,
       not_37_out, not_38_out, not_39_out, not_40_out, not_41_out, not_42_out, not_43_out;

  nand _42151 (_42151_out, not_1_out, not_6_out);
  not not_1 (not_1_out, _1);
  and _44151 (_44151_out, _44154_out, not_8_out);
  and _44154 (_44154_out, pack_enable, _45147_out);
  nand _45147 (_45147_out, _45163_out, _45158_out, _45166_out);
  and _45158 (_45158_out, _46174_out, _45160_out);
  and _45163 (_45163_out, _45170_out, _46176_out);
  nand _45170 (_45170_out, _0, _45171_out, _46184_out);
  and _45171 (_45171_out, do1, not_2_out);
  not not_2 (not_2_out, _3);
  or _42152 (_42152_out, _42151_out, _43158_out);
  nand _42149 (_42149_out, not_3_out, not_12_out);
  nand _43158 (_43158_out, not_5_out, not_4_out);
  not not_3 (not_3_out, _0);
  not not_4 (not_4_out, do1);
  not not_5 (not_5_out, _0);
  not not_6 (not_6_out, _2);
  nor _3382 (unit03_ie1, mclk, _39134_out);
  DFFR_logic _43141 (.clk(mclk), .in(_44169_out), .nres(nres), .out_4(_43141_out_4));
  or _44169 (_44169_out, _44151_out, _44150_out);
  and _44150 (_44150_out, not_7_out, _43141_out_4);
  not not_7 (not_7_out, _44155_out);
  not not_8 (not_8_out, _43141_out_4);
  and _44155 (_44155_out, not_9_out, ctrl4_s);
  not not_9 (not_9_out, _45147_out);
  or _42150 (_42150_out, _42149_out, _43156_out);
  nand _43153 (_43153_out, not_10_out, do0);
  nand _43156 (_43156_out, do0, not_11_out);
  not not_10 (not_10_out, _0);
  not not_11 (not_11_out, do1);
  not not_12 (not_12_out, _1);
  nand _39134 (_39134_out, _43141_out_4, ctrl4_s);
  or _45145 (_45145_out, _45146_out, _45144_out);
  and _45146 (_45146_out, _45152_out, not_13_out);
  not not_13 (not_13_out, _44148_out_4);
  and _45152 (_45152_out, pack_enable, _46170_out);
  not not_14 (not_14_out, _46170_out);
  nand _46170 (_46170_out, _46171_out, _46172_out, _45166_out);
  and _46171 (_46171_out, _46173_out, _47136_out);
  nand _46173 (_46173_out, _46177_out, _46182_out, not_42_out);
  or _43154 (_43154_out, _43153_out, _43157_out);
  nand _43157 (_43157_out, not_17_out, not_16_out);
  nand _46180 (_46180_out, not_15_out, do0);
  not not_15 (not_15_out, do1);
  not not_16 (not_16_out, _2);
  not not_17 (not_17_out, _1);
  nor _44106 (unit03_ie2, mclk, nbefore_clk);
  nand _44147 (nbefore_clk, _44148_out_4, ctrl4_s);
  DFFR_logic _44148 (.clk(mclk), .in(_45145_out), .nres(nres), .out_4(_44148_out_4));
  and _45144 (_45144_out, not_18_out, _44148_out_4);
  not not_18 (not_18_out, _45150_out);
  and _45150 (_45150_out, not_14_out, ctrl4_s);
  or _46178 (_46178_out, _46180_out, _46179_out);
  nand _46179 (_46179_out, not_19_out, _0);
  nand _45168 (_45168_out, _0, not_20_out);
  not not_19 (not_19_out, _1);
  or _44120 (clk57, mclk, nbefore_clk);
  or _45167 (_45167_out, _45168_out, _45169_out);
  nand _44169_2 (_44169_2_out, do0, not_22_out);
  nand _45169 (_45169_out, _1, _2);
  not not_20 (not_20_out, do1);
  or _44165 (_44165_out, _44169_2_out, _44164_out);
  nand _44164 (_44164_out, not_21_out, _1);
  nand _44171 (_44171_out, not_23_out, do0);
  not not_21 (not_21_out, _0);
  not not_22 (not_22_out, do1);
  not not_23 (not_23_out, do1);
  or _44172 (_44172_out, _44171_out, _44173_out);
  nand _44173 (_44173_out, _0, _1);
  or or_1 (clk14_12, mclk, nand_2_out);
  nand _41174 (_41174_out, _41158_out, _42146_out, _47142_out);
  and _41158 (_41158_out, _42152_out, _42150_out);
  or or_2 (clk14_11, mclk, nand_1_out);
  nand nand_1 (nand_1_out, _41156_out, pack_enable);
  nand nand_2 (nand_2_out, _41174_out, pack_enable);
  nand _41156 (_41156_out, _42146_out, _47142_out, _42147_out);
  and _42146 (_42146_out, _43154_out, _46174_out);
  or or_3 (clk14_10, mclk, nand_3_out);
  or or_4 (clk14_9, mclk, nand_4_out);
  nand nand_3 (nand_3_out, _41155_out, pack_enable);
  nand nand_4 (nand_4_out, _41152_out, pack_enable);
  nand _41152 (_41152_out, _42143_out, _45162_out, _42141_out);
  nand _41155 (_41155_out, _47142_out, _42147_out, _42144_out);
  and _47142 (_47142_out, _47141_out, nand_7_out);
  and _42147 (_42147_out, _42150_out, _42148_out);
  or or_5 (clk14_5, mclk, nand_5_out);
  nand nand_5 (nand_5_out, _41151_out, pack_enable);
  nand _41151 (_41151_out, _45162_out, _42142_out, _42141_out);
  and _42144 (_42144_out, _46174_out, _43151_out);
  and _42143 (_42143_out, _43151_out, _45161_out);
  or or_6 (clk14_4, mclk, nand_6_out);
  nand nand_6 (nand_6_out, _42140_out, pack_enable);
  nand _42140 (_42140_out, _45162_out, _42142_out, _43149_out);
  and _45162 (_45162_out, _46178_out, _46176_out);
  nand _46174 (_46174_out, _46175_out, _47145_out, not_42_out);
  and _46175 (_46175_out, not_25_out, _1);
  not not_24 (not_24_out, _2);
  not not_25 (not_25_out, _0);
  nand _42141 (_42141_out, not_26_out, _45165_out, _44174_out);
  and _42142 (_42142_out, _45161_out, _43150_out);
  not not_26 (not_26_out, _0);
  nand _47141 (_47141_out, _46177_out, and_1_out, not_42_out);
  and _46177 (_46177_out, not_27_out, not_28_out);
  and _47145 (_47145_out, not_24_out, _3);
  not not_27 (not_27_out, _0);
  not not_28 (not_28_out, _1);
  not not_29 (not_29_out, _2);
  nand _43149 (_43149_out, _0, _45165_out, _44174_out);
  not not_30 (not_30_out, _0);
  nand nand_7 (nand_7_out, and_1_out, and_2_out, not_42_out);
  and and_1 (and_1_out, not_29_out, not_31_out);
  and and_2 (and_2_out, _1, _0);
  not not_31 (not_31_out, _3);
  not not_32 (not_32_out, _2);
  nand _44161 (_44161_out, _0, _45165_out, _46184_out);
  nand _43148 (_43148_out, not_30_out, _45165_out, _46184_out);
  nand _42148 (_42148_out, _43158_2_out, _0, _45165_out);
  and _43158_2 (_43158_2_out, not_32_out, not_34_out);
  and _45165 (_45165_out, not_33_out, not_35_out);
  not not_33 (not_33_out, do0);
  not not_34 (not_34_out, _1);
  not not_35 (not_35_out, do1);
  and _44162 (_44162_out, _44165_out, _45159_out);
  and _43147 (_43147_out, _43152_out, _47137_out);
  nand _43151 (_43151_out, _43155_out, _44174_out, not_37_out);
  and _44174 (_44174_out, _1, not_36_out);
  and _43155 (_43155_out, do0, do1);
  not not_36 (not_36_out, _2);
  not not_37 (not_37_out, _0);
  not not_38 (not_38_out, _1);
  or or_7 (clk14_2, mclk, nand_8_out);
  nand nand_8 (nand_8_out, _43146_out, pack_enable);
  nand _43146 (_43146_out, _43148_out, _44162_out, _43147_out);
  and _44159 (_44159_out, _47137_out, _44163_out);
  nand _45161 (_45161_out, _0, _46182_out, not_42_out);
  nand _46176 (_46176_out, _46175_out, and_1_out, not_42_out);
  and _46184 (_46184_out, not_38_out, _2);
  and _46182 (_46182_out, not_39_out, _2);
  not not_39 (not_39_out, _3);
  or or_8 (clk14_7, mclk, nand_9_out);
  or or_9 (clk14_1, mclk, nand_10_out);
  nand nand_9 (nand_9_out, _44157_out, pack_enable);
  nand nand_10 (nand_10_out, _43145_out, pack_enable);
  nand _44157 (_44157_out, _44161_out, _44162_out, _44159_out);
  nand _43145 (_43145_out, _44161_out, _44162_out, _43147_out);
  and _44167 (_44167_out, _44168_out, _44172_out);
  and _44160 (_44160_out, _44163_out, _47139_out);
  nand _43150 (_43150_out, _43155_out, _46184_out, not_41_out);
  and _47140 (_47140_out, _0, not_40_out);
  and _45172 (_45172_out, _2, _1);
  not not_40 (not_40_out, _1);
  or or_10 (clk14_6, mclk, nand_11_out);
  or or_11 (clk14_8, mclk, nand_13_out);
  nand nand_11 (nand_11_out, _44158_out, pack_enable);
  nand _45155 (_45155_out, _44167_out, _46172_out, _47135_out);
  nand _44158 (_44158_out, _44160_out, _44167_out, _47135_out);
  and _46172 (_46172_out, _45160_out, _47139_out);
  nand _45159 (_45159_out, not_41_out, _46182_out, not_42_out);
  not not_41 (not_41_out, _0);
  or or_12 (clk14_3, mclk, nand_12_out);
  nand nand_12 (nand_12_out, _45156_out, pack_enable);
  nand nand_13 (nand_13_out, _45155_out, pack_enable);
  nand _45156 (_45156_out, _46172_out, _47135_out, _45166_out);
  and _47135 (_47135_out, _47138_out, _47136_out);
  and _45166 (_45166_out, _45167_out, _44172_out);
  nand _43152 (_43152_out, _0, _43158_2_out, _43155_out);
  nand _47137 (_47137_out, _47145_out, _47140_out, not_42_out);
  nand _44163 (_44163_out, _0, _44174_out, _43155_out);
  nand _44168 (_44168_out, not_41_out, _45165_out, _45172_out);
  nand _47138 (_47138_out, _47140_out, and_1_out, not_42_out);
  nand _45160 (_45160_out, _0, _43155_out, _46184_out);
  nand _47139 (_47139_out, _47145_out, and_2_out, not_42_out);
  nand _47136 (_47136_out, _47145_out, _46177_out, not_42_out);
  not not_42 (not_42_out, _47143_out);
  nand _47143 (_47143_out, not_43_out, do1);
  not not_43 (not_43_out, do0);

  // Notes on the sheet:
  //   Data output depth
  //   0 - 4bit, 1 - 8bit, 2 - 24bit, 3 - 15bit
  //   and current counter value
  //   Pack CLK generator
  //   Generates number of clocks for pack triggers
  //   allows correctly store input data in
  //   triggers depending on data output depth
  //   do = 3: 0x0000001F 0x001F0000 0x000003E0
  //   0x03E00000 0x0000FC00 0xFC000000
  //   do = 0: 0x0000000F 0x000000F0 0x00000F00 0x0000F000
  //   0x000F0000 0x00F00000 0x0F000000 0xF0000000
  //   do = 1: 0x000000FF 0x0000FF00 0x00FF0000 0xFF000000
  //   0x000000FF 0x0000FF00 0x00FF0000 0xFF000000
  //   do = 2: 0x000000FF 0xFF000000 0x0000FF00 0x000000FF
  //   0x00FF0000 0x0000FF00 0x00FF0000 0x0000FF00
  //   0xFF000000 0x00FF0000 0x000000FF 0xFF000000
  //   12  12  12  12  11  10  10  10  9  9  5  5  4  4  4  4  2  2  2  2  1  7  7  7  6  6  8  8  3  3  3  3
endmodule

module YUV_result_rounding (
  input  dos,
  input  do1,
  input  do0,
  input  _0,
  input  _1,
  input  _2,
  input  _3,
  input  _4,
  input  _5,
  input  _6,
  input  _7,
  input  _2_2,
  input  _3_2,
  input  _4_2,
  input  _5_2,
  input  _6_2,
  input  _7_2,
  input  _8,
  input  _9,
  input  _10,
  input  _11,
  output _0_2,
  output _1_2,
  output _2_3,
  output _3_3,
  output _4_3,
  output _5_3,
  output _6_3,
  output _7_3
);

  wire _34119_out, _34124_out, _34125_out, _35130_out, _35131_out, _35132_out, _35133_out, _35134_out,
       _35135_out, _35136_out, _35137_out, _35139_out, _35140_out, _36132_out, _36133_out, _36134_out,
       _36135_out, _36136_out, _36137_out, _36139_out, _36141_out, _36142_out, _36143_out, _36144_out,
       _37120_out, _37121_out, _37122_out, _37126_out, _37129_out, and_1_out, and_2_out, and_3_out,
       and_4_out, and_5_out, and_6_out, and_7_out, and_8_out, and_9_out, and_10_out, imux_1_out, imux_2_out,
       imux_3_out, imux_4_out, imux_5_out, imux_6_out, imux_7_out, imux_8_out, imux_9_out, n4_mux_1_out,
       nand_1_out, nand_2_out, nor_1_out, nor_2_out, nor_3_out, not_1_out, not_2_out, not_3_out, not_4_out,
       or_3_out, or_6_out, xor_1_out, xor_2_out, xor_3_out, xor_4_out;

  _4_mux u_4_mux_1 (.out(n4_mux_1_out), .s1(do1), ._3(nor_1_out), ._2(nor_3_out), ._1(_7), ._0(nor_2_out), .s0(do0));
  nor nor_1 (nor_1_out, and_2_out, imux_9_out);
  nor nor_2 (nor_2_out, and_1_out, imux_9_out);
  and and_1 (and_1_out, _35140_out, _36139_out);
  and and_2 (and_2_out, _35140_out, _36144_out);
  nand _34119 (_34119_out, do1, do0);
  nor _37121 (_37121_out, do1, do0);
  xor xor_1 (xor_1_out, dos, not_1_out);
  not not_1 (not_1_out, n4_mux_1_out);
  nor nor_3 (nor_3_out, imux_9_out, and_3_out);
  and and_3 (and_3_out, _37129_out, _36144_out, _35140_out);
  nand _36135 (_36135_out, _36137_out, _36136_out, _36142_out);
  nor _36136 (_36136_out, imux_2_out, imux_1_out, imux_3_out);
  and _36137 (_36137_out, _3_2, not_2_out, do1);
  not not_2 (not_2_out, do0);
  IMUX _36133 (.b___in0(nand_1_out), .c___in1(_36135_out), .out(_36133_out), .sel(_34119_out));
  nand nand_1 (nand_1_out, _5_2, nand_2_out);
  nand nand_2 (nand_2_out, imux_9_out, _36144_out, _35140_out);
  IMUX _37122 (.b___in0(_37120_out), .c___in1(_37126_out), .out(_37122_out), .sel(_37121_out));
  and _37120 (_37120_out, _36133_out, not_3_out);
  not not_3 (not_3_out, imux_4_out);
  and _37126 (_37126_out, _3, _36141_out);
  nand _36141 (_36141_out, imux_9_out, _35140_out, _36139_out);
  nand _36134 (_36134_out, _36137_out, _36142_out);
  nand _36142 (_36142_out, _36143_out, _35139_out);
  and _36143 (_36143_out, _37129_out, _36144_out);
  nor _37129 (_37129_out, not_4_out, imux_2_out, imux_1_out);
  nor _36144 (_36144_out, imux_3_out, imux_4_out, imux_5_out);
  not not_4 (not_4_out, _3_2);
  or _35131 (_35131_out, imux_9_out, _35137_out);
  nor _36139 (_36139_out, imux_5_out, imux_4_out);
  and _35139 (_35139_out, _35140_out, imux_9_out);
  nor _35140 (_35140_out, imux_6_out, imux_7_out, imux_8_out);
  and _35130 (_35130_out, _35137_out, imux_9_out);
  xor _35137 (_35137_out, _35136_out, imux_8_out);
  or _35136 (_35136_out, _37122_out, _35135_out);
  or _35135 (_35135_out, imux_5_out, imux_6_out, imux_7_out);
  or or_1 (_0_2, and_4_out, _35130_out);
  and and_4 (and_4_out, xor_2_out, _35131_out);
  xor xor_2 (xor_2_out, imux_2_out, _36134_out);
  IMUX imux_1 (.b___in0(_1), .c___in1(_4_2), .out(imux_1_out), .sel(do1));
  IMUX imux_2 (.b___in0(_0), .c___in1(_2_2), .out(imux_2_out), .sel(do1));
  or or_2 (_1_2, and_5_out, _35130_out);
  and and_5 (and_5_out, xor_3_out, _35131_out);
  xor xor_3 (xor_3_out, imux_1_out, or_3_out);
  xor xor_4 (xor_4_out, imux_3_out, or_6_out);
  or or_3 (or_3_out, _36134_out, imux_2_out);
  IMUX imux_3 (.b___in0(_2), .c___in1(_5_2), .out(imux_3_out), .sel(do1));
  or or_4 (_3_3, and_6_out, _35130_out);
  or or_5 (_2_3, and_7_out, _35130_out);
  and and_6 (and_6_out, _36132_out, _35131_out);
  and and_7 (and_7_out, xor_4_out, _35131_out);
  xnor _36132 (_36132_out, imux_4_out, _36133_out);
  or or_6 (or_6_out, _36134_out, imux_2_out, imux_1_out);
  IMUX imux_4 (.b___in0(_3), .c___in1(_6_2), .out(imux_4_out), .sel(do1));
  or or_7 (_4_3, and_8_out, _35130_out);
  and and_8 (and_8_out, _35132_out, _35131_out);
  xor _35132 (_35132_out, imux_5_out, _37122_out);
  IMUX imux_5 (.b___in0(_4), .c___in1(_7_2), .out(imux_5_out), .sel(do1));
  or or_8 (_5_3, and_9_out, _35130_out);
  and and_9 (and_9_out, _34124_out, _35131_out);
  xor _34124 (_34124_out, imux_6_out, _35133_out);
  xor _34125 (_34125_out, imux_7_out, _35134_out);
  or _35133 (_35133_out, _37122_out, imux_5_out);
  IMUX imux_6 (.b___in0(_5), .c___in1(_8), .out(imux_6_out), .sel(do1));
  or or_9 (_6_3, and_10_out, _35130_out);
  not not_5 (_7_3, xor_1_out);
  and and_10 (and_10_out, _34125_out, _35131_out);
  or _35134 (_35134_out, _37122_out, imux_5_out, imux_6_out);
  IMUX imux_7 (.b___in0(_6), .c___in1(_9), .out(imux_7_out), .sel(do1));
  IMUX imux_8 (.b___in0(_7), .c___in1(_10), .out(imux_8_out), .sel(do1));
  IMUX imux_9 (.b___in0(_7), .c___in1(_11), .out(imux_9_out), .sel(do1));

  // Notes on the sheet:
  //   4_
  //   do == 0 (4bit)
  //   do == 1 (8bit)
  //    output = input
  //   output = clamp( -8, 7, ceil( input / 16.0f ) )
  //   res2_
  //   do == 2 (24bit)
  //   output = clamp( -128, 127, ceil( input / 8.0f ) )
  //   do == 3 (15bit)
  //   output = clamp( -16, 15, ceil( input / 64.0f ) )
endmodule

module MDEC_bus_unit03_ac (
  input  clk65,
  input  nres,
  output nout_res_8,
  output unit03_oa0,
  output unit03_oa1,
  output unit03_oa2,
  output unit03_oa3,
  output unit03_oa4,
  output unit03_oa5
);

  wire and_1_out, nand_2_out, nor_1_out, nor_2_out, nor_3_out, not_1_out, not_2_out, xor_1_out, xor_2_out,
       xor_3_out, xor_4_out, xor_5_out;

  DFFR_logic dffr_logic_1 (.clk(clk65), .in(not_1_out), .nres(nres), .out_4(unit03_oa0));
  not not_1 (not_1_out, unit03_oa0);
  DFFR_logic dffr_logic_2 (.clk(clk65), .in(xor_1_out), .nres(nres), .out_4(unit03_oa1));
  xor xor_1 (xor_1_out, unit03_oa0, unit03_oa1);
  and and_1 (and_1_out, unit03_oa1, unit03_oa0);
  DFFR_logic dffr_logic_3 (.clk(clk65), .in(xor_2_out), .nres(nres), .out_4(unit03_oa2));
  xor xor_2 (xor_2_out, and_1_out, unit03_oa2);
  not not_2 (not_2_out, nout_res_8);
  nand nand_1 (nout_res_8, unit03_oa2, and_1_out);
  DFFR_logic dffr_logic_4 (.clk(clk65), .in(xor_3_out), .nres(nres), .out_4(unit03_oa3));
  xor xor_3 (xor_3_out, not_2_out, unit03_oa3);
  nor nor_1 (nor_1_out, nand_2_out, unit03_oa5);
  nand nand_2 (nand_2_out, unit03_oa3, not_2_out);
  DFFR_logic dffr_logic_5 (.clk(clk65), .in(xor_4_out), .nres(nres), .out_4(unit03_oa4));
  xor xor_4 (xor_4_out, nor_1_out, unit03_oa4);
  nor nor_2 (nor_2_out, nand_2_out, nor_3_out);
  DFFR_logic dffr_logic_6 (.clk(clk65), .in(xor_5_out), .nres(nres), .out_4(unit03_oa5));
  xor xor_5 (xor_5_out, nor_2_out, unit03_oa5);
  nor nor_3 (nor_3_out, unit03_oa4, unit03_oa5);

  // Notes on the sheet:
  //   Unit03 Output Address Counter
  //   Counts from 0 to 0x2F (0-47). This is size of Unit03
  //   On each 8 (7, 15,23 ...) generates out_res_8 signal for MDEC control
endmodule
module YUV_other (
  input  in_1,
  input  sel1,
  input  in_3,
  input  f11,
  input  f5,
  input  f6,
  input  f8,
  input  f7,
  input  f4,
  input  f9,
  input  f10,
  input  f3,
  input  f2,
  input  f1,
  input  f0,
  input  in_16,
  input  nthis_enables_yuv_to_rgb,
  input  in_18,
  input  in_19,
  input  in_20,
  input  in_21,
  input  _00,
  input  _01,
  input  _02,
  input  _03,
  input  _04,
  input  _05,
  input  _06,
  input  _07,
  input  sel1_2,
  input  _00_2,
  input  _01_2,
  input  _02_2,
  input  _03_2,
  input  _04_2,
  input  _05_2,
  input  _06_2,
  input  _07_2,
  input  _08,
  input  _09,
  input  _10,
  input  _11,
  input  _12,
  input  _13,
  input  _14,
  input  _15,
  output c_start
);

  wire and_1_out, and_2_out, and_3_out, and_4_out, and_5_out, and_6_out, and_7_out, and_8_out, and_9_out,
       and_10_out, and_11_out, and_12_out, and_13_out, and_14_out, and_15_out, and_16_out, and_17_out,
       and_18_out, and_19_out, and_20_out, and_21_out, and_22_out, and_23_out, and_24_out, and_25_out,
       and_26_out, and_27_out, and_28_out, and_29_out, and_30_out, and_31_out, and_32_out, and_33_out,
       and_34_out, and_35_out, and_36_out, and_37_out, and_38_out, and_39_out, and_40_out, buffer_1_out,
       clk44_out, clk45_out, clk47_2_out, clk47_out, clk51_out, clk52_out, clk53_out, clk54_out, clk55_out,
       clk56_out, d_ff_1_q, d_ff_2_q, d_ff_3_q, d_ff_4_q, d_ff_5_q, d_ff_6_q, d_ff_7_q, d_ff_8_q, d_ff_9_q,
       d_ff_10_q, d_ff_11_q, d_ff_12_q, d_ff_13_q, d_ff_14_q, d_ff_15_q, d_ff_16_q, d_ff_17_q, d_ff_18_q,
       d_ff_19_q, d_ff_20_q, d_ff_21_q, d_ff_23_q, d_ff_24_q, d_ff_26_q, d_ff_27_q, d_ff_29_q, d_ff_30_q,
       d_ff_32_q, d_ff_33_q, d_ff_35_q, d_ff_36_q, d_ff_38_q, d_ff_39_q, d_ff_42_q, d_ff_43_q, d_ff_44_q,
       d_ff_46_q, d_ff_47_q, d_ff_48_q, d_ff_51_q, d_ff_52_q, d_ff_55_q, d_ff_56_q, d_ff_60_q, d_ff_61_q,
       d_ff_62_q, d_ff_63_q, d_ff_65_q, d_ff_66_q, d_ff_68_q, d_ff_69_q, d_ff_71_q, d_ff_72_q, d_ff_74_q,
       d_ff_75_q, dffr_logic_1_out_4, dffr_logic_2_out_4, dffr_logic_3_out_4, dffr_logic_4_out_4,
       dffr_logic_5_out_4, dffr_logic_6_out_4, dffr_logic_7_out_4, dffr_logic_8_out_4, dffr_logic_9_out_4,
       dffr_logic_10_out_4, dffr_logic_11_out_4, dffr_logic_12_out_4, dffr_logic_13_out_4,
       dffr_logic_14_out_4, dffr_logic_15_out_4, dffr_logic_16_out_4, dffr_logic_17_out_4,
       dffr_logic_18_out_4, dffr_logic_19_out_4, dffr_logic_20_out_4, dffr_logic_21_out_4,
       dffr_logic_22_out_4, dffr_logic_23_out_4, imux_1_out, imux_2_out, imux_3_out, imux_4_out, imux_5_out,
       imux_6_out, imux_7_out, imux_8_out, imux_9_out, imux_10_out, imux_11_out, imux_12_out, imux_13_out,
       imux_14_out, imux_15_out, imux_16_out, imux_17_out, imux_18_out, imux_19_out, imux_20_out,
       imux_21_out, imux_22_out, imux_23_out, imux_24_out, imux_25_out, imux_26_out, imux_27_out,
       imux_28_out, n4_mux_1_out, n4_mux_2_out, n4_mux_3_out, n4_mux_4_out, n4_mux_5_out, n4_mux_6_out,
       n4_mux_7_out, n4_mux_8_out, n4_mux_9_out, n4_mux_10_out, n4_mux_11_out, n4_mux_12_out, n4_mux_13_out,
       n4_mux_14_out, n4_mux_15_out, n4_mux_16_out, n4_mux_17_out, nand_1_out, nand_2_out, nand_3_out,
       nand_4_out, nand_5_out, nand_6_out, nand_7_out, nand_8_out, nand_9_out, nand_10_out, nand_11_out,
       nand_12_out, nand_13_out, nand_14_out, nand_15_out, nand_16_out, nand_17_out, nand_18_out,
       nand_19_out, nand_20_out, nand_21_out, nand_23_out, nand_24_out, nand_25_out, nand_26_out,
       nand_27_out, nand_28_out, nand_29_out, nand_30_out, nor_1_out, nor_2_out, nor_3_out, nor_4_out,
       nor_5_out, nor_6_out, nor_7_out, nor_8_out, nor_9_out, nor_10_out, nor_11_out, nor_12_out, nor_13_out,
       nor_14_out, nor_15_out, nor_16_out, nor_17_out, not_1_out, not_2_out, not_3_out, not_4_out, not_5_out,
       not_6_out, not_7_out, not_8_out, not_9_out, not_10_out, not_11_out, not_12_out, not_13_out,
       not_14_out, not_15_out, not_16_out, not_17_out, not_18_out, not_19_out, not_20_out, not_21_out,
       not_22_out, not_23_out, not_24_out, not_25_out, not_26_out, not_27_out, not_28_out, not_29_out,
       not_30_out, not_31_out, not_32_out, not_33_out, not_34_out, not_35_out, not_36_out, not_37_out,
       not_38_out, not_39_out, not_40_out, not_41_out, not_42_out, not_43_out, not_44_out, not_45_out,
       not_46_out, not_47_out, not_48_out, not_49_out, not_50_out, not_51_out, not_52_out, not_53_out,
       not_54_out, not_55_out, not_56_out, not_57_out, not_58_out, not_59_out, not_60_out, not_61_out,
       not_62_out, not_63_out, not_64_out, not_65_out, not_66_out, not_67_out, not_68_out, not_69_out,
       not_70_out, not_71_out, not_72_out, not_73_out, not_74_out, or_1_out, or_2_out, or_3_out, or_4_out,
       or_5_out, or_6_out, or_7_out, or_8_out, or_9_out, or_10_out, or_11_out, or_12_out, or_13_out,
       or_14_out, or_15_out, or_16_out, or_17_out, or_18_out, or_19_out, or_20_out, or_21_out, or_22_out,
       or_23_out, or_24_out, or_25_out, or_26_out, or_27_out, xnor_1_out, xnor_2_out, xnor_3_out, xnor_4_out,
       xnor_5_out, xnor_6_out, xnor_7_out, xnor_8_out, xnor_9_out, xnor_10_out, xor_1_out, xor_2_out,
       xor_3_out, xor_4_out, xor_5_out, xor_6_out, xor_7_out, xor_8_out, xor_9_out, xor_10_out, xor_11_out,
       xor_12_out, xor_13_out, xor_14_out, xor_15_out, xor_16_out, xor_17_out, xor_18_out;

  Clock clk47 (.out(clk47_out));
  D_Flip_Flop d_ff_1 (.clk(clk47_out), .D(xnor_1_out), .Q(d_ff_1_q));  // open: Qn, preset, en, reset
  IMUX imux_1 (.b___in0(not_1_out), .c___in1(not_2_out), .out(imux_1_out), .sel(sel1));
  not not_1 (not_1_out, n4_mux_1_out);
  _4_mux u_4_mux_1 (
    .out(n4_mux_1_out), .s1(xnor_10_out), ._3(and_7_out), ._2(xor_8_out), ._1(and_5_out), ._0(buffer_1_out),
    .s0(xnor_10_out));
  not not_2 (not_2_out, d_ff_2_q);
  D_Flip_Flop d_ff_2 (.clk(clk47_out), .D(xor_2_out), .Q(d_ff_2_q));  // open: Qn, preset, en, reset
  IMUX imux_2 (.b___in0(not_3_out), .c___in1(not_4_out), .out(imux_2_out), .sel(sel1));
  not not_3 (not_3_out, n4_mux_2_out);
  _4_mux u_4_mux_2 (
    .out(n4_mux_2_out), .s1(not_40_out), ._3(and_7_out), ._2(xor_8_out), ._1(and_5_out), ._0(buffer_1_out),
    .s0(xnor_10_out));
  not not_4 (not_4_out, d_ff_3_q);
  D_Flip_Flop d_ff_3 (.clk(clk47_out), .D(imux_7_out), .Q(d_ff_3_q));  // open: Qn, preset, en, reset
  nor nor_1 (nor_1_out, and_2_out, and_1_out, and_3_out);
  and and_1 (and_1_out, not_20_out, imux_1_out);
  and and_2 (and_2_out, not_20_out, imux_17_out);
  IMUX imux_3 (.b___in0(not_5_out), .c___in1(not_6_out), .out(imux_3_out), .sel(sel1));
  not not_5 (not_5_out, n4_mux_3_out);
  _4_mux u_4_mux_3 (
    .out(n4_mux_3_out), .s1(1'b0), ._3(and_7_out), ._2(xor_8_out), ._1(and_5_out), ._0(buffer_1_out),
    .s0(not_40_out));
  not not_6 (not_6_out, d_ff_4_q);
  D_Flip_Flop d_ff_4 (.clk(clk47_out), .D(xnor_4_out), .Q(d_ff_4_q));  // open: Qn, preset, en, reset
  nand nand_1 (nand_1_out, nand_2_out, or_1_out);
  or or_1 (or_1_out, nor_2_out, nor_1_out);
  nand nand_2 (nand_2_out, not_22_out, imux_2_out);
  nor nor_2 (nor_2_out, imux_2_out, not_22_out);
  and and_3 (and_3_out, imux_1_out, imux_17_out);
  IMUX imux_4 (.b___in0(not_7_out), .c___in1(not_8_out), .out(imux_4_out), .sel(sel1));
  not not_7 (not_7_out, n4_mux_4_out);
  _4_mux u_4_mux_4 (
    .out(n4_mux_4_out), .s1(not_41_out), ._3(and_7_out), ._2(xor_8_out), ._1(and_5_out), ._0(buffer_1_out),
    .s0(1'b0));
  not not_8 (not_8_out, d_ff_5_q);
  D_Flip_Flop d_ff_5 (.clk(clk47_out), .D(xnor_5_out), .Q(d_ff_5_q));  // open: Qn, preset, en, reset
  xor xor_1 (xor_1_out, not_20_out, xor_3_out);
  IMUX imux_5 (.b___in0(not_9_out), .c___in1(not_10_out), .out(imux_5_out), .sel(sel1));
  not not_9 (not_9_out, n4_mux_5_out);
  _4_mux u_4_mux_5 (
    .out(n4_mux_5_out), .s1(nand_20_out), ._3(and_7_out), ._2(xor_8_out), ._1(and_5_out), ._0(buffer_1_out),
    .s0(not_41_out));
  not not_10 (not_10_out, d_ff_6_q);
  D_Flip_Flop d_ff_6 (.clk(clk47_out), .D(xor_9_out), .Q(d_ff_6_q));  // open: Qn, preset, en, reset
  xnor xnor_1 (xnor_1_out, nor_1_out, xor_4_out);
  xor xor_2 (xor_2_out, nand_1_out, xor_5_out);
  xor xor_3 (xor_3_out, imux_1_out, imux_17_out);
  xor xor_4 (xor_4_out, not_22_out, imux_2_out);
  IMUX imux_6 (.b___in0(not_11_out), .c___in1(not_12_out), .out(imux_6_out), .sel(sel1));
  not not_11 (not_11_out, n4_mux_6_out);
  _4_mux u_4_mux_6 (
    .out(n4_mux_6_out), .s1(in_21), ._3(and_7_out), ._2(xor_8_out), ._1(and_5_out), ._0(buffer_1_out),
    .s0(nand_20_out));
  not not_12 (not_12_out, d_ff_7_q);
  D_Flip_Flop d_ff_7 (.clk(clk47_out), .D(imux_19_out), .Q(d_ff_7_q));  // open: Qn, preset, en, reset
  IMUX imux_7 (.b___in0(xnor_2_out), .c___in1(xor_6_out), .out(imux_7_out), .sel(nand_1_out));
  xnor xnor_2 (xnor_2_out, nand_3_out, xnor_3_out);
  xor xor_5 (xor_5_out, not_24_out, imux_3_out);
  xnor xnor_3 (xnor_3_out, not_27_out, imux_4_out);
  nand nand_3 (nand_3_out, not_24_out, imux_3_out);
  IMUX imux_8 (.b___in0(not_13_out), .c___in1(not_14_out), .out(imux_8_out), .sel(sel1));
  not not_13 (not_13_out, n4_mux_7_out);
  _4_mux u_4_mux_7 (
    .out(n4_mux_7_out), .s1(1'b1), ._3(and_7_out), ._2(xor_8_out), ._1(and_5_out), ._0(buffer_1_out),
    .s0(in_21));
  not not_14 (not_14_out, d_ff_8_q);
  D_Flip_Flop d_ff_8 (.clk(clk47_out), .D(xor_15_out), .Q(d_ff_8_q));  // open: Qn, preset, en, reset
  IMUX imux_9 (.b___in0(nand_4_out), .c___in1(or_6_out), .out(imux_9_out), .sel(xnor_3_out));
  xor xor_6 (xor_6_out, xnor_3_out, or_3_out);
  nand nand_4 (nand_4_out, or_2_out, and_4_out);
  or or_2 (or_2_out, nor_1_out, nand_5_out);
  or or_3 (or_3_out, not_24_out, imux_3_out);
  nand nand_5 (nand_5_out, or_5_out, or_4_out);
  or or_4 (or_4_out, not_24_out, imux_3_out);
  or or_5 (or_5_out, not_22_out, imux_2_out);
  IMUX imux_10 (.b___in0(not_15_out), .c___in1(not_16_out), .out(imux_10_out), .sel(sel1));
  not not_15 (not_15_out, n4_mux_8_out);
  buf buffer_1 (buffer_1_out, d_ff_13_q);
  not not_16 (not_16_out, d_ff_9_q);
  D_Flip_Flop d_ff_9 (.clk(clk47_out), .D(xor_16_out), .Q(d_ff_9_q));  // open: Qn, preset, en, reset
  xnor xnor_4 (xnor_4_out, imux_9_out, xor_7_out);
  xor xor_7 (xor_7_out, not_29_out, imux_5_out);
  or or_6 (or_6_out, not_27_out, imux_4_out);
  and and_4 (and_4_out, nand_3_out, or_7_out);
  or or_7 (or_7_out, nand_6_out, nor_3_out);
  nand nand_6 (nand_6_out, not_22_out, imux_2_out);
  nor nor_3 (nor_3_out, not_24_out, imux_3_out);
  IMUX imux_11 (.b___in0(imux_14_out), .c___in1(not_17_out), .out(imux_11_out), .sel(sel1));
  _4_mux u_4_mux_8 (
    .out(n4_mux_8_out), .s1(not_40_out), ._3(and_7_out), ._2(xor_8_out), ._1(and_5_out), ._0(buffer_1_out),
    .s0(1'b1));
  and and_5 (and_5_out, d_ff_11_q, d_ff_13_q);
  Clock clk44 (.out(clk44_out));
  not not_17 (not_17_out, d_ff_10_q);
  D_Flip_Flop d_ff_10 (.clk(clk47_out), .D(xor_17_out), .Q(d_ff_10_q));  // open: Qn, preset, en, reset
  xnor xnor_5 (xnor_5_out, imux_12_out, xor_10_out);
  IMUX imux_12 (.b___in0(or_8_out), .c___in1(and_6_out), .out(imux_12_out), .sel(imux_9_out));
  or or_8 (or_8_out, not_29_out, imux_5_out);
  and and_6 (and_6_out, not_29_out, imux_5_out);
  IMUX imux_13 (.b___in0(imux_14_out), .c___in1(nand_7_out), .out(imux_13_out), .sel(sel1));
  IMUX imux_14 (.b___in0(buffer_1_out), .c___in1(and_7_out), .out(imux_14_out), .sel(not_40_out));
  xor xor_8 (xor_8_out, d_ff_11_q, d_ff_13_q);
  and and_7 (and_7_out, d_ff_11_q, not_18_out);
  not not_18 (not_18_out, d_ff_13_q);
  D_Flip_Flop d_ff_11 (.clk(clk44_out), .D(not_19_out), .Q(d_ff_11_q));  // open: Qn, preset, en, reset
  not not_19 (not_19_out, imux_15_out);
  IMUX imux_15 (.b___in0(_00_2), .c___in1(d_ff_11_q), .out(imux_15_out), .sel(sel1_2));
  nand nand_7 (nand_7_out, d_ff_10_q, d_ff_12_q);
  D_Flip_Flop d_ff_12 (.clk(clk47_out), .D(nand_19_out), .Q(d_ff_12_q));  // open: Qn, preset, en, reset
  xor xor_9 (xor_9_out, nand_8_out, xor_11_out);
  nand nand_8 (nand_8_out, nand_9_out, or_9_out);
  xor xor_10 (xor_10_out, not_31_out, imux_6_out);
  nand nand_9 (nand_9_out, not_31_out, imux_6_out);
  not not_20 (not_20_out, nand_10_out);
  nand nand_10 (nand_10_out, nand_11_out, d_ff_15_q);
  nand nand_11 (nand_11_out, d_ff_13_q, d_ff_14_q, d_ff_15_q);
  D_Flip_Flop d_ff_13 (.clk(clk44_out), .D(not_21_out), .Q(d_ff_13_q));  // open: Qn, preset, en, reset
  not not_21 (not_21_out, imux_16_out);
  IMUX imux_16 (.b___in0(_01_2), .c___in1(d_ff_16_q), .out(imux_16_out), .sel(sel1_2));
  or or_9 (or_9_out, imux_12_out, nor_4_out);
  xor xor_11 (xor_11_out, not_33_out, imux_8_out);
  nor nor_4 (nor_4_out, not_31_out, imux_6_out);
  not not_22 (not_22_out, n4_mux_9_out);
  IMUX imux_17 (.b___in0(nand_10_out), .c___in1(nand_13_out), .out(imux_17_out), .sel(not_39_out));
  _4_mux u_4_mux_9 (
    .out(n4_mux_9_out), .s1(xnor_10_out), ._3(or_12_out), ._2(nand_13_out), ._1(or_10_out), ._0(nand_10_out),
    .s0(not_39_out));
  or or_10 (or_10_out, xor_12_out, nor_5_out);
  xor xor_12 (xor_12_out, d_ff_13_q, xor_13_out);
  nor nor_5 (nor_5_out, d_ff_13_q, d_ff_14_q, d_ff_15_q);
  xor xor_13 (xor_13_out, d_ff_14_q, d_ff_15_q);
  D_Flip_Flop d_ff_14 (.clk(clk44_out), .D(not_23_out), .Q(d_ff_14_q));  // open: Qn, preset, en, reset
  not not_23 (not_23_out, imux_18_out);
  IMUX imux_18 (.b___in0(_02_2), .c___in1(d_ff_17_q), .out(imux_18_out), .sel(sel1_2));
  IMUX imux_19 (.b___in0(xnor_6_out), .c___in1(xor_14_out), .out(imux_19_out), .sel(nand_8_out));
  xnor xnor_6 (xnor_6_out, nand_12_out, xnor_7_out);
  xor xor_14 (xor_14_out, xnor_7_out, or_11_out);
  nand nand_12 (nand_12_out, not_33_out, imux_8_out);
  or or_11 (or_11_out, not_33_out, imux_8_out);
  xnor xnor_7 (xnor_7_out, not_35_out, imux_10_out);
  not not_24 (not_24_out, n4_mux_10_out);
  nand nand_13 (nand_13_out, nand_11_out, xor_12_out);
  or or_12 (or_12_out, nor_5_out, d_ff_15_q);
  D_Flip_Flop d_ff_15 (.clk(clk44_out), .D(not_25_out), .Q(d_ff_15_q));  // open: Qn, preset, en, reset
  not not_25 (not_25_out, imux_20_out);
  IMUX imux_20 (.b___in0(_03_2), .c___in1(d_ff_18_q), .out(imux_20_out), .sel(sel1_2));
  xor xor_15 (xor_15_out, xnor_8_out, imux_21_out);
  IMUX imux_21 (.b___in0(nand_14_out), .c___in1(or_15_out), .out(imux_21_out), .sel(xnor_7_out));
  nand nand_14 (nand_14_out, or_13_out, and_9_out);
  or or_13 (or_13_out, imux_12_out, nand_15_out);
  xnor xnor_8 (xnor_8_out, not_37_out, imux_11_out);
  nand nand_15 (nand_15_out, or_14_out, or_17_out);
  or or_14 (or_14_out, not_31_out, imux_6_out);
  _4_mux u_4_mux_10 (
    .out(n4_mux_10_out), .s1(xnor_10_out), ._3(or_12_out), ._2(nand_13_out), ._1(or_10_out),
    ._0(nand_10_out), .s0(xnor_10_out));
  D_Flip_Flop d_ff_16 (.clk(clk44_out), .D(not_26_out), .Q(d_ff_16_q));  // open: Qn, preset, en, reset
  not not_26 (not_26_out, imux_22_out);
  IMUX imux_22 (.b___in0(_03_2), .c___in1(d_ff_19_q), .out(imux_22_out), .sel(sel1_2));
  xor xor_16 (xor_16_out, nand_18_out, xor_18_out);
  and and_8 (and_8_out, not_38_out, imux_13_out);
  and and_9 (and_9_out, nand_12_out, or_16_out);
  nand nand_16 (nand_16_out, not_37_out, imux_11_out);
  or or_15 (or_15_out, imux_10_out, not_35_out);
  or or_16 (or_16_out, nand_17_out, nor_7_out);
  nand nand_17 (nand_17_out, not_31_out, imux_6_out);
  or or_17 (or_17_out, not_33_out, imux_8_out);
  not not_27 (not_27_out, n4_mux_11_out);
  _4_mux u_4_mux_11 (
    .out(n4_mux_11_out), .s1(not_40_out), ._3(or_12_out), ._2(nand_13_out), ._1(or_10_out), ._0(nand_10_out),
    .s0(xnor_10_out));
  D_Flip_Flop d_ff_17 (.clk(clk44_out), .D(not_28_out), .Q(d_ff_17_q));  // open: Qn, preset, en, reset
  not not_28 (not_28_out, imux_23_out);
  IMUX imux_23 (.b___in0(_04_2), .c___in1(d_ff_20_q), .out(imux_23_out), .sel(sel1_2));
  xor xor_17 (xor_17_out, nor_6_out, xnor_9_out);
  nor nor_6 (nor_6_out, and_8_out, and_10_out);
  and and_10 (and_10_out, nand_18_out, xor_18_out);
  xor xor_18 (xor_18_out, not_38_out, imux_13_out);
  nand nand_18 (nand_18_out, nand_16_out, or_18_out);
  or or_18 (or_18_out, imux_21_out, xnor_8_out);
  nor nor_7 (nor_7_out, not_33_out, imux_8_out);
  not not_29 (not_29_out, n4_mux_12_out);
  _4_mux u_4_mux_12 (
    .out(n4_mux_12_out), .s1(1'b0), ._3(or_12_out), ._2(nand_13_out), ._1(or_10_out), ._0(nand_10_out),
    .s0(not_40_out));
  D_Flip_Flop d_ff_18 (.clk(clk44_out), .D(not_30_out), .Q(d_ff_18_q));  // open: Qn, preset, en, reset
  not not_30 (not_30_out, imux_24_out);
  IMUX imux_24 (.b___in0(_05_2), .c___in1(d_ff_21_q), .out(imux_24_out), .sel(sel1_2));
  nand nand_19 (nand_19_out, not_20_out, not_40_out);
  xnor xnor_9 (xnor_9_out, imux_28_out, imux_13_out);
  not not_31 (not_31_out, n4_mux_13_out);
  _4_mux u_4_mux_13 (
    .out(n4_mux_13_out), .s1(not_41_out), ._3(or_12_out), ._2(nand_13_out), ._1(or_10_out), ._0(nand_10_out),
    .s0(1'b0));
  D_Flip_Flop d_ff_19 (.clk(clk44_out), .D(not_32_out), .Q(d_ff_19_q));  // open: Qn, preset, en, reset
  not not_32 (not_32_out, imux_25_out);
  IMUX imux_25 (.b___in0(_05_2), .c___in1(d_ff_13_q), .out(imux_25_out), .sel(sel1_2));
  not not_33 (not_33_out, n4_mux_14_out);
  _4_mux u_4_mux_14 (
    .out(n4_mux_14_out), .s1(nand_20_out), ._3(or_12_out), ._2(nand_13_out), ._1(or_10_out),
    ._0(nand_10_out), .s0(not_41_out));
  D_Flip_Flop d_ff_20 (.clk(clk44_out), .D(not_34_out), .Q(d_ff_20_q));  // open: Qn, preset, en, reset
  not not_34 (not_34_out, imux_26_out);
  IMUX imux_26 (.b___in0(_06_2), .c___in1(d_ff_14_q), .out(imux_26_out), .sel(sel1_2));
  not not_35 (not_35_out, n4_mux_15_out);
  _4_mux u_4_mux_15 (
    .out(n4_mux_15_out), .s1(in_21), ._3(or_12_out), ._2(nand_13_out), ._1(or_10_out), ._0(nand_10_out),
    .s0(nand_20_out));
  D_Flip_Flop d_ff_21 (.clk(clk44_out), .D(not_36_out), .Q(d_ff_21_q));  // open: Qn, preset, en, reset
  not not_36 (not_36_out, imux_27_out);
  IMUX imux_27 (.b___in0(_07_2), .c___in1(d_ff_15_q), .out(imux_27_out), .sel(sel1_2));
  not not_37 (not_37_out, n4_mux_16_out);
  _4_mux u_4_mux_16 (
    .out(n4_mux_16_out), .s1(1'b1), ._3(or_12_out), ._2(nand_13_out), ._1(or_10_out), ._0(nand_10_out),
    .s0(in_21));
  not not_38 (not_38_out, n4_mux_17_out);
  _4_mux u_4_mux_17 (
    .out(n4_mux_17_out), .s1(not_40_out), ._3(or_12_out), ._2(nand_13_out), ._1(or_10_out), ._0(nand_10_out),
    .s0(1'b1));
  IMUX imux_28 (.b___in0(nand_10_out), .c___in1(or_12_out), .out(imux_28_out), .sel(not_40_out));
  not not_39 (not_39_out, in_21);
  not not_40 (not_40_out, xnor_10_out);
  xnor xnor_10 (xnor_10_out, in_20, in_21);
  nand nand_20 (nand_20_out, in_21, not_41_out);
  not not_41 (not_41_out, in_20);
  nand nand_21 (nand_21_out, in_16, f11);
  and and_11 (and_11_out, not_43_out, not_42_out);
  not not_42 (not_42_out, f6);
  not not_43 (not_43_out, f5);
  nand nand_22 (c_start, nand_21_out, or_19_out);
  nand nand_23 (nand_23_out, and_11_out, and_12_out);
  and and_12 (and_12_out, nor_9_out, nor_8_out);
  nor nor_8 (nor_8_out, f7, f4);
  nor nor_9 (nor_9_out, f8, nthis_enables_yuv_to_rgb);
  or or_19 (or_19_out, nand_23_out, nand_24_out);
  nand nand_24 (nand_24_out, and_13_out, and_14_out);
  and and_13 (and_13_out, nor_11_out, nor_10_out);
  nor nor_10 (nor_10_out, f1, f0);
  nor nor_11 (nor_11_out, f3, f2);
  and and_14 (and_14_out, not_44_out, not_45_out);
  not not_44 (not_44_out, f9);
  not not_45 (not_45_out, f10);
  Clock clk45 (.out(clk45_out));
  Clock clk55 (.out(clk55_out));
  D_Flip_Flop d_ff_22 (.clk(clk55_out), .D(d_ff_23_q));  // open: Q, Qn, preset, en, reset
  Clock clk53 (.out(clk53_out));
  D_Flip_Flop d_ff_23 (.clk(clk53_out), .D(d_ff_24_q), .Q(d_ff_23_q));  // open: Qn, preset, en, reset
  Clock clk51 (.out(clk51_out));
  D_Flip_Flop d_ff_24 (.clk(clk51_out), .D(_00), .Q(d_ff_24_q));  // open: Qn, preset, en, reset
  Clock clk47_2 (.out(clk47_2_out));
  and and_15 (and_15_out, 1'b1, not_47_out);
  _4_mux u_4_mux_18 ();  // open: out, s1, _3, _2, _1, _0, s0
  D_Flip_Flop d_ff_25 (.clk(clk55_out), .D(d_ff_26_q));  // open: Q, Qn, preset, en, reset
  D_Flip_Flop d_ff_26 (.clk(clk53_out), .D(d_ff_27_q), .Q(d_ff_26_q));  // open: Qn, preset, en, reset
  D_Flip_Flop d_ff_27 (.clk(clk51_out), .D(_01), .Q(d_ff_27_q));  // open: Qn, preset, en, reset
  // Probe on not_46_out
  not not_46 (not_46_out, dffr_logic_1_out_4);
  DFFR_logic dffr_logic_1 (.clk(clk47_2_out), .in(or_20_out), .nres(in_1), .out_4(dffr_logic_1_out_4));
  or or_20 (or_20_out, and_15_out, and_16_out);
  and and_16 (and_16_out, not_48_out, dffr_logic_1_out_4);
  and and_17 (and_17_out, dffr_logic_1_out_4, not_53_out);
  not not_47 (not_47_out, dffr_logic_1_out_4);
  not not_48 (not_48_out, 1'b1);
  nand nand_25 (nand_25_out, in_18, dffr_logic_19_out_4);
  and and_18 (and_18_out, not_50_out, not_49_out);
  not not_49 (not_49_out, dffr_logic_14_out_4);
  not not_50 (not_50_out, dffr_logic_13_out_4);
  _4_mux u_4_mux_19 ();  // open: out, s1, _3, _2, _1, _0, s0
  D_Flip_Flop d_ff_28 (.clk(clk55_out), .D(d_ff_29_q));  // open: Q, Qn, preset, en, reset
  D_Flip_Flop d_ff_29 (.clk(clk53_out), .D(d_ff_30_q), .Q(d_ff_29_q));  // open: Qn, preset, en, reset
  D_Flip_Flop d_ff_30 (.clk(clk51_out), .D(_02), .Q(d_ff_30_q));  // open: Qn, preset, en, reset
  // Probe on not_51_out
  not not_51 (not_51_out, dffr_logic_2_out_4);
  DFFR_logic dffr_logic_2 (.clk(clk47_2_out), .in(or_21_out), .nres(in_1), .out_4(dffr_logic_2_out_4));
  or or_21 (or_21_out, and_17_out, and_20_out);
  and and_19 (and_19_out, and_21_out, not_54_out);
  and and_20 (and_20_out, not_52_out, dffr_logic_2_out_4);
  not not_52 (not_52_out, dffr_logic_1_out_4);
  not not_53 (not_53_out, dffr_logic_2_out_4);
  and and_21 (and_21_out, dffr_logic_2_out_4, dffr_logic_1_out_4);
  nand nand_26 (nand_26_out, nand_25_out, or_23_out);
  nand nand_27 (nand_27_out, and_18_out, and_22_out);
  and and_22 (and_22_out, nor_13_out, nor_12_out);
  nor nor_12 (nor_12_out, dffr_logic_10_out_4, dffr_logic_11_out_4);
  nor nor_13 (nor_13_out, dffr_logic_6_out_4, dffr_logic_8_out_4);
  _4_mux u_4_mux_20 ();  // open: out, s1, _3, _2, _1, _0, s0
  D_Flip_Flop d_ff_31 (.clk(clk55_out), .D(d_ff_32_q));  // open: Q, Qn, preset, en, reset
  D_Flip_Flop d_ff_32 (.clk(clk53_out), .D(d_ff_33_q), .Q(d_ff_32_q));  // open: Qn, preset, en, reset
  D_Flip_Flop d_ff_33 (.clk(clk51_out), .D(_03), .Q(d_ff_33_q));  // open: Qn, preset, en, reset
  DFFR_logic dffr_logic_3 (.clk(clk47_2_out), .in(or_22_out), .nres(in_1), .out_4(dffr_logic_3_out_4));
  or or_22 (or_22_out, and_19_out, and_24_out);
  and and_23 (and_23_out, and_25_out, not_58_out);
  and and_24 (and_24_out, not_55_out, dffr_logic_3_out_4);
  not not_54 (not_54_out, dffr_logic_3_out_4);
  not not_55 (not_55_out, and_21_out);
  and and_25 (and_25_out, dffr_logic_3_out_4, and_21_out);
  or or_23 (or_23_out, nand_27_out, nand_28_out);
  nand nand_28 (nand_28_out, and_26_out, and_30_out);
  and and_26 (and_26_out, nor_14_out, nor_15_out);
  nor nor_14 (nor_14_out, dffr_logic_16_out_4, in_19);
  nor nor_15 (nor_15_out, dffr_logic_15_out_4, dffr_logic_12_out_4);
  _4_mux u_4_mux_21 ();  // open: out, s1, _3, _2, _1, _0, s0
  D_Flip_Flop d_ff_34 (.clk(clk55_out), .D(d_ff_35_q));  // open: Q, Qn, preset, en, reset
  D_Flip_Flop d_ff_35 (.clk(clk53_out), .D(d_ff_36_q), .Q(d_ff_35_q));  // open: Qn, preset, en, reset
  D_Flip_Flop d_ff_36 (.clk(clk51_out), .D(_04), .Q(d_ff_36_q));  // open: Qn, preset, en, reset
  // Probe on not_56_out
  not not_56 (not_56_out, dffr_logic_4_out_4);
  DFFR_logic dffr_logic_4 (.clk(clk47_2_out), .in(or_24_out), .nres(in_1), .out_4(dffr_logic_4_out_4));
  or or_24 (or_24_out, and_23_out, and_27_out);
  and and_27 (and_27_out, not_57_out, dffr_logic_4_out_4);
  and and_28 (and_28_out, and_29_out, not_62_out);
  not not_57 (not_57_out, and_25_out);
  not not_58 (not_58_out, dffr_logic_4_out_4);
  and and_29 (and_29_out, dffr_logic_4_out_4, and_25_out);
  and and_30 (and_30_out, not_59_out, not_60_out);
  not not_59 (not_59_out, dffr_logic_17_out_4);
  not not_60 (not_60_out, dffr_logic_18_out_4);
  nor nor_16 (nor_16_out, dffr_logic_11_out_4, dffr_logic_12_out_4);
  _4_mux u_4_mux_22 ();  // open: out, s1, _3, _2, _1, _0, s0
  D_Flip_Flop d_ff_37 (.clk(clk55_out), .D(d_ff_38_q));  // open: Q, Qn, preset, en, reset
  D_Flip_Flop d_ff_38 (.clk(clk53_out), .D(d_ff_39_q), .Q(d_ff_38_q));  // open: Qn, preset, en, reset
  D_Flip_Flop d_ff_39 (.clk(clk51_out), .D(_05), .Q(d_ff_39_q));  // open: Qn, preset, en, reset
  // Probe on not_61_out
  not not_61 (not_61_out, dffr_logic_5_out_4);
  DFFR_logic dffr_logic_5 (.clk(clk47_2_out), .in(or_25_out), .nres(in_1), .out_4(dffr_logic_5_out_4));
  or or_25 (or_25_out, and_28_out, and_31_out);
  and and_31 (and_31_out, not_63_out, dffr_logic_5_out_4);
  and and_32 (and_32_out, and_33_out, not_68_out);
  not not_62 (not_62_out, dffr_logic_5_out_4);
  not not_63 (not_63_out, and_29_out);
  and and_33 (and_33_out, dffr_logic_5_out_4, and_29_out);
  D_Flip_Flop d_ff_40 (.clk(clk45_out));  // open: D, Q, Qn, preset, en, reset
  nand nand_29 (nand_29_out, and_35_out, and_34_out, not_70_out);
  and and_34 (and_34_out, not_65_out, not_66_out);
  and and_35 (and_35_out, nor_16_out, not_64_out);
  not not_64 (not_64_out, dffr_logic_19_out_4);
  not not_65 (not_65_out, dffr_logic_17_out_4);
  not not_66 (not_66_out, dffr_logic_18_out_4);
  DFFR_logic dffr_logic_6 (.clk(clk45_out), .in(nand_26_out), .nres(in_3), .out_4(dffr_logic_6_out_4));
  _4_mux u_4_mux_23 ();  // open: out, s1, _3, _2, _1, _0, s0
  D_Flip_Flop d_ff_41 (.clk(clk55_out), .D(d_ff_42_q));  // open: Q, Qn, preset, en, reset
  D_Flip_Flop d_ff_42 (.clk(clk53_out), .D(d_ff_43_q), .Q(d_ff_42_q));  // open: Qn, preset, en, reset
  D_Flip_Flop d_ff_43 (.clk(clk51_out), .D(_06), .Q(d_ff_43_q));  // open: Qn, preset, en, reset
  // Probe on not_67_out
  not not_67 (not_67_out, dffr_logic_7_out_4);
  DFFR_logic dffr_logic_7 (.clk(clk47_2_out), .in(or_26_out), .nres(in_1), .out_4(dffr_logic_7_out_4));
  or or_26 (or_26_out, and_32_out, and_37_out);
  and and_36 (and_36_out, and_38_out, not_74_out);
  and and_37 (and_37_out, not_69_out, dffr_logic_7_out_4);
  not not_68 (not_68_out, dffr_logic_7_out_4);
  not not_69 (not_69_out, and_33_out);
  and and_38 (and_38_out, dffr_logic_7_out_4, and_33_out);
  D_Flip_Flop d_ff_44 (.clk(clk45_out), .D(nand_29_out), .Q(d_ff_44_q));  // open: Qn, preset, en, reset
  nand nand_30 (nand_30_out, not_70_out, and_34_out, and_39_out);
  and and_39 (and_39_out, nor_17_out, not_71_out);
  not not_70 (not_70_out, dffr_logic_13_out_4);
  nor nor_17 (nor_17_out, dffr_logic_15_out_4, dffr_logic_16_out_4);
  not not_71 (not_71_out, dffr_logic_19_out_4);
  DFFR_logic dffr_logic_8 (.clk(clk45_out), .in(dffr_logic_6_out_4), .nres(in_3), .out_4(dffr_logic_8_out_4));
  D_Flip_Flop d_ff_45 (.clk(clk55_out), .D(d_ff_46_q));  // open: Q, Qn, preset, en, reset
  D_Flip_Flop d_ff_46 (.clk(clk53_out), .D(d_ff_47_q), .Q(d_ff_46_q));  // open: Qn, preset, en, reset
  D_Flip_Flop d_ff_47 (.clk(clk51_out), .D(_07), .Q(d_ff_47_q));  // open: Qn, preset, en, reset
  // Probe on not_72_out
  not not_72 (not_72_out, dffr_logic_9_out_4);
  DFFR_logic dffr_logic_9 (.clk(clk47_2_out), .in(or_27_out), .nres(in_1), .out_4(dffr_logic_9_out_4));
  or or_27 (or_27_out, and_36_out, and_40_out);
  and and_40 (and_40_out, not_73_out, dffr_logic_9_out_4);
  not not_73 (not_73_out, and_38_out);
  not not_74 (not_74_out, dffr_logic_9_out_4);
  D_Flip_Flop d_ff_48 (.clk(clk45_out), .D(nand_30_out), .Q(d_ff_48_q));  // open: Qn, preset, en, reset
  DFFR_logic dffr_logic_10 (.clk(clk45_out), .in(dffr_logic_8_out_4), .nres(in_3), .out_4(dffr_logic_10_out_4));
  _4_mux u_4_mux_24 ();  // open: out, s1, _3, _2, _1, _0, s0
  Clock clk56 (.out(clk56_out));
  Clock clk54 (.out(clk54_out));
  Clock clk52 (.out(clk52_out));
  D_Flip_Flop d_ff_49 (.clk(clk45_out));  // open: D, Q, Qn, preset, en, reset
  DFFR_logic dffr_logic_11 (.clk(clk45_out), .in(dffr_logic_10_out_4), .nres(in_3), .out_4(dffr_logic_11_out_4));
  _4_mux u_4_mux_25 ();  // open: out, s1, _3, _2, _1, _0, s0
  D_Flip_Flop d_ff_50 (.clk(clk56_out), .D(d_ff_51_q));  // open: Q, Qn, preset, en, reset
  D_Flip_Flop d_ff_51 (.clk(clk54_out), .D(d_ff_52_q), .Q(d_ff_51_q));  // open: Qn, preset, en, reset
  D_Flip_Flop d_ff_52 (.clk(clk52_out), .D(_00), .Q(d_ff_52_q));  // open: Qn, preset, en, reset
  D_Flip_Flop d_ff_53 (.clk(clk45_out));  // open: D, Q, Qn, preset, en, reset
  DFFR_logic dffr_logic_12 (.clk(clk45_out), .in(dffr_logic_11_out_4), .nres(in_3), .out_4(dffr_logic_12_out_4));
  _4_mux u_4_mux_26 ();  // open: out, s1, _3, _2, _1, _0, s0
  D_Flip_Flop d_ff_54 (.clk(clk56_out), .D(d_ff_55_q));  // open: Q, Qn, preset, en, reset
  D_Flip_Flop d_ff_55 (.clk(clk54_out), .D(d_ff_56_q), .Q(d_ff_55_q));  // open: Qn, preset, en, reset
  D_Flip_Flop d_ff_56 (.clk(clk52_out), .D(_01), .Q(d_ff_56_q));  // open: Qn, preset, en, reset
  D_Flip_Flop d_ff_57 (.clk(clk45_out));  // open: D, Q, Qn, preset, en, reset
  DFFR_logic dffr_logic_13 (.clk(clk45_out), .in(dffr_logic_12_out_4), .nres(in_3), .out_4(dffr_logic_13_out_4));
  _4_mux u_4_mux_27 ();  // open: out, s1, _3, _2, _1, _0, s0
  D_Flip_Flop d_ff_58 (.clk(clk56_out), .D(d_ff_60_q));  // open: Q, Qn, preset, en, reset
  D_Flip_Flop d_ff_59 (.clk(clk56_out), .D(d_ff_61_q));  // open: Q, Qn, preset, en, reset
  D_Flip_Flop d_ff_60 (.clk(clk54_out), .D(d_ff_62_q), .Q(d_ff_60_q));  // open: Qn, preset, en, reset
  D_Flip_Flop d_ff_61 (.clk(clk54_out), .D(d_ff_63_q), .Q(d_ff_61_q));  // open: Qn, preset, en, reset
  D_Flip_Flop d_ff_62 (.clk(clk52_out), .D(_03), .Q(d_ff_62_q));  // open: Qn, preset, en, reset
  D_Flip_Flop d_ff_63 (.clk(clk52_out), .D(_02), .Q(d_ff_63_q));  // open: Qn, preset, en, reset
  DFFR_logic dffr_logic_14 (.clk(clk45_out), .in(dffr_logic_13_out_4), .nres(in_3), .out_4(dffr_logic_14_out_4));
  _4_mux u_4_mux_28 ();  // open: out, s1, _3, _2, _1, _0, s0
  D_Flip_Flop d_ff_64 (.clk(clk56_out), .D(d_ff_65_q));  // open: Q, Qn, preset, en, reset
  D_Flip_Flop d_ff_65 (.clk(clk54_out), .D(d_ff_66_q), .Q(d_ff_65_q));  // open: Qn, preset, en, reset
  D_Flip_Flop d_ff_66 (.clk(clk52_out), .D(_04), .Q(d_ff_66_q));  // open: Qn, preset, en, reset
  DFFR_logic dffr_logic_15 (.clk(clk45_out), .in(dffr_logic_14_out_4), .nres(in_3), .out_4(dffr_logic_15_out_4));
  _4_mux u_4_mux_29 ();  // open: out, s1, _3, _2, _1, _0, s0
  D_Flip_Flop d_ff_67 (.clk(clk56_out), .D(d_ff_68_q));  // open: Q, Qn, preset, en, reset
  D_Flip_Flop d_ff_68 (.clk(clk54_out), .D(d_ff_69_q), .Q(d_ff_68_q));  // open: Qn, preset, en, reset
  D_Flip_Flop d_ff_69 (.clk(clk52_out), .D(_05), .Q(d_ff_69_q));  // open: Qn, preset, en, reset
  DFFR_logic dffr_logic_16 (.clk(clk45_out), .in(dffr_logic_15_out_4), .nres(in_3), .out_4(dffr_logic_16_out_4));
  D_Flip_Flop d_ff_70 (.clk(clk56_out), .D(d_ff_71_q));  // open: Q, Qn, preset, en, reset
  D_Flip_Flop d_ff_71 (.clk(clk54_out), .D(d_ff_72_q), .Q(d_ff_71_q));  // open: Qn, preset, en, reset
  D_Flip_Flop d_ff_72 (.clk(clk52_out), .D(_06), .Q(d_ff_72_q));  // open: Qn, preset, en, reset
  DFFR_logic dffr_logic_17 (.clk(clk45_out), .in(dffr_logic_16_out_4), .nres(in_3), .out_4(dffr_logic_17_out_4));
  D_Flip_Flop d_ff_73 (.clk(clk56_out), .D(d_ff_74_q));  // open: Q, Qn, preset, en, reset
  D_Flip_Flop d_ff_74 (.clk(clk54_out), .D(d_ff_75_q), .Q(d_ff_74_q));  // open: Qn, preset, en, reset
  D_Flip_Flop d_ff_75 (.clk(clk52_out), .D(_07), .Q(d_ff_75_q));  // open: Qn, preset, en, reset
  DFFR_logic dffr_logic_18 (.clk(clk45_out), .in(dffr_logic_17_out_4), .nres(in_3), .out_4(dffr_logic_18_out_4));
  DFFR_logic dffr_logic_19 (.clk(clk45_out), .in(dffr_logic_18_out_4), .nres(in_3), .out_4(dffr_logic_19_out_4));
  DFFR_logic dffr_logic_20 (.clk(clk45_out), .in(dffr_logic_19_out_4), .nres(in_3), .out_4(dffr_logic_20_out_4));
  DFFR_logic dffr_logic_21 (.clk(clk45_out), .in(dffr_logic_20_out_4), .nres(in_3), .out_4(dffr_logic_21_out_4));
  DFFR_logic dffr_logic_22 (.clk(clk45_out), .in(dffr_logic_21_out_4), .nres(in_3), .out_4(dffr_logic_22_out_4));
  DFFR_logic dffr_logic_23 (.clk(clk45_out), .in(dffr_logic_22_out_4), .nres(in_3), .out_4(dffr_logic_23_out_4));

  assign _08 = _00_2;
  assign _09 = _01_2;
  assign _10 = _02_2;
  assign _11 = _03_2;
  assign _12 = _04_2;
  assign _13 = _05_2;
  assign _14 = _06_2;
  assign _15 = _07_2;

  // Notes on the sheet:
  //   _14: pull=up
  //   _10: pull=up
  //   _12: pull=up
  //   _08: pull=up
  //   _13: pull=up
  //   _15: pull=up
  //   _11: pull=up
  //   _09: pull=up
  //   Unit20 output
  //   IDCT output
endmodule

module MDEC (
  input  nres,
  input  c8,
  input  lum_col,
  input  nres_2,
  input  c9,
  input  d1,
  input  data_from_address,
  input  com_dec_block_s,
  input  c5,
  input  c4,
  input  c2,
  input  stages_empty,
  input  c3,
  input  c3_2,
  input  c1,
  input  c2_2,
  input  c9_2,
  input  c4_2,
  input  c5_2,
  input  d5,
  input  dir,
  input  d2,
  input  com_busy,
  input  RLE_data_ended,
  input  com_dec_block_s_2,
  input  c9_3,
  input  com_dec_block_s_3,
  input  d6,
  input  load_data_exist,
  input  address_checker_1,
  input  mdec_data_load_command,
  input  RLE_data_ended_2,
  input  rle_finished,
  input  load_data_exist_2,
  input  dir_2,
  input  c9_4,
  input  dir_3,
  input  d4,
  input  d1_2,
  input  load_finished,
  input  d10,
  input  d5_2,
  input  dff4773,
  input  load_finished_2,
  input  load_finished_3,
  input  c9_5,
  input  d4_2,
  input  d1_3,
  input  c1_2,
  input  rf1,
  input  rf0,
  input  load_data_exist_3,
  input  dir_4,
  input  load_data_exist_4,
  input  RLE_data_ended_3,
  input  IDCT_cnt2_1fe,
  input  load_finished_4,
  input  rf1_2,
  input  rf0_2,
  input  d1_4,
  input  c5_3,
  input  dir_5,
  input  d4_3,
  input  rf1_3,
  input  rf0_3,
  input  d1_5,
  input  c1_3,
  input  c2_3,
  input  c3_3,
  input  c4_3,
  input  rle_finished_2,
  input  data_from_address_2,
  input  rle_finished_3,
  input  rle_finished_4,
  input  IDCT_cnt2_1fe_2,
  input  com_dec_block_s_4,
  input  load_finished_5,
  input  IDCT_cnt2_1fe_3,
  input  RLE_data_ended_4,
  input  RLE_data_ended_5,
  input  dir_6,
  input  d4_4,
  input  d1_6,
  input  c1_4,
  input  d4_5,
  input  load_data_exist_5,
  input  load_data_exist_6,
  input  rf1_4,
  input  rf0_4,
  input  d1_7,
  input  c1_5,
  input  c2_4,
  input  load_finished_6,
  input  rle_finished_5,
  input  IDCT_cnt2_1fe_4,
  input  load_data_exist_7,
  input  nres_3,
  input  in_98,
  input  sod_sel,
  input  com2_2,
  input  nres10,
  input  res,
  input  dir_7,
  input  load_quant,
  input  d4_6,
  input  i0,
  input  i1,
  input  i2,
  input  i3,
  input  i4,
  input  rf1_5,
  input  rf0_5,
  input  com2_s,
  input  nres_4,
  input  com1_s,
  input  rle_finished_6,
  input  o0,
  input  o1,
  input  o2,
  input  o3,
  input  o4,
  input  com0_s,
  input  com_busy_2,
  input  unit04_oe1,
  input  IDCT_cnt2_1fe_5,
  input  mdec_data_load_command_2,
  input  in_127,
  input  in_128,
  input  in_129,
  input  in_130,
  input  in_131,
  input  in_132,
  input  in_133,
  input  in_134,
  input  in_135,
  input  in_136,
  input  in_137,
  input  in_138,
  input  in_139,
  input  in_140,
  input  in_141,
  input  in_142,
  input  rle_finished_7,
  input  IDCT_cnt2_1fe_6,
  input  command0,
  input  command1,
  input  command2,
  input  in_148,
  input  u6,
  input  vwr,
  input  com2_1,
  input  _5388,
  input  _5071,
  input  in_154,
  input  in_155,
  input  in_156,
  input  in_157,
  input  in_158,
  input  u9___cnt2_0x3f_not_ovfl,
  input  ctrl0,
  input  yuv_res_0x7,
  input  c6,
  input  rle_finished_8,
  input  res_2,
  input  res_3,
  input  res_4,
  input  in_167,
  input  in_168,
  input  in_169,
  input  com100,
  input  do1,
  input  rle_finished_9,
  input  nres_5,
  input  yuv_res_8,
  input  h2,
  input  nout_res_8,
  input  in_177,
  input  in_178,
  input  in_179,
  output rle_finished_10,
  output dir_8,
  output c8_2,
  output unit00_a0,
  output unit00_a1,
  output unit00_a2,
  output unit00_a3,
  output unit00_a4,
  output nres_6,
  output nload_finished,
  output _0,
  output _1,
  output _2,
  output _3,
  output _4,
  output unit00_ie,
  output address_checker_1_2,
  output out_197,
  output out_198,
  output out_199,
  output unit04_ie2,
  output clk60,
  output sod_sel_2,
  output clk62,
  output nres10_2,
  output clk61,
  output unit04_ie1,
  output load_quant__32_item,
  output unk,
  output clk66,
  output clk63,
  output clk64,
  output clk12,
  output g12_to_unit0_addr_sel_S1,
  output g11_to_unit0_addr_sel_S0,
  output g4,
  output g8___enable_cnt2,
  output g10,
  output g8___enable_cnt2_2,
  output g7,
  output g6,
  output g5,
  output g9,
  output g3,
  output g2_on_g1,
  output g1___enable_cnt0,
  output ncnt0_run,
  output ncnt2_run,
  output ctrl4,
  output curb0,
  output curb1,
  output curb2,
  output out_232,
  output h8,
  output h9,
  output h10,
  output clk13,
  output h2_2
);

  wire _3683_out, _3765_out, _3870_out, _3945_out, _3973_out, _3987_out, _3990_out, _4047_out, _4051_out,
       _4064_out, _4066_out, _4070_out, _4071_out_4, _4089_out, _4177_out, _4188_out, _4189_out, _4190_out,
       _4191_out, _4194_out_4, _4278_out, _4279_out, _4281_out, _4284_out, _4290_out, _4291_2_out,
       _4291_out_4, _4376_out, _4377_out, _4378_out, _4379_out, _4380_out, _4381_out, _4483_out, _4484_out,
       _4485_out, _4486_out, _4487_out, _4488_out, _4489_out, _4491_out, _4493_out, _4575_out, _4577_out,
       _4580_out, _4585_2_out, _4585_out, _4589_out, _4593_q, _4595_out, _4598_out, _4599_out, _4683_out,
       _4684_out, _4685_out, _4687_out, _4688_out, _4689_out, _4691_out, _4695_out_4, _4746_out, _4747_out,
       _4748_out, _4749_out, _4751_2_out, _4751_out, _4752_out, _4753_out, _4754_out, _4755_out, _4756_out,
       _4758_out, _4759_out, _4760_out, _4761_out, _4775_q, _4776_out, _4777_out, _4785_out, _4786_out,
       _4787_out, _4788_out, _4789_out, _4790_out, _4791_out, _4845_out, _4846_2_out, _4846_out, _4848_2_out,
       _4848_out, _4850_2_out, _4850_out, _4851_2_out, _4851_out, _4852_out, _4853_out, _4854_out, _4855_out,
       _4856_out, _4858_out, _4867_out_4, _4875_out, _4880_out, _4881_out, _4883_out, _4884_out, _4891_2_out,
       _4891_out, _4892_q, _4954_out, _4956_out, _4957_out, _4961_out, _4963_out, _5071_out, _5074_out,
       _5167_out, _5172_out, _5193_2_q, _5193_q, _5388_out, _40667_out, _44101_out, _44108_q, _44111_q,
       _45101_out, _45104_out, _45105_out, _45106_out, _46100_out, _46106_out, _46107_q, _46110_out,
       _46113_out, _46114_out, _46115_out, _46116_out, _46117_out, _46118_out, _46119_q, _49101_2_q,
       _49101_3_q, _49101_4_q, _49101_q, _52101_2_q, _53115_out, and_1_out, and_2_out, and_3_out, and_4_out,
       and_5_out, and_6_out, and_7_out, and_8_out, and_9_out, and_10_out, and_11_out, and_12_out, and_13_out,
       and_14_out, and_15_out, and_16_out, and_17_out, and_18_out, and_19_out, and_20_out, and_21_out,
       and_22_out, and_23_out, and_24_out, and_25_out, and_26_out, and_27_out, and_28_out, and_29_out,
       and_30_out, and_31_out, and_32_out, and_33_out, and_34_out, and_35_out, and_36_out, and_37_out,
       and_38_out, and_39_out, and_40_out, and_42_out, and_43_out, clock_1_out, clock_2_out, clock_3_out,
       clock_4_out, clock_5_out, d_ff_2_q, d_ff_3_q, dffr_logic_1_out_4, dffr_logic_2_out_4,
       dffr_logic_3_out_4, dffr_logic_4_out_4, dffr_logic_5_out_4, dffr_logic_6_out_4, dffr_logic_7_out_4,
       dffr_logic_8_out_4, dffr_logic_9_out_4, dffr_logic_10_out_4, dffr_logic_11_out_4, dffr_logic_12_out_4,
       dffr_logic_13_out_4, dffr_logic_14_out_4, dffr_logic_15_out_4, dffr_logic_16_out_4, fa_1_out1___cout,
       fa_1_out2___sum, fa_2_out1___cout, fa_2_out2___sum, fa_3_out2___sum, fa_4_out1___cout,
       fa_4_out2___sum, fa_5_out1___cout, fa_5_out2___sum, fa_6_out2___sum, fa_7_out1___cout,
       fa_7_out2___sum, fa_8_out1___cout, fa_8_out2___sum, fa_9_out2___sum, fa_10_out1___cout,
       fa_10_out2___sum, fa_11_out2___sum, fa_12_out1___cout, fa_12_out2___sum, fa_13_out1___cout,
       fa_13_out2___sum, fa_14_out1___cout, fa_14_out2___sum, fa_15_out2___sum, fa_16_out2___sum, imux_1_out,
       imux_2_out, imux_3_out, imux_4_out, imux_5_out, imux_6_out, imux_7_out, imux_8_out, imux_9_out,
       imux_10_out, imux_11_out, imux_12_out, imux_13_out, imux_14_out, imux_15_out, imux_16_out,
       imux_17_out, imux_18_out, imux_19_out, imux_20_out, imux_21_out, imux_22_out, imux_23_out,
       imux_24_out, imux_25_out, imux_26_out, imux_27_out, imux_28_out, mclk_2_out, mclk_3_out, mclk_4_out,
       mclk_5_out, mclk_6_out, mclk_7_out, mclk_8_out, mclk_out, multiplexer_1_out, multiplexer_2_out,
       multiplexer_3_out, multiplexer_4_out, multiplexer_5_out, multiplexer_6_out, multiplexer_7_out,
       multiplexer_8_out, n4_mux_1_out, n4_mux_2_out, n4_mux_3_out, n4_mux_4_out, n4_mux_5_out, nand_1_out,
       nand_2_out, nand_3_out, nand_4_out, nand_5_out, nand_6_out, nand_7_out, nand_8_out, nand_9_out,
       nand_10_out, nand_11_out, nand_12_out, nand_13_out, nand_14_out, nand_15_out, nand_16_out,
       nand_17_out, nand_19_out, nand_20_out, nand_21_out, nand_22_out, nand_23_out, nand_24_out,
       nand_25_out, nand_26_out, nand_27_out, nand_28_out, nand_29_out, nand_30_out, nand_31_out,
       nand_32_out, nand_33_out, nand_34_out, nand_35_out, nand_36_out, nand_37_out, nand_38_out,
       nand_39_out, nand_40_out, nand_41_out, nand_42_out, nand_43_out, nand_44_out, nand_45_out,
       nand_46_out, nand_47_out, nand_48_out, nand_49_out, nand_50_out, nand_51_out, nand_52_out,
       nand_53_out, nand_54_out, nand_55_out, nand_56_out, nand_57_out, nand_58_out, nand_59_out,
       nand_60_out, nand_61_out, nand_62_out, nand_63_out, nand_64_out, nand_65_out, nand_66_out,
       nand_67_out, nand_68_out, nand_69_out, nand_70_out, nand_71_out, nand_72_out, nand_73_out,
       nand_74_out, nand_75_out, nand_76_out, nand_77_out, nand_78_out, nand_79_out, nand_80_out,
       nand_81_out, nand_82_out, nand_83_out, nand_84_out, nand_85_out, nand_86_out, nand_87_out,
       nand_89_out, nand_90_out, nand_91_out, nand_92_out, nand_93_out, nand_94_out, nor_4_out, nor_5_out,
       nor_6_out, nor_7_out, nor_8_out, nor_9_out, nor_10_out, nor_11_out, nor_12_out, not_1_out, not_2_out,
       not_3_out, not_4_out, not_5_out, not_6_out, not_7_out, not_8_out, not_9_out, not_10_out, not_11_out,
       not_12_out, not_14_out, not_15_out, not_17_out, not_18_out, not_19_out, not_20_out, not_22_out,
       not_24_out, not_25_out, not_27_out, not_28_out, not_29_out, not_30_out, not_31_out, not_32_out,
       not_33_out, not_34_out, not_35_out, not_36_out, not_37_out, not_38_out, not_39_out, not_40_out,
       not_41_out, not_42_out, not_44_out, not_45_out, not_46_out, not_47_out, not_48_out, not_49_out,
       not_50_out, not_51_out, not_52_out, not_53_out, not_54_out, not_55_out, not_56_out, not_57_out,
       not_58_out, not_59_out, not_60_out, not_61_out, not_62_out, not_63_out, not_64_out, not_65_out,
       not_66_out, not_67_out, not_68_out, not_69_out, not_70_out, not_71_out, not_72_out, not_73_out,
       not_74_out, not_75_out, not_76_out, not_77_out, not_78_out, not_79_out, not_80_out, not_81_out,
       not_82_out, not_83_out, not_84_out, not_85_out, not_86_out, not_87_out, not_88_out, not_89_out,
       not_90_out, not_91_out, not_92_out, not_93_out, not_94_out, not_95_out, not_96_out, not_97_out,
       not_98_out, not_99_out, not_100_out, not_101_out, not_102_out, not_103_out, not_104_out, not_105_out,
       not_106_out, not_107_out, not_108_out, not_109_out, not_110_out, not_111_out, not_112_out,
       not_113_out, not_114_out, not_115_out, not_116_out, not_117_out, not_118_out, or_1_out, or_4_out,
       or_5_out, or_6_out, or_7_out, or_8_out, or_9_out, or_11_out, or_12_out, or_13_out, or_14_out,
       or_15_out, or_16_out, or_17_out, or_18_out, or_19_out, or_20_out, or_22_out, or_24_out, or_27_out,
       or_28_out, or_29_out, or_30_out, or_31_out, or_32_out, or_33_out, or_34_out, rle_1_ie1, rle_1_oe1,
       undriven, undriven_2, undriven_3, undriven_4, undriven_5, undriven_6, undriven_7, undriven_8,
       undriven_9, undriven_10, undriven_11, undriven_12, undriven_13, undriven_14, undriven_15, undriven_16,
       undriven_17, undriven_18, undriven_19, undriven_20, xnor_1_out, xnor_2_out, xnor_3_out, xnor_4_out,
       xnor_5_out, xor_1_out, xor_2_out, xor_3_out, xor_4_out, xor_5_out, xor_6_out, xor_7_out, xor_8_out,
       xor_9_out, xor_10_out, xor_11_out, xor_12_out, xor_13_out, xor_14_out, xor_15_out, xor_16_out,
       xor_17_out, xor_18_out, xor_19_out;
  wire [5:0] rle_1_address_for_decoded_data;
  wire [6:0] rle_1_address_for_rle_input;
  wire [6:6] rle_1_ie2;
  wire [11:0] rle_1_decoded_data;
  wire [15:0] ram_1_data;

  Clock mclk (.out(mclk_out));
  nand _4785 (_4785_out, RLE_data_ended_2, c9_4);
  nand nand_1 (nand_1_out, or_1_out, not_1_out);
  not not_1 (not_1_out, load_finished_3);
  or or_1 (or_1_out, load_data_exist_4, dir_3);
  Clock clock_1 (.out(clock_1_out));
  D_Flip_Flop _46107 (.clk(mclk_out), .D(_46106_out), .Q(_46107_q));  // open: Qn, preset, en, reset
  and _46106 (_46106_out, _4777_out, nres_2);
  nand _4777 (_4777_out, _4785_out, _4776_out);
  nand _4776 (_4776_out, not_2_out, and_1_out);
  not not_2 (not_2_out, nand_1_out);
  and and_1 (and_1_out, not_3_out, _46107_q);
  not not_3 (not_3_out, nand_2_out);
  nand nand_2 (nand_2_out, nand_3_out, not_4_out);
  nand nand_3 (nand_3_out, d4, rle_finished);
  not not_4 (not_4_out, d1_2);
  and _4746 (_4746_out, u6, _4845_out);
  IMUX _4845 (.b___in0(not_5_out), .c___in1(not_6_out), .out(_4845_out), .sel(g5));
  // Probe on _46107_q
  nand nand_4 (nand_4_out, rle_finished_6, and_3_out);
  D_Flip_Flop _4955 (.clk(clock_1_out), .D(_4746_out), .Q(g12_to_unit0_addr_sel_S1));  // open: Qn, preset, en, reset
  not not_5 (not_5_out, g12_to_unit0_addr_sel_S1);
  not not_6 (not_6_out, rle_finished_8);
  Clock mclk_2 (.out(mclk_2_out));
  nand _4883 (_4883_out, nand_6_out, nand_5_out);
  nand nand_5 (nand_5_out, not_8_out, and_4_out);
  nand nand_6 (nand_6_out, data_from_address_2, and_2_out);
  and and_2 (and_2_out, c9_5, rle_finished_3, not_7_out);
  not not_7 (not_7_out, RLE_data_ended_3);
  not not_8 (not_8_out, nand_7_out);
  nand nand_7 (nand_7_out, rf0, IDCT_cnt2_1fe);
  nand nand_8 (nand_8_out, d4_6, and_3_out);
  and and_3 (and_3_out, unit04_oe1, xnor_1_out);
  xnor xnor_1 (xnor_1_out, i0, o0);
  D_Flip_Flop _4955_2 (.clk(clock_1_out), .D(_4954_out), .Q(g11_to_unit0_addr_sel_S0));  // open: Qn, preset, en, reset
  and _4954 (_4954_out, u6, _4956_out);
  IMUX _4956 (.b___in0(g11_to_unit0_addr_sel_S0), .c___in1(_4852_out), .out(_4956_out), .sel(_4957_out));
  nand _4957 (_4957_out, _4851_2_out, not_9_out, g11_to_unit0_addr_sel_S0);
  and _4852 (_4852_out, _4755_out, _4761_out, _4853_out);
  not not_9 (not_9_out, g5);
  nor _4755 (_4755_out, g8___enable_cnt2_2, g6);
  D_Flip_Flop _4775 (.clk(mclk_out), .D(_4880_out), .Q(_4775_q));  // open: Qn, preset, en, reset
  and _4880 (_4880_out, _4881_out, nres_2);
  or _4881 (_4881_out, _4883_out, _4884_out);
  nand _4884 (_4884_out, nand_9_out, nand_10_out);
  nand nand_9 (nand_9_out, nand_11_out, c1_2);
  nand nand_10 (nand_10_out, nand_15_out, _4775_q);
  and and_4 (and_4_out, c1_2, not_10_out);
  not not_10 (not_10_out, nand_11_out);
  nand nand_11 (nand_11_out, nand_12_out, not_11_out);
  nand nand_12 (nand_12_out, d4_2, rle_finished_3);
  not not_11 (not_11_out, d1_3);
  or or_2 (address_checker_1_2, nand_4_out, nand_13_out);
  nand nand_13 (nand_13_out, and_5_out, and_6_out);
  and and_5 (and_5_out, xnor_2_out, xnor_3_out);
  xnor xnor_2 (xnor_2_out, i1, o1);
  xnor xnor_3 (xnor_3_out, i2, o2);
  nand _4961 (_4961_out, u6, imux_1_out);
  IMUX imux_1 (.b___in0(g4), .c___in1(not_15_out), .out(imux_1_out), .sel(g5));
  or or_3 (clk13, mclk_2_out, h2_2);
  D_Flip_Flop d_ff_1 (.clk(mclk_2_out), .D(nand_14_out), .Q(h2_2));  // open: Qn, preset, en, reset
  nand nand_14 (nand_14_out, multiplexer_1_out, nres_5);
  Multiplexer #(.enable("false")) multiplexer_1 (.in0(in_178), .in1(in_179), .out(multiplexer_1_out), .sel(in_177));
  // Probe on _4775_q
  nand nand_15 (nand_15_out, nand_17_out, nand_16_out);
  nand nand_16 (nand_16_out, rf0, d1_3);
  nand nand_17 (nand_17_out, not_12_out, or_4_out);
  or or_4 (or_4_out, rf1, rf0);
  not not_12 (not_12_out, IDCT_cnt2_1fe);
  not not_13 (unit00_a0, n4_mux_1_out);
  _4_mux u_4_mux_1 (
    .out(n4_mux_1_out), .s1(undriven), ._3(undriven_6), ._2(undriven_5), ._1(undriven_4), ._0(undriven_4),
    .s0(undriven_2));
  nand nand_18 (out_197, or_5_out, nand_20_out, not_14_out);
  not not_14 (not_14_out, rf0_5);
  or or_5 (or_5_out, nand_8_out, nand_19_out);
  nand nand_19 (nand_19_out, and_5_out, and_6_out);
  and and_6 (and_6_out, xnor_4_out, xnor_5_out);
  xnor xnor_4 (xnor_4_out, i3, o3);
  xnor xnor_5 (xnor_5_out, i4, o4);
  D_Flip_Flop _4962 (.clk(clock_1_out), .D(_4961_out), .Q(g4));  // open: Qn, preset, en, reset
  not not_15 (not_15_out, rle_finished_8);
  nand _4751 (_4751_out, undriven_3, g8___enable_cnt2);
  or or_6 (or_6_out, load_data_exist_7, dir_6);
  not not_16 (unit00_a1, n4_mux_2_out);
  _4_mux u_4_mux_2 (
    .out(n4_mux_2_out), .s1(undriven), ._3(undriven_10), ._2(undriven_9), ._0(undriven_7), .s0(undriven_7));  // open: _1
  nand nand_20 (nand_20_out, not_17_out, rf1_5);
  not not_17 (not_17_out, IDCT_cnt2_1fe_5);
  D_Flip_Flop _4847 (.clk(clock_1_out), .D(_4846_out), .Q(g8___enable_cnt2));  // open: Qn, preset, en, reset
  and _4846 (_4846_out, u6, _4848_out);
  nand _4848 (_4848_out, _4751_out, _4850_out, _4851_out);
  nand _4850 (_4850_out, g5, rle_finished_8);
  nand _4851 (_4851_out, rle_finished_8, undriven_8);
  and _46118 (_46118_out, _46114_out, nres_2);
  nand _46114 (_46114_out, _4891_out, _45101_out);
  nand _4891 (_4891_out, data_from_address, and_7_out);
  nand _45101 (_45101_out, and_8_out, not_18_out);
  not not_18 (not_18_out, c3_2);
  and and_7 (and_7_out, RLE_data_ended_5, rle_finished_4, c9_3);
  and and_8 (and_8_out, nand_22_out, and_9_out);
  and and_9 (and_9_out, not_19_out, c1_4);
  not not_19 (not_19_out, nand_21_out);
  nand nand_21 (nand_21_out, nand_23_out, not_22_out);
  nand nand_22 (nand_22_out, or_6_out, not_20_out);
  not not_20 (not_20_out, load_finished_6);
  nand nand_23 (nand_23_out, d4_4, rle_finished_4);
  not not_21 (unit00_a2, n4_mux_3_out);
  // Probe on _46119_q
  D_Flip_Flop _46119 (.clk(mclk_out), .D(_46118_out), .Q(_46119_q));  // open: Qn, preset, en, reset
  not not_22 (not_22_out, d1_6);
  _4_mux u_4_mux_3 (
    .out(n4_mux_3_out), .s1(undriven), ._3(undriven_13), ._2(undriven_12), ._1(undriven_11),
    ._0(undriven_11), .s0(undriven_2));
  not not_23 (unit00_a3, n4_mux_4_out);
  _4_mux u_4_mux_4 (
    .out(n4_mux_4_out), .s1(undriven), ._3(undriven_16), ._2(undriven_15), ._1(undriven_14),
    ._0(undriven_14), .s0(undriven_2));
  nand _4278 (_4278_out, u6, _4279_out);
  IMUX _4279 (.b___in0(g10), .c___in1(u9___cnt2_0x3f_not_ovfl), .out(_4279_out), .sel(g2_on_g1));
  and _45106 (_45106_out, _45105_out, nres_2);
  IMUX _45105 (.b___in0(_44111_q), .c___in1(_45104_out), .out(_45105_out), .sel(_46110_out));
  nand _45104 (_45104_out, not_25_out, not_24_out, _44111_q);
  nor _46110 (_46110_out, c1, c2_2, c9_2);
  not not_24 (not_24_out, c5_2);
  not not_25 (not_25_out, c4_2);
  not not_26 (unit00_a4, n4_mux_5_out);
  _4_mux u_4_mux_5 (
    .out(n4_mux_5_out), .s1(undriven), ._3(undriven_19), ._2(undriven_18), ._1(undriven_17),
    ._0(undriven_17), .s0(undriven_2));
  D_Flip_Flop _4175 (.clk(clock_1_out), .D(_4278_out), .Q(g10));  // open: Qn, preset, en, reset
  and _4846_2 (_4846_2_out, u6, _4848_2_out);
  nand _4751_2 (_4751_2_out, _4963_out, g8___enable_cnt2_2);
  // Probe on _44111_q
  D_Flip_Flop _44111 (.clk(mclk_out), .D(_45106_out), .Q(_44111_q));  // open: Qn, preset, en, reset
  D_Flip_Flop _4847_2 (.clk(clock_1_out), .D(_4846_2_out), .Q(g8___enable_cnt2_2));  // open: Qn, preset, en, reset
  nand _4848_2 (_4848_2_out, _4751_2_out, _4850_2_out, _4851_2_out);
  nand _4851_2 (_4851_2_out, rle_finished_8, _4858_out);
  nand _4850_2 (_4850_2_out, g5, rle_finished_8);
  nand _5074 (_5074_out, _4875_out, dff4773);
  and _4875 (_4875_out, not_27_out, d5_2);
  not not_27 (not_27_out, _46100_out);
  nand _46100 (_46100_out, load_finished, _4585_out);
  or _4585 (_4585_out, dir_8, load_data_exist_2);
  and _4856 (_4856_out, u6, _4855_out);
  nand _4855 (_4855_out, _4853_out, _4759_out);
  nand _4853 (_4853_out, _4858_out, not_29_out);
  nand _4759 (_4759_out, not_28_out, _4758_out);
  not not_28 (not_28_out, c6);
  not not_29 (not_29_out, rle_finished_8);
  and _4858 (_4858_out, not_30_out, g7);
  not not_30 (not_30_out, c6);
  D_Flip_Flop _5168 (.clk(mclk_out), .D(_5167_out), .Q(dir_8));  // open: Qn, preset, en, reset
  nand _5167 (_5167_out, nres_2, _5172_out);
  IMUX _5172 (.b___in0(multiplexer_2_out), .c___in1(_5074_out), .out(_5172_out), .sel(d5_2));
  Multiplexer multiplexer_2 (.in0(dir_8), .in1(not_31_out), .out(multiplexer_2_out), .sel(d10));  // open: en
  not not_31 (not_31_out, dff4773);
  Clock clock_2 (.out(clock_2_out));
  D_Flip_Flop _4857 (.clk(clock_1_out), .D(_4856_out), .Q(g7));  // open: Qn, preset, en, reset
  and _4683 (_4683_out, u6, _4684_out);
  nand _4760 (_4760_out, _4758_out, c6);
  and _4758 (_4758_out, not_32_out, g8___enable_cnt2_2);
  not not_32 (not_32_out, _4963_out);
  nand _4963 (_4963_out, in_167, in_168, not_33_out);
  not not_33 (not_33_out, rle_finished_8);
  nor nor_1 (unit04_ie1, clock_2_out, nand_25_out);
  D_Flip_Flop _4682 (.clk(clock_1_out), .D(_4683_out), .Q(g6));  // open: Qn, preset, en, reset
  nand _4684 (_4684_out, _4760_out, _4685_out);
  nand _4685 (_4685_out, ctrl0, g6);
  nand _4854 (_4854_out, g5, not_34_out);
  not not_34 (not_34_out, rle_finished_8);
  nand nand_24 (nand_24_out, com_dec_block_s_3, and_10_out);
  and and_10 (and_10_out, d5, not_35_out);
  not not_35 (not_35_out, or_7_out);
  or or_7 (or_7_out, dir, load_data_exist);
  nor nor_2 (unit04_ie2, clock_2_out, nand_25_out);
  nor nor_3 (unit00_ie, clock_2_out, or_8_out);
  nand nand_25 (nand_25_out, not_36_out, _44101_out);
  or or_8 (or_8_out, _44101_out, dir_7);
  not not_36 (not_36_out, dir_7);
  nand _44101 (_44101_out, com0_s, com1_s, not_37_out);
  not not_37 (not_37_out, com2_s);
  or _4752 (_4752_out, _4754_out, _4753_out);
  nand _4753 (_4753_out, u6, _4761_out);
  nand _4754 (_4754_out, _4854_out, _4756_out);
  nand _4756 (_4756_out, g6, not_38_out);
  nand _4761 (_4761_out, c6, g7);
  not not_38 (not_38_out, ctrl0);
  // Probe on d_ff_2_q
  D_Flip_Flop d_ff_2 (.clk(mclk_out), .D(nand_26_out), .Q(d_ff_2_q));  // open: Qn, preset, en, reset
  nand nand_26 (nand_26_out, nres_2, nand_24_out, imux_2_out);
  IMUX imux_2 (.b___in0(d_ff_2_q), .c___in1(nand_27_out), .out(imux_2_out), .sel(d2));
  nand nand_27 (nand_27_out, mdec_data_load_command, not_39_out);
  not not_39 (not_39_out, com_busy);
  D_Flip_Flop _4571 (.clk(clock_1_out), .D(_4752_out), .Q(g5));  // open: Qn, preset, en, reset
  or _3986 (clk60, clock_2_out, _3987_out);
  DFFR_logic _4071 (.clk(clock_2_out), .in(_4089_out), .nres(nres_4), .out_4(_4071_out_4));
  nor _4089 (_4089_out, _40667_out, _4070_out);
  nand _40667 (_40667_out, not_41_out, not_40_out);
  not not_40 (not_40_out, command1);
  not not_41 (not_41_out, command2);
  and and_11 (and_11_out, nand_28_out, nres_2);
  nand nand_28 (nand_28_out, nand_29_out, nand_30_out);
  nand nand_29 (nand_29_out, and_12_out, RLE_data_ended);
  nand nand_30 (nand_30_out, not_42_out, d_ff_3_q);
  not not_42 (not_42_out, stages_empty);
  and and_12 (and_12_out, address_checker_1, d6);
  or _3989 (clk61, clock_2_out, sod_sel_2);
  and _3987 (_3987_out, dir_7, _4071_out_4, sod_sel_2);
  not not_43 (sod_sel_2, _4291_out_4);
  DFFR_logic _4291 (.clk(clock_2_out), .in(not_44_out), .nres(nres_4), .out_4(_4291_out_4));
  not not_44 (not_44_out, _4589_out);
  nand _4589 (_4589_out, not_45_out, mdec_data_load_command_2);
  nand _4070 (_4070_out, command0, _4291_out_4);
  not not_45 (not_45_out, com_busy_2);
  and _4493 (_4493_out, u6, _4491_out);
  nand _4491 (_4491_out, _4489_out, _4580_out);
  nand _4489 (_4489_out, not_46_out, g9);
  nand _4580 (_4580_out, _4687_out, _4381_out);
  not not_46 (not_46_out, yuv_res_0x7);
  and _4381 (_4381_out, g1___enable_cnt0, not_48_out);
  and _4687 (_4687_out, not_47_out, c6);
  not not_47 (not_47_out, g8___enable_cnt2_2);
  RAM #(.addrWidth(7), .dataWidth(16), .bus("separate")) ram_1 (
    .addr(rle_1_address_for_rle_input), .data(ram_1_data), .ld(or_9_out));  // open: din, str, sel, clk, clr
  // Probe on d_ff_3_q
  D_Flip_Flop d_ff_3 (.clk(mclk_out), .D(and_11_out), .Q(d_ff_3_q));  // open: Qn, preset, en, reset
  or _4496 (clk62, clock_2_out, dir_7);
  D_Flip_Flop _4490 (.clk(clock_1_out), .D(_4493_out), .Q(g9));  // open: Qn, preset, en, reset
  and _4691 (_4691_out, u6, _4689_out);
  nand _4688 (_4688_out, _4381_out, not_49_out);
  not not_48 (not_48_out, _4376_out);
  or or_9 (or_9_out, rle_1_oe1, rle_1_address_for_rle_input[6]);
  DFFR_logic _4698 (.clk(clock_2_out), .in(_4585_2_out), .nres(nres_4), .out_4(nres10_2));
  or _4585_2 (_4585_2_out, nand_87_out, dir_7);
  D_Flip_Flop _4579 (.clk(clock_1_out), .D(_4691_out), .Q(g3));  // open: Qn, preset, en, reset
  nand _4689 (_4689_out, _4688_out, _4488_out);
  nand _4486 (_4486_out, u9___cnt2_0x3f_not_ovfl, g2_on_g1);
  not not_49 (not_49_out, _4687_out);
  nand _4488 (_4488_out, _4577_out, u9___cnt2_0x3f_not_ovfl);
  or or_10 (nload_finished, dir_7, nand_38_out, nor_4_out);
  or _4484 (_4484_out, _4485_out, _4483_out);
  nand _4483 (_4483_out, u6, _4487_out);
  nand _4485 (_4485_out, _4486_out, _4575_out);
  nand _4575 (_4575_out, g3, g4);
  nand _4487 (_4487_out, g9, yuv_res_0x7);
  D_Flip_Flop _4375 (.clk(clock_1_out), .D(_4484_out), .Q(g2_on_g1));  // open: Qn, preset, en, reset
  and _4284 (_4284_out, u6, _4379_out);
  nand _4378 (_4378_out, _4577_out, not_50_out);
  not not_50 (not_50_out, u9___cnt2_0x3f_not_ovfl);
  and _4577 (_4577_out, g3, not_51_out);
  not not_51 (not_51_out, g4);
  nand nand_31 (nand_31_out, d1, and_13_out);
  and and_13 (and_13_out, c2, not_55_out);
  nand nand_32 (nand_32_out, nand_33_out, nand_37_out);
  nand nand_33 (nand_33_out, not_52_out, or_11_out);
  or or_11 (or_11_out, rf1_2, rf0_2);
  not not_52 (not_52_out, IDCT_cnt2_1fe_2);
  DFFR_logic _4582 (.clk(clk62), .in(not_53_out), .nres(nres10), .out_4(_0));
  not not_53 (not_53_out, _0);
  D_Flip_Flop _4283 (.clk(clock_1_out), .D(_4284_out), .Q(g1___enable_cnt0));  // open: Qn, preset, en, reset
  nand _4379 (_4379_out, _4378_out, _4377_out, _4380_out);
  nand _4380 (_4380_out, _4376_out, g1___enable_cnt0);
  nand _4377 (_4377_out, g2_on_g1, not_54_out);
  not not_54 (not_54_out, u9___cnt2_0x3f_not_ovfl);
  nand _4376 (_4376_out, u9___cnt2_0x3f_not_ovfl, ctrl0);
  Clock mclk_3 (.out(mclk_3_out));
  // Probe on _4593_q
  D_Flip_Flop _4593 (.clk(mclk_out), .D(_4595_out), .Q(_4593_q));  // open: Qn, preset, en, reset
  nand _4595 (_4595_out, nand_31_out, nand_34_out, nres_2);
  nand nand_34 (nand_34_out, nand_35_out, _4593_q);
  nand nand_35 (nand_35_out, nand_36_out, com_dec_block_s);
  not not_55 (not_55_out, nand_32_out);
  nand nand_36 (nand_36_out, or_12_out, not_56_out);
  or or_12 (or_12_out, load_data_exist_3, dir_2);
  nand nand_37 (nand_37_out, rf0_2, d1_4);
  DFFR_logic _4495 (.clk(clk62), .in(xor_1_out), .nres(nres10), .out_4(_1));
  xor xor_1 (xor_1_out, _0, _1);
  and and_14 (and_14_out, _1, _0);
  nand _4177 (_4177_out, u6, _4281_out);
  xnor _4281 (_4281_out, _4379_out, ncnt0_run);
  not not_56 (not_56_out, load_finished_2);
  DFFR_logic _4285 (.clk(clk62), .in(xor_2_out), .nres(nres10), .out_4(_2));
  xor xor_2 (xor_2_out, and_14_out, _2);
  and and_15 (and_15_out, _2, and_14_out);
  nor nor_4 (nor_4_out, _4, not_58_out);
  D_Flip_Flop _4176 (.clk(clock_1_out), .D(_4177_out), .Q(ncnt0_run));  // open: Qn, preset, en, reset
  nand _4747 (_4747_out, u6, _4748_out);
  IMUX _4748 (.b___in0(ncnt2_run), .c___in1(_4749_out), .out(_4748_out), .sel(g8___enable_cnt2_2));
  // Probe on _44108_q
  nand _4598 (_4598_out, undriven_20, _4599_out, nres_2);
  nand _4599 (_4599_out, not_57_out, _44108_q);
  // NOT_Gate not_57 has open pins: in=open, out=not_57_out
  DFFR_logic _4584 (.clk(clk62), .in(xor_3_out), .nres(nres10), .out_4(_3));
  xor xor_3 (xor_3_out, and_15_out, _3);
  nor nor_5 (nor_5_out, nand_38_out, not_59_out);
  nand nand_38 (nand_38_out, _3, and_15_out);
  not not_58 (not_58_out, load_quant);
  D_Flip_Flop _4176_2 (.clk(clock_1_out), .D(_4747_out), .Q(ncnt2_run));  // open: Qn, preset, en, reset
  nand _4749 (_4749_out, _4963_out, ncnt2_run);
  RLE rle_1 (
    .ie1(rle_1_ie1), .ie2(rle_1_ie2[6]), .oe1(rle_1_oe1), .oe2(rle_1_address_for_rle_input[6]), .nres(nres),
    .c8(c8), .Decoded_data(rle_1_decoded_data), .Address_for_decoded_data(rle_1_address_for_decoded_data),
    .mclk(mclk_3_out), .RLE_input(ram_1_data), .Address_for_RLE_input(rle_1_address_for_rle_input[5:0]),
    .lum_col(lum_col), .rle_finished(rle_finished_10));  // open: lc_n0, nFE00, ac4_q_nfull, ac4_d_nfull, ch0_0, ch1_3, rle_data_ended, nc8__kill, in_2
  D_Flip_Flop _44108 (.clk(mclk_out), .D(_4598_out), .Q(_44108_q));  // open: Qn, preset, en, reset
  DFFR_logic _4286 (.clk(clk62), .in(xor_4_out), .nres(nres10), .out_4(_4));
  xor xor_4 (xor_4_out, nor_5_out, _4);
  not not_59 (not_59_out, load_quant);
  or or_13 (or_13_out, rle_1_ie1, rle_1_ie2[6]);
  nand nand_39 (nand_39_out, c5_3, not_60_out);
  not not_60 (not_60_out, nand_40_out);
  nand nand_40 (nand_40_out, not_61_out, nand_41_out);
  not not_61 (not_61_out, com_dec_block_s_4);
  nand nand_41 (nand_41_out, or_14_out, not_63_out);
  and and_16 (and_16_out, not_62_out, c1_3);
  or or_14 (or_14_out, load_data_exist_6, dir_5);
  not not_62 (not_62_out, nand_42_out);
  not not_63 (not_63_out, load_finished_5);
  nand nand_42 (nand_42_out, nand_43_out, not_64_out);
  nand nand_43 (nand_43_out, d4_3, rle_finished_2);
  not not_64 (not_64_out, d1_5);
  Clock clock_3 (.out(clock_3_out));
  Clock clock_4 (.out(clock_4_out));
  and _4791 (_4791_out, _4787_out, nres_2);
  nand _4787 (_4787_out, _46116_out, _46115_out, _4891_2_out);
  and _46116 (_46116_out, nand_39_out, nand_45_out);
  and _46115 (_46115_out, not_65_out, nand_44_out);
  not not_65 (not_65_out, c4_3);
  nand nand_44 (nand_44_out, not_66_out, and_17_out);
  nand nand_45 (nand_45_out, and_18_out, c3_3);
  and and_17 (and_17_out, c2_3, not_70_out);
  not not_66 (not_66_out, c1_3);
  and and_18 (and_18_out, and_19_out, nand_46_out);
  and and_19 (and_19_out, nand_41_out, and_16_out);
  nand nand_46 (nand_46_out, not_67_out, rf0_3);
  nand nand_47 (nand_47_out, not_67_out, or_15_out);
  or or_15 (or_15_out, rf1_3, rf0_3);
  not not_67 (not_67_out, IDCT_cnt2_1fe_3);
  DFFR_logic _4194 (.clk(clk61), .in(_3765_out), .nres(nres_4), .out_4(_4194_out_4));
  RAM #(.addrWidth(7), .dataWidth(12), .bus("separate")) ram_2 (
    .addr({rle_1_ie2[6], rle_1_address_for_decoded_data}), .din(rle_1_decoded_data), .str(or_13_out),
    .clk(clock_4_out));  // open: data, sel, ld, clr
  // Probe on _4892_q
  D_Flip_Flop _4892 (.clk(mclk_out), .D(_4791_out), .Q(_4892_q));  // open: Qn, preset, en, reset
  nand _4891_2 (_4891_2_out, not_69_out, not_68_out, _4892_q);
  not not_68 (not_68_out, rle_finished_2);
  not not_69 (not_69_out, RLE_data_ended_4);
  not not_70 (not_70_out, nand_48_out);
  nand nand_48 (nand_48_out, nand_47_out, nand_49_out);
  nand nand_49 (nand_49_out, rf0_3, d1_5);
  IMUX imux_3 (.b___in0(and_22_out), .c___in1(dffr_logic_1_out_4), .out(imux_3_out), .sel(sod_sel));
  nand _3765 (_3765_out, not_73_out, not_71_out, not_72_out);
  not not_71 (not_71_out, command0);
  not not_72 (not_72_out, not_75_out);
  not not_73 (not_73_out, in_127);
  DFFR_logic dffr_logic_1 (.clk(clock_3_out), .in(imux_3_out), .nres(nres_3), .out_4(dffr_logic_1_out_4));
  IMUX imux_4 (.b___in0(and_23_out), .c___in1(xor_5_out), .out(imux_4_out), .sel(sod_sel));
  xor xor_5 (xor_5_out, dffr_logic_1_out_4, dffr_logic_2_out_4);
  or or_16 (or_16_out, nor_6_out, in_131);
  nor nor_6 (nor_6_out, and_20_out, not_75_out);
  and and_20 (and_20_out, _3683_out, _3990_out);
  nand _3990 (_3990_out, command0, command1);
  nand _3683 (_3683_out, not_74_out, in_127);
  not not_74 (not_74_out, command0);
  Clock clock_5 (.out(clock_5_out));
  IDCT idct_1 ();  // open: result1__use_previous_result_in_summation, cnt2_ovfl, stm_sel1, Address_for_STM_data, clk1, ncnt1_1, ncnt1_2, ncnt1_3, clk3, cnt1_0, rle_sel, ncnt2_ovfl, Address_for_RLE_data, ncnt2_ovfl_3, u9__XXXX111111, CTRL4, ncnt2_run, Address_for_store_row_multiplication, CTRL4_2, cnt2_0, cnt2_1, cnt2_2, cnt2_3, ncnt2_ovfl_s, ncnt2_ovfl_4, ncnt2_run_2, result2, cnt0_ovfl, clk6, clk7, ncnt3_0, ncnt3_1, ncnt3_2, ncnt3_3, clk8, cnt3_0, stm_sel2, ncnt0_ovfl, Address_for_STM_data_2, Address_for_read_row_multiplication_result, ctrl4_s, clk9, ncnt0_ovfl_3, ncnt0_run, nRES_2, nRES_3, nRES_4, ctrl4_s_2, cnt0_0, cnt0_1, cnt0_2, cnt0_3, ncnt0_ovfl_s, ncnt0_ovfl_2, ncnt0_run_2, Address_for_store_row_multiplication_2, ncnt0_full, ncnt2_ovfl_2, ctrl3__X111111110, nres
  DFFR_logic dffr_logic_2 (.clk(clock_3_out), .in(imux_4_out), .nres(nres_3), .out_4(dffr_logic_2_out_4));
  IMUX imux_5 (.b___in0(and_25_out), .c___in1(xor_6_out), .out(imux_5_out), .sel(sod_sel));
  xor xor_6 (xor_6_out, dffr_logic_4_out_4, or_17_out);
  or or_17 (or_17_out, dffr_logic_1_out_4, dffr_logic_2_out_4);
  not not_75 (not_75_out, _4064_out);
  and _4064 (_4064_out, command1, not_76_out);
  not not_76 (not_76_out, command2);
  nand nand_50 (nand_50_out, nand_51_out, nand_54_out);
  nand nand_51 (nand_51_out, not_77_out, com2_1, in_154);
  not not_77 (not_77_out, _53115_out);
  not _53115 (_53115_out, vwr);
  not u__5388 (_5388_out, _5388);
  Clock mclk_4 (.out(mclk_4_out));
  and and_21 (and_21_out, not_78_out, c2_4);
  not not_78 (not_78_out, nand_52_out);
  nand nand_52 (nand_52_out, nand_53_out, nand_56_out);
  nand nand_53 (nand_53_out, not_79_out, or_18_out);
  or or_18 (or_18_out, rf1_4, rf0_4);
  not not_79 (not_79_out, IDCT_cnt2_1fe_4);
  DFFR_logic dffr_logic_3 (.clk(clock_3_out), .in(imux_6_out), .nres(nres_3), .out_4(dffr_logic_3_out_4));
  DFFR_logic dffr_logic_4 (.clk(clock_3_out), .in(imux_5_out), .nres(nres_3), .out_4(dffr_logic_4_out_4));
  IMUX imux_6 (.b___in0(and_24_out), .c___in1(xor_7_out), .out(imux_6_out), .sel(sod_sel));
  xor xor_7 (xor_7_out, dffr_logic_3_out_4, or_19_out);
  or or_19 (or_19_out, or_17_out, dffr_logic_4_out_4);
  and and_22 (and_22_out, not_81_out, not_75_out);
  and and_23 (and_23_out, not_80_out, not_75_out);
  not not_80 (not_80_out, in_128);
  not not_81 (not_81_out, in_127);
  DFFR_logic _4773 (.clk(clock_5_out), .in(nand_50_out), .nres(in_148), .out_4(unk));
  nand nand_54 (nand_54_out, _5388_out, and_26_out);
  not u__5071 (_5071_out, _5071);
  nand nand_55 (nand_55_out, and_21_out, not_82_out);
  not not_82 (not_82_out, c1_5);
  nand nand_56 (nand_56_out, rf0_4, d1_7);
  DFFR_logic dffr_logic_5 (.clk(clock_3_out), .in(imux_7_out), .nres(nres_3), .out_4(dffr_logic_5_out_4));
  IMUX imux_7 (.b___in0(nand_61_out), .c___in1(xor_8_out), .out(imux_7_out), .sel(sod_sel));
  xor xor_8 (xor_8_out, dffr_logic_5_out_4, or_20_out);
  or or_20 (or_20_out, or_19_out, dffr_logic_3_out_4);
  and and_24 (and_24_out, not_84_out, not_75_out);
  and and_25 (and_25_out, not_83_out, not_75_out);
  not not_83 (not_83_out, in_129);
  not not_84 (not_84_out, in_130);
  or or_21 (clk66, clock_5_out, not_89_out);
  DFFR_logic _4867 (.clk(clock_5_out), .in(not_85_out), .nres(in_148), .out_4(_4867_out_4));
  not not_85 (not_85_out, nand_64_out);
  and and_26 (and_26_out, _5071_out, nor_7_out);
  nor nor_7 (nor_7_out, _53115_out, in_155);
  and _4190 (_4190_out, in_169, _4066_out);
  nor _4786 (_4786_out, not_86_out, c9);
  not not_86 (not_86_out, nres_2);
  nand nand_57 (nand_57_out, and_27_out, not_93_out);
  and and_27 (and_27_out, nand_55_out, c2_4);
  nand nand_58 (nand_58_out, not_79_out, rf0_4);
  and and_28 (and_28_out, not_87_out, c1_5);
  not not_87 (not_87_out, nand_59_out);
  nand nand_59 (nand_59_out, nand_60_out, not_93_out);
  nand nand_60 (nand_60_out, d4_5, rle_finished_5);
  DFFR_logic dffr_logic_6 (.clk(clock_3_out), .in(imux_8_out), .nres(nres_3), .out_4(dffr_logic_6_out_4));
  IMUX imux_8 (.b___in0(nand_62_out), .c___in1(xor_9_out), .out(imux_8_out), .sel(sod_sel));
  IMUX imux_9 (.b___in0(nand_69_out), .c___in1(xor_10_out), .out(imux_9_out), .sel(sod_sel));
  xor xor_9 (xor_9_out, dffr_logic_6_out_4, or_22_out);
  or or_22 (or_22_out, or_20_out, dffr_logic_5_out_4);
  not not_88 (not_88_out, or_22_out);
  nand nand_61 (nand_61_out, _3765_out, or_16_out);
  nand nand_62 (nand_62_out, in_132, not_75_out);
  or or_23 (clk63, clock_5_out, not_95_out);
  not not_89 (not_89_out, _4867_out_4);
  nand nand_63 (nand_63_out, nand_64_out, not_96_out);
  nand nand_64 (nand_64_out, and_26_out, not_90_out);
  not not_90 (not_90_out, _5388_out);
  nand _4788 (_4788_out, _4786_out, _4789_out);
  nand _4789 (_4789_out, _46117_out, _46113_out, _4790_out);
  nand _46113 (_46113_out, not_91_out, c5);
  and _46117 (_46117_out, nand_57_out, nand_65_out);
  not not_91 (not_91_out, nand_66_out);
  nand nand_65 (nand_65_out, and_29_out, c3);
  nand nand_66 (nand_66_out, nand_67_out, com_dec_block_s_2);
  and and_29 (and_29_out, nand_58_out, and_30_out);
  and and_30 (and_30_out, and_28_out, nand_67_out);
  nand nand_67 (nand_67_out, or_24_out, not_92_out);
  not not_92 (not_92_out, load_finished_4);
  or or_24 (or_24_out, load_data_exist_5, dir_4);
  not not_93 (not_93_out, d1_7);
  DFFR_logic dffr_logic_7 (.clk(clock_3_out), .in(imux_9_out), .nres(nres_3), .out_4(dffr_logic_7_out_4));
  IMUX imux_10 (.b___in0(nand_70_out), .c___in1(xor_11_out), .out(imux_10_out), .sel(sod_sel));
  xor xor_10 (xor_10_out, dffr_logic_7_out_4, nand_68_out);
  nand nand_68 (nand_68_out, not_88_out, not_94_out);
  not not_94 (not_94_out, dffr_logic_6_out_4);
  nand nand_69 (nand_69_out, in_133, not_75_out);
  nand nand_70 (nand_70_out, in_134, not_75_out);
  or or_25 (clk12, clock_5_out, not_95_out);
  or or_26 (clk64, clock_5_out, not_95_out);
  not not_95 (not_95_out, _4695_out_4);
  DFFR_logic _4695 (.clk(clock_5_out), .in(nand_63_out), .nres(in_148), .out_4(_4695_out_4));
  not not_96 (not_96_out, nand_50_out);
  D_Flip_Flop _3984 (.clk(mclk_4_out), .D(_4189_out), .Q(curb0));  // open: Qn, preset, en, reset
  and _4189 (_4189_out, res_2, multiplexer_3_out, _4191_out);
  Multiplexer multiplexer_3 (.in0(fa_1_out2___sum), .in1(curb0), .out(multiplexer_3_out), .sel(_4190_out));  // open: en
  fa fa_1 (
    .out2___sum(fa_1_out2___sum), .out1___cout(fa_1_out1___cout), .in3___cin(1'b0), .in2___b(1'b1),
    .in1___a(curb0));
  D_Flip_Flop _4997 (.clk(mclk_out), .D(_4788_out), .Q(c8_2));  // open: Qn, preset, en, reset
  and _4790 (_4790_out, not_97_out, c8_2);
  not not_97 (not_97_out, c4);
  DFFR_logic dffr_logic_8 (.clk(clock_3_out), .in(imux_10_out), .nres(nres_3), .out_4(dffr_logic_8_out_4));
  IMUX imux_11 (.b___in0(nand_73_out), .c___in1(xor_12_out), .out(imux_11_out), .sel(sod_sel));
  xor xor_11 (xor_11_out, dffr_logic_8_out_4, nand_71_out);
  nand nand_71 (nand_71_out, not_88_out, not_98_out);
  not not_98 (not_98_out, or_27_out);
  or or_27 (or_27_out, dffr_logic_6_out_4, dffr_logic_7_out_4);
  nand nand_72 (nand_72_out, in_136, not_75_out);
  nand nand_73 (nand_73_out, in_135, not_75_out);
  and _4188 (_4188_out, res_2, multiplexer_4_out, _4191_out);
  Multiplexer multiplexer_4 (.in0(fa_2_out2___sum), .in1(curb1), .out(multiplexer_4_out), .sel(_4190_out));  // open: en
  DFFR_logic dffr_logic_9 (.clk(clock_3_out), .in(imux_11_out), .nres(nres_3), .out_4(dffr_logic_9_out_4));
  IMUX imux_12 (.b___in0(nand_72_out), .c___in1(xor_13_out), .out(imux_12_out), .sel(sod_sel));
  xor xor_12 (xor_12_out, dffr_logic_9_out_4, nand_74_out);
  xor xor_13 (xor_13_out, dffr_logic_10_out_4, nand_78_out);
  nand nand_74 (nand_74_out, not_88_out, not_99_out);
  not not_99 (not_99_out, or_28_out);
  or or_28 (or_28_out, or_27_out, dffr_logic_8_out_4);
  nand nand_75 (nand_75_out, in_137, not_75_out);
  nand nand_76 (nand_76_out, in_138, not_75_out);
  D_Flip_Flop _4184 (.clk(mclk_4_out), .D(_4188_out), .Q(curb1));  // open: Qn, preset, en, reset
  fa fa_2 (
    .out2___sum(fa_2_out2___sum), .out1___cout(fa_2_out1___cout), .in3___cin(1'b0),
    .in2___b(fa_1_out1___cout), .in1___a(curb1));
  DFFR_logic dffr_logic_10 (.clk(clock_3_out), .in(imux_12_out), .nres(nres_3), .out_4(dffr_logic_10_out_4));
  IMUX imux_13 (.b___in0(nand_75_out), .c___in1(xor_14_out), .out(imux_13_out), .sel(sod_sel));
  xor xor_14 (xor_14_out, dffr_logic_12_out_4, nand_77_out);
  nand nand_77 (nand_77_out, not_88_out, not_101_out);
  nand nand_78 (nand_78_out, not_88_out, not_100_out);
  not not_100 (not_100_out, or_29_out);
  or or_29 (or_29_out, or_28_out, dffr_logic_9_out_4);
  nand nand_79 (nand_79_out, in_140, not_75_out);
  nand nand_80 (nand_80_out, in_139, not_75_out);
  D_Flip_Flop _4395 (.clk(mclk_4_out), .D(_4291_2_out), .Q(curb2));  // open: Qn, preset, en, reset
  nand _4291_2 (_4291_2_out, res_2, _4290_out);
  nand _4290 (_4290_out, multiplexer_5_out, _4191_out);
  Multiplexer multiplexer_5 (.in0(fa_3_out2___sum), .in1(curb2), .out(multiplexer_5_out), .sel(_4190_out));  // open: en
  fa fa_3 (
    .out2___sum(fa_3_out2___sum), .in3___cin(1'b0), .in2___b(fa_2_out1___cout), .in1___a(curb2));  // open: out1___cout
  DFFR_logic dffr_logic_11 (.clk(clock_3_out), .in(imux_14_out), .nres(nres_3), .out_4(dffr_logic_11_out_4));
  DFFR_logic dffr_logic_12 (.clk(clock_3_out), .in(imux_13_out), .nres(nres_3), .out_4(dffr_logic_12_out_4));
  IMUX imux_14 (.b___in0(nand_76_out), .c___in1(xor_15_out), .out(imux_14_out), .sel(sod_sel));
  xor xor_15 (xor_15_out, dffr_logic_11_out_4, nand_81_out);
  nand nand_81 (nand_81_out, not_88_out, nor_8_out);
  not not_101 (not_101_out, or_30_out);
  nor nor_8 (nor_8_out, or_30_out, dffr_logic_12_out_4);
  or or_30 (or_30_out, or_29_out, dffr_logic_10_out_4);
  nand nand_82 (nand_82_out, in_142, not_75_out);
  nand nand_83 (nand_83_out, in_141, not_75_out);
  nand _4191 (_4191_out, in_169, not_102_out);
  not not_102 (not_102_out, _4066_out);
  nand _4066 (_4066_out, curb0, not_103_out, curb2);
  not not_103 (not_103_out, curb1);
  DFFR_logic dffr_logic_13 (.clk(clock_3_out), .in(imux_15_out), .nres(nres_3), .out_4(dffr_logic_13_out_4));
  IMUX imux_15 (.b___in0(nand_80_out), .c___in1(xor_16_out), .out(imux_15_out), .sel(sod_sel));
  xor xor_16 (xor_16_out, dffr_logic_13_out_4, nand_84_out);
  nand nand_84 (nand_84_out, not_88_out, nor_9_out);
  nor nor_9 (nor_9_out, or_30_out, or_31_out);
  or or_31 (or_31_out, dffr_logic_12_out_4, dffr_logic_11_out_4);
  DFFR_logic dffr_logic_14 (.clk(clock_3_out), .in(imux_17_out), .nres(nres_3), .out_4(dffr_logic_14_out_4));
  IMUX imux_16 (.b___in0(nand_83_out), .c___in1(xor_18_out), .out(imux_16_out), .sel(sod_sel));
  IMUX imux_17 (.b___in0(nand_79_out), .c___in1(xor_17_out), .out(imux_17_out), .sel(sod_sel));
  xor xor_17 (xor_17_out, dffr_logic_14_out_4, nand_85_out);
  nand nand_85 (nand_85_out, not_88_out, nor_10_out);
  nor nor_10 (nor_10_out, or_30_out, or_32_out);
  or or_32 (or_32_out, or_31_out, dffr_logic_13_out_4);
  Clock mclk_5 (.out(mclk_5_out));
  DFFR_logic dffr_logic_15 (.clk(clock_3_out), .in(imux_16_out), .nres(nres_3), .out_4(dffr_logic_15_out_4));
  IMUX imux_18 (.b___in0(nand_82_out), .c___in1(xor_19_out), .out(imux_18_out), .sel(sod_sel));
  xor xor_18 (xor_18_out, dffr_logic_15_out_4, nand_86_out);
  nand nand_86 (nand_86_out, not_88_out, nor_11_out);
  nor nor_11 (nor_11_out, or_30_out, or_33_out);
  or or_33 (or_33_out, or_32_out, dffr_logic_14_out_4);
  fa fa_4 (
    .out2___sum(fa_4_out2___sum), .out1___cout(fa_4_out1___cout), .in3___cin(1'b0), .in2___b(1'b1),
    .in1___a(h8));
  DFFR_logic dffr_logic_16 (.clk(clock_3_out), .in(imux_18_out), .nres(nres_3), .out_4(dffr_logic_16_out_4));
  xor xor_19 (xor_19_out, dffr_logic_16_out_4, nand_87_out);
  nand nand_87 (nand_87_out, not_88_out, not_104_out, nor_12_out);
  not not_104 (not_104_out, or_33_out);
  nor nor_12 (nor_12_out, or_30_out, dffr_logic_15_out_4);
  fa fa_5 (
    .out2___sum(fa_5_out2___sum), .out1___cout(fa_5_out1___cout), .in3___cin(1'b0),
    .in2___b(fa_4_out1___cout), .in1___a(h8));
  fa fa_6 (
    .out2___sum(fa_6_out2___sum), .in3___cin(1'b0), .in2___b(fa_5_out1___cout), .in1___a(h10));  // open: out1___cout
  D_Flip_Flop _4174 (.clk(mclk_5_out), .D(_4047_out), .Q(h8));  // open: Qn, preset, en, reset
  and _4047 (_4047_out, res_4, imux_19_out);
  IMUX imux_19 (.b___in0(imux_20_out), .c___in1(not_105_out), .out(imux_19_out), .sel(_3945_out));
  not not_105 (not_105_out, fa_4_out2___sum);
  IMUX imux_20 (.b___in0(h8), .c___in1(fa_7_out2___sum), .out(imux_20_out), .sel(_3973_out));
  and _3870 (_3870_out, res_4, imux_21_out);
  IMUX imux_21 (.b___in0(imux_22_out), .c___in1(not_107_out), .out(imux_21_out), .sel(_3945_out));
  IMUX imux_22 (.b___in0(h9), .c___in1(fa_8_out2___sum), .out(imux_22_out), .sel(_3973_out));
  fa fa_7 (
    .out2___sum(fa_7_out2___sum), .out1___cout(fa_7_out1___cout), .in3___cin(1'b0), .in2___b(1'b1),
    .in1___a(h8));
  nand nand_88 (ctrl4, not_106_out, in_157, in_158);
  not not_106 (not_106_out, in_156);
  D_Flip_Flop _3971 (.clk(mclk_5_out), .D(_3870_out), .Q(h9));  // open: Qn, preset, en, reset
  not not_107 (not_107_out, fa_5_out2___sum);
  fa fa_8 (
    .out2___sum(fa_8_out2___sum), .out1___cout(fa_8_out1___cout), .in3___cin(1'b1),
    .in2___b(fa_7_out1___cout), .in1___a(h9));
  D_Flip_Flop _4052 (.clk(mclk_5_out), .D(_4051_out), .Q(h10));  // open: Qn, preset, en, reset
  and _4051 (_4051_out, res_4, imux_23_out);
  IMUX imux_23 (.b___in0(imux_24_out), .c___in1(not_108_out), .out(imux_23_out), .sel(_3945_out));
  not not_108 (not_108_out, fa_6_out2___sum);
  IMUX imux_24 (.b___in0(h10), .c___in1(fa_9_out2___sum), .out(imux_24_out), .sel(_3973_out));
  and _3945 (_3945_out, yuv_res_8, or_34_out);
  fa fa_9 (
    .out2___sum(fa_9_out2___sum), .in3___cin(1'b1), .in2___b(fa_8_out1___cout), .in1___a(h10));  // open: out1___cout
  and _3973 (_3973_out, not_110_out, not_109_out);
  not not_109 (not_109_out, or_34_out);
  not not_110 (not_110_out, yuv_res_8);
  or or_34 (or_34_out, h2, nout_res_8);
  Clock mclk_6 (.out(mclk_6_out));
  and and_31 (and_31_out, in_98, _49101_2_q);
  D_Flip_Flop _49101 (.clk(mclk_6_out), .D(and_31_out), .Q(_49101_q));  // open: Qn, preset, en, reset
  Clock mclk_7 (.out(mclk_7_out));
  and and_32 (and_32_out, and_33_out, nand_90_out);
  and and_33 (and_33_out, com100, rle_finished_9, do1);
  D_Flip_Flop _49101_2 (.clk(mclk_6_out), .D(and_34_out), .Q(_49101_2_q));  // open: Qn, preset, en, reset
  and and_34 (and_34_out, in_98, _49101_4_q);
  Clock mclk_8 (.out(mclk_8_out));
  fa fa_10 (
    .out2___sum(fa_10_out2___sum), .out1___cout(fa_10_out1___cout), .in3___cin(1'b0), .in2___b(1'b1),
    .in1___a(out_198));
  nand nand_89 (nand_89_out, and_33_out, not_111_out);
  not not_111 (not_111_out, nand_90_out);
  nand nand_90 (nand_90_out, out_232, not_112_out, _49101_3_q);
  not not_112 (not_112_out, _5193_2_q);
  and and_35 (and_35_out, in_98, _5193_q);
  fa fa_11 (
    .out2___sum(fa_11_out2___sum), .in3___cin(1'b0), .in2___b(fa_10_out1___cout), .in1___a(out_199));  // open: out1___cout
  D_Flip_Flop _49101_3 (.clk(mclk_7_out), .D(and_36_out), .Q(_49101_3_q));  // open: Qn, preset, en, reset
  and and_36 (and_36_out, res_3, nand_89_out, multiplexer_6_out);
  Multiplexer multiplexer_6 (
    .in0(fa_12_out2___sum), .in1(_49101_3_q), .out(multiplexer_6_out), .sel(and_32_out));  // open: en
  fa fa_12 (
    .out2___sum(fa_12_out2___sum), .out1___cout(fa_12_out1___cout), .in3___cin(_49101_3_q), .in2___b(1'b1),
    .in1___a(1'b0));
  D_Flip_Flop _49101_4 (.clk(mclk_6_out), .D(and_35_out), .Q(_49101_4_q));  // open: Qn, preset, en, reset
  D_Flip_Flop d_ff_4 (.clk(mclk_8_out), .D(and_37_out), .Q(out_198));  // open: Qn, preset, en, reset
  and and_37 (and_37_out, res, imux_25_out);
  IMUX imux_25 (.b___in0(imux_26_out), .c___in1(not_113_out), .out(imux_25_out), .sel(and_42_out));
  not not_113 (not_113_out, fa_10_out2___sum);
  IMUX imux_26 (.b___in0(out_198), .c___in1(fa_13_out2___sum), .out(imux_26_out), .sel(and_43_out));
  and and_38 (and_38_out, res_3, nand_89_out, multiplexer_7_out);
  Multiplexer multiplexer_7 (
    .in0(fa_14_out2___sum), .in1(_5193_2_q), .out(multiplexer_7_out), .sel(and_32_out));  // open: en
  D_Flip_Flop _5193 (.clk(mclk_6_out), .D(and_39_out), .Q(_5193_q));  // open: Qn, preset, en, reset
  and and_39 (and_39_out, in_98, com2_2, _52101_2_q);
  and and_40 (and_40_out, res, imux_27_out);
  fa fa_13 (
    .out2___sum(fa_13_out2___sum), .out1___cout(fa_13_out1___cout), .in3___cin(1'b0), .in2___b(1'b1),
    .in1___a(out_198));
  D_Flip_Flop _5193_2 (.clk(mclk_7_out), .D(and_38_out), .Q(_5193_2_q));  // open: Qn, preset, en, reset
  fa fa_14 (
    .out2___sum(fa_14_out2___sum), .out1___cout(fa_14_out1___cout), .in3___cin(_5193_2_q),
    .in2___b(fa_12_out1___cout), .in1___a(1'b0));
  nand nand_91 (nand_91_out, in_98, nand_92_out, not_114_out);
  not not_114 (not_114_out, _49101_q);
  nand nand_92 (nand_92_out, not_115_out, _52101_2_q);
  not not_115 (not_115_out, com2_2);
  D_Flip_Flop d_ff_5 (.clk(mclk_8_out), .D(and_40_out), .Q(out_199));  // open: Qn, preset, en, reset
  IMUX imux_27 (.b___in0(imux_28_out), .c___in1(not_116_out), .out(imux_27_out), .sel(and_42_out));
  not not_116 (not_116_out, fa_11_out2___sum);
  IMUX imux_28 (.b___in0(out_199), .c___in1(fa_15_out2___sum), .out(imux_28_out), .sel(and_43_out));
  fa fa_15 (
    .out2___sum(fa_15_out2___sum), .in3___cin(1'b1), .in2___b(fa_13_out1___cout), .in1___a(out_199));  // open: out1___cout
  D_Flip_Flop _52101 (.clk(mclk_7_out), .D(nand_93_out), .Q(out_232));  // open: Qn, preset, en, reset
  nand nand_93 (nand_93_out, res_3, nand_94_out);
  nand nand_94 (nand_94_out, multiplexer_8_out, nand_89_out);
  Multiplexer multiplexer_8 (
    .in0(fa_16_out2___sum), .in1(out_232), .out(multiplexer_8_out), .sel(and_32_out));  // open: en
  fa fa_16 (
    .out2___sum(fa_16_out2___sum), .in3___cin(out_232), .in2___b(fa_14_out1___cout), .in1___a(1'b0));  // open: out1___cout
  and and_41 (nres_6, _52101_2_q, in_98);
  D_Flip_Flop _52101_2 (.clk(mclk_6_out), .D(nand_91_out), .Q(_52101_2_q));  // open: Qn, preset, en, reset
  and and_42 (and_42_out, not_117_out, rle_finished_7);
  and and_43 (and_43_out, not_118_out, IDCT_cnt2_1fe_6);
  not not_117 (not_117_out, IDCT_cnt2_1fe_6);
  not not_118 (not_118_out, rle_finished_7);

  assign load_quant__32_item = load_quant;

  // Notes on the sheet:
  //   data finished,
  //   d1 or d4 and rle_finished
  //   RLE Control
  //   set when c9 and data for RLE encoding ended
  //   lifted when next block load finished,
  //   Signal for uploading data from Unit03 to DB
  //   YUV Control
  //   select write encoded data (0)
  //   or read it for idct (1)
  //   IDCT Control
  //   UNIT04
  //   Load Counter
  //   UNIT05
  //   storred (clk66) command bit1
  //   This starts loading of data to mdec and reading commant
  //   low value - start RLE encoding
  //   read data from db
  //   Load Counter For Register
  //   read data and command from db
endmodule
