// Logisim project IDCT.circ as structural Verilog: 12 circuits, main circuit IDCT_pass1
module IDCT_pass1 (
  input  D5,
  input  D4,
  input  D3,
  input  D2,
  input  D1,
  input  D0,
  input  _00,
  input  _01,
  input  _02,
  input  _03,
  input  _04,
  input  _05,
  input  _06,
  input  _07,
  input  _08,
  input  _09,
  input  _10,
  input  _11,
  input  _12
);

  wire mux_control_1_l0_d1, mux_control_1_l0_d2, mux_control_1_l1_d1, mux_control_1_l1_d2,
       mux_control_1_l2_d1, mux_control_1_l2_d2, mux_control_1_l3_d1, mux_control_1_l3_d2,
       mux_control_1_l4_d1, mux_control_1_l4_d2, mux_control_1_l5_d1, mux_control_1_l5_d2, muxs_1_l0_00,
       muxs_1_l0_01, muxs_1_l0_02, muxs_1_l0_03, muxs_1_l0_04, muxs_1_l0_05, muxs_1_l0_06, muxs_1_l0_07,
       muxs_1_l0_08, muxs_1_l0_09, muxs_1_l0_10, muxs_1_l0_11, muxs_1_l0_12, muxs_1_l0_13, muxs_1_l1_00,
       muxs_1_l1_01, muxs_1_l1_02, muxs_1_l1_03, muxs_1_l1_04, muxs_1_l1_05, muxs_1_l1_06, muxs_1_l1_07,
       muxs_1_l1_08, muxs_1_l1_09, muxs_1_l1_10, muxs_1_l1_11, muxs_1_l1_12, muxs_1_l1_13, muxs_1_l2_00,
       muxs_1_l2_01, muxs_1_l2_02, muxs_1_l2_03, muxs_1_l2_04, muxs_1_l2_05, muxs_1_l2_06, muxs_1_l2_07,
       muxs_1_l2_08, muxs_1_l2_09, muxs_1_l2_10, muxs_1_l2_11, muxs_1_l2_12, muxs_1_l2_13, muxs_1_l3_00,
       muxs_1_l3_01, muxs_1_l3_02, muxs_1_l3_03, muxs_1_l3_04, muxs_1_l3_05, muxs_1_l3_06, muxs_1_l3_07,
       muxs_1_l3_08, muxs_1_l3_09, muxs_1_l3_10, muxs_1_l3_11, muxs_1_l3_12, muxs_1_l3_13, muxs_1_l4_00,
       muxs_1_l4_01, muxs_1_l4_02, muxs_1_l4_03, muxs_1_l4_04, muxs_1_l4_05, muxs_1_l4_06, muxs_1_l4_07,
       muxs_1_l4_08, muxs_1_l4_09, muxs_1_l4_10, muxs_1_l4_11, muxs_1_l4_12, muxs_1_l4_13, muxs_1_l5_00,
       muxs_1_l5_01, muxs_1_l5_02, muxs_1_l5_03, muxs_1_l5_04, muxs_1_l5_05, muxs_1_l5_06, muxs_1_l5_07,
       muxs_1_l5_08, muxs_1_l5_09, muxs_1_l5_10, muxs_1_l5_11, muxs_1_l5_12, muxs_1_l5_13, not_1_out,
       not_2_out, not_3_out, not_4_out, not_5_out, not_6_out, not_7_out, not_8_out, not_9_out, not_10_out,
       not_11_out, not_12_out;

  not not_1 (not_1_out, D5);
  not not_2 (not_2_out, D4);
  not not_3 (not_3_out, D3);
  not not_4 (not_4_out, D2);
  not not_5 (not_5_out, D1);
  not not_6 (not_6_out, D0);
  MUX_CONTROL mux_control_1 (
    ._11(D5), ._10(not_1_out), ._09(D4), ._08(not_2_out), ._07(D3), ._06(not_3_out), ._05(D2),
    ._04(not_4_out), ._03(D1), ._02(not_5_out), ._01(D0), ._00(not_6_out), .L5_D2(mux_control_1_l5_d2),
    .L5_D1(mux_control_1_l5_d1), .L4_D2(mux_control_1_l4_d2), .L4_D1(mux_control_1_l4_d1),
    .L3_D2(mux_control_1_l3_d2), .L3_D1(mux_control_1_l3_d1), .L2_D2(mux_control_1_l2_d2),
    .L2_D1(mux_control_1_l2_d1), .L1_D2(mux_control_1_l1_d2), .L1_D1(mux_control_1_l1_d1),
    .L0_D2(mux_control_1_l0_d2), .L0_D1(mux_control_1_l0_d1));
  MUXs muxs_1 (
    .L5_C1(D5), .L5_C2(not_7_out), .L5_D1(mux_control_1_l5_d1), .L5_D2(mux_control_1_l5_d2), .L4_C1(D4),
    .L4_C2(not_8_out), .L4_D1(mux_control_1_l4_d1), .L4_D2(mux_control_1_l4_d2), .L3_C1(D3),
    .L3_C2(not_9_out), .L3_D1(mux_control_1_l3_d1), .L3_D2(mux_control_1_l3_d2), .L2_C1(D2),
    .L2_C2(not_10_out), .L2_D1(mux_control_1_l2_d1), .L2_D2(mux_control_1_l2_d2), .L1_C1(D1),
    .L1_C2(not_11_out), .L1_D1(mux_control_1_l1_d1), .L1_D2(mux_control_1_l1_d2), .L0_C1(D0),
    .L0_C2(not_12_out), .L0_D1(mux_control_1_l0_d1), .L0_D2(mux_control_1_l0_d2), .S0(_00), .S1(_01),
    .S2(_02), .S3(_03), .S4(_04), .S5(_05), .S6(_06), .S7(_07), .S8(_08), .S9(_09), .S10(_10), .S11(_11),
    .S12(_12), .L4_00(muxs_1_l4_00), .L4_01(muxs_1_l4_01), .L4_02(muxs_1_l4_02), .L4_04(muxs_1_l4_04),
    .L4_05(muxs_1_l4_05), .L4_03(muxs_1_l4_03), .L4_06(muxs_1_l4_06), .L4_07(muxs_1_l4_07),
    .L4_08(muxs_1_l4_08), .L4_09(muxs_1_l4_09), .L4_10(muxs_1_l4_10), .L4_11(muxs_1_l4_11),
    .L4_12(muxs_1_l4_12), .L4_13(muxs_1_l4_13), .L3_00(muxs_1_l3_00), .L3_01(muxs_1_l3_01),
    .L3_02(muxs_1_l3_02), .L3_03(muxs_1_l3_03), .L3_04(muxs_1_l3_04), .L3_05(muxs_1_l3_05),
    .L3_06(muxs_1_l3_06), .L3_07(muxs_1_l3_07), .L3_08(muxs_1_l3_08), .L3_09(muxs_1_l3_09),
    .L3_10(muxs_1_l3_10), .L3_11(muxs_1_l3_11), .L3_12(muxs_1_l3_12), .L3_13(muxs_1_l3_13),
    .L5_00(muxs_1_l5_00), .L5_01(muxs_1_l5_01), .L5_02(muxs_1_l5_02), .L5_03(muxs_1_l5_03),
    .L5_04(muxs_1_l5_04), .L5_05(muxs_1_l5_05), .L5_06(muxs_1_l5_06), .L5_07(muxs_1_l5_07),
    .L5_08(muxs_1_l5_08), .L5_09(muxs_1_l5_09), .L5_10(muxs_1_l5_10), .L5_11(muxs_1_l5_11),
    .L5_12(muxs_1_l5_12), .L5_13(muxs_1_l5_13), .L2_00(muxs_1_l2_00), .L2_01(muxs_1_l2_01),
    .L2_02(muxs_1_l2_02), .L2_03(muxs_1_l2_03), .L2_04(muxs_1_l2_04), .L2_05(muxs_1_l2_05),
    .L2_06(muxs_1_l2_06), .L2_07(muxs_1_l2_07), .L2_08(muxs_1_l2_08), .L2_09(muxs_1_l2_09),
    .L2_10(muxs_1_l2_10), .L2_11(muxs_1_l2_11), .L2_12(muxs_1_l2_12), .L2_13(muxs_1_l2_13),
    .L1_00(muxs_1_l1_00), .L1_01(muxs_1_l1_01), .L1_02(muxs_1_l1_02), .L1_03(muxs_1_l1_03),
    .L1_04(muxs_1_l1_04), .L1_05(muxs_1_l1_05), .L1_06(muxs_1_l1_06), .L1_07(muxs_1_l1_07),
    .L1_08(muxs_1_l1_08), .L1_09(muxs_1_l1_09), .L1_10(muxs_1_l1_10), .L1_11(muxs_1_l1_11),
    .L1_12(muxs_1_l1_12), .L1_13(muxs_1_l1_13), .L0_00(muxs_1_l0_00), .L0_01(muxs_1_l0_01),
    .L0_02(muxs_1_l0_02), .L0_03(muxs_1_l0_03), .L0_04(muxs_1_l0_04), .L0_05(muxs_1_l0_05),
    .L0_06(muxs_1_l0_06), .L0_07(muxs_1_l0_07), .L0_08(muxs_1_l0_08), .L0_09(muxs_1_l0_09),
    .L0_10(muxs_1_l0_10), .L0_11(muxs_1_l0_11), .L0_12(muxs_1_l0_12), .L0_13(muxs_1_l0_13));
  not not_7 (not_7_out, D5);
  not not_8 (not_8_out, D4);
  not not_9 (not_9_out, D3);
  not not_10 (not_10_out, D2);
  not not_11 (not_11_out, D1);
  not not_12 (not_12_out, D0);
endmodule

module HA (
  input  in2___b,
  input  in1___a,
  output out2___sum,
  output out1___cout
);

  wire transistor_3_out, transistor_5_out, transistor_6_out, transistor_13_out;

  Transistor #(.gate("br")) transistor_1 (.in(1'b1), .out(out2___sum), .gate(transistor_3_out));
  Transistor #(.gate("br")) transistor_2 (.in(1'b1), .out(out1___cout), .gate(transistor_6_out));
  Transistor #(.gate("br")) transistor_3 (.in(in2___b), .out(transistor_3_out), .gate(transistor_5_out));
  Transistor #(.gate("br")) transistor_4 (.in(transistor_5_out), .out(transistor_3_out), .gate(in2___b));
  Transistor #(.gate("br")) transistor_5 (.in(1'b1), .out(transistor_5_out), .gate(in1___a));
  Transistor #(.gate("br")) transistor_6 (.in(1'b1), .out(transistor_6_out), .gate(in2___b));
  Transistor #(.gate("br")) transistor_7 (.in(1'b1), .out(transistor_6_out), .gate(in1___a));
  Transistor #(.\type ("n")) transistor_8 (.in(1'b0), .out(out2___sum), .gate(transistor_3_out));
  Transistor #(.\type ("n")) transistor_9 (.in(1'b0), .out(out1___cout), .gate(transistor_6_out));
  Transistor #(.\type ("n")) transistor_10 (.in(in2___b), .out(transistor_3_out), .gate(in1___a));
  Transistor #(.\type ("n")) transistor_11 (.in(in1___a), .out(transistor_3_out), .gate(in2___b));
  Transistor #(.\type ("n")) transistor_12 (.in(1'b0), .out(transistor_5_out), .gate(in1___a));
  Transistor #(.\type ("n")) transistor_13 (.in(1'b0), .out(transistor_13_out), .gate(in2___b));
  Transistor #(.\type ("n")) transistor_14 (.in(transistor_13_out), .out(transistor_6_out), .gate(in1___a));

  // Notes on the sheet:
  //   HALF ADDER
endmodule

module FA (
  input  in3___cin,
  input  in2___b,
  input  in1___a,
  output out2___sum,
  output out1___cout
);

  wire transistor_1_out, transistor_3_out, transistor_6_out, transistor_8_out, transistor_9_out,
       transistor_11_out;

  Transistor #(.gate("br")) transistor_1 (.in(in3___cin), .out(transistor_1_out), .gate(transistor_9_out));
  Transistor #(.gate("br")) transistor_2 (.in(transistor_3_out), .out(transistor_1_out), .gate(transistor_11_out));
  Transistor #(.gate("br")) transistor_3 (.in(1'b1), .out(transistor_3_out), .gate(in3___cin));
  Transistor #(.gate("br")) transistor_4 (.in(1'b1), .out(out2___sum), .gate(transistor_1_out));
  Transistor #(.gate("br")) transistor_5 (.in(1'b1), .out(out1___cout), .gate(transistor_6_out));
  Transistor #(.gate("br")) transistor_6 (.in(transistor_3_out), .out(transistor_6_out), .gate(transistor_9_out));
  Transistor #(.gate("br")) transistor_7 (.in(transistor_8_out), .out(transistor_6_out), .gate(transistor_11_out));
  Transistor #(.gate("br")) transistor_8 (.in(1'b1), .out(transistor_8_out), .gate(in2___b));
  Transistor #(.gate("br")) transistor_9 (.in(transistor_8_out), .out(transistor_9_out), .gate(in1___a));
  Transistor #(.gate("br")) transistor_10 (.in(in1___a), .out(transistor_9_out), .gate(transistor_8_out));
  Transistor #(.gate("br")) transistor_11 (.in(in1___a), .out(transistor_11_out), .gate(in2___b));
  Transistor #(.gate("br")) transistor_12 (.in(in2___b), .out(transistor_11_out), .gate(in1___a));
  Transistor #(.\type ("n")) transistor_13 (.in(in3___cin), .out(transistor_1_out), .gate(transistor_11_out));
  Transistor #(.\type ("n")) transistor_14 (.in(transistor_3_out), .out(transistor_1_out), .gate(transistor_9_out));
  Transistor #(.\type ("n")) transistor_15 (.in(1'b0), .out(transistor_3_out), .gate(in3___cin));
  Transistor #(.\type ("n")) transistor_16 (.in(1'b0), .out(out2___sum), .gate(transistor_1_out));
  Transistor #(.\type ("n")) transistor_17 (.in(1'b0), .out(out1___cout), .gate(transistor_6_out));
  Transistor #(.\type ("n")) transistor_18 (.in(transistor_3_out), .out(transistor_6_out), .gate(transistor_11_out));
  Transistor #(.\type ("n")) transistor_19 (.in(transistor_8_out), .out(transistor_6_out), .gate(transistor_9_out));
  Transistor #(.\type ("n")) transistor_20 (.in(1'b0), .out(transistor_8_out), .gate(in2___b));
  Transistor #(.\type ("n")) transistor_21 (.in(transistor_8_out), .out(transistor_11_out), .gate(in1___a));
  Transistor #(.\type ("n")) transistor_22 (.in(in1___a), .out(transistor_11_out), .gate(transistor_8_out));
  Transistor #(.\type ("n")) transistor_23 (.in(in1___a), .out(transistor_9_out), .gate(in2___b));
  Transistor #(.\type ("n")) transistor_24 (.in(in2___b), .out(transistor_9_out), .gate(in1___a));

  // Notes on the sheet:
  //   FULL ADDER
  //   xor
  //   xnor
endmodule

module CA (
  input  a,
  input  b,
  output out1___sum,
  output out2___cout
);

  wire transistor_3_out, transistor_5_out, transistor_6_out, transistor_7_out;

  Transistor #(.gate("br")) transistor_1 (.in(1'b1), .out(out1___sum), .gate(transistor_3_out));
  Transistor #(.gate("br")) transistor_2 (.in(1'b1), .out(out2___cout), .gate(transistor_7_out));
  Transistor #(.gate("br")) transistor_3 (.in(a), .out(transistor_3_out), .gate(b));
  Transistor #(.gate("br")) transistor_4 (.in(b), .out(transistor_3_out), .gate(a));
  Transistor #(.gate("br")) transistor_5 (.in(1'b1), .out(transistor_5_out), .gate(b));
  Transistor #(.gate("br")) transistor_6 (.in(1'b1), .out(transistor_6_out), .gate(a));
  Transistor #(.gate("br")) transistor_7 (.in(transistor_6_out), .out(transistor_7_out), .gate(b));
  Transistor #(.\type ("n")) transistor_8 (.in(1'b0), .out(out1___sum), .gate(transistor_3_out));
  Transistor #(.\type ("n")) transistor_9 (.in(1'b0), .out(out2___cout), .gate(transistor_7_out));
  Transistor #(.\type ("n")) transistor_10 (.in(a), .out(transistor_3_out), .gate(transistor_5_out));
  Transistor #(.\type ("n")) transistor_11 (.in(transistor_5_out), .out(transistor_3_out), .gate(a));
  Transistor #(.\type ("n")) transistor_12 (.in(1'b0), .out(transistor_5_out), .gate(b));
  Transistor #(.\type ("n")) transistor_13 (.in(1'b0), .out(transistor_7_out), .gate(a));
  Transistor #(.\type ("n")) transistor_14 (.in(1'b0), .out(transistor_7_out), .gate(b));

  // Notes on the sheet:
  //   CARRY ADDER
  //   (full adder with cin = 1)
  //   out1 = XNOR(a,b)
  //   out2 = OR(a,b)
endmodule

module MUX_ARRAY (
  input  C1,
  input  C2,
  input  in,
  input  _01,
  input  _00,
  input  _11,
  input  _10,
  input  _21,
  input  _20,
  input  _31,
  input  _30,
  input  D1,
  input  D2,
  output _02,
  output _12,
  output _22,
  output _32,
  output out
);

  wire transistor_2_out, transistor_5_out, transistor_7_out, transistor_8_out, transistor_9_out,
       transistor_13_out, transistor_14_out, transistor_15_out, transistor_18_out, transistor_21_out,
       transistor_26_out, transistor_29_out, transistor_31_out, transistor_32_out, transistor_33_out,
       transistor_37_out, transistor_38_out, transistor_40_out, transistor_43_out, transistor_45_out,
       transistor_49_out;

  Transistor #(.gate("br")) transistor_1 (.in(transistor_7_out), .out(_02), .gate(transistor_9_out));
  Transistor #(.gate("br")) transistor_2 (.in(1'b1), .out(transistor_2_out), .gate(in));
  Transistor #(.gate("br")) transistor_3 (.in(transistor_2_out), .out(_02), .gate(D1));
  Transistor #(.\type ("n")) transistor_4 (.in(transistor_5_out), .out(_02), .gate(D2));
  Transistor #(.\type ("n")) transistor_5 (.in(1'b0), .out(transistor_5_out), .gate(in));
  Transistor #(.\type ("n")) transistor_6 (.in(transistor_8_out), .out(_02), .gate(D1));
  Transistor #(.gate("br")) transistor_7 (.in(1'b1), .out(transistor_7_out), .gate(D2));
  Transistor #(.\type ("n")) transistor_8 (.in(1'b0), .out(transistor_8_out), .gate(transistor_9_out));
  Transistor #(.gate("br")) transistor_9 (.in(_01), .out(transistor_9_out), .gate(C1));
  Transistor #(.gate("br")) transistor_10 (.in(_00), .out(transistor_9_out), .gate(C2));
  Transistor #(.\type ("n")) transistor_11 (.in(_01), .out(transistor_9_out), .gate(C2));
  Transistor #(.\type ("n")) transistor_12 (.in(_00), .out(transistor_9_out), .gate(C1));
  Transistor #(.gate("br")) transistor_13 (.in(1'b1), .out(transistor_13_out), .gate(transistor_9_out));
  Transistor #(.\type ("n")) transistor_14 (.in(1'b0), .out(transistor_14_out), .gate(transistor_9_out));
  Transistor #(.gate("br")) transistor_15 (.in(1'b1), .out(transistor_15_out), .gate(D2));
  Transistor #(.gate("br")) transistor_16 (.in(transistor_13_out), .out(_12), .gate(D1));
  Transistor #(.gate("br")) transistor_17 (.in(transistor_15_out), .out(_12), .gate(transistor_21_out));
  Transistor #(.\type ("n")) transistor_18 (.in(1'b0), .out(transistor_18_out), .gate(transistor_21_out));
  Transistor #(.\type ("n")) transistor_19 (.in(transistor_18_out), .out(_12), .gate(D1));
  Transistor #(.\type ("n")) transistor_20 (.in(transistor_14_out), .out(_12), .gate(D2));
  Transistor #(.gate("br")) transistor_21 (.in(_11), .out(transistor_21_out), .gate(C1));
  Transistor #(.gate("br")) transistor_22 (.in(_10), .out(transistor_21_out), .gate(C2));
  Transistor #(.\type ("n")) transistor_23 (.in(_11), .out(transistor_21_out), .gate(C2));
  Transistor #(.\type ("n")) transistor_24 (.in(_10), .out(transistor_21_out), .gate(C1));
  Transistor #(.gate("br")) transistor_25 (.in(transistor_31_out), .out(_22), .gate(transistor_33_out));
  Transistor #(.gate("br")) transistor_26 (.in(1'b1), .out(transistor_26_out), .gate(transistor_21_out));
  Transistor #(.gate("br")) transistor_27 (.in(transistor_26_out), .out(_22), .gate(D1));
  Transistor #(.\type ("n")) transistor_28 (.in(transistor_32_out), .out(_22), .gate(D1));
  Transistor #(.\type ("n")) transistor_29 (.in(1'b0), .out(transistor_29_out), .gate(transistor_21_out));
  Transistor #(.\type ("n")) transistor_30 (.in(transistor_29_out), .out(_22), .gate(D2));
  Transistor #(.gate("br")) transistor_31 (.in(1'b1), .out(transistor_31_out), .gate(D2));
  Transistor #(.\type ("n")) transistor_32 (.in(1'b0), .out(transistor_32_out), .gate(transistor_33_out));
  Transistor #(.gate("br")) transistor_33 (.in(_21), .out(transistor_33_out), .gate(C1));
  Transistor #(.gate("br")) transistor_34 (.in(_20), .out(transistor_33_out), .gate(C2));
  Transistor #(.\type ("n")) transistor_35 (.in(_21), .out(transistor_33_out), .gate(C2));
  Transistor #(.\type ("n")) transistor_36 (.in(_20), .out(transistor_33_out), .gate(C1));
  Transistor #(.gate("br")) transistor_37 (.in(1'b1), .out(transistor_37_out), .gate(transistor_33_out));
  Transistor #(.\type ("n")) transistor_38 (.in(1'b0), .out(transistor_38_out), .gate(transistor_33_out));
  Transistor #(.gate("br")) transistor_39 (.in(transistor_37_out), .out(_32), .gate(D1));
  Transistor #(.gate("br")) transistor_40 (.in(1'b1), .out(transistor_40_out), .gate(D2));
  Transistor #(.gate("br")) transistor_41 (.in(transistor_40_out), .out(_32), .gate(transistor_45_out));
  Transistor #(.\type ("n")) transistor_42 (.in(transistor_38_out), .out(_32), .gate(D2));
  Transistor #(.\type ("n")) transistor_43 (.in(1'b0), .out(transistor_43_out), .gate(transistor_45_out));
  Transistor #(.\type ("n")) transistor_44 (.in(transistor_43_out), .out(_32), .gate(D1));
  Transistor #(.gate("br")) transistor_45 (.in(_30), .out(transistor_45_out), .gate(C2));
  Transistor #(.gate("br")) transistor_46 (.in(_31), .out(transistor_45_out), .gate(C1));
  Transistor #(.\type ("n")) transistor_47 (.in(_31), .out(transistor_45_out), .gate(C2));
  Transistor #(.\type ("n")) transistor_48 (.in(_30), .out(transistor_45_out), .gate(C1));
  Transistor #(.gate("br")) transistor_49 (.in(1'b1), .out(transistor_49_out), .gate(transistor_45_out));
  Transistor #(.\type ("n")) transistor_50 (.in(1'b0), .out(transistor_49_out), .gate(transistor_45_out));
  Transistor #(.gate("br")) transistor_51 (.in(1'b1), .out(out), .gate(transistor_49_out));
  Transistor #(.\type ("n")) transistor_52 (.in(1'b0), .out(out), .gate(transistor_49_out));

  // Notes on the sheet:
  //   MUX ARRAY
endmodule

module MUX_ARRAY_LOGIC (
  input  C1,
  input  D1,
  input  in,
  input  _01,
  input  _00,
  input  _11,
  input  _10,
  input  _21,
  input  _20,
  input  _31,
  input  _30,
  output _02,
  output _12,
  output _22,
  output _32,
  output out
);

  wire multiplexer_1_out, multiplexer_2_out, multiplexer_3_out, multiplexer_5_out, multiplexer_6_out,
       multiplexer_7_out, multiplexer_8_out;

  Multiplexer multiplexer_1 (.in0(_01), .in1(_00), .out(multiplexer_1_out), .sel(C1));  // open: en
  Multiplexer multiplexer_2 (.in0(_11), .in1(_10), .out(multiplexer_2_out), .sel(C1));  // open: en
  Multiplexer multiplexer_3 (.in0(_21), .in1(_20), .out(multiplexer_3_out), .sel(C1));  // open: en
  Multiplexer multiplexer_4 (.in0(_31), .in1(_30), .out(out), .sel(C1));  // open: en
  Multiplexer multiplexer_5 (.in0(in), .in1(multiplexer_1_out), .out(multiplexer_5_out), .sel(D1));  // open: en
  Multiplexer multiplexer_6 (
    .in0(multiplexer_1_out), .in1(multiplexer_2_out), .out(multiplexer_6_out), .sel(D1));  // open: en
  Multiplexer multiplexer_7 (
    .in0(multiplexer_2_out), .in1(multiplexer_3_out), .out(multiplexer_7_out), .sel(D1));  // open: en
  Multiplexer multiplexer_8 (.in0(multiplexer_3_out), .in1(out), .out(multiplexer_8_out), .sel(D1));  // open: en
  not not_1 (_02, multiplexer_5_out);
  not not_2 (_12, multiplexer_6_out);
  not not_3 (_22, multiplexer_7_out);
  not not_4 (_32, multiplexer_8_out);

  // Notes on the sheet:
  //   MUX ARRAY
endmodule

module WS1 (
  input  in5,
  input  in4,
  input  in3,
  input  in2,
  input  in1,
  output out2,
  output out3,
  output out1
);

  wire transistor_1_out, transistor_3_out, transistor_5_out, transistor_6_out, transistor_9_out,
       transistor_11_out, transistor_13_out, transistor_15_out, transistor_19_out, transistor_23_out,
       transistor_27_out, transistor_39_out, transistor_43_out;

  Transistor #(.gate("br")) transistor_1 (.in(1'b1), .out(transistor_1_out), .gate(transistor_3_out));
  Transistor #(.\type ("n")) transistor_2 (.in(1'b0), .out(transistor_1_out), .gate(transistor_3_out));
  Transistor #(.gate("br")) transistor_3 (.in(1'b1), .out(transistor_3_out), .gate(in5));
  Transistor #(.\type ("n")) transistor_4 (.in(1'b0), .out(transistor_3_out), .gate(in5));
  Transistor #(.gate("br")) transistor_5 (.in(in4), .out(transistor_5_out), .gate(transistor_3_out));
  Transistor #(.gate("br")) transistor_6 (.in(1'b1), .out(transistor_6_out), .gate(in4));
  Transistor #(.gate("br")) transistor_7 (.in(transistor_6_out), .out(transistor_5_out), .gate(in5));
  Transistor #(.\type ("n")) transistor_8 (.in(in4), .out(transistor_5_out), .gate(in5));
  Transistor #(.\type ("n")) transistor_9 (.in(1'b0), .out(transistor_9_out), .gate(in4));
  Transistor #(.\type ("n")) transistor_10 (.in(transistor_9_out), .out(transistor_5_out), .gate(transistor_3_out));
  Transistor #(.gate("br")) transistor_11 (.in(1'b1), .out(transistor_11_out), .gate(transistor_5_out));
  Transistor #(.\type ("n")) transistor_12 (.in(1'b0), .out(transistor_11_out), .gate(transistor_5_out));
  Transistor #(.gate("br")) transistor_13 (.in(1'b1), .out(transistor_13_out), .gate(transistor_11_out));
  Transistor #(.\type ("n")) transistor_14 (.in(1'b0), .out(transistor_13_out), .gate(transistor_11_out));
  Transistor transistor_15 (.in(in3), .out(transistor_15_out), .gate(transistor_13_out));
  Transistor #(.gate("br")) transistor_16 (.in(transistor_13_out), .out(transistor_15_out), .gate(in3));
  Transistor #(.\type ("n")) transistor_17 (.in(transistor_11_out), .out(transistor_15_out), .gate(in3));
  Transistor #(.\type ("n"), .gate("br")) transistor_18 (.in(in3), .out(transistor_15_out), .gate(transistor_11_out));
  Transistor #(.gate("br")) transistor_19 (.in(transistor_1_out), .out(transistor_19_out), .gate(transistor_11_out));
  Transistor #(.gate("br")) transistor_20 (.in(in3), .out(transistor_19_out), .gate(transistor_5_out));
  Transistor #(.\type ("n")) transistor_21 (.in(in3), .out(transistor_19_out), .gate(transistor_11_out));
  Transistor #(.\type ("n")) transistor_22 (.in(transistor_1_out), .out(transistor_19_out), .gate(transistor_5_out));
  Transistor #(.gate("br")) transistor_23 (.in(in2), .out(transistor_23_out), .gate(transistor_5_out));
  Transistor #(.gate("br")) transistor_24 (.in(transistor_1_out), .out(transistor_23_out), .gate(transistor_11_out));
  Transistor #(.\type ("n")) transistor_25 (.in(transistor_1_out), .out(transistor_23_out), .gate(transistor_5_out));
  Transistor #(.\type ("n")) transistor_26 (.in(in2), .out(transistor_23_out), .gate(transistor_11_out));
  Transistor #(.gate("br")) transistor_27 (.in(transistor_13_out), .out(transistor_27_out), .gate(in2));
  Transistor transistor_28 (.in(in2), .out(transistor_27_out), .gate(transistor_13_out));
  Transistor #(.\type ("n"), .gate("br")) transistor_29 (.in(in2), .out(transistor_27_out), .gate(transistor_11_out));
  Transistor #(.\type ("n")) transistor_30 (.in(transistor_11_out), .out(transistor_27_out), .gate(in2));
  Transistor #(.gate("br")) transistor_31 (.in(1'b1), .out(out2), .gate(transistor_23_out));
  Transistor #(.gate("br")) transistor_32 (.in(1'b1), .out(out2), .gate(transistor_23_out));
  Transistor #(.\type ("n")) transistor_33 (.in(1'b0), .out(out2), .gate(transistor_23_out));
  Transistor #(.\type ("n")) transistor_34 (.in(1'b0), .out(out2), .gate(transistor_23_out));
  Transistor #(.gate("br")) transistor_35 (.in(1'b1), .out(out3), .gate(transistor_19_out));
  Transistor #(.gate("br")) transistor_36 (.in(1'b1), .out(out3), .gate(transistor_19_out));
  Transistor #(.\type ("n")) transistor_37 (.in(1'b0), .out(out3), .gate(transistor_19_out));
  Transistor #(.\type ("n")) transistor_38 (.in(1'b0), .out(out3), .gate(transistor_19_out));
  Transistor #(.gate("br")) transistor_39 (.in(transistor_15_out), .out(transistor_39_out), .gate(transistor_43_out));
  Transistor #(.gate("br")) transistor_40 (.in(transistor_27_out), .out(transistor_39_out), .gate(in1));
  Transistor #(.\type ("n")) transistor_41 (.in(transistor_27_out), .out(transistor_39_out), .gate(transistor_43_out));
  Transistor #(.\type ("n")) transistor_42 (.in(transistor_15_out), .out(transistor_39_out), .gate(in1));
  Transistor #(.gate("br")) transistor_43 (.in(1'b1), .out(transistor_43_out), .gate(in1));
  Transistor #(.\type ("n")) transistor_44 (.in(1'b0), .out(transistor_43_out), .gate(in1));
  Transistor #(.gate("br")) transistor_45 (.in(1'b1), .out(out1), .gate(transistor_39_out));
  Transistor #(.gate("br")) transistor_46 (.in(1'b1), .out(out1), .gate(transistor_39_out));
  Transistor #(.\type ("n")) transistor_47 (.in(1'b0), .out(out1), .gate(transistor_39_out));
  Transistor #(.\type ("n")) transistor_48 (.in(1'b0), .out(out1), .gate(transistor_39_out));

  // Notes on the sheet:
  //   in5'
  //   XNOR
  //   x
  //   !x
  //   x2
  //   s1
  //   s0
endmodule

module WS2 (
  input  in5,
  input  in4,
  input  in3,
  input  in2,
  input  in1,
  output out2,
  output out3,
  output out1
);

  wire transistor_1_out, transistor_3_out, transistor_5_out, transistor_6_out, transistor_7_out,
       transistor_11_out, transistor_13_out, transistor_15_out, transistor_19_out, transistor_23_out,
       transistor_27_out, transistor_39_out, transistor_43_out;

  Transistor #(.gate("br")) transistor_1 (.in(1'b1), .out(transistor_1_out), .gate(in5));
  Transistor #(.\type ("n")) transistor_2 (.in(1'b0), .out(transistor_1_out), .gate(in5));
  Transistor #(.gate("br")) transistor_3 (.in(1'b1), .out(transistor_3_out), .gate(in5));
  Transistor #(.\type ("n")) transistor_4 (.in(1'b0), .out(transistor_3_out), .gate(in5));
  Transistor #(.gate("br")) transistor_5 (.in(1'b1), .out(transistor_5_out), .gate(in4));
  Transistor #(.\type ("n")) transistor_6 (.in(1'b0), .out(transistor_6_out), .gate(in4));
  Transistor #(.gate("br")) transistor_7 (.in(transistor_5_out), .out(transistor_7_out), .gate(in5));
  Transistor #(.gate("br")) transistor_8 (.in(in4), .out(transistor_7_out), .gate(transistor_3_out));
  Transistor #(.\type ("n")) transistor_9 (.in(transistor_6_out), .out(transistor_7_out), .gate(transistor_3_out));
  Transistor #(.\type ("n")) transistor_10 (.in(in4), .out(transistor_7_out), .gate(in5));
  Transistor #(.gate("br")) transistor_11 (.in(1'b1), .out(transistor_11_out), .gate(transistor_7_out));
  Transistor #(.\type ("n")) transistor_12 (.in(1'b0), .out(transistor_11_out), .gate(transistor_7_out));
  Transistor #(.gate("br")) transistor_13 (.in(1'b1), .out(transistor_13_out), .gate(transistor_11_out));
  Transistor #(.\type ("n")) transistor_14 (.in(1'b0), .out(transistor_13_out), .gate(transistor_11_out));
  Transistor #(.gate("br")) transistor_15 (.in(transistor_11_out), .out(transistor_15_out), .gate(in3));
  Transistor #(.\type ("n")) transistor_16 (.in(transistor_13_out), .out(transistor_15_out), .gate(in3));
  Transistor #(.gate("br")) transistor_17 (.in(in3), .out(transistor_15_out), .gate(transistor_11_out));
  Transistor #(.\type ("n")) transistor_18 (.in(in3), .out(transistor_15_out), .gate(transistor_13_out));
  Transistor #(.gate("br")) transistor_19 (.in(transistor_1_out), .out(transistor_19_out), .gate(transistor_11_out));
  Transistor #(.gate("br")) transistor_20 (.in(in3), .out(transistor_19_out), .gate(transistor_7_out));
  Transistor #(.\type ("n")) transistor_21 (.in(in3), .out(transistor_19_out), .gate(transistor_11_out));
  Transistor #(.\type ("n")) transistor_22 (.in(transistor_1_out), .out(transistor_19_out), .gate(transistor_7_out));
  Transistor #(.gate("br")) transistor_23 (.in(transistor_1_out), .out(transistor_23_out), .gate(transistor_11_out));
  Transistor #(.gate("br")) transistor_24 (.in(in2), .out(transistor_23_out), .gate(transistor_7_out));
  Transistor #(.\type ("n")) transistor_25 (.in(in2), .out(transistor_23_out), .gate(transistor_11_out));
  Transistor #(.\type ("n")) transistor_26 (.in(transistor_1_out), .out(transistor_23_out), .gate(transistor_7_out));
  Transistor #(.gate("br")) transistor_27 (.in(transistor_11_out), .out(transistor_27_out), .gate(in2));
  Transistor #(.gate("br")) transistor_28 (.in(in2), .out(transistor_27_out), .gate(transistor_11_out));
  Transistor #(.\type ("n")) transistor_29 (.in(transistor_13_out), .out(transistor_27_out), .gate(in2));
  Transistor #(.\type ("n")) transistor_30 (.in(in2), .out(transistor_27_out), .gate(transistor_13_out));
  Transistor #(.gate("br")) transistor_31 (.in(1'b1), .out(out2), .gate(transistor_23_out));
  Transistor #(.gate("br")) transistor_32 (.in(1'b1), .out(out2), .gate(transistor_23_out));
  Transistor #(.\type ("n")) transistor_33 (.in(1'b0), .out(out2), .gate(transistor_23_out));
  Transistor #(.\type ("n")) transistor_34 (.in(1'b0), .out(out2), .gate(transistor_23_out));
  Transistor #(.gate("br")) transistor_35 (.in(1'b1), .out(out3), .gate(transistor_19_out));
  Transistor #(.gate("br")) transistor_36 (.in(1'b1), .out(out3), .gate(transistor_19_out));
  Transistor #(.\type ("n")) transistor_37 (.in(1'b0), .out(out3), .gate(transistor_19_out));
  Transistor #(.\type ("n")) transistor_38 (.in(1'b0), .out(out3), .gate(transistor_19_out));
  Transistor #(.gate("br")) transistor_39 (.in(transistor_27_out), .out(transistor_39_out), .gate(in1));
  Transistor #(.gate("br")) transistor_40 (.in(transistor_15_out), .out(transistor_39_out), .gate(transistor_43_out));
  Transistor #(.\type ("n")) transistor_41 (.in(transistor_15_out), .out(transistor_39_out), .gate(in1));
  Transistor #(.\type ("n")) transistor_42 (.in(transistor_27_out), .out(transistor_39_out), .gate(transistor_43_out));
  Transistor #(.gate("br")) transistor_43 (.in(1'b1), .out(transistor_43_out), .gate(in1));
  Transistor #(.\type ("n")) transistor_44 (.in(1'b0), .out(transistor_43_out), .gate(in1));
  Transistor #(.gate("br")) transistor_45 (.in(1'b1), .out(out1), .gate(transistor_39_out));
  Transistor #(.gate("br")) transistor_46 (.in(1'b1), .out(out1), .gate(transistor_39_out));
  Transistor #(.\type ("n")) transistor_47 (.in(1'b0), .out(out1), .gate(transistor_39_out));
  Transistor #(.\type ("n")) transistor_48 (.in(1'b0), .out(out1), .gate(transistor_39_out));

  // Notes on the sheet:
  //   !in5'
  //   XNOR
  //   x
  //   !x
  //   x2
  //   s1
  //   s0
endmodule

module IMUX (
  input  sel,
  input  b___in0,
  input  c___in1,
  output out
);

  wire transistor_2_out, transistor_3_out;

  Transistor #(.gate("br")) transistor_1 (.in(1'b1), .out(out), .gate(transistor_3_out));
  Transistor #(.gate("br")) transistor_2 (.in(1'b1), .out(transistor_2_out), .gate(sel));
  Transistor #(.gate("br")) transistor_3 (.in(b___in0), .out(transistor_3_out), .gate(sel));
  Transistor #(.gate("br")) transistor_4 (.in(c___in1), .out(transistor_3_out), .gate(transistor_2_out));
  Transistor #(.\type ("n")) transistor_5 (.in(1'b0), .out(out), .gate(transistor_3_out));
  Transistor #(.\type ("n")) transistor_6 (.in(1'b0), .out(transistor_2_out), .gate(sel));
  Transistor #(.\type ("n")) transistor_7 (.in(b___in0), .out(transistor_3_out), .gate(transistor_2_out));
  Transistor #(.\type ("n")) transistor_8 (.in(c___in1), .out(transistor_3_out), .gate(sel));

  // Notes on the sheet:
  //   INVERTING MUX
endmodule

module _12_OAI (
  input  a,
  input  b,
  input  c,
  output out
);

  wire transistor_3_out, transistor_5_out;

  Transistor #(.gate("br")) transistor_1 (.in(1'b1), .out(out), .gate(a));
  Transistor #(.gate("br")) transistor_2 (.in(transistor_3_out), .out(out), .gate(b));
  Transistor #(.gate("br")) transistor_3 (.in(1'b1), .out(transistor_3_out), .gate(c));
  Transistor #(.\type ("n")) transistor_4 (.in(transistor_5_out), .out(out), .gate(a));
  Transistor #(.\type ("n")) transistor_5 (.in(1'b0), .out(transistor_5_out), .gate(b));
  Transistor #(.\type ("n")) transistor_6 (.in(1'b0), .out(transistor_5_out), .gate(c));

  // Notes on the sheet:
  //   12-OAI
  //   out = ~ (a & (b|c))
endmodule

module MUX_CONTROL (
  input  _11,
  input  _10,
  input  _09,
  input  _08,
  input  _07,
  input  _06,
  input  _05,
  input  _04,
  input  _03,
  input  _02,
  input  _01,
  input  _00,
  output L5_D2,
  output L5_D1,
  output L4_D2,
  output L4_D1,
  output L3_D2,
  output L3_D1,
  output L2_D2,
  output L2_D1,
  output L1_D2,
  output L1_D1,
  output L0_D2,
  output L0_D1
);

  wire nand_1_out, nand_2_out, nand_3_out, nand_4_out, nand_5_out, nand_6_out, xnor_1_out, xnor_2_out,
       xnor_3_out, xnor_4_out, xnor_5_out, xnor_6_out, xor_1_out, xor_2_out, xor_3_out, xor_4_out, xor_5_out,
       xor_6_out;

  xor xor_1 (xor_1_out, _11, _10);
  xnor xnor_1 (xnor_1_out, _10, _09);
  xor xor_2 (xor_2_out, _09, _08);
  xnor xnor_2 (xnor_2_out, _08, _07);
  xor xor_3 (xor_3_out, _07, _06);
  xnor xnor_3 (xnor_3_out, _06, _05);
  xor xor_4 (xor_4_out, _05, _04);
  xnor xnor_4 (xnor_4_out, _04, _03);
  xor xor_5 (xor_5_out, _03, _02);
  xnor xnor_5 (xnor_5_out, _02, _01);
  xor xor_6 (xor_6_out, _01, _00);
  xnor xnor_6 (xnor_6_out, _00, 1'b0);
  nand nand_1 (nand_1_out, xor_1_out, xnor_1_out);
  nand nand_2 (nand_2_out, xor_2_out, xnor_2_out);
  nand nand_3 (nand_3_out, xor_3_out, xnor_3_out);
  nand nand_4 (nand_4_out, xor_4_out, xnor_4_out);
  nand nand_5 (nand_5_out, xor_5_out, xnor_5_out);
  nand nand_6 (nand_6_out, xor_6_out, xnor_6_out);
  not not_1 (L5_D2, nand_1_out);
  not not_2 (L5_D1, xnor_1_out);
  not not_3 (L4_D2, nand_2_out);
  not not_4 (L4_D1, xnor_2_out);
  not not_5 (L3_D2, nand_3_out);
  not not_6 (L3_D1, xnor_3_out);
  not not_7 (L2_D2, nand_4_out);
  not not_8 (L2_D1, xnor_4_out);
  not not_9 (L1_D2, nand_5_out);
  not not_10 (L1_D1, xnor_5_out);
  not not_11 (L0_D2, nand_6_out);
  not not_12 (L0_D1, xnor_6_out);
endmodule

module MUXs (
  input  L5_C1,
  input  L5_C2,
  input  L5_D1,
  input  L5_D2,
  input  L4_C1,
  input  L4_C2,
  input  L4_D1,
  input  L4_D2,
  input  L3_C1,
  input  L3_C2,
  input  L3_D1,
  input  L3_D2,
  input  L2_C1,
  input  L2_C2,
  input  L2_D1,
  input  L2_D2,
  input  L1_C1,
  input  L1_C2,
  input  L1_D1,
  input  L1_D2,
  input  L0_C1,
  input  L0_C2,
  input  L0_D1,
  input  L0_D2,
  input  S0,
  input  S1,
  input  S2,
  input  S3,
  input  S4,
  input  S5,
  input  S6,
  input  S7,
  input  S8,
  input  S9,
  input  S10,
  input  S11,
  input  S12,
  output L5_00,
  output L5_01,
  output L5_02,
  output L5_03,
  output L5_04,
  output L5_05,
  output L5_06,
  output L5_07,
  output L5_08,
  output L5_09,
  output L5_10,
  output L5_11,
  output L5_12,
  output L5_13,
  output L4_00,
  output L4_01,
  output L4_02,
  output L4_03,
  output L4_04,
  output L4_05,
  output L4_06,
  output L4_07,
  output L4_08,
  output L4_09,
  output L4_10,
  output L4_11,
  output L4_12,
  output L4_13,
  output L3_00,
  output L3_01,
  output L3_02,
  output L3_03,
  output L3_04,
  output L3_05,
  output L3_06,
  output L3_07,
  output L3_08,
  output L3_09,
  output L3_10,
  output L3_11,
  output L3_12,
  output L3_13,
  output L2_00,
  output L2_01,
  output L2_02,
  output L2_03,
  output L2_04,
  output L2_05,
  output L2_06,
  output L2_07,
  output L2_08,
  output L2_09,
  output L2_10,
  output L2_11,
  output L2_12,
  output L2_13,
  output L1_00,
  output L1_01,
  output L1_02,
  output L1_03,
  output L1_04,
  output L1_05,
  output L1_06,
  output L1_07,
  output L1_08,
  output L1_09,
  output L1_10,
  output L1_11,
  output L1_12,
  output L1_13,
  output L0_00,
  output L0_01,
  output L0_02,
  output L0_03,
  output L0_04,
  output L0_05,
  output L0_06,
  output L0_07,
  output L0_08,
  output L0_09,
  output L0_10,
  output L0_11,
  output L0_12,
  output L0_13
);

  wire mux_array_1_out, mux_array_2_out, mux_array_3_out, mux_array_4_out, mux_array_5_out, mux_array_6_out,
       mux_array_7_out, mux_array_8_out, mux_array_9_out, mux_array_10_out, mux_array_11_out,
       mux_array_12_out, mux_array_13_out, mux_array_14_out, mux_array_15_out, mux_array_16_out,
       mux_array_17_out, mux_array_18_out, not_1_out, not_2_out, not_3_out, not_4_out, not_5_out, not_6_out,
       not_7_out, not_8_out, not_9_out, not_10_out, not_11_out, not_12_out, not_13_out, not_14_out;

  not not_1 (not_1_out, S0);
  not not_2 (not_2_out, S1);
  MUX_ARRAY mux_array_1 (
    .C1(L5_C1), .C2(L5_C2), .in(1'b1), .D1(L5_D1), .D2(L5_D2), .out(mux_array_1_out), ._22(L5_00),
    ._32(L5_01), ._01(1'b0), ._00(1'b0), ._11(L5_C2), ._10(L5_C2), ._21(not_1_out), ._20(S0),
    ._31(not_2_out), ._30(S1));  // open: _02, _12
  MUX_ARRAY mux_array_2 (
    .C1(L4_C1), .C2(L4_C2), .in(1'b1), .D1(L4_D1), .D2(L4_D2), .out(mux_array_2_out), ._22(L4_00),
    ._32(L4_01), ._01(1'b0), ._00(1'b0), ._11(L4_C2), ._10(L4_C2), ._21(not_1_out), ._20(S0),
    ._31(not_2_out), ._30(S1));  // open: _02, _12
  MUX_ARRAY mux_array_3 (
    .C1(L3_C1), .C2(L3_C2), .in(1'b1), .D1(L3_D1), .D2(L3_D2), .out(mux_array_3_out), ._22(L3_00),
    ._32(L3_01), ._01(1'b0), ._00(1'b0), ._11(L3_C2), ._10(L3_C2), ._21(not_1_out), ._20(S0),
    ._31(not_2_out), ._30(S1));  // open: _02, _12
  MUX_ARRAY mux_array_4 (
    .C1(L2_C1), .C2(L2_C2), .in(1'b1), .D1(L2_D1), .D2(L2_D2), .out(mux_array_4_out), ._22(L2_00),
    ._32(L2_01), ._01(1'b0), ._00(1'b0), ._11(L2_C2), ._10(L2_C2), ._21(not_1_out), ._20(S0),
    ._31(not_2_out), ._30(S1));  // open: _02, _12
  MUX_ARRAY mux_array_5 (
    .C1(L1_C1), .C2(L1_C2), .in(1'b1), .D1(L1_D1), .D2(L1_D2), .out(mux_array_5_out), ._22(L1_00),
    ._32(L1_01), ._01(1'b0), ._00(1'b0), ._11(L1_C2), ._10(L1_C2), ._21(not_1_out), ._20(S0),
    ._31(not_2_out), ._30(S1));  // open: _02, _12
  MUX_ARRAY mux_array_6 (
    .C1(L0_C1), .C2(L0_C2), .in(1'b1), .D1(L0_D1), .D2(L0_D2), .out(mux_array_6_out), ._22(L0_00),
    ._32(L0_01), ._01(1'b0), ._00(1'b0), ._11(L0_C2), ._10(L0_C2), ._21(not_1_out), ._20(S0),
    ._31(not_2_out), ._30(S1));  // open: _02, _12
  not not_3 (not_3_out, S2);
  not not_4 (not_4_out, S3);
  not not_5 (not_5_out, S4);
  not not_6 (not_6_out, S5);
  MUX_ARRAY mux_array_7 (
    .C1(L5_C1), .C2(L5_C2), .in(mux_array_1_out), .D1(L5_D1), .D2(L5_D2), .out(mux_array_7_out), ._02(L5_02),
    ._12(L5_03), ._22(L5_04), ._32(L5_05), ._01(S2), ._00(not_3_out), ._11(not_4_out), ._10(S3),
    ._21(not_5_out), ._20(S4), ._31(not_6_out), ._30(S5));
  MUX_ARRAY mux_array_8 (
    .C1(L4_C1), .C2(L4_C2), .in(mux_array_2_out), .D1(L4_D1), .D2(L4_D2), .out(mux_array_8_out), ._02(L4_02),
    ._12(L4_03), ._22(L4_04), ._32(L4_05), ._01(S2), ._00(not_3_out), ._11(not_4_out), ._10(S3),
    ._21(not_5_out), ._20(S4), ._31(not_6_out), ._30(S5));
  MUX_ARRAY mux_array_9 (
    .C1(L3_C1), .C2(L3_C2), .in(mux_array_3_out), .D1(L3_D1), .D2(L3_D2), .out(mux_array_9_out), ._02(L3_02),
    ._12(L3_03), ._22(L3_04), ._32(L3_05), ._01(S2), ._00(not_3_out), ._11(not_4_out), ._10(S3),
    ._21(not_5_out), ._20(S4), ._31(not_6_out), ._30(S5));
  MUX_ARRAY mux_array_10 (
    .C1(L2_C1), .C2(L2_C2), .in(mux_array_4_out), .D1(L2_D1), .D2(L2_D2), .out(mux_array_10_out),
    ._02(L2_02), ._12(L2_03), ._22(L2_04), ._32(L2_05), ._01(S2), ._00(not_3_out), ._11(not_4_out), ._10(S3),
    ._21(not_5_out), ._20(S4), ._31(not_6_out), ._30(S5));
  MUX_ARRAY mux_array_11 (
    .C1(L1_C1), .C2(L1_C2), .in(mux_array_5_out), .D1(L1_D1), .D2(L1_D2), .out(mux_array_11_out),
    ._02(L1_02), ._12(L1_03), ._22(L1_04), ._32(L1_05), ._01(S2), ._00(not_3_out), ._11(not_4_out), ._10(S3),
    ._21(not_5_out), ._20(S4), ._31(not_6_out), ._30(S5));
  MUX_ARRAY mux_array_12 (
    .C1(L0_C1), .C2(L0_C2), .in(mux_array_6_out), .D1(L0_D1), .D2(L0_D2), .out(mux_array_12_out),
    ._02(L0_02), ._12(L0_03), ._22(L0_04), ._32(L0_05), ._01(S2), ._00(not_3_out), ._11(not_4_out), ._10(S3),
    ._21(not_5_out), ._20(S4), ._31(not_6_out), ._30(S5));
  not not_7 (not_7_out, S6);
  not not_8 (not_8_out, S7);
  not not_9 (not_9_out, S8);
  MUX_ARRAY mux_array_13 (
    .C1(L5_C1), .C2(L5_C2), .in(mux_array_7_out), .D1(L5_D1), .D2(L5_D2), .out(mux_array_13_out),
    ._02(L5_06), ._12(L5_07), ._22(L5_08), ._32(L5_09), ._01(S6), ._00(not_7_out), ._11(not_8_out), ._10(S7),
    ._21(not_9_out), ._20(S8), ._31(not_10_out), ._30(S9));
  MUX_ARRAY mux_array_14 (
    .C1(L4_C1), .C2(L4_C2), .in(mux_array_8_out), .D1(L4_D1), .D2(L4_D2), .out(mux_array_14_out),
    ._02(L4_06), ._12(L4_07), ._22(L4_08), ._32(L4_09), ._01(S6), ._00(not_7_out), ._11(not_8_out), ._10(S7),
    ._21(not_9_out), ._20(S8), ._31(not_10_out), ._30(S9));
  MUX_ARRAY mux_array_15 (
    .C1(L3_C1), .C2(L3_C2), .in(mux_array_9_out), .D1(L3_D1), .D2(L3_D2), .out(mux_array_15_out),
    ._02(L3_06), ._12(L3_07), ._22(L3_08), ._32(L3_09), ._01(S6), ._00(not_7_out), ._11(not_8_out), ._10(S7),
    ._21(not_9_out), ._20(S8), ._31(not_10_out), ._30(S9));
  MUX_ARRAY mux_array_16 (
    .C1(L2_C1), .C2(L2_C2), .in(mux_array_10_out), .D1(L2_D1), .D2(L2_D2), .out(mux_array_16_out),
    ._02(L2_06), ._12(L2_07), ._22(L2_08), ._32(L2_09), ._01(S6), ._00(not_7_out), ._11(not_8_out), ._10(S7),
    ._21(not_9_out), ._20(S8), ._31(not_10_out), ._30(S9));
  MUX_ARRAY mux_array_17 (
    .C1(L1_C1), .C2(L1_C2), .in(mux_array_11_out), .D1(L1_D1), .D2(L1_D2), .out(mux_array_17_out),
    ._02(L1_06), ._12(L1_07), ._22(L1_08), ._32(L1_09), ._01(S6), ._00(not_7_out), ._11(not_8_out), ._10(S7),
    ._21(not_9_out), ._20(S8), ._31(not_10_out), ._30(S9));
  MUX_ARRAY mux_array_18 (
    .C1(L0_C1), .C2(L0_C2), .in(mux_array_12_out), .D1(L0_D1), .D2(L0_D2), .out(mux_array_18_out),
    ._02(L0_06), ._12(L0_07), ._22(L0_08), ._32(L0_09), ._01(S6), ._00(not_7_out), ._11(not_8_out), ._10(S7),
    ._21(not_9_out), ._20(S8), ._31(not_10_out), ._30(S9));
  not not_10 (not_10_out, S9);
  not not_11 (not_11_out, S10);
  not not_12 (not_12_out, S11);
  not not_13 (not_13_out, S12);
  MUX_ARRAY mux_array_19 (
    .C1(L5_C1), .C2(L5_C2), .in(mux_array_13_out), .D1(L5_D1), .D2(L5_D2), ._02(L5_10), ._12(L5_11),
    ._22(L5_12), ._32(L5_13), ._01(S10), ._00(not_11_out), ._11(not_12_out), ._10(S11), ._21(not_13_out),
    ._20(S12), ._31(not_14_out), ._30(S12));  // open: out
  MUX_ARRAY mux_array_20 (
    .C1(L4_C1), .C2(L4_C2), .in(mux_array_14_out), .D1(L4_D1), .D2(L4_D2), ._02(L4_10), ._12(L4_11),
    ._22(L4_12), ._32(L4_13), ._01(S10), ._00(not_11_out), ._11(not_12_out), ._10(S11), ._21(not_13_out),
    ._20(S12), ._31(not_14_out), ._30(S12));  // open: out
  MUX_ARRAY mux_array_21 (
    .C1(L3_C1), .C2(L3_C2), .in(mux_array_15_out), .D1(L3_D1), .D2(L3_D2), ._02(L3_10), ._12(L3_11),
    ._22(L3_12), ._32(L3_13), ._01(S10), ._00(not_11_out), ._11(not_12_out), ._10(S11), ._21(not_13_out),
    ._20(S12), ._31(not_14_out), ._30(S12));  // open: out
  MUX_ARRAY mux_array_22 (
    .C1(L2_C1), .C2(L2_C2), .in(mux_array_16_out), .D1(L2_D1), .D2(L2_D2), ._02(L2_10), ._12(L2_11),
    ._22(L2_12), ._32(L2_13), ._01(S10), ._00(not_11_out), ._11(not_12_out), ._10(S11), ._21(not_13_out),
    ._20(S12), ._31(not_14_out), ._30(S12));  // open: out
  MUX_ARRAY mux_array_23 (
    .C1(L1_C1), .C2(L1_C2), .in(mux_array_17_out), .D1(L1_D1), .D2(L1_D2), ._02(L1_10), ._12(L1_11),
    ._22(L1_12), ._32(L1_13), ._01(S10), ._00(not_11_out), ._11(not_12_out), ._10(S11), ._21(not_13_out),
    ._20(S12), ._31(not_14_out), ._30(S12));  // open: out
  MUX_ARRAY mux_array_24 (
    .C1(L0_C1), .C2(L0_C2), .in(mux_array_18_out), .D1(L0_D1), .D2(L0_D2), ._02(L0_10), ._12(L0_11),
    ._22(L0_12), ._32(L0_13), ._01(S10), ._00(not_11_out), ._11(not_12_out), ._10(S11), ._21(not_13_out),
    ._20(S12), ._31(not_14_out), ._30(S12));  // open: out
  not not_14 (not_14_out, S12);
endmodule
