// Logisim project 3-MUX3X.circ as structural Verilog: 1 circuit, main circuit main
module main (
  input  s0,
  input  s1,
  input  in0,
  input  in1,
  input  in2,
  output out_6
);

  wire multiplexer_1_out, multiplexer_2_out, not_1_out, not_2_out, not_3_out;

  not not_1 (not_1_out, in0);
  not not_2 (not_2_out, in1);
  Multiplexer multiplexer_1 (.in0(not_1_out), .in1(not_2_out), .out(multiplexer_1_out), .sel(s0));  // open: en
  not not_3 (not_3_out, in2);
  Multiplexer multiplexer_2 (.in0(multiplexer_1_out), .in1(not_3_out), .out(multiplexer_2_out), .sel(s1));  // open: en
  not not_4 (out_6, multiplexer_2_out);
endmodule
