// Logisim project DFFR.circ as structural Verilog: 4 circuits, main circuit DFFR_trans
module DFFR_trans (
  input  CLK,
  input  nres,
  input  in,
  output out
);

  wire transistor_2_out, transistor_3_out, transistor_4_out, transistor_6_out, transistor_7_out,
       transistor_9_out, transistor_10_out, transistor_12_out, transistor_14_out, transistor_19_out,
       transistor_20_out, transistor_24_out, transistor_25_out;

  Transistor #(.gate("br")) transistor_1 (.in(1'b1), .out(out), .gate(transistor_4_out));
  Transistor #(.gate("br")) transistor_2 (.in(1'b1), .out(transistor_2_out), .gate(transistor_3_out));
  Transistor #(.gate("br")) transistor_3 (.in(1'b1), .out(transistor_3_out), .gate(CLK));
  Transistor #(.gate("br")) transistor_4 (.in(1'b1), .out(transistor_4_out), .gate(transistor_7_out));
  Transistor #(.gate("br")) transistor_5 (.in(1'b1), .out(transistor_4_out), .gate(nres));
  Transistor #(.gate("br")) transistor_6 (.in(1'b1), .out(transistor_6_out), .gate(transistor_4_out));
  Transistor #(.gate("br")) transistor_7 (.in(transistor_6_out), .out(transistor_7_out), .gate(transistor_2_out));
  Transistor #(.gate("br")) transistor_8 (.in(transistor_9_out), .out(transistor_7_out), .gate(transistor_3_out));
  Transistor #(.gate("br")) transistor_9 (.in(1'b1), .out(transistor_9_out), .gate(transistor_12_out));
  Transistor #(.gate("br")) transistor_10 (.in(1'b1), .out(transistor_10_out), .gate(nres));
  Transistor #(.gate("br")) transistor_11 (.in(1'b1), .out(transistor_10_out), .gate(transistor_9_out));
  Transistor #(.gate("br")) transistor_12 (.in(transistor_10_out), .out(transistor_12_out), .gate(transistor_3_out));
  Transistor #(.gate("br")) transistor_13 (.in(transistor_14_out), .out(transistor_12_out), .gate(transistor_2_out));
  Transistor #(.gate("br")) transistor_14 (.in(1'b1), .out(transistor_14_out), .gate(in));
  Transistor #(.\type ("n")) transistor_15 (.in(1'b0), .out(out), .gate(transistor_4_out));
  Transistor #(.\type ("n")) transistor_16 (.in(1'b0), .out(transistor_2_out), .gate(transistor_3_out));
  Transistor #(.\type ("n")) transistor_17 (.in(1'b0), .out(transistor_3_out), .gate(CLK));
  Transistor #(.\type ("n")) transistor_18 (.in(transistor_19_out), .out(transistor_4_out), .gate(transistor_7_out));
  Transistor #(.\type ("n")) transistor_19 (.in(1'b0), .out(transistor_19_out), .gate(nres));
  Transistor #(.\type ("n")) transistor_20 (.in(1'b0), .out(transistor_20_out), .gate(transistor_4_out));
  Transistor #(.\type ("n")) transistor_21 (.in(transistor_20_out), .out(transistor_7_out), .gate(transistor_3_out));
  Transistor #(.\type ("n")) transistor_22 (.in(transistor_9_out), .out(transistor_7_out), .gate(transistor_2_out));
  Transistor #(.\type ("n")) transistor_23 (.in(1'b0), .out(transistor_9_out), .gate(transistor_12_out));
  Transistor #(.\type ("n")) transistor_24 (.in(1'b0), .out(transistor_24_out), .gate(nres));
  Transistor #(.\type ("n")) transistor_25 (.in(transistor_24_out), .out(transistor_25_out), .gate(transistor_9_out));
  Transistor #(.\type ("n")) transistor_26 (.in(transistor_25_out), .out(transistor_12_out), .gate(transistor_2_out));
  Transistor #(.\type ("n")) transistor_27 (.in(transistor_14_out), .out(transistor_12_out), .gate(transistor_3_out));
  Transistor #(.\type ("n")) transistor_28 (.in(1'b0), .out(transistor_14_out), .gate(in));

  // Notes on the sheet:
  //   2
  //   1
endmodule

module DFFR_logic (
  input  clk,
  input  in,
  input  nres,
  output out_4
);

  wire multiplexer_1_out, multiplexer_2_out, nand_1_out, nand_2_out, not_1_out, not_2_out, not_3_out,
       not_4_out;

  not not_1 (not_1_out, clk);
  not not_2 (not_2_out, in);
  Multiplexer multiplexer_1 (.in0(nand_1_out), .in1(not_2_out), .out(multiplexer_1_out), .sel(not_1_out));  // open: en
  nand nand_1 (nand_1_out, not_3_out, nres);
  not not_3 (not_3_out, multiplexer_1_out);
  not not_4 (not_4_out, nand_2_out);
  Multiplexer multiplexer_2 (.in0(not_4_out), .in1(not_3_out), .out(multiplexer_2_out), .sel(clk));  // open: en
  nand nand_2 (nand_2_out, multiplexer_2_out, nres);
  not not_5 (out_4, nand_2_out);
endmodule

module NOR_AND (
  input  a,
  input  b,
  input  c,
  input  d,
  output out
);

  wire and_1_out, nor_1_out;

  and and_1 (and_1_out, c, d);
  nor nor_1 (nor_1_out, a, b);
  or or_1 (out, nor_1_out, and_1_out);
endmodule

module idct_counters (
  input  nRES,
  output out_2,
  output out_3,
  output out_4,
  output out_5,
  output out_6,
  output out_7,
  output out_8,
  output out_9,
  output out_10
);

  wire _0_2_out, _0_out, _2_out, _4_out, _6_out, clock_1_out, nor_and_1_out, nor_and_2_out, nor_and_3_out,
       not_1_out, or_1_out, or_2_out, or_3_out, or_4_out, or_5_out, or_6_out, or_7_out;

  not not_1 (not_1_out, out_2);
  or or_1 (or_1_out, not_1_out, out_3);
  or or_2 (or_2_out, or_1_out, out_4);
  or or_3 (or_3_out, or_2_out, out_5);
  or or_4 (or_4_out, or_3_out, out_6);
  or or_5 (or_5_out, or_4_out, out_7);
  buf or_6 (or_6_out, out_8);  // OR_Gate
  or or_7 (or_7_out, or_6_out, out_9);
  Clock #(.highDuration(4), .lowDuration(4)) clock_1 (.out(clock_1_out));
  NOR_AND _0 (.a(not_1_out), .b(out_3), .c(not_1_out), .d(out_3), .out(_0_out));
  NOR_AND _0_2 (.a(or_1_out), .b(out_4), .c(or_1_out), .d(out_4), .out(_0_2_out));
  NOR_AND nor_and_1 (.a(or_2_out), .b(out_5), .c(or_2_out), .d(out_5), .out(nor_and_1_out));
  NOR_AND _2 (.a(or_3_out), .b(out_6), .c(or_3_out), .d(out_6), .out(_2_out));
  NOR_AND nor_and_2 (.a(or_4_out), .b(out_7), .c(or_4_out), .d(out_7), .out(nor_and_2_out));
  NOR_AND _4 (.a(or_5_out), .b(out_8), .c(or_5_out), .d(out_8), .out(_4_out));
  NOR_AND nor_and_3 (.a(or_6_out), .b(out_9), .c(or_6_out), .d(out_9), .out(nor_and_3_out));
  NOR_AND _6 (.a(or_7_out), .b(out_10), .c(or_7_out), .d(out_10), .out(_6_out));
  DFFR_logic dffr_logic_1 (.clk(clock_1_out), .in(not_1_out), .nres(nRES), .out_4(out_2));
  DFFR_logic dffr_logic_2 (.clk(clock_1_out), .in(_0_out), .nres(nRES), .out_4(out_3));
  DFFR_logic dffr_logic_3 (.clk(clock_1_out), .in(_0_2_out), .nres(nRES), .out_4(out_4));
  DFFR_logic dffr_logic_4 (.clk(clock_1_out), .in(nor_and_1_out), .nres(nRES), .out_4(out_5));
  DFFR_logic dffr_logic_5 (.clk(clock_1_out), .in(_2_out), .nres(nRES), .out_4(out_6));
  DFFR_logic dffr_logic_6 (.clk(clock_1_out), .in(nor_and_2_out), .nres(nRES), .out_4(out_7));
  DFFR_logic dffr_logic_7 (.clk(clock_1_out), .in(_4_out), .nres(nRES), .out_4(out_8));
  DFFR_logic dffr_logic_8 (.clk(clock_1_out), .in(nor_and_3_out), .nres(nRES), .out_4(out_9));
  DFFR_logic dffr_logic_9 (.clk(clock_1_out), .in(_6_out), .nres(nRES), .out_4(out_10));
endmodule
