// Logisim project NOT_DFFR.circ as structural Verilog: 1 circuit, main circuit main
module main (
  input  nRES,
  input  in,
  output out
);

  wire CLK_out, multiplexer_1_out, multiplexer_2_out, nand_1_out, nand_2_out, not_1_out, not_2_out, not_3_out;

  Clock #(.highDuration(4), .lowDuration(4)) CLK (.out(CLK_out));
  not not_1 (not_1_out, in);
  nand nand_1 (nand_1_out, nRES, not_2_out);
  Multiplexer multiplexer_1 (.in0(nand_1_out), .in1(not_1_out), .out(multiplexer_1_out), .sel(CLK_out));  // open: en
  not not_2 (not_2_out, multiplexer_1_out);
  not not_3 (not_3_out, CLK_out);
  not not_4 (out, nand_2_out);
  Multiplexer multiplexer_2 (.in0(out), .in1(not_2_out), .out(multiplexer_2_out), .sel(not_3_out));  // open: en
  nand nand_2 (nand_2_out, nRES, multiplexer_2_out);

  // Notes on the sheet:
  //   /DFFR
endmodule
