// Logisim project nDFF.circ as structural Verilog: 1 circuit, main circuit main
module main (
  input  in,
  output nout
);

  wire CLK_out, multiplexer_1_out, multiplexer_2_out, not_1_out, not_2_out, not_3_out, not_4_out, not_5_out,
       not_6_out;

  Clock #(.highDuration(4), .lowDuration(4)) CLK (.out(CLK_out));
  not not_1 (not_1_out, CLK_out);
  not not_2 (not_2_out, in);
  Multiplexer multiplexer_1 (.in0(not_3_out), .in1(not_2_out), .out(multiplexer_1_out), .sel(CLK_out));  // open: en
  not not_3 (not_3_out, not_4_out);
  not not_4 (not_4_out, multiplexer_1_out);
  Multiplexer multiplexer_2 (.in0(not_5_out), .in1(not_4_out), .out(multiplexer_2_out), .sel(not_1_out));  // open: en
  not not_5 (not_5_out, not_6_out);
  not not_6 (not_6_out, multiplexer_2_out);
  not not_7 (nout, not_6_out);

  // Notes on the sheet:
  //   1
  //   2
endmodule
