// Logisim project nDLATCH.circ as structural Verilog: 1 circuit, main circuit main
module main (
  input  in,
  output out
);

  wire clock_1_out, transistor_1_out, transistor_3_out, transistor_4_out, transistor_6_out, transistor_7_out,
       transistor_8_out;

  Transistor transistor_1 (.in(1'b1), .out(transistor_1_out), .gate(transistor_3_out));
  Transistor #(.gate("br")) transistor_2 (.in(1'b1), .out(out), .gate(transistor_4_out));
  Transistor #(.gate("br")) transistor_3 (.in(1'b1), .out(transistor_3_out), .gate(transistor_4_out));
  Transistor #(.gate("br")) transistor_4 (.in(transistor_1_out), .out(transistor_4_out), .gate(transistor_8_out));
  Transistor transistor_5 (.in(transistor_6_out), .out(transistor_4_out), .gate(transistor_7_out));
  Transistor #(.gate("br")) transistor_6 (.in(1'b1), .out(transistor_6_out), .gate(in));
  Transistor #(.gate("br")) transistor_7 (.in(1'b1), .out(transistor_7_out), .gate(transistor_8_out));
  Clock #(.highDuration(4), .lowDuration(4)) clock_1 (.out(clock_1_out));
  Transistor #(.gate("br")) transistor_8 (.in(1'b1), .out(transistor_8_out), .gate(clock_1_out));
  Transistor #(.\type ("n")) transistor_9 (.in(1'b0), .out(out), .gate(transistor_4_out));
  Transistor #(.\type ("n")) transistor_10 (.in(1'b0), .out(transistor_3_out), .gate(transistor_4_out));
  Transistor #(.\type ("n")) transistor_11 (.in(1'b0), .out(transistor_1_out), .gate(transistor_3_out));
  Transistor #(.\type ("n")) transistor_12 (.in(transistor_1_out), .out(transistor_4_out), .gate(transistor_7_out));
  Transistor #(.\type ("n"), .gate("br")) transistor_13 (
    .in(transistor_6_out), .out(transistor_4_out), .gate(transistor_8_out));
  Transistor #(.\type ("n")) transistor_14 (.in(1'b0), .out(transistor_6_out), .gate(in));
  Transistor #(.\type ("n")) transistor_15 (.in(1'b0), .out(transistor_7_out), .gate(transistor_8_out));
  Transistor #(.\type ("n")) transistor_16 (.in(1'b0), .out(transistor_8_out), .gate(clock_1_out));

  // Notes on the sheet:
  //   CLK'
  //   /CLK'
endmodule
