// Logisim project nSR.circ as structural Verilog: 1 circuit, main circuit main
module main (
  input  EN,
  input  in,
  output nout
);

  wire multiplexer_1_out, multiplexer_2_out, not_1_out, not_2_out, not_3_out, not_4_out, not_5_out,
       not_6_out, not_7_out, not_8_out;

  not not_1 (not_1_out, EN);
  not not_2 (not_2_out, in);
  not not_3 (not_3_out, not_1_out);
  Multiplexer multiplexer_1 (.in0(not_4_out), .in1(not_2_out), .out(multiplexer_1_out), .sel(not_3_out));  // open: en
  not not_4 (not_4_out, not_5_out);
  not not_5 (not_5_out, multiplexer_1_out);
  not not_6 (not_6_out, not_5_out);
  Multiplexer multiplexer_2 (.in0(not_7_out), .in1(not_6_out), .out(multiplexer_2_out), .sel(not_1_out));  // open: en
  not not_7 (not_7_out, not_8_out);
  not not_8 (not_8_out, multiplexer_2_out);
  not not_9 (nout, not_8_out);

  // Notes on the sheet:
  //   EN
  //   in
  //   /out
  //   1
  //   2
endmodule
