// Logisim project 004.circ as structural Verilog: 9 circuits, main circuit main
module main (
  input  in1,
  input  in2,
  input  in3,
  input  in4,
  input  in5,
  input  in6,
  input  in7,
  input  in8,
  input  in9,
  input  in10,
  output out2,
  output out1
);

  wire _009_out, _010_out, _011_out, _013_out, _027_out, _104_out, _119_out, _120_out, _121_out, _212_out,
       _302_out, _304_out, _305_out, _314_out, _414_out, _416_out, _422_out, _602_out, not_1_out, not_2_out,
       not_3_out, not_4_out, not_5_out, not_6_out, not_7_out, not_8_out;

  or _212 (_212_out, in1, _414_out, _011_out);
  not not_1 (not_1_out, in1);
  buf _104 (_104_out, not_1_out);  // OR_Gate
  or _011 (_011_out, in2, _013_out);
  not not_2 (not_2_out, in2);
  // OR_Gate _211 has open pins: in0=not_2_out, out=open
  not not_3 (not_3_out, in3);
  not not_4 (not_4_out, in4);
  not not_5 (not_5_out, in5);
  not not_6 (not_6_out, in6);
  not not_7 (not_7_out, in7);
  not not_8 (not_8_out, in8);
  not not_9 (out1, in9);
  // Buffer _103 has open pins: in=_104_out, out=open
  nand _009 (_009_out, not_3_out, not_5_out);
  _22_OAI _318 (.c(in7));  // open: a, b, d, out
  // OR_Gate _301 has open pins: in0=in8, in1=_302_out, out=open
  // OR_Gate _617 has open pins: in0=not_8_out, out=open
  not _314 (_314_out, _305_out);
  // NAND_Gate _105 has open pins: in0=not_3_out, in1=not_5_out, out=open
  // NAND_Gate _215 has open pins: in0=in3, in1=in6, in2=_314_out, out=open
  // OR_Gate _624 has open pins: in0=not_6_out, out=open
  nand _414 (_414_out, not_4_out, not_7_out);
  // OR_Gate _026 has open pins: in0=in7, out=open
  or _304 (_304_out, in8, _302_out);
  // NAND_Gate _421 has open pins: in0=not_2_out, in1=in7, out=open
  not _422 (_422_out, _305_out);
  // OR_Gate _208 has open pins: in0=in1, in1=_009_out, out=open
  // OR_Gate _106 has open pins: in0=not_1_out, out=open
  // OR_Gate _012 has open pins: in0=in2, in1=_013_out, out=open
  // NAND_Gate _423 has open pins: in0=in3, in1=in6, in2=_422_out, out=open
  nand _302 (_302_out, in4, in7);
  // NAND_Gate _503 has open pins: in0=not_4_out, in1=in7, out=open
  // OR_Gate _258 has open pins: in0=in5, out=open
  // OR_Gate _461 has open pins: in0=not_5_out, out=open
  nand _013 (_013_out, in6, not_8_out);
  buf _010 (_010_out, _013_out);
  // NOR_Gate _640 has open pins: in0=not_6_out, out=open
  // OR_Gate _253 has open pins: in0=in7, out=open
  // OR_Gate _410 has open pins: in0=in8, out=open
  _22_OAI _430 (.b(not_8_out));  // open: a, c, d, out
  not _416 (_416_out, _009_out);
  // NAND_Gate _404 has open pins: in0=in4, in1=in7, out=open
  // OR_Gate _316 has open pins: in0=in1, in1=_009_out, out=open
  // NAND_Gate _116 has open pins: in0=not_1_out, in1=not_5_out, out=open
  // OR_Gate _310 has open pins: in0=in2, out=open
  // OR_Gate _710 has open pins: in0=not_2_out, in1=_602_out, out=open
  // NAND_Gate _428 has open pins: in0=in3, out=open
  NAND_XOR _514 (.b(_416_out), .d(not_3_out));  // open: a, c, out
  // NAND_Gate _250 has open pins: in0=in7, out=open
  // NOR_Gate _251 has open pins: in0=in5, out=open
  or _305 (_305_out, not_5_out, _304_out);
  // NAND_Gate _229 has open pins: in0=in6, out=open
  // OR_Gate _646 has open pins: in0=not_6_out, out=open
  // NOR_Gate _507 has open pins: in0=in8, out=open
  // OR_Gate _306 has open pins: in0=not_5_out, in1=_304_out, out=open
  // OR_Gate _460 has open pins: in0=not_6_out, out=open
  NOR_NAND _348 (.a(in7));  // open: b, c, d, out_5
  NAND_NOR _511 (.a(in1), .d(not_6_out));  // open: out_5, b, c
  // NAND_Gate _425 has open pins: in0=not_1_out, in1=in5, out=open
  // OR_Gate _016 has open pins: in0=in2, out=open
  _12_OAI u_12_oai_1 (.a(not_2_out));  // open: out, b, c
  // OR_Gate _433 has open pins: in0=in3, out=open
  // OR_Gate _321 has open pins: in0=not_3_out, out=open
  // NAND_Gate _502 has open pins: in0=in4, in1=in7, out=open
  // OR_Gate _315 has open pins: in0=in2, out=open
  // OR_Gate _232 has open pins: in0=not_2_out, out=open
  _12_OAI _620 (.a(not_8_out));  // open: out, b, c
  // OR_Gate _048 has open pins: in0=not_1_out, in1=_602_out, out=open
  // OR_Gate _609 has open pins: in0=in2, out=open
  // OR_Gate _713 has open pins: in0=not_2_out, out=open
  NOR_NAND _633 (.d(in3));  // open: a, b, c, out_5
  // OR_Gate _336 has open pins: in0=in3, out=open
  _22_OAI u_22_oai_1 (.a(not_3_out));  // open: b, c, d, out
  _22_OAI _516 (.a(not_7_out), .b(not_6_out), .c(in8), .d(not_4_out));  // open: out
  // OR_Gate _320 has open pins: in0=not_5_out, out=open
  // OR_Gate _227 has open pins: in0=in6, out=open
  _22_OAI _515 (.b(in1), .c(in3));  // open: a, d, out
  // OR_Gate _221 has open pins: in0=in4, out=open
  _12_OAI _358 (.c(in5));  // open: out, a, b
  // NOR_Gate _142 has open pins: in0=not_5_out, out=open
  nand _602 (_602_out, not_6_out, in8);
  // NAND_Gate _463 has open pins: in0=not_1_out, in1=in7, out=open
  // OR_Gate _441 has open pins: in0=not_8_out, out=open
  // OR_Gate _226 has open pins: in0=in4, out=open
  // OR_Gate _610 has open pins: in0=not_4_out, out=open
  NAND_NOR _555 (.c(in5));  // open: out_5, a, b, d
  // NAND_Gate _608 has open pins: in0=in1, in1=not_3_out, out=open
  // OR_Gate _554 has open pins: in0=not_1_out, out=open
  // NAND_Gate _614 has open pins: in0=in2, in1=not_4_out, out=open
  _12_OAI _355 (.c(not_5_out));  // open: out, a, b
  // OR_Gate _344 has open pins: in0=in6, out=open
  // NAND_Gate _411 has open pins: in0=not_6_out, in1=not_8_out, out=open
  // NOR_Gate _457 has open pins: in0=in7, out=open
  _12_OAI _622 (.a(in8));  // open: out, b, c
  // NAND_Gate _525 has open pins: in0=in4, in1=not_6_out, out=open
  NOR_NAND nor_nand_1 (.d(in1));  // open: a, b, c, out_5
  _12_OAI u_12_oai_2 (.a(not_1_out));  // open: out, b, c
  _12_OAI u_12_oai_3 (.a(in2));  // open: out, b, c
  // NAND_Gate _720 has open pins: in0=not_2_out, in1=not_3_out, out=open
  // OR_Gate _216 has open pins: in0=in4, out=open
  // NAND_Gate _424 has open pins: in0=not_4_out, in1=not_7_out, out=open
  // OR_Gate _543 has open pins: in0=in5, out=open
  _12_OAI _723 (.c(not_5_out));  // open: out, a, b
  // NAND_Gate _631 has open pins: in0=in6, in1=in7, out=open
  // OR_Gate _149 has open pins: in0=in7, out=open
  // NAND_Gate _537 has open pins: in0=not_3_out, in1=in7, out=open
  // NOR_Gate _442 has open pins: in0=not_8_out, out=open
  // OR_Gate _712 has open pins: in0=not_5_out, out=open
  // NAND_Gate _432 has open pins: in0=in1, in1=in5, out=open
  // NOR_Gate _448 has open pins: in0=not_1_out, out=open
  // OR_Gate _328 has open pins: in0=in2, out=open
  // OR_Gate _462 has open pins: in0=in3, out=open
  // NAND_Gate _722 has open pins: in0=not_3_out, in1=in5, out=open
  // OR_Gate _437 has open pins: in0=in4, in1=in6, out=open
  // OR_Gate _619 has open pins: in0=not_4_out, in1=_602_out, out=open
  // OR_Gate _616 has open pins: in0=in5, in1=not_6_out, out=open
  // NOR_Gate _643 has open pins: in0=not_5_out, out=open
  // NAND_Gate _420 has open pins: in0=in6, in1=in8, out=open
  // NOR_Gate _642 has open pins: in0=in7, out=open
  _12_OAI _449 (.c(in8));  // open: out, a, b
  _12_OAI _233 (.c(not_8_out));  // open: out, a, b
  _12_OAI u_12_oai_4 (.a(in1));  // open: out, b, c
  // OR_Gate _029 has open pins: in0=not_1_out, out=open
  // NOR_Gate _632 has open pins: in0=in2, out=open
  // NAND_Gate _647 has open pins: in0=not_2_out, in1=in3, out=open
  // OR_Gate _556 has open pins: in0=not_3_out, in1=_602_out, out=open
  // OR_Gate _335 has open pins: in0=in4, out=open
  // NOR_Gate _549 has open pins: in0=not_4_out, out=open
  // NAND_Gate _224 has open pins: in0=in5, out=open
  // OR_Gate _638 has open pins: in0=not_5_out, out=open
  NAND_XOR _512 (.c(in6), .d(_305_out));  // open: a, b, out
  _12_OAI _521 (.a(not_6_out), .c(_305_out));  // open: out, b
  _12_OAI _529 (.a(in7));  // open: out, b, c
  _12_OAI u_12_oai_5 (.a(in1));  // open: out, b, c
  // OR_Gate _112 has open pins: in0=not_1_out, out=open
  // NAND_Gate _649 has open pins: in0=in2, in1=in3, out=open
  // NAND_Gate _261 has open pins: in0=in3, in1=in5, in2=in7, out=open
  // OR_Gate _219 has open pins: in0=not_1_out, in1=_305_out, out=open
  // OR_Gate _050 has open pins: in0=not_2_out, out=open
  // OR_Gate _356 has open pins: in0=not_3_out, out=open
  // OR_Gate _445 has open pins: in0=in4, out=open
  // OR_Gate _025 has open pins: in0=in5, out=open
  _12_OAI _426 (.a(in6));  // open: out, b, c
  _12_OAI _524 (.a(in7));  // open: out, b, c
  NAND_XOR _124 (.a(not_8_out));  // open: b, c, d, out
  // OR_Gate _627 has open pins: in0=in1, out=open
  // NOR_Gate _453 has open pins: in0=not_4_out, out=open
  // NAND_Gate _717 has open pins: in0=not_2_out, in1=in8, out=open
  // NAND_Gate _015 has open pins: in0=not_1_out, in1=not_5_out, out=open
  // NOR_Gate _635 has open pins: in0=in7, out=open
  // NOR_Gate _456 has open pins: in0=in1, in1=_602_out, out=open
  // OR_Gate _307 has open pins: in0=not_1_out, in1=not_6_out, out=open
  // OR_Gate _044 has open pins: in0=not_2_out, in1=in7, out=open
  // NOR_Gate _134 has open pins: in0=not_8_out, out=open
  NOR_AND nor_and_1 (.b(in2), .c(in2));  // open: out_5, a, d
  _12_OAI _357 (.a(in5), .c(in2));  // open: out, b
  // OR_Gate _716 has open pins: in0=in4, in1=_602_out, out=open
  // NAND_Gate _347 has open pins: in0=not_4_out, out=open
  _22_AOI u_22_aoi_1 (.a(in6), .d(not_6_out));  // open: b, c, out
  NOR_AND nor_and_2 (.a(in1), .c(in1));  // open: out_5, b, d
  // OR_Gate _141 has open pins: in0=not_2_out, out=open
  NOR_NAND _346 (.d(in4));  // open: a, b, c, out_5
  _12_OAI _438 (.a(in7), .c(in8));  // open: out, b
  // NAND_Gate _513 has open pins: in0=not_1_out, out=open
  // NOR_Gate _247 has open pins: in0=in2, out=open
  // NOR_Gate _628 has open pins: in0=not_2_out, out=open
  // OR_Gate _539 has open pins: in0=not_4_out, out=open
  // NAND_Gate _352 has open pins: in0=in1, in1=in3, out=open
  // OR_Gate _719 has open pins: in0=in7, in1=_602_out, out=open
  // NAND_Gate _518 has open pins: in0=not_1_out, in1=in3, in2=not_7_out, out=open
  // OR_Gate _256 has open pins: in0=in4, out=open
  // NAND_Gate _237 has open pins: in0=in2, in1=not_5_out, out=open
  // NAND_Gate _607 has open pins: in0=in6, in1=in8, out=open
  // OR_Gate _148 has open pins: in0=in4, in1=_602_out, out=open
  // NAND_Gate _342 has open pins: in0=in2, in1=in8, out=open
  // OR_Gate _637 has open pins: in0=in4, out=open
  // AND_Gate _022 has open pins: in0=_212_out, out=open
  or _027 (_027_out, _212_out, _009_out);
  // NAND_Gate _031 has open pins: in0=_212_out, out=open
  // OR_Gate _037 has open pins: in2=_602_out, out=open
  // OR_Gate _110 has open pins: in0=_212_out, in1=_009_out, out=open
  // NAND_Gate _117 has open pins: in1=_305_out, out=open
  // OR_Gate _118 has open pins: in0=_009_out, out=open
  not _119 (_119_out, _027_out);  // NAND_Gate
  nor _120 (_120_out, _119_out, _121_out);
  not _121 (_121_out, _305_out);  // NAND_Gate
  // OR_Gate _222 has open pins: in0=_009_out, in2=_602_out, out=open
  // OR_Gate or_1 is placed but not wired
  // OR_Gate or_2 is placed but not wired
  // OR_Gate _510 has open pins: in0=_602_out, out=open
  // OR_Gate _606 has open pins: in1=_602_out, out=open
  // OR_Gate _611 has open pins: in1=_602_out, out=open
  // OR_Gate _708 has open pins: in0=_602_out, out=open
  not _101 (out2, _120_out);

  // Notes on the sheet:
  //   x14
  //   x17
  //   x16
  //   x13
  //   x8
  //   x9
  //   x15
  //   x10
  //   x8
  //   x10
  //   x10
  //   x7
  //   x13
  //   x0???
  //   x6
  //   x8
  //   +BUS_KEEPER
endmodule

module _12_OAI (
  input  a,
  input  b,
  input  c,
  output out
);

  wire transistor_3_out, transistor_5_out;

  Transistor #(.gate("br")) transistor_1 (.in(1'b1), .out(out), .gate(a));
  Transistor #(.gate("br")) transistor_2 (.in(transistor_3_out), .out(out), .gate(b));
  Transistor #(.gate("br")) transistor_3 (.in(1'b1), .out(transistor_3_out), .gate(c));
  Transistor #(.\type ("n")) transistor_4 (.in(transistor_5_out), .out(out), .gate(a));
  Transistor #(.\type ("n")) transistor_5 (.in(1'b0), .out(transistor_5_out), .gate(b));
  Transistor #(.\type ("n")) transistor_6 (.in(1'b0), .out(transistor_5_out), .gate(c));
endmodule

module NAND_NOR (
  input  a,
  input  b,
  input  c,
  input  d,
  output out_5
);

  wire transistor_3_out, transistor_5_out, transistor_6_out;

  Transistor #(.gate("br")) transistor_1 (.in(1'b1), .out(out_5), .gate(a));
  Transistor #(.gate("br")) transistor_2 (.in(1'b1), .out(out_5), .gate(b));
  Transistor #(.gate("br")) transistor_3 (.in(1'b1), .out(transistor_3_out), .gate(c));
  Transistor #(.gate("br")) transistor_4 (.in(transistor_3_out), .out(out_5), .gate(d));
  Transistor #(.\type ("n")) transistor_5 (.in(1'b0), .out(transistor_5_out), .gate(a));
  Transistor #(.\type ("n")) transistor_6 (.in(transistor_5_out), .out(transistor_6_out), .gate(b));
  Transistor #(.\type ("n")) transistor_7 (.in(transistor_6_out), .out(out_5), .gate(c));
  Transistor #(.\type ("n")) transistor_8 (.in(transistor_6_out), .out(out_5), .gate(d));

  // Notes on the sheet:
  //   NAND
  //   NOR
  //   out = NAND(a,b) | NOR(c,d)
endmodule

module _22_OAI (
  input  a,
  input  b,
  input  c,
  input  d,
  output out
);

  wire transistor_1_out, transistor_4_out, transistor_7_out;

  Transistor #(.gate("br")) transistor_1 (.in(1'b1), .out(transistor_1_out), .gate(a));
  Transistor #(.gate("br")) transistor_2 (.in(transistor_1_out), .out(out), .gate(b));
  Transistor #(.gate("br")) transistor_3 (.in(transistor_4_out), .out(out), .gate(c));
  Transistor #(.gate("br")) transistor_4 (.in(1'b1), .out(transistor_4_out), .gate(d));
  Transistor #(.\type ("n")) transistor_5 (.in(transistor_7_out), .out(out), .gate(a));
  Transistor #(.\type ("n")) transistor_6 (.in(transistor_7_out), .out(out), .gate(b));
  Transistor #(.\type ("n")) transistor_7 (.in(1'b0), .out(transistor_7_out), .gate(c));
  Transistor #(.\type ("n")) transistor_8 (.in(1'b0), .out(transistor_7_out), .gate(d));

  // Notes on the sheet:
  //   out = NAND(a|b, c|d)
endmodule

module _22_AOI (
  input  a,
  input  b,
  input  c,
  input  d,
  output out
);

  wire and_1_out, and_2_out;

  and and_1 (and_1_out, a, b);
  and and_2 (and_2_out, c, d);
  nor nor_1 (out, and_1_out, and_2_out);
endmodule

module NOR_NAND (
  input  a,
  input  b,
  input  c,
  input  d,
  output out_5
);

  wire nand_1_out, nor_1_out;

  nor nor_1 (nor_1_out, a, b);
  nand nand_1 (nand_1_out, c, d);
  and and_1 (out_5, nor_1_out, nand_1_out);
endmodule

module NOR_AND (
  input  a,
  input  b,
  input  c,
  input  d,
  output out_5
);

  wire and_1_out, nor_1_out;

  and and_1 (and_1_out, c, d);
  nor nor_1 (nor_1_out, a, b);
  or or_1 (out_5, nor_1_out, and_1_out);
endmodule

module NAND_XOR (
  input  a,
  input  b,
  input  c,
  input  d,
  output out
);

  wire nand_1_out, xor_1_out;

  nand nand_1 (nand_1_out, a, b);
  xor xor_1 (xor_1_out, c, d);
  and and_1 (out, nand_1_out, xor_1_out);
endmodule

module _002_out (
  input  RES2_16,
  input  RES2_15,
  input  RES2_14,
  input  RES2_13,
  input  RES2_15_2,
  input  RES2_11,
  input  RES2_10,
  input  RES2_9,
  input  RES2_8,
  input  RES2_7,
  output out6,
  output out5,
  output out4,
  output out3,
  output out2,
  output out1,
  output out0,
  output out7
);

  wire and_1_out, and_2_out, and_3_out, and_4_out, and_5_out, and_6_out, and_7_out, and_8_out, and_9_out,
       and_10_out, n12_oai_1_out, n12_oai_3_out, n12_oai_5_out, n12_oai_7_out, n12_oai_9_out, n12_oai_11_out,
       n12_oai_13_out, n12_oai_15_out, nand_1_out, nand_2_out, nand_3_out, not_1_out, not_2_out, not_3_out,
       not_4_out, not_5_out, not_6_out, not_7_out, not_8_out, or_1_out, or_2_out, or_3_out;

  and and_1 (and_1_out, RES2_16, n12_oai_1_out);
  or or_1 (or_1_out, RES2_16, n12_oai_1_out);
  _12_OAI u_12_oai_1 (.out(n12_oai_1_out), .a(not_1_out), .b(RES2_15), .c(and_3_out));
  not not_1 (not_1_out, and_2_out);
  and and_2 (and_2_out, RES2_15, and_3_out);
  _12_OAI u_12_oai_2 (.out(out6), .a(or_1_out), .b(n12_oai_3_out), .c(and_1_out));
  _12_OAI u_12_oai_3 (.out(n12_oai_3_out), .a(not_2_out), .b(RES2_14), .c(and_4_out));
  not not_2 (not_2_out, and_3_out);
  and and_3 (and_3_out, RES2_14, and_4_out);
  _12_OAI u_12_oai_4 (.out(out5), .a(or_1_out), .b(n12_oai_5_out), .c(and_1_out));
  _12_OAI u_12_oai_5 (.out(n12_oai_5_out), .a(not_3_out), .b(RES2_13), .c(and_5_out));
  not not_3 (not_3_out, and_4_out);
  and and_4 (and_4_out, RES2_13, and_5_out);
  _12_OAI u_12_oai_6 (.out(out4), .a(or_1_out), .b(n12_oai_7_out), .c(and_1_out));
  _12_OAI u_12_oai_7 (.out(n12_oai_7_out), .a(not_4_out), .b(RES2_15_2), .c(and_6_out));
  not not_4 (not_4_out, and_5_out);
  and and_5 (and_5_out, RES2_15_2, and_6_out);
  _12_OAI u_12_oai_8 (.out(out3), .a(or_1_out), .b(n12_oai_9_out), .c(and_1_out));
  _12_OAI u_12_oai_9 (.out(n12_oai_9_out), .a(not_5_out), .b(RES2_11), .c(and_7_out));
  not not_5 (not_5_out, and_6_out);
  and and_6 (and_6_out, RES2_11, and_7_out);
  _12_OAI u_12_oai_10 (.out(out2), .a(or_1_out), .b(n12_oai_11_out), .c(and_1_out));
  _12_OAI u_12_oai_11 (.out(n12_oai_11_out), .a(not_6_out), .b(RES2_10), .c(and_8_out));
  not not_6 (not_6_out, and_7_out);
  and and_7 (and_7_out, RES2_10, and_8_out);
  _12_OAI u_12_oai_12 (.out(out1), .a(or_1_out), .b(n12_oai_13_out), .c(and_1_out));
  _12_OAI u_12_oai_13 (.out(n12_oai_13_out), .a(not_7_out), .b(RES2_9), .c(and_9_out));
  not not_7 (not_7_out, and_8_out);
  and and_8 (and_8_out, RES2_9, and_9_out);
  _12_OAI u_12_oai_14 (.out(out0), .a(or_1_out), .b(n12_oai_15_out), .c(and_1_out));
  _12_OAI u_12_oai_15 (.out(n12_oai_15_out), .a(not_8_out), .b(RES2_8), .c(RES2_7));
  not not_8 (not_8_out, and_9_out);
  and and_9 (and_9_out, RES2_8, and_10_out);
  and and_10 (and_10_out, RES2_7, or_2_out);
  and and_11 (out7, RES2_16, or_3_out);
  or or_2 (or_2_out, or_3_out, RES2_16);
  or or_3 (or_3_out, nand_1_out, nand_2_out, nand_3_out);
  nand nand_1 (nand_1_out, RES2_7, RES2_8, RES2_9);
  nand nand_2 (nand_2_out, RES2_10, RES2_11, RES2_15_2);
  nand nand_3 (nand_3_out, RES2_13, RES2_14, RES2_15);
endmodule
