// Logisim project Dcache_control.circ as structural Verilog
module main (
  input  nRES,
  input  RW__unk3,
  input  nWORD,
  input  nBS0,
  input  nBS1,
  input  BYTESEL,
  input  nBS2,
  input  nRWC__unk2,
  input  nBS3,
  input  nRES_2,
  input  nBS0_2,
  input  nBS1_2,
  input  RW__unk3_2,
  input  nRWC__unk2_2,
  input  nBS2_2,
  input  nBS3_2,
  input  nBS4,
  input  nWORD_2,
  input  nBS5,
  input  BYTESEL__unk1,
  input  BS0,
  input  nRWC__unk2_3,
  input  RW__unk3_3,
  output BS0_2,
  output BS1,
  output RW__2,
  output BS2,
  output nRW__1,
  output RW__unk3_4,
  output BS3,
  output nRWC__unk2_4,
  output RW,
  output BYTESEL__unk1_2,
  output nRW,
  output DO_RW__Y2,
  output BYTE_EN
);

  wire and_1_out, and_2_out, controlled_buffer_1_out, controlled_buffer_3_out, controlled_buffer_4_out,
       CS_2_out, CS_out, nand_1_out, nand_2_out, nand_3_out, nand_4_out, nand_5_out, nand_6_out, nor_1_out,
       nor_2_out, nor_3_out, not_1_out, not_2_out, not_3_out, not_4_out, not_5_out, not_6_out, not_7_out,
       not_8_out, not_9_out, not_10_out, not_11_out, not_12_out, not_13_out, not_14_out, not_15_out,
       not_16_out, not_17_out, not_18_out, not_23_out, not_25_out, not_26_out, not_27_out, not_29_out,
       or_1_out, or_2_out, undriven;

  Clock #(.highDuration(4), .lowDuration(4)) CS (.out(CS_out));
  Clock #(.highDuration(4), .lowDuration(4)) CS_2 (.out(CS_2_out));
  not not_1 (not_1_out, nRES);
  not not_2 (not_2_out, nWORD);
  not not_3 (not_3_out, CS_out);
  not not_4 (not_4_out, nRES_2);
  or or_1 (or_1_out, not_4_out, not_5_out);
  not not_5 (not_5_out, nRWC__unk2_2);
  not not_6 (not_6_out, nWORD_2);
  or or_2 (or_2_out, not_6_out, BYTESEL__unk1);
  not not_7 (not_7_out, RW__unk3_3);
  not not_8 (not_8_out, not_7_out);
  not not_9 (not_9_out, not_1_out);
  not not_10 (not_10_out, not_11_out);
  not not_11 (not_11_out, not_3_out);
  not not_12 (not_12_out, not_8_out);
  not not_13 (not_13_out, not_12_out);
  not not_14 (not_14_out, not_9_out);
  assign controlled_buffer_1_out = not_14_out ? 1'b1 : 1'bz;  // Controlled_Buffer controlled_buffer_1
  not not_15 (not_15_out, not_10_out);
  not not_16 (not_16_out, not_15_out);
  not not_17 (not_17_out, not_16_out);
  not not_18 (not_18_out, nRWC__unk2);
  assign controlled_buffer_1_out = not_18_out ? 1'b1 : 1'bz;  // Controlled_Buffer controlled_buffer_2
  S_R_Flip_Flop s_r_ff_1 (.S(or_2_out), .clk(CS_2_out), .Q(RW), .Qn(nRW), .reset(or_1_out));  // open: R, preset, en
  nand nand_1 (nand_1_out, RW__unk3_3, nand_2_out);
  nand nand_2 (nand_2_out, nand_1_out, nand_3_out);
  assign controlled_buffer_3_out = not_17_out ? 1'b0 : 1'bz;  // Controlled_Buffer controlled_buffer_3
  assign controlled_buffer_4_out = not_3_out ? controlled_buffer_3_out : 1'bz;  // Controlled_Buffer controlled_buffer_4
  nand nand_3 (nand_3_out, and_2_out, and_1_out);
  assign controlled_buffer_1_out = not_2_out ? controlled_buffer_4_out : 1'bz;  // Controlled_Buffer controlled_buffer_5
  assign controlled_buffer_1_out = BYTESEL ? controlled_buffer_4_out : 1'bz;  // Controlled_Buffer controlled_buffer_6
  nand nand_4 (nand_4_out, nBS0_2, nBS1_2, nBS2_2);
  nor nor_1 (nor_1_out, nand_4_out, nand_5_out);
  nand nand_5 (nand_5_out, nBS3_2, nBS4, nBS5);
  not not_19 (BYTESEL__unk1_2, nor_1_out);
  and and_1 (and_1_out, undriven, nand_6_out);
  not not_20 (RW__unk3_4, controlled_buffer_1_out);
  not not_21 (controlled_buffer_1_out, RW__unk3_4);
  not not_22 (nRW__1, RW__unk3_4);
  not not_23 (not_23_out, and_1_out);
  nand nand_6 (nand_6_out, not_23_out, and_2_out);
  not not_24 (RW__2, nRW__1);
  not not_25 (not_25_out, RW__unk3_2);
  and and_2 (and_2_out, nRWC__unk2_3, RW__unk3_3);
  nor nor_2 (nor_2_out, not_25_out, nor_3_out);
  nor nor_3 (nor_3_out, nor_2_out, 1'b0);
  not not_26 (not_26_out, and_2_out);
  not not_27 (not_27_out, RW__unk3);
  not not_28 (nRWC__unk2_4, not_29_out);
  not not_29 (not_29_out, nor_3_out);
  and and_3 (BYTE_EN, BS0, and_2_out);
  D_Flip_Flop #(.trigger("high")) d_ff_1 (.clk(not_27_out), .D(nBS0), .Qn(BS0_2));  // open: Q, preset, en, reset
  D_Flip_Flop #(.trigger("high")) d_ff_2 (.clk(not_27_out), .D(nBS1), .Qn(BS1));  // open: Q, preset, en, reset
  D_Flip_Flop #(.trigger("high")) d_ff_3 (.clk(not_27_out), .D(nBS2), .Qn(BS2));  // open: Q, preset, en, reset
  D_Flip_Flop #(.trigger("high")) d_ff_4 (.clk(not_27_out), .D(nBS3), .Qn(BS3));  // open: Q, preset, en, reset
  or or_3 (DO_RW__Y2, not_13_out, and_2_out);
  // NOT_Gate not_30 is placed but not wired

  // Notes on the sheet:
  //   Read/Write Control
  //   falling edge (negedge) detect
  //   negedge
  //   RW_DELAY (unk3P)
  //   I
  //   Read/Write Control
  //   II
  //   Byte Select
  //   out
  //   III
  //   else out = Z;
  //   Bi-latch
  //   "Memory" part of RS
  //   if (#RES == 0 || #RWC == 0) out = 1;
  //   Sorry for coloring but Logisim doesn't support bi-latches
  //   IV
  //   else if ((#WORD == 0 || BYTESEL) && negedge #CS) out = 0; 
  //   Read/Write Clear (Disabled)
  //   #IE
  //   V
  //   IE
  //   RW_DELAY (unk3P)
endmodule

module LATCH (
  input  EN,
  input  in,
  output out
);

  D_Flip_Flop #(.trigger("high")) d_ff_1 (.clk(EN), .D(in), .Q(out));  // open: Qn, preset, en, reset
endmodule

module RW_Control (
  input  nRES,
  input  nWORD,
  input  nCS,
  input  BYTESEL,
  input  nRWC__unk2,
  output RW__2,
  output nRW__1,
  output RW__unk3
);

  wire controlled_buffer_1_out, controlled_buffer_3_out, controlled_buffer_4_out, not_1_out, not_2_out,
       not_3_out, not_4_out, not_5_out, not_6_out, not_7_out, not_8_out, not_9_out, not_10_out, not_11_out;

  not not_1 (not_1_out, nRES);
  not not_2 (not_2_out, nWORD);
  not not_3 (not_3_out, nCS);
  not not_4 (not_4_out, not_1_out);
  not not_5 (not_5_out, not_3_out);
  not not_6 (not_6_out, not_4_out);
  assign controlled_buffer_1_out = not_6_out ? 1'b1 : 1'bz;  // Controlled_Buffer controlled_buffer_1
  not not_7 (not_7_out, not_5_out);
  not not_8 (not_8_out, not_7_out);
  not not_9 (not_9_out, not_8_out);
  not not_10 (not_10_out, nRWC__unk2);
  assign controlled_buffer_1_out = not_10_out ? 1'b1 : 1'bz;  // Controlled_Buffer controlled_buffer_2
  not not_11 (not_11_out, not_9_out);
  assign controlled_buffer_3_out = not_11_out ? 1'b0 : 1'bz;  // Controlled_Buffer controlled_buffer_3
  assign controlled_buffer_4_out = not_3_out ? controlled_buffer_3_out : 1'bz;  // Controlled_Buffer controlled_buffer_4
  assign controlled_buffer_1_out = not_2_out ? controlled_buffer_4_out : 1'bz;  // Controlled_Buffer controlled_buffer_5
  assign controlled_buffer_1_out = BYTESEL ? controlled_buffer_4_out : 1'bz;  // Controlled_Buffer controlled_buffer_6
  not not_12 (RW__unk3, controlled_buffer_1_out);
  not not_13 (controlled_buffer_1_out, RW__unk3);
  not not_14 (nRW__1, RW__unk3);
  not not_15 (RW__2, nRW__1);

  // Notes on the sheet:
  //   falling edge (negedge) detect
  //   Read/Write Control
  //   out
  //   else out = Z;
  //   Bi-latch
  //   "Memory" part of RS
  //   if (#RES == 0 || #RWC == 0) out = 1;
  //   Sorry for coloring but Logisim doesn't support bi-latches
  //   else if ((#WORD == 0 || BYTESEL) && negedge #CS) out = 0; 
endmodule

module Byte_Select (
  input  nBS0,
  input  nBS1,
  input  nBS2,
  input  nBS3,
  input  nBS4,
  input  nBS5,
  output BYTESEL__unk1
);

  wire nand_1_out, nand_2_out, nor_1_out;

  nand nand_1 (nand_1_out, nBS0, nBS1, nBS2);
  nand nand_2 (nand_2_out, nBS3, nBS4, nBS5);
  nor nor_1 (nor_1_out, nand_1_out, nand_2_out);
  not not_1 (BYTESEL__unk1, nor_1_out);

  // Notes on the sheet:
  //   Byte Select
endmodule

module Cell_Array (
  input  _0,
  input  _0_2,
  input  _1,
  input  _1_2,
  input  _2,
  input  _2_2,
  input  _3,
  input  _3_2,
  input  _4,
  input  _4_2,
  input  _5,
  input  _5_2,
  input  _6,
  input  _6_2,
  input  _7,
  input  _7_2,
  input  ROW_0,
  input  ROW_1,
  input  ROW_2,
  input  ROW_3,
  input  ROW_4,
  input  ROW_5,
  input  ROW_6,
  input  ROW_7
);

  wire controlled_buffer_2_out, controlled_buffer_4_out, controlled_buffer_6_out, controlled_buffer_8_out,
       controlled_buffer_10_out, controlled_buffer_12_out, controlled_buffer_14_out,
       controlled_buffer_16_out, controlled_buffer_20_out, controlled_buffer_24_out,
       controlled_buffer_27_out, controlled_buffer_32_out, controlled_buffer_35_out,
       controlled_buffer_39_out, controlled_buffer_44_out, controlled_buffer_48_out,
       controlled_buffer_51_out, controlled_buffer_55_out, controlled_buffer_60_out,
       controlled_buffer_63_out, controlled_buffer_68_out, controlled_buffer_72_out,
       controlled_buffer_75_out, controlled_buffer_79_out, controlled_buffer_84_out,
       controlled_buffer_88_out, controlled_buffer_92_out, controlled_buffer_95_out,
       controlled_buffer_99_out, controlled_buffer_103_out, controlled_buffer_107_out,
       controlled_buffer_112_out, controlled_buffer_115_out, controlled_buffer_119_out,
       controlled_buffer_124_out, controlled_buffer_127_out, controlled_buffer_132_out,
       controlled_buffer_135_out, controlled_buffer_140_out, controlled_buffer_144_out,
       controlled_buffer_148_out, controlled_buffer_152_out, controlled_buffer_155_out,
       controlled_buffer_160_out, controlled_buffer_163_out, controlled_buffer_167_out,
       controlled_buffer_172_out, controlled_buffer_175_out, controlled_buffer_180_out,
       controlled_buffer_183_out, controlled_buffer_187_out, controlled_buffer_192_out,
       controlled_buffer_195_out, controlled_buffer_199_out, controlled_buffer_203_out,
       controlled_buffer_208_out, controlled_buffer_211_out, controlled_buffer_215_out,
       controlled_buffer_220_out, controlled_buffer_223_out, controlled_buffer_227_out,
       controlled_buffer_232_out, controlled_buffer_235_out, controlled_buffer_239_out, not_1_out, not_2_out,
       not_3_out, not_4_out, not_5_out, not_6_out, not_7_out, not_8_out, not_10_out, not_12_out, not_14_out,
       not_16_out, not_18_out, not_20_out, not_22_out, not_24_out, not_26_out, not_28_out, not_30_out,
       not_32_out, not_34_out, not_36_out, not_38_out, not_40_out, not_42_out, not_44_out, not_46_out,
       not_48_out, not_50_out, not_52_out, not_54_out, not_56_out, not_58_out, not_60_out, not_62_out,
       not_64_out, not_66_out, not_68_out, not_70_out, not_72_out, not_74_out, not_76_out, not_78_out,
       not_80_out, not_82_out, not_84_out, not_86_out, not_88_out, not_90_out, not_92_out, not_94_out,
       not_96_out, not_98_out, not_100_out, not_102_out, not_104_out, not_106_out, not_108_out, not_110_out,
       not_112_out, not_114_out, not_116_out, not_118_out, not_120_out;

  assign _0 = ROW_0 ? controlled_buffer_2_out : 1'bz;  // Controlled_Buffer controlled_buffer_1
  assign controlled_buffer_2_out = ROW_0 ? _0 : 1'bz;  // Controlled_Buffer controlled_buffer_2
  not not_1 (not_1_out, controlled_buffer_2_out);
  assign _0 = ROW_1 ? controlled_buffer_4_out : 1'bz;  // Controlled_Buffer controlled_buffer_3
  assign controlled_buffer_4_out = ROW_1 ? _0 : 1'bz;  // Controlled_Buffer controlled_buffer_4
  not not_2 (not_2_out, controlled_buffer_4_out);
  assign _0 = ROW_2 ? controlled_buffer_6_out : 1'bz;  // Controlled_Buffer controlled_buffer_5
  assign controlled_buffer_6_out = ROW_2 ? _0 : 1'bz;  // Controlled_Buffer controlled_buffer_6
  not not_3 (not_3_out, controlled_buffer_6_out);
  assign _0 = ROW_3 ? controlled_buffer_8_out : 1'bz;  // Controlled_Buffer controlled_buffer_7
  assign controlled_buffer_8_out = ROW_3 ? _0 : 1'bz;  // Controlled_Buffer controlled_buffer_8
  not not_4 (not_4_out, controlled_buffer_8_out);
  assign _0 = ROW_4 ? controlled_buffer_10_out : 1'bz;  // Controlled_Buffer controlled_buffer_9
  assign controlled_buffer_10_out = ROW_4 ? _0 : 1'bz;  // Controlled_Buffer controlled_buffer_10
  not not_5 (not_5_out, controlled_buffer_10_out);
  assign _0 = ROW_5 ? controlled_buffer_12_out : 1'bz;  // Controlled_Buffer controlled_buffer_11
  assign controlled_buffer_12_out = ROW_5 ? _0 : 1'bz;  // Controlled_Buffer controlled_buffer_12
  not not_6 (not_6_out, controlled_buffer_12_out);
  assign _0 = ROW_6 ? controlled_buffer_14_out : 1'bz;  // Controlled_Buffer controlled_buffer_13
  assign controlled_buffer_14_out = ROW_6 ? _0 : 1'bz;  // Controlled_Buffer controlled_buffer_14
  not not_7 (not_7_out, controlled_buffer_14_out);
  assign _0 = ROW_7 ? controlled_buffer_16_out : 1'bz;  // Controlled_Buffer controlled_buffer_15
  assign controlled_buffer_16_out = ROW_7 ? _0 : 1'bz;  // Controlled_Buffer controlled_buffer_16
  not not_8 (not_8_out, controlled_buffer_16_out);
  assign _1 = ROW_0 ? controlled_buffer_20_out : 1'bz;  // Controlled_Buffer controlled_buffer_17
  assign _0_2 = ROW_0 ? controlled_buffer_2_out : 1'bz;  // Controlled_Buffer controlled_buffer_18
  assign controlled_buffer_2_out = ROW_0 ? _0_2 : 1'bz;  // Controlled_Buffer controlled_buffer_19
  assign controlled_buffer_20_out = ROW_0 ? _1 : 1'bz;  // Controlled_Buffer controlled_buffer_20
  not not_9 (controlled_buffer_2_out, not_1_out);
  not not_10 (not_10_out, controlled_buffer_20_out);
  assign _0_2 = ROW_1 ? controlled_buffer_4_out : 1'bz;  // Controlled_Buffer controlled_buffer_21
  assign _1 = ROW_1 ? controlled_buffer_24_out : 1'bz;  // Controlled_Buffer controlled_buffer_22
  assign controlled_buffer_4_out = ROW_1 ? _0_2 : 1'bz;  // Controlled_Buffer controlled_buffer_23
  assign controlled_buffer_24_out = ROW_1 ? _1 : 1'bz;  // Controlled_Buffer controlled_buffer_24
  not not_11 (controlled_buffer_4_out, not_2_out);
  not not_12 (not_12_out, controlled_buffer_24_out);
  assign _0_2 = ROW_2 ? controlled_buffer_6_out : 1'bz;  // Controlled_Buffer controlled_buffer_25
  assign _1 = ROW_2 ? controlled_buffer_27_out : 1'bz;  // Controlled_Buffer controlled_buffer_26
  assign controlled_buffer_27_out = ROW_2 ? _1 : 1'bz;  // Controlled_Buffer controlled_buffer_27
  assign controlled_buffer_6_out = ROW_2 ? _0_2 : 1'bz;  // Controlled_Buffer controlled_buffer_28
  not not_13 (controlled_buffer_6_out, not_3_out);
  not not_14 (not_14_out, controlled_buffer_27_out);
  assign _0_2 = ROW_3 ? controlled_buffer_8_out : 1'bz;  // Controlled_Buffer controlled_buffer_29
  assign _1 = ROW_3 ? controlled_buffer_32_out : 1'bz;  // Controlled_Buffer controlled_buffer_30
  assign controlled_buffer_8_out = ROW_3 ? _0_2 : 1'bz;  // Controlled_Buffer controlled_buffer_31
  assign controlled_buffer_32_out = ROW_3 ? _1 : 1'bz;  // Controlled_Buffer controlled_buffer_32
  not not_15 (controlled_buffer_8_out, not_4_out);
  not not_16 (not_16_out, controlled_buffer_32_out);
  assign _1 = ROW_4 ? controlled_buffer_35_out : 1'bz;  // Controlled_Buffer controlled_buffer_33
  assign _0_2 = ROW_4 ? controlled_buffer_10_out : 1'bz;  // Controlled_Buffer controlled_buffer_34
  assign controlled_buffer_35_out = ROW_4 ? _1 : 1'bz;  // Controlled_Buffer controlled_buffer_35
  assign controlled_buffer_10_out = ROW_4 ? _0_2 : 1'bz;  // Controlled_Buffer controlled_buffer_36
  not not_17 (controlled_buffer_10_out, not_5_out);
  not not_18 (not_18_out, controlled_buffer_35_out);
  assign _1 = ROW_5 ? controlled_buffer_39_out : 1'bz;  // Controlled_Buffer controlled_buffer_37
  assign _0_2 = ROW_5 ? controlled_buffer_12_out : 1'bz;  // Controlled_Buffer controlled_buffer_38
  assign controlled_buffer_39_out = ROW_5 ? _1 : 1'bz;  // Controlled_Buffer controlled_buffer_39
  assign controlled_buffer_12_out = ROW_5 ? _0_2 : 1'bz;  // Controlled_Buffer controlled_buffer_40
  not not_19 (controlled_buffer_12_out, not_6_out);
  not not_20 (not_20_out, controlled_buffer_39_out);
  assign _0_2 = ROW_6 ? controlled_buffer_14_out : 1'bz;  // Controlled_Buffer controlled_buffer_41
  assign _1 = ROW_6 ? controlled_buffer_44_out : 1'bz;  // Controlled_Buffer controlled_buffer_42
  assign controlled_buffer_14_out = ROW_6 ? _0_2 : 1'bz;  // Controlled_Buffer controlled_buffer_43
  assign controlled_buffer_44_out = ROW_6 ? _1 : 1'bz;  // Controlled_Buffer controlled_buffer_44
  not not_21 (controlled_buffer_14_out, not_7_out);
  not not_22 (not_22_out, controlled_buffer_44_out);
  assign _1 = ROW_7 ? controlled_buffer_48_out : 1'bz;  // Controlled_Buffer controlled_buffer_45
  assign _0_2 = ROW_7 ? controlled_buffer_16_out : 1'bz;  // Controlled_Buffer controlled_buffer_46
  assign controlled_buffer_16_out = ROW_7 ? _0_2 : 1'bz;  // Controlled_Buffer controlled_buffer_47
  assign controlled_buffer_48_out = ROW_7 ? _1 : 1'bz;  // Controlled_Buffer controlled_buffer_48
  not not_23 (controlled_buffer_16_out, not_8_out);
  not not_24 (not_24_out, controlled_buffer_48_out);
  assign _1_2 = ROW_0 ? controlled_buffer_20_out : 1'bz;  // Controlled_Buffer controlled_buffer_49
  assign _2 = ROW_0 ? controlled_buffer_51_out : 1'bz;  // Controlled_Buffer controlled_buffer_50
  assign controlled_buffer_51_out = ROW_0 ? _2 : 1'bz;  // Controlled_Buffer controlled_buffer_51
  assign controlled_buffer_20_out = ROW_0 ? _1_2 : 1'bz;  // Controlled_Buffer controlled_buffer_52
  not not_25 (controlled_buffer_20_out, not_10_out);
  not not_26 (not_26_out, controlled_buffer_51_out);
  assign _2 = ROW_1 ? controlled_buffer_55_out : 1'bz;  // Controlled_Buffer controlled_buffer_53
  assign _1_2 = ROW_1 ? controlled_buffer_24_out : 1'bz;  // Controlled_Buffer controlled_buffer_54
  assign controlled_buffer_55_out = ROW_1 ? _2 : 1'bz;  // Controlled_Buffer controlled_buffer_55
  assign controlled_buffer_24_out = ROW_1 ? _1_2 : 1'bz;  // Controlled_Buffer controlled_buffer_56
  not not_27 (controlled_buffer_24_out, not_12_out);
  not not_28 (not_28_out, controlled_buffer_55_out);
  assign _1_2 = ROW_2 ? controlled_buffer_27_out : 1'bz;  // Controlled_Buffer controlled_buffer_57
  assign _2 = ROW_2 ? controlled_buffer_60_out : 1'bz;  // Controlled_Buffer controlled_buffer_58
  assign controlled_buffer_27_out = ROW_2 ? _1_2 : 1'bz;  // Controlled_Buffer controlled_buffer_59
  assign controlled_buffer_60_out = ROW_2 ? _2 : 1'bz;  // Controlled_Buffer controlled_buffer_60
  not not_29 (controlled_buffer_27_out, not_14_out);
  not not_30 (not_30_out, controlled_buffer_60_out);
  assign _2 = ROW_3 ? controlled_buffer_63_out : 1'bz;  // Controlled_Buffer controlled_buffer_61
  assign _1_2 = ROW_3 ? controlled_buffer_32_out : 1'bz;  // Controlled_Buffer controlled_buffer_62
  assign controlled_buffer_63_out = ROW_3 ? _2 : 1'bz;  // Controlled_Buffer controlled_buffer_63
  assign controlled_buffer_32_out = ROW_3 ? _1_2 : 1'bz;  // Controlled_Buffer controlled_buffer_64
  not not_31 (controlled_buffer_32_out, not_16_out);
  not not_32 (not_32_out, controlled_buffer_63_out);
  assign _2 = ROW_4 ? controlled_buffer_68_out : 1'bz;  // Controlled_Buffer controlled_buffer_65
  assign _1_2 = ROW_4 ? controlled_buffer_35_out : 1'bz;  // Controlled_Buffer controlled_buffer_66
  assign controlled_buffer_35_out = ROW_4 ? _1_2 : 1'bz;  // Controlled_Buffer controlled_buffer_67
  assign controlled_buffer_68_out = ROW_4 ? _2 : 1'bz;  // Controlled_Buffer controlled_buffer_68
  not not_33 (controlled_buffer_35_out, not_18_out);
  not not_34 (not_34_out, controlled_buffer_68_out);
  assign _1_2 = ROW_5 ? controlled_buffer_39_out : 1'bz;  // Controlled_Buffer controlled_buffer_69
  assign _2 = ROW_5 ? controlled_buffer_72_out : 1'bz;  // Controlled_Buffer controlled_buffer_70
  assign controlled_buffer_39_out = ROW_5 ? _1_2 : 1'bz;  // Controlled_Buffer controlled_buffer_71
  assign controlled_buffer_72_out = ROW_5 ? _2 : 1'bz;  // Controlled_Buffer controlled_buffer_72
  not not_35 (controlled_buffer_39_out, not_20_out);
  not not_36 (not_36_out, controlled_buffer_72_out);
  assign _2 = ROW_6 ? controlled_buffer_75_out : 1'bz;  // Controlled_Buffer controlled_buffer_73
  assign _1_2 = ROW_6 ? controlled_buffer_44_out : 1'bz;  // Controlled_Buffer controlled_buffer_74
  assign controlled_buffer_75_out = ROW_6 ? _2 : 1'bz;  // Controlled_Buffer controlled_buffer_75
  assign controlled_buffer_44_out = ROW_6 ? _1_2 : 1'bz;  // Controlled_Buffer controlled_buffer_76
  not not_37 (controlled_buffer_44_out, not_22_out);
  not not_38 (not_38_out, controlled_buffer_75_out);
  assign _2 = ROW_7 ? controlled_buffer_79_out : 1'bz;  // Controlled_Buffer controlled_buffer_77
  assign _1_2 = ROW_7 ? controlled_buffer_48_out : 1'bz;  // Controlled_Buffer controlled_buffer_78
  assign controlled_buffer_79_out = ROW_7 ? _2 : 1'bz;  // Controlled_Buffer controlled_buffer_79
  assign controlled_buffer_48_out = ROW_7 ? _1_2 : 1'bz;  // Controlled_Buffer controlled_buffer_80
  not not_39 (controlled_buffer_48_out, not_24_out);
  not not_40 (not_40_out, controlled_buffer_79_out);
  assign _2_2 = ROW_0 ? controlled_buffer_51_out : 1'bz;  // Controlled_Buffer controlled_buffer_81
  assign _3 = ROW_0 ? controlled_buffer_84_out : 1'bz;  // Controlled_Buffer controlled_buffer_82
  assign controlled_buffer_51_out = ROW_0 ? _2_2 : 1'bz;  // Controlled_Buffer controlled_buffer_83
  assign controlled_buffer_84_out = ROW_0 ? _3 : 1'bz;  // Controlled_Buffer controlled_buffer_84
  not not_41 (controlled_buffer_51_out, not_26_out);
  not not_42 (not_42_out, controlled_buffer_84_out);
  assign _2_2 = ROW_1 ? controlled_buffer_55_out : 1'bz;  // Controlled_Buffer controlled_buffer_85
  assign _3 = ROW_1 ? controlled_buffer_88_out : 1'bz;  // Controlled_Buffer controlled_buffer_86
  assign controlled_buffer_55_out = ROW_1 ? _2_2 : 1'bz;  // Controlled_Buffer controlled_buffer_87
  assign controlled_buffer_88_out = ROW_1 ? _3 : 1'bz;  // Controlled_Buffer controlled_buffer_88
  not not_43 (controlled_buffer_55_out, not_28_out);
  not not_44 (not_44_out, controlled_buffer_88_out);
  assign _2_2 = ROW_2 ? controlled_buffer_60_out : 1'bz;  // Controlled_Buffer controlled_buffer_89
  assign _3 = ROW_2 ? controlled_buffer_92_out : 1'bz;  // Controlled_Buffer controlled_buffer_90
  assign controlled_buffer_60_out = ROW_2 ? _2_2 : 1'bz;  // Controlled_Buffer controlled_buffer_91
  assign controlled_buffer_92_out = ROW_2 ? _3 : 1'bz;  // Controlled_Buffer controlled_buffer_92
  not not_45 (controlled_buffer_60_out, not_30_out);
  not not_46 (not_46_out, controlled_buffer_92_out);
  assign _3 = ROW_3 ? controlled_buffer_95_out : 1'bz;  // Controlled_Buffer controlled_buffer_93
  assign _2_2 = ROW_3 ? controlled_buffer_63_out : 1'bz;  // Controlled_Buffer controlled_buffer_94
  assign controlled_buffer_95_out = ROW_3 ? _3 : 1'bz;  // Controlled_Buffer controlled_buffer_95
  assign controlled_buffer_63_out = ROW_3 ? _2_2 : 1'bz;  // Controlled_Buffer controlled_buffer_96
  not not_47 (controlled_buffer_63_out, not_32_out);
  not not_48 (not_48_out, controlled_buffer_95_out);
  assign _2_2 = ROW_4 ? controlled_buffer_68_out : 1'bz;  // Controlled_Buffer controlled_buffer_97
  assign _3 = ROW_4 ? controlled_buffer_99_out : 1'bz;  // Controlled_Buffer controlled_buffer_98
  assign controlled_buffer_99_out = ROW_4 ? _3 : 1'bz;  // Controlled_Buffer controlled_buffer_99
  assign controlled_buffer_68_out = ROW_4 ? _2_2 : 1'bz;  // Controlled_Buffer controlled_buffer_100
  not not_49 (controlled_buffer_68_out, not_34_out);
  not not_50 (not_50_out, controlled_buffer_99_out);
  assign _3 = ROW_5 ? controlled_buffer_103_out : 1'bz;  // Controlled_Buffer controlled_buffer_101
  assign _2_2 = ROW_5 ? controlled_buffer_72_out : 1'bz;  // Controlled_Buffer controlled_buffer_102
  assign controlled_buffer_103_out = ROW_5 ? _3 : 1'bz;  // Controlled_Buffer controlled_buffer_103
  assign controlled_buffer_72_out = ROW_5 ? _2_2 : 1'bz;  // Controlled_Buffer controlled_buffer_104
  not not_51 (controlled_buffer_72_out, not_36_out);
  not not_52 (not_52_out, controlled_buffer_103_out);
  assign _2_2 = ROW_6 ? controlled_buffer_75_out : 1'bz;  // Controlled_Buffer controlled_buffer_105
  assign _3 = ROW_6 ? controlled_buffer_107_out : 1'bz;  // Controlled_Buffer controlled_buffer_106
  assign controlled_buffer_107_out = ROW_6 ? _3 : 1'bz;  // Controlled_Buffer controlled_buffer_107
  assign controlled_buffer_75_out = ROW_6 ? _2_2 : 1'bz;  // Controlled_Buffer controlled_buffer_108
  not not_53 (controlled_buffer_75_out, not_38_out);
  not not_54 (not_54_out, controlled_buffer_107_out);
  assign _2_2 = ROW_7 ? controlled_buffer_79_out : 1'bz;  // Controlled_Buffer controlled_buffer_109
  assign _3 = ROW_7 ? controlled_buffer_112_out : 1'bz;  // Controlled_Buffer controlled_buffer_110
  assign controlled_buffer_79_out = ROW_7 ? _2_2 : 1'bz;  // Controlled_Buffer controlled_buffer_111
  assign controlled_buffer_112_out = ROW_7 ? _3 : 1'bz;  // Controlled_Buffer controlled_buffer_112
  not not_55 (controlled_buffer_79_out, not_40_out);
  not not_56 (not_56_out, controlled_buffer_112_out);
  assign _4 = ROW_0 ? controlled_buffer_115_out : 1'bz;  // Controlled_Buffer controlled_buffer_113
  assign _3_2 = ROW_0 ? controlled_buffer_84_out : 1'bz;  // Controlled_Buffer controlled_buffer_114
  assign controlled_buffer_115_out = ROW_0 ? _4 : 1'bz;  // Controlled_Buffer controlled_buffer_115
  assign controlled_buffer_84_out = ROW_0 ? _3_2 : 1'bz;  // Controlled_Buffer controlled_buffer_116
  not not_57 (controlled_buffer_84_out, not_42_out);
  not not_58 (not_58_out, controlled_buffer_115_out);
  assign _3_2 = ROW_1 ? controlled_buffer_88_out : 1'bz;  // Controlled_Buffer controlled_buffer_117
  assign _4 = ROW_1 ? controlled_buffer_119_out : 1'bz;  // Controlled_Buffer controlled_buffer_118
  assign controlled_buffer_119_out = ROW_1 ? _4 : 1'bz;  // Controlled_Buffer controlled_buffer_119
  assign controlled_buffer_88_out = ROW_1 ? _3_2 : 1'bz;  // Controlled_Buffer controlled_buffer_120
  not not_59 (controlled_buffer_88_out, not_44_out);
  not not_60 (not_60_out, controlled_buffer_119_out);
  assign _4 = ROW_2 ? controlled_buffer_124_out : 1'bz;  // Controlled_Buffer controlled_buffer_121
  assign _3_2 = ROW_2 ? controlled_buffer_92_out : 1'bz;  // Controlled_Buffer controlled_buffer_122
  assign controlled_buffer_92_out = ROW_2 ? _3_2 : 1'bz;  // Controlled_Buffer controlled_buffer_123
  assign controlled_buffer_124_out = ROW_2 ? _4 : 1'bz;  // Controlled_Buffer controlled_buffer_124
  not not_61 (controlled_buffer_92_out, not_46_out);
  not not_62 (not_62_out, controlled_buffer_124_out);
  assign _4 = ROW_3 ? controlled_buffer_127_out : 1'bz;  // Controlled_Buffer controlled_buffer_125
  assign _3_2 = ROW_3 ? controlled_buffer_95_out : 1'bz;  // Controlled_Buffer controlled_buffer_126
  assign controlled_buffer_127_out = ROW_3 ? _4 : 1'bz;  // Controlled_Buffer controlled_buffer_127
  assign controlled_buffer_95_out = ROW_3 ? _3_2 : 1'bz;  // Controlled_Buffer controlled_buffer_128
  not not_63 (controlled_buffer_95_out, not_48_out);
  not not_64 (not_64_out, controlled_buffer_127_out);
  assign _4 = ROW_4 ? controlled_buffer_132_out : 1'bz;  // Controlled_Buffer controlled_buffer_129
  assign _3_2 = ROW_4 ? controlled_buffer_99_out : 1'bz;  // Controlled_Buffer controlled_buffer_130
  assign controlled_buffer_99_out = ROW_4 ? _3_2 : 1'bz;  // Controlled_Buffer controlled_buffer_131
  assign controlled_buffer_132_out = ROW_4 ? _4 : 1'bz;  // Controlled_Buffer controlled_buffer_132
  not not_65 (controlled_buffer_99_out, not_50_out);
  not not_66 (not_66_out, controlled_buffer_132_out);
  assign _4 = ROW_5 ? controlled_buffer_135_out : 1'bz;  // Controlled_Buffer controlled_buffer_133
  assign _3_2 = ROW_5 ? controlled_buffer_103_out : 1'bz;  // Controlled_Buffer controlled_buffer_134
  assign controlled_buffer_135_out = ROW_5 ? _4 : 1'bz;  // Controlled_Buffer controlled_buffer_135
  assign controlled_buffer_103_out = ROW_5 ? _3_2 : 1'bz;  // Controlled_Buffer controlled_buffer_136
  not not_67 (controlled_buffer_103_out, not_52_out);
  not not_68 (not_68_out, controlled_buffer_135_out);
  assign _4 = ROW_6 ? controlled_buffer_140_out : 1'bz;  // Controlled_Buffer controlled_buffer_137
  assign _3_2 = ROW_6 ? controlled_buffer_107_out : 1'bz;  // Controlled_Buffer controlled_buffer_138
  assign controlled_buffer_107_out = ROW_6 ? _3_2 : 1'bz;  // Controlled_Buffer controlled_buffer_139
  assign controlled_buffer_140_out = ROW_6 ? _4 : 1'bz;  // Controlled_Buffer controlled_buffer_140
  not not_69 (controlled_buffer_107_out, not_54_out);
  not not_70 (not_70_out, controlled_buffer_140_out);
  assign _4 = ROW_7 ? controlled_buffer_144_out : 1'bz;  // Controlled_Buffer controlled_buffer_141
  assign _3_2 = ROW_7 ? controlled_buffer_112_out : 1'bz;  // Controlled_Buffer controlled_buffer_142
  assign controlled_buffer_112_out = ROW_7 ? _3_2 : 1'bz;  // Controlled_Buffer controlled_buffer_143
  assign controlled_buffer_144_out = ROW_7 ? _4 : 1'bz;  // Controlled_Buffer controlled_buffer_144
  not not_71 (controlled_buffer_112_out, not_56_out);
  not not_72 (not_72_out, controlled_buffer_144_out);
  assign _5 = ROW_0 ? controlled_buffer_148_out : 1'bz;  // Controlled_Buffer controlled_buffer_145
  assign _4_2 = ROW_0 ? controlled_buffer_115_out : 1'bz;  // Controlled_Buffer controlled_buffer_146
  assign controlled_buffer_115_out = ROW_0 ? _4_2 : 1'bz;  // Controlled_Buffer controlled_buffer_147
  assign controlled_buffer_148_out = ROW_0 ? _5 : 1'bz;  // Controlled_Buffer controlled_buffer_148
  not not_73 (controlled_buffer_115_out, not_58_out);
  not not_74 (not_74_out, controlled_buffer_148_out);
  assign _4_2 = ROW_1 ? controlled_buffer_119_out : 1'bz;  // Controlled_Buffer controlled_buffer_149
  assign _5 = ROW_1 ? controlled_buffer_152_out : 1'bz;  // Controlled_Buffer controlled_buffer_150
  assign controlled_buffer_119_out = ROW_1 ? _4_2 : 1'bz;  // Controlled_Buffer controlled_buffer_151
  assign controlled_buffer_152_out = ROW_1 ? _5 : 1'bz;  // Controlled_Buffer controlled_buffer_152
  not not_75 (controlled_buffer_119_out, not_60_out);
  not not_76 (not_76_out, controlled_buffer_152_out);
  assign _4_2 = ROW_2 ? controlled_buffer_124_out : 1'bz;  // Controlled_Buffer controlled_buffer_153
  assign _5 = ROW_2 ? controlled_buffer_155_out : 1'bz;  // Controlled_Buffer controlled_buffer_154
  assign controlled_buffer_155_out = ROW_2 ? _5 : 1'bz;  // Controlled_Buffer controlled_buffer_155
  assign controlled_buffer_124_out = ROW_2 ? _4_2 : 1'bz;  // Controlled_Buffer controlled_buffer_156
  not not_77 (controlled_buffer_124_out, not_62_out);
  not not_78 (not_78_out, controlled_buffer_155_out);
  assign _5 = ROW_3 ? controlled_buffer_160_out : 1'bz;  // Controlled_Buffer controlled_buffer_157
  assign _4_2 = ROW_3 ? controlled_buffer_127_out : 1'bz;  // Controlled_Buffer controlled_buffer_158
  assign controlled_buffer_127_out = ROW_3 ? _4_2 : 1'bz;  // Controlled_Buffer controlled_buffer_159
  assign controlled_buffer_160_out = ROW_3 ? _5 : 1'bz;  // Controlled_Buffer controlled_buffer_160
  not not_79 (controlled_buffer_127_out, not_64_out);
  not not_80 (not_80_out, controlled_buffer_160_out);
  assign _4_2 = ROW_4 ? controlled_buffer_132_out : 1'bz;  // Controlled_Buffer controlled_buffer_161
  assign _5 = ROW_4 ? controlled_buffer_163_out : 1'bz;  // Controlled_Buffer controlled_buffer_162
  assign controlled_buffer_163_out = ROW_4 ? _5 : 1'bz;  // Controlled_Buffer controlled_buffer_163
  assign controlled_buffer_132_out = ROW_4 ? _4_2 : 1'bz;  // Controlled_Buffer controlled_buffer_164
  not not_81 (controlled_buffer_132_out, not_66_out);
  not not_82 (not_82_out, controlled_buffer_163_out);
  assign _5 = ROW_5 ? controlled_buffer_167_out : 1'bz;  // Controlled_Buffer controlled_buffer_165
  assign _4_2 = ROW_5 ? controlled_buffer_135_out : 1'bz;  // Controlled_Buffer controlled_buffer_166
  assign controlled_buffer_167_out = ROW_5 ? _5 : 1'bz;  // Controlled_Buffer controlled_buffer_167
  assign controlled_buffer_135_out = ROW_5 ? _4_2 : 1'bz;  // Controlled_Buffer controlled_buffer_168
  not not_83 (controlled_buffer_135_out, not_68_out);
  not not_84 (not_84_out, controlled_buffer_167_out);
  assign _4_2 = ROW_6 ? controlled_buffer_140_out : 1'bz;  // Controlled_Buffer controlled_buffer_169
  assign _5 = ROW_6 ? controlled_buffer_172_out : 1'bz;  // Controlled_Buffer controlled_buffer_170
  assign controlled_buffer_140_out = ROW_6 ? _4_2 : 1'bz;  // Controlled_Buffer controlled_buffer_171
  assign controlled_buffer_172_out = ROW_6 ? _5 : 1'bz;  // Controlled_Buffer controlled_buffer_172
  not not_85 (controlled_buffer_140_out, not_70_out);
  not not_86 (not_86_out, controlled_buffer_172_out);
  assign _4_2 = ROW_7 ? controlled_buffer_144_out : 1'bz;  // Controlled_Buffer controlled_buffer_173
  assign _5 = ROW_7 ? controlled_buffer_175_out : 1'bz;  // Controlled_Buffer controlled_buffer_174
  assign controlled_buffer_175_out = ROW_7 ? _5 : 1'bz;  // Controlled_Buffer controlled_buffer_175
  assign controlled_buffer_144_out = ROW_7 ? _4_2 : 1'bz;  // Controlled_Buffer controlled_buffer_176
  not not_87 (controlled_buffer_144_out, not_72_out);
  not not_88 (not_88_out, controlled_buffer_175_out);
  assign _6 = ROW_0 ? controlled_buffer_180_out : 1'bz;  // Controlled_Buffer controlled_buffer_177
  assign _5_2 = ROW_0 ? controlled_buffer_148_out : 1'bz;  // Controlled_Buffer controlled_buffer_178
  assign controlled_buffer_148_out = ROW_0 ? _5_2 : 1'bz;  // Controlled_Buffer controlled_buffer_179
  assign controlled_buffer_180_out = ROW_0 ? _6 : 1'bz;  // Controlled_Buffer controlled_buffer_180
  not not_89 (controlled_buffer_148_out, not_74_out);
  not not_90 (not_90_out, controlled_buffer_180_out);
  assign _6 = ROW_1 ? controlled_buffer_183_out : 1'bz;  // Controlled_Buffer controlled_buffer_181
  assign _5_2 = ROW_1 ? controlled_buffer_152_out : 1'bz;  // Controlled_Buffer controlled_buffer_182
  assign controlled_buffer_183_out = ROW_1 ? _6 : 1'bz;  // Controlled_Buffer controlled_buffer_183
  assign controlled_buffer_152_out = ROW_1 ? _5_2 : 1'bz;  // Controlled_Buffer controlled_buffer_184
  not not_91 (controlled_buffer_152_out, not_76_out);
  not not_92 (not_92_out, controlled_buffer_183_out);
  assign _6 = ROW_2 ? controlled_buffer_187_out : 1'bz;  // Controlled_Buffer controlled_buffer_185
  assign _5_2 = ROW_2 ? controlled_buffer_155_out : 1'bz;  // Controlled_Buffer controlled_buffer_186
  assign controlled_buffer_187_out = ROW_2 ? _6 : 1'bz;  // Controlled_Buffer controlled_buffer_187
  assign controlled_buffer_155_out = ROW_2 ? _5_2 : 1'bz;  // Controlled_Buffer controlled_buffer_188
  not not_93 (controlled_buffer_155_out, not_78_out);
  not not_94 (not_94_out, controlled_buffer_187_out);
  assign _6 = ROW_3 ? controlled_buffer_192_out : 1'bz;  // Controlled_Buffer controlled_buffer_189
  assign _5_2 = ROW_3 ? controlled_buffer_160_out : 1'bz;  // Controlled_Buffer controlled_buffer_190
  assign controlled_buffer_160_out = ROW_3 ? _5_2 : 1'bz;  // Controlled_Buffer controlled_buffer_191
  assign controlled_buffer_192_out = ROW_3 ? _6 : 1'bz;  // Controlled_Buffer controlled_buffer_192
  not not_95 (controlled_buffer_160_out, not_80_out);
  not not_96 (not_96_out, controlled_buffer_192_out);
  assign _6 = ROW_4 ? controlled_buffer_195_out : 1'bz;  // Controlled_Buffer controlled_buffer_193
  assign _5_2 = ROW_4 ? controlled_buffer_163_out : 1'bz;  // Controlled_Buffer controlled_buffer_194
  assign controlled_buffer_195_out = ROW_4 ? _6 : 1'bz;  // Controlled_Buffer controlled_buffer_195
  assign controlled_buffer_163_out = ROW_4 ? _5_2 : 1'bz;  // Controlled_Buffer controlled_buffer_196
  not not_97 (controlled_buffer_163_out, not_82_out);
  not not_98 (not_98_out, controlled_buffer_195_out);
  assign _6 = ROW_5 ? controlled_buffer_199_out : 1'bz;  // Controlled_Buffer controlled_buffer_197
  assign _5_2 = ROW_5 ? controlled_buffer_167_out : 1'bz;  // Controlled_Buffer controlled_buffer_198
  assign controlled_buffer_199_out = ROW_5 ? _6 : 1'bz;  // Controlled_Buffer controlled_buffer_199
  assign controlled_buffer_167_out = ROW_5 ? _5_2 : 1'bz;  // Controlled_Buffer controlled_buffer_200
  not not_99 (controlled_buffer_167_out, not_84_out);
  not not_100 (not_100_out, controlled_buffer_199_out);
  assign _5_2 = ROW_6 ? controlled_buffer_172_out : 1'bz;  // Controlled_Buffer controlled_buffer_201
  assign _6 = ROW_6 ? controlled_buffer_203_out : 1'bz;  // Controlled_Buffer controlled_buffer_202
  assign controlled_buffer_203_out = ROW_6 ? _6 : 1'bz;  // Controlled_Buffer controlled_buffer_203
  assign controlled_buffer_172_out = ROW_6 ? _5_2 : 1'bz;  // Controlled_Buffer controlled_buffer_204
  not not_101 (controlled_buffer_172_out, not_86_out);
  not not_102 (not_102_out, controlled_buffer_203_out);
  assign _5_2 = ROW_7 ? controlled_buffer_175_out : 1'bz;  // Controlled_Buffer controlled_buffer_205
  assign _6 = ROW_7 ? controlled_buffer_208_out : 1'bz;  // Controlled_Buffer controlled_buffer_206
  assign controlled_buffer_175_out = ROW_7 ? _5_2 : 1'bz;  // Controlled_Buffer controlled_buffer_207
  assign controlled_buffer_208_out = ROW_7 ? _6 : 1'bz;  // Controlled_Buffer controlled_buffer_208
  not not_103 (controlled_buffer_175_out, not_88_out);
  not not_104 (not_104_out, controlled_buffer_208_out);
  assign _7 = ROW_0 ? controlled_buffer_211_out : 1'bz;  // Controlled_Buffer controlled_buffer_209
  assign _6_2 = ROW_0 ? controlled_buffer_180_out : 1'bz;  // Controlled_Buffer controlled_buffer_210
  assign controlled_buffer_211_out = ROW_0 ? _7 : 1'bz;  // Controlled_Buffer controlled_buffer_211
  assign controlled_buffer_180_out = ROW_0 ? _6_2 : 1'bz;  // Controlled_Buffer controlled_buffer_212
  not not_105 (controlled_buffer_180_out, not_90_out);
  not not_106 (not_106_out, controlled_buffer_211_out);
  assign _6_2 = ROW_1 ? controlled_buffer_183_out : 1'bz;  // Controlled_Buffer controlled_buffer_213
  assign _7 = ROW_1 ? controlled_buffer_215_out : 1'bz;  // Controlled_Buffer controlled_buffer_214
  assign controlled_buffer_215_out = ROW_1 ? _7 : 1'bz;  // Controlled_Buffer controlled_buffer_215
  assign controlled_buffer_183_out = ROW_1 ? _6_2 : 1'bz;  // Controlled_Buffer controlled_buffer_216
  not not_107 (controlled_buffer_183_out, not_92_out);
  not not_108 (not_108_out, controlled_buffer_215_out);
  assign _7 = ROW_2 ? controlled_buffer_220_out : 1'bz;  // Controlled_Buffer controlled_buffer_217
  assign _6_2 = ROW_2 ? controlled_buffer_187_out : 1'bz;  // Controlled_Buffer controlled_buffer_218
  assign controlled_buffer_187_out = ROW_2 ? _6_2 : 1'bz;  // Controlled_Buffer controlled_buffer_219
  assign controlled_buffer_220_out = ROW_2 ? _7 : 1'bz;  // Controlled_Buffer controlled_buffer_220
  not not_109 (controlled_buffer_187_out, not_94_out);
  not not_110 (not_110_out, controlled_buffer_220_out);
  assign _7 = ROW_3 ? controlled_buffer_223_out : 1'bz;  // Controlled_Buffer controlled_buffer_221
  assign _6_2 = ROW_3 ? controlled_buffer_192_out : 1'bz;  // Controlled_Buffer controlled_buffer_222
  assign controlled_buffer_223_out = ROW_3 ? _7 : 1'bz;  // Controlled_Buffer controlled_buffer_223
  assign controlled_buffer_192_out = ROW_3 ? _6_2 : 1'bz;  // Controlled_Buffer controlled_buffer_224
  not not_111 (controlled_buffer_192_out, not_96_out);
  not not_112 (not_112_out, controlled_buffer_223_out);
  assign _6_2 = ROW_4 ? controlled_buffer_195_out : 1'bz;  // Controlled_Buffer controlled_buffer_225
  assign _7 = ROW_4 ? controlled_buffer_227_out : 1'bz;  // Controlled_Buffer controlled_buffer_226
  assign controlled_buffer_227_out = ROW_4 ? _7 : 1'bz;  // Controlled_Buffer controlled_buffer_227
  assign controlled_buffer_195_out = ROW_4 ? _6_2 : 1'bz;  // Controlled_Buffer controlled_buffer_228
  not not_113 (controlled_buffer_195_out, not_98_out);
  not not_114 (not_114_out, controlled_buffer_227_out);
  assign _7 = ROW_5 ? controlled_buffer_232_out : 1'bz;  // Controlled_Buffer controlled_buffer_229
  assign _6_2 = ROW_5 ? controlled_buffer_199_out : 1'bz;  // Controlled_Buffer controlled_buffer_230
  assign controlled_buffer_199_out = ROW_5 ? _6_2 : 1'bz;  // Controlled_Buffer controlled_buffer_231
  assign controlled_buffer_232_out = ROW_5 ? _7 : 1'bz;  // Controlled_Buffer controlled_buffer_232
  not not_115 (controlled_buffer_199_out, not_100_out);
  not not_116 (not_116_out, controlled_buffer_232_out);
  assign _7 = ROW_6 ? controlled_buffer_235_out : 1'bz;  // Controlled_Buffer controlled_buffer_233
  assign _6_2 = ROW_6 ? controlled_buffer_203_out : 1'bz;  // Controlled_Buffer controlled_buffer_234
  assign controlled_buffer_235_out = ROW_6 ? _7 : 1'bz;  // Controlled_Buffer controlled_buffer_235
  assign controlled_buffer_203_out = ROW_6 ? _6_2 : 1'bz;  // Controlled_Buffer controlled_buffer_236
  not not_117 (controlled_buffer_203_out, not_102_out);
  not not_118 (not_118_out, controlled_buffer_235_out);
  assign _6_2 = ROW_7 ? controlled_buffer_208_out : 1'bz;  // Controlled_Buffer controlled_buffer_237
  assign _7 = ROW_7 ? controlled_buffer_239_out : 1'bz;  // Controlled_Buffer controlled_buffer_238
  assign controlled_buffer_239_out = ROW_7 ? _7 : 1'bz;  // Controlled_Buffer controlled_buffer_239
  assign controlled_buffer_208_out = ROW_7 ? _6_2 : 1'bz;  // Controlled_Buffer controlled_buffer_240
  not not_119 (controlled_buffer_208_out, not_104_out);
  not not_120 (not_120_out, controlled_buffer_239_out);
  assign _7_2 = ROW_0 ? controlled_buffer_211_out : 1'bz;  // Controlled_Buffer controlled_buffer_241
  assign controlled_buffer_211_out = ROW_0 ? _7_2 : 1'bz;  // Controlled_Buffer controlled_buffer_242
  not not_121 (controlled_buffer_211_out, not_106_out);
  assign _7_2 = ROW_1 ? controlled_buffer_215_out : 1'bz;  // Controlled_Buffer controlled_buffer_243
  assign controlled_buffer_215_out = ROW_1 ? _7_2 : 1'bz;  // Controlled_Buffer controlled_buffer_244
  not not_122 (controlled_buffer_215_out, not_108_out);
  assign _7_2 = ROW_2 ? controlled_buffer_220_out : 1'bz;  // Controlled_Buffer controlled_buffer_245
  assign controlled_buffer_220_out = ROW_2 ? _7_2 : 1'bz;  // Controlled_Buffer controlled_buffer_246
  not not_123 (controlled_buffer_220_out, not_110_out);
  assign _7_2 = ROW_3 ? controlled_buffer_223_out : 1'bz;  // Controlled_Buffer controlled_buffer_247
  assign controlled_buffer_223_out = ROW_3 ? _7_2 : 1'bz;  // Controlled_Buffer controlled_buffer_248
  not not_124 (controlled_buffer_223_out, not_112_out);
  assign _7_2 = ROW_4 ? controlled_buffer_227_out : 1'bz;  // Controlled_Buffer controlled_buffer_249
  assign controlled_buffer_227_out = ROW_4 ? _7_2 : 1'bz;  // Controlled_Buffer controlled_buffer_250
  not not_125 (controlled_buffer_227_out, not_114_out);
  assign _7_2 = ROW_5 ? controlled_buffer_232_out : 1'bz;  // Controlled_Buffer controlled_buffer_251
  assign controlled_buffer_232_out = ROW_5 ? _7_2 : 1'bz;  // Controlled_Buffer controlled_buffer_252
  not not_126 (controlled_buffer_232_out, not_116_out);
  assign _7_2 = ROW_6 ? controlled_buffer_235_out : 1'bz;  // Controlled_Buffer controlled_buffer_253
  assign controlled_buffer_235_out = ROW_6 ? _7_2 : 1'bz;  // Controlled_Buffer controlled_buffer_254
  not not_127 (controlled_buffer_235_out, not_118_out);
  assign _7_2 = ROW_7 ? controlled_buffer_239_out : 1'bz;  // Controlled_Buffer controlled_buffer_255
  assign controlled_buffer_239_out = ROW_7 ? _7_2 : 1'bz;  // Controlled_Buffer controlled_buffer_256
  not not_128 (controlled_buffer_239_out, not_120_out);
endmodule

module _1_to_2 (
  input  _0,
  output _0_2,
  output _0_3
);

  not not_1 (_0_3, _0);

  assign _0_2 = _0;
endmodule

module _2_to_4 (
  input  _0,
  input  _1,
  output _10,
  output _11,
  output _00,
  output _01
);

  wire not_1_out, not_2_out, transistor_1_out, transistor_2_out, transistor_3_out, transistor_4_out,
       transistor_5_out, transistor_6_out;

  not not_1 (not_1_out, _0);
  not not_2 (not_2_out, _1);
  Transistor #(.\type ("n")) transistor_1 (.in(1'b0), .out(transistor_1_out), .gate(_1));
  Transistor #(.\type ("n")) transistor_2 (.in(1'b0), .out(transistor_2_out), .gate(not_2_out));
  Transistor #(.\type ("n")) transistor_3 (.in(transistor_1_out), .out(transistor_3_out), .gate(_0));
  Transistor #(.\type ("n")) transistor_4 (.in(transistor_2_out), .out(transistor_4_out), .gate(not_1_out));
  Transistor #(.\type ("n")) transistor_5 (.in(transistor_1_out), .out(transistor_5_out), .gate(not_1_out));
  Transistor #(.\type ("n")) transistor_6 (.in(transistor_2_out), .out(transistor_6_out), .gate(_0));
  Transistor transistor_7 (.in(1'b1), .out(transistor_5_out), .gate(not_1_out));
  Transistor transistor_8 (.in(1'b1), .out(transistor_4_out), .gate(not_1_out));
  Transistor transistor_9 (.in(1'b1), .out(transistor_3_out), .gate(_1));
  Transistor transistor_10 (.in(1'b1), .out(transistor_6_out), .gate(not_2_out));
  Transistor transistor_11 (.in(1'b1), .out(transistor_5_out), .gate(_1));
  Transistor transistor_12 (.in(1'b1), .out(transistor_4_out), .gate(not_2_out));
  Transistor transistor_13 (.in(1'b1), .out(transistor_3_out), .gate(_0));
  Transistor transistor_14 (.in(1'b1), .out(transistor_6_out), .gate(_0));
  not not_3 (_10, transistor_5_out);
  not not_4 (_11, transistor_3_out);
  not not_5 (_00, transistor_4_out);
  not not_6 (_01, transistor_6_out);
endmodule

module _4_ZAND (
  input  in_1,
  input  in_2,
  input  in_3,
  input  in_4,
  output out_5
);

  wire nand_1_out, not_1_out, not_2_out;

  not not_1 (not_1_out, nand_1_out);
  nand nand_1 (nand_1_out, in_1, in_2, in_3, in_4);
  not not_2 (not_2_out, not_1_out);
  not not_3 (out_5, not_2_out);
endmodule

module _2_to_4_Latched (
  input  R0,
  input  R1,
  input  nRES,
  output _00,
  output _01,
  output _10,
  output _11
);

  wire multiplexer_1_out, multiplexer_2_out, multiplexer_3_out, multiplexer_4_out, multiplexer_5_out,
       multiplexer_6_out, multiplexer_7_out, multiplexer_8_out, multiplexer_9_out, multiplexer_10_out,
       not_1_out, not_2_out, not_3_out, undriven, undriven_2, undriven_3, undriven_4;

  not not_1 (not_1_out, R0);
  not not_2 (not_2_out, R1);
  Multiplexer multiplexer_1 (.in0(undriven), .in1(1'b1), .out(multiplexer_1_out), .sel(not_1_out));  // open: en
  Multiplexer multiplexer_2 (
    .in0(undriven_2), .in1(multiplexer_1_out), .out(multiplexer_2_out), .sel(not_2_out));  // open: en
  Multiplexer multiplexer_3 (.in1(multiplexer_1_out), .out(multiplexer_3_out), .sel(R1));  // open: in0, en
  not not_3 (not_3_out, R1);
  Multiplexer multiplexer_4 (.in0(undriven_3), .in1(1'b1), .out(multiplexer_4_out), .sel(R0));  // open: en
  Multiplexer multiplexer_5 (.in0(1'b0), .in1(multiplexer_2_out), .out(multiplexer_5_out), .sel(nRES));  // open: en
  Multiplexer multiplexer_6 (.in0(1'b0), .in1(multiplexer_9_out), .out(multiplexer_6_out), .sel(nRES));  // open: en
  Multiplexer multiplexer_7 (.in0(1'b0), .in1(multiplexer_3_out), .out(multiplexer_7_out), .sel(nRES));  // open: en
  Multiplexer multiplexer_8 (.in0(1'b0), .in1(multiplexer_10_out), .out(multiplexer_8_out), .sel(nRES));  // open: en
  Multiplexer multiplexer_9 (
    .in0(undriven_4), .in1(multiplexer_4_out), .out(multiplexer_9_out), .sel(not_3_out));  // open: en
  Multiplexer multiplexer_10 (.in1(multiplexer_4_out), .out(multiplexer_10_out), .sel(R1));  // open: in0, en
  LATCH latch_1 (.EN(1'b1), .in(multiplexer_5_out), .out(_00));
  LATCH latch_2 (.EN(1'b1), .in(multiplexer_6_out), .out(_01));
  LATCH latch_3 (.EN(1'b1), .in(multiplexer_7_out), .out(_10));
  LATCH latch_4 (.EN(1'b1), .in(multiplexer_8_out), .out(_11));
endmodule

module draft (
  input  nRES,
  input  nWORD,
  input  nCS,
  input  nBS0,
  input  nBS1,
  input  nBS2,
  input  nBS3,
  input  DEBUG_RW,
  input  A0,
  input  A1,
  input  A2,
  input  R0,
  input  R1,
  input  R2,
  input  R3,
  input  R4
);

  wire latch_1_out, latch_2_out, latch_3_out, latch_4_out, latch_5_out, latch_6_out, latch_7_out,
       latch_8_out, latch_9_out, latch_10_out, latch_11_out, latch_12_out, latch_13_out, latch_14_out,
       latch_15_out, n1_to_2_1__0_2, n1_to_2_1__0_3, n1_to_2_2__0_2, n1_to_2_2__0_3, n1_to_2_3__0_2,
       n1_to_2_3__0_3, n2_to_4_1__00, n2_to_4_1__01, n2_to_4_1__10, n2_to_4_1__11, n2_to_4_2__00,
       n2_to_4_2__01, n2_to_4_latched_1__00, n2_to_4_latched_1__01, n2_to_4_latched_1__10,
       n2_to_4_latched_1__11, n4_zand_1_out_5, n4_zand_2_out_5, n4_zand_3_out_5, n4_zand_4_out_5,
       n4_zand_5_out_5, n4_zand_6_out_5, n4_zand_7_out_5, n4_zand_8_out_5, n4_zand_9_out_5, n4_zand_10_out_5,
       n4_zand_11_out_5, n4_zand_12_out_5, n4_zand_13_out_5, n4_zand_14_out_5, n4_zand_15_out_5,
       n4_zand_16_out_5, n4_zand_17_out_5, n4_zand_18_out_5, n4_zand_19_out_5, n4_zand_20_out_5,
       n4_zand_21_out_5, n4_zand_22_out_5, n4_zand_23_out_5, n4_zand_24_out_5, n4_zand_25_out_5,
       n4_zand_26_out_5, n4_zand_27_out_5, n4_zand_28_out_5, n4_zand_29_out_5, n4_zand_30_out_5,
       n4_zand_31_out_5, n4_zand_32_out_5, nand_1_out, not_1_out, not_2_out, not_3_out, not_4_out, not_5_out,
       not_6_out, not_7_out, rw_control_1_nrw__1, rw_control_1_rw__2, rw_control_1_rw__unk3, undriven,
       undriven_2, undriven_3, undriven_4, undriven_5, undriven_6, undriven_7, undriven_8, undriven_9,
       undriven_10, undriven_11, undriven_12, undriven_13, undriven_14, undriven_15, undriven_16,
       undriven_17, undriven_18, undriven_19, undriven_20, undriven_21, undriven_22, undriven_23,
       undriven_24, undriven_25, undriven_26, undriven_27, undriven_28, undriven_29, undriven_30,
       undriven_31, undriven_32, undriven_33, undriven_34, undriven_35, undriven_36, undriven_37,
       undriven_38, undriven_39, undriven_40, undriven_41, undriven_42, undriven_43, undriven_44,
       undriven_45, undriven_46, undriven_47, undriven_48, undriven_49, undriven_50, undriven_51,
       undriven_52, undriven_53, undriven_54, undriven_55, undriven_56, undriven_57, undriven_58,
       undriven_59, undriven_60, undriven_61, undriven_62, undriven_63, undriven_64;

  not not_1 (not_1_out, DEBUG_RW);
  LATCH latch_1 (.EN(not_1_out), .in(A0), .out(latch_1_out));
  LATCH latch_2 (.EN(not_1_out), .in(A1), .out(latch_2_out));
  LATCH latch_3 (.EN(not_1_out), .in(A2), .out(latch_3_out));
  LATCH latch_4 (.EN(not_1_out), .in(R0), .out(latch_4_out));
  LATCH latch_5 (.EN(not_1_out), .in(R1), .out(latch_5_out));
  LATCH latch_6 (.EN(not_1_out), .in(R2), .out(latch_6_out));
  LATCH latch_7 (.EN(not_1_out), .in(R3), .out(latch_7_out));
  LATCH latch_8 (.EN(not_1_out), .in(R4), .out(latch_8_out));
  LATCH latch_9 (.EN(not_1_out), .in(1'b0), .out(latch_9_out));
  RW_Control rw_control_1 (
    .nRES(nRES), .nWORD(nWORD), .BYTESEL(nand_1_out), .nRWC__unk2(1'b1), .RW__2(rw_control_1_rw__2),
    .nRW__1(rw_control_1_nrw__1), .RW__unk3(rw_control_1_rw__unk3), .nCS(nCS));
  nand nand_1 (nand_1_out, nBS0, nBS1, nBS2, nBS3, 1'b1, 1'b1);
  _1_to_2 u_1_to_2_1 (._0(latch_1_out), ._0_2(n1_to_2_1__0_2), ._0_3(n1_to_2_1__0_3));
  _1_to_2 u_1_to_2_2 (._0(latch_2_out), ._0_2(n1_to_2_2__0_2), ._0_3(n1_to_2_2__0_3));
  _1_to_2 u_1_to_2_3 (._0(latch_3_out), ._0_2(n1_to_2_3__0_2), ._0_3(n1_to_2_3__0_3));
  _2_to_4_Latched u_2_to_4_latched_1 (
    .R0(latch_4_out), .R1(latch_5_out), .nRES(DEBUG_RW), ._00(n2_to_4_latched_1__00),
    ._01(n2_to_4_latched_1__01), ._10(n2_to_4_latched_1__10), ._11(n2_to_4_latched_1__11));
  _2_to_4 u_2_to_4_1 (
    ._0(latch_6_out), ._1(latch_7_out), ._00(n2_to_4_1__00), ._01(n2_to_4_1__01), ._10(n2_to_4_1__10),
    ._11(n2_to_4_1__11));
  _2_to_4 u_2_to_4_2 (._0(latch_8_out), ._1(latch_9_out), ._00(n2_to_4_2__00), ._01(n2_to_4_2__01));  // open: _10, _11
  LATCH latch_10 (.EN(rw_control_1_rw__2), .in(nBS0), .out(latch_10_out));
  not not_2 (not_2_out, latch_10_out);
  LATCH latch_11 (.EN(rw_control_1_rw__2), .in(nBS1), .out(latch_11_out));
  not not_3 (not_3_out, latch_11_out);
  not not_4 (not_4_out, latch_12_out);
  LATCH latch_12 (.EN(rw_control_1_rw__2), .in(nBS2), .out(latch_12_out));
  not not_5 (not_5_out, latch_13_out);
  LATCH latch_13 (.EN(rw_control_1_rw__2), .in(nBS3), .out(latch_13_out));
  LATCH latch_14 (.EN(rw_control_1_rw__2), .in(1'b1), .out(latch_14_out));
  not not_6 (not_6_out, latch_14_out);
  LATCH latch_15 (.EN(rw_control_1_rw__2), .in(1'b1), .out(latch_15_out));
  not not_7 (not_7_out, latch_15_out);
  _4_ZAND u_4_zand_1 (
    .in_1(n2_to_4_latched_1__00), .in_2(n2_to_4_1__00), .in_3(n2_to_4_2__00), .in_4(1'b1),
    .out_5(n4_zand_1_out_5));
  _4_ZAND u_4_zand_2 (
    .in_1(n2_to_4_latched_1__10), .in_2(n2_to_4_1__00), .in_3(n2_to_4_2__00), .in_4(1'b1),
    .out_5(n4_zand_2_out_5));
  _4_ZAND u_4_zand_3 (
    .in_1(n2_to_4_latched_1__01), .in_2(n2_to_4_1__00), .in_3(n2_to_4_2__00), .in_4(1'b1),
    .out_5(n4_zand_3_out_5));
  _4_ZAND u_4_zand_4 (
    .in_1(n2_to_4_latched_1__11), .in_2(n2_to_4_1__00), .in_3(n2_to_4_2__00), .in_4(1'b1),
    .out_5(n4_zand_4_out_5));
  _4_ZAND u_4_zand_5 (
    .in_1(n2_to_4_latched_1__00), .in_2(n2_to_4_1__01), .in_3(n2_to_4_2__00), .in_4(1'b1),
    .out_5(n4_zand_5_out_5));
  _4_ZAND u_4_zand_6 (
    .in_1(n2_to_4_latched_1__10), .in_2(n2_to_4_1__01), .in_3(n2_to_4_2__00), .in_4(1'b1),
    .out_5(n4_zand_6_out_5));
  _4_ZAND u_4_zand_7 (
    .in_1(n2_to_4_latched_1__01), .in_2(n2_to_4_1__01), .in_3(n2_to_4_2__00), .in_4(1'b1),
    .out_5(n4_zand_7_out_5));
  _4_ZAND u_4_zand_8 (
    .in_1(n2_to_4_latched_1__11), .in_2(n2_to_4_1__01), .in_3(n2_to_4_2__00), .in_4(1'b1),
    .out_5(n4_zand_8_out_5));
  _4_ZAND u_4_zand_9 (
    .in_1(n2_to_4_latched_1__00), .in_2(n2_to_4_1__10), .in_3(n2_to_4_2__00), .in_4(1'b1),
    .out_5(n4_zand_9_out_5));
  _4_ZAND u_4_zand_10 (
    .in_1(n2_to_4_latched_1__10), .in_2(n2_to_4_1__10), .in_3(n2_to_4_2__00), .in_4(1'b1),
    .out_5(n4_zand_10_out_5));
  _4_ZAND u_4_zand_11 (
    .in_1(n2_to_4_latched_1__01), .in_2(n2_to_4_1__10), .in_3(n2_to_4_2__00), .in_4(1'b1),
    .out_5(n4_zand_11_out_5));
  _4_ZAND u_4_zand_12 (
    .in_1(n2_to_4_latched_1__11), .in_2(n2_to_4_1__10), .in_3(n2_to_4_2__00), .in_4(1'b1),
    .out_5(n4_zand_12_out_5));
  _4_ZAND u_4_zand_13 (
    .in_1(n2_to_4_latched_1__00), .in_2(n2_to_4_1__11), .in_3(n2_to_4_2__00), .in_4(1'b1),
    .out_5(n4_zand_13_out_5));
  _4_ZAND u_4_zand_14 (
    .in_1(n2_to_4_latched_1__10), .in_2(n2_to_4_1__11), .in_3(n2_to_4_2__00), .in_4(1'b1),
    .out_5(n4_zand_14_out_5));
  _4_ZAND u_4_zand_15 (
    .in_1(n2_to_4_latched_1__01), .in_2(n2_to_4_1__11), .in_3(n2_to_4_2__00), .in_4(1'b1),
    .out_5(n4_zand_15_out_5));
  _4_ZAND u_4_zand_16 (
    .in_1(n2_to_4_latched_1__11), .in_2(n2_to_4_1__11), .in_3(n2_to_4_2__00), .in_4(1'b1),
    .out_5(n4_zand_16_out_5));
  _4_ZAND u_4_zand_17 (
    .in_1(n2_to_4_latched_1__00), .in_2(n2_to_4_1__00), .in_3(n2_to_4_2__01), .in_4(1'b1),
    .out_5(n4_zand_17_out_5));
  _4_ZAND u_4_zand_18 (
    .in_1(n2_to_4_latched_1__10), .in_2(n2_to_4_1__00), .in_3(n2_to_4_2__01), .in_4(1'b1),
    .out_5(n4_zand_18_out_5));
  _4_ZAND u_4_zand_19 (
    .in_1(n2_to_4_latched_1__01), .in_2(n2_to_4_1__00), .in_3(n2_to_4_2__01), .in_4(1'b1),
    .out_5(n4_zand_19_out_5));
  _4_ZAND u_4_zand_20 (
    .in_1(n2_to_4_latched_1__11), .in_2(n2_to_4_1__00), .in_3(n2_to_4_2__01), .in_4(1'b1),
    .out_5(n4_zand_20_out_5));
  _4_ZAND u_4_zand_21 (
    .in_1(n2_to_4_latched_1__00), .in_2(n2_to_4_1__00), .in_3(n2_to_4_2__01), .in_4(1'b1),
    .out_5(n4_zand_21_out_5));
  _4_ZAND u_4_zand_22 (
    .in_1(n2_to_4_latched_1__10), .in_2(n2_to_4_1__00), .in_3(n2_to_4_2__01), .in_4(1'b1),
    .out_5(n4_zand_22_out_5));
  _4_ZAND u_4_zand_23 (
    .in_1(n2_to_4_latched_1__01), .in_2(n2_to_4_1__00), .in_3(n2_to_4_2__01), .in_4(1'b1),
    .out_5(n4_zand_23_out_5));
  _4_ZAND u_4_zand_24 (
    .in_1(n2_to_4_latched_1__11), .in_2(n2_to_4_1__00), .in_3(n2_to_4_2__01), .in_4(1'b1),
    .out_5(n4_zand_24_out_5));
  _4_ZAND u_4_zand_25 (
    .in_1(n2_to_4_latched_1__00), .in_2(n2_to_4_1__10), .in_3(n2_to_4_2__01), .in_4(1'b1),
    .out_5(n4_zand_25_out_5));
  _4_ZAND u_4_zand_26 (
    .in_1(n2_to_4_latched_1__10), .in_2(n2_to_4_1__10), .in_3(n2_to_4_2__01), .in_4(1'b1),
    .out_5(n4_zand_26_out_5));
  _4_ZAND u_4_zand_27 (
    .in_1(n2_to_4_latched_1__01), .in_2(n2_to_4_1__10), .in_3(n2_to_4_2__01), .in_4(1'b1),
    .out_5(n4_zand_27_out_5));
  _4_ZAND u_4_zand_28 (
    .in_1(n2_to_4_latched_1__11), .in_2(n2_to_4_1__10), .in_3(n2_to_4_2__01), .in_4(1'b1),
    .out_5(n4_zand_28_out_5));
  _4_ZAND u_4_zand_29 (
    .in_1(n2_to_4_latched_1__00), .in_2(n2_to_4_1__11), .in_3(n2_to_4_2__01), .in_4(1'b1),
    .out_5(n4_zand_29_out_5));
  _4_ZAND u_4_zand_30 (
    .in_1(n2_to_4_latched_1__10), .in_2(n2_to_4_1__11), .in_3(n2_to_4_2__01), .in_4(1'b1),
    .out_5(n4_zand_30_out_5));
  _4_ZAND u_4_zand_31 (
    .in_1(n2_to_4_latched_1__01), .in_2(n2_to_4_1__11), .in_3(n2_to_4_2__01), .in_4(1'b1),
    .out_5(n4_zand_31_out_5));
  _4_ZAND u_4_zand_32 (
    .in_1(n2_to_4_latched_1__11), .in_2(n2_to_4_1__11), .in_3(n2_to_4_2__01), .in_4(1'b1),
    .out_5(n4_zand_32_out_5));
  Cell_Array cell_array_1 (
    .ROW_0(n4_zand_1_out_5), ._0(undriven), ._0_2(undriven_2), ._1(undriven_3), ._1_2(undriven_4),
    ._2(undriven_5), ._2_2(undriven_6), ._3(undriven_7), ._3_2(undriven_8), ._4(undriven_9),
    ._4_2(undriven_10), ._5(undriven_11), ._5_2(undriven_12), ._6(undriven_13), ._6_2(undriven_14),
    ._7(undriven_15), ._7_2(undriven_16), .ROW_1(n4_zand_3_out_5), .ROW_2(n4_zand_2_out_5),
    .ROW_3(n4_zand_4_out_5), .ROW_4(n4_zand_5_out_5), .ROW_5(n4_zand_7_out_5), .ROW_6(n4_zand_6_out_5),
    .ROW_7(n4_zand_8_out_5));
  Cell_Array cell_array_2 (
    .ROW_0(n4_zand_9_out_5), ._0(undriven), ._0_2(undriven_2), ._1(undriven_3), ._1_2(undriven_4),
    ._2(undriven_5), ._2_2(undriven_6), ._3(undriven_7), ._3_2(undriven_8), ._4(undriven_9),
    ._4_2(undriven_10), ._5(undriven_11), ._5_2(undriven_12), ._6(undriven_13), ._6_2(undriven_14),
    ._7(undriven_15), ._7_2(undriven_16), .ROW_1(n4_zand_11_out_5), .ROW_2(n4_zand_10_out_5),
    .ROW_3(n4_zand_12_out_5), .ROW_4(n4_zand_13_out_5), .ROW_5(n4_zand_15_out_5), .ROW_6(n4_zand_14_out_5),
    .ROW_7(n4_zand_16_out_5));
  Cell_Array cell_array_3 (
    .ROW_0(n4_zand_17_out_5), ._0(undriven), ._0_2(undriven_2), ._1(undriven_3), ._1_2(undriven_4),
    ._2(undriven_5), ._2_2(undriven_6), ._3(undriven_7), ._3_2(undriven_8), ._4(undriven_9),
    ._4_2(undriven_10), ._5(undriven_11), ._5_2(undriven_12), ._6(undriven_13), ._6_2(undriven_14),
    ._7(undriven_15), ._7_2(undriven_16), .ROW_1(n4_zand_19_out_5), .ROW_2(n4_zand_18_out_5),
    .ROW_3(n4_zand_20_out_5), .ROW_4(n4_zand_21_out_5), .ROW_5(n4_zand_23_out_5), .ROW_6(n4_zand_22_out_5),
    .ROW_7(n4_zand_24_out_5));
  Cell_Array cell_array_4 (
    .ROW_0(n4_zand_25_out_5), ._0(undriven), ._0_2(undriven_2), ._1(undriven_3), ._1_2(undriven_4),
    ._2(undriven_5), ._2_2(undriven_6), ._3(undriven_7), ._3_2(undriven_8), ._4(undriven_9),
    ._4_2(undriven_10), ._5(undriven_11), ._5_2(undriven_12), ._6(undriven_13), ._6_2(undriven_14),
    ._7(undriven_15), ._7_2(undriven_16), .ROW_1(n4_zand_27_out_5), .ROW_2(n4_zand_26_out_5),
    .ROW_3(n4_zand_28_out_5), .ROW_4(n4_zand_29_out_5), .ROW_5(n4_zand_31_out_5), .ROW_6(n4_zand_30_out_5),
    .ROW_7(n4_zand_32_out_5));
  Cell_Array cell_array_5 (
    .ROW_0(n4_zand_1_out_5), ._0(undriven_17), ._0_2(undriven_18), ._1(undriven_19), ._1_2(undriven_20),
    ._2(undriven_21), ._2_2(undriven_22), ._3(undriven_23), ._3_2(undriven_24), ._4(undriven_25),
    ._4_2(undriven_26), ._5(undriven_27), ._5_2(undriven_28), ._6(undriven_29), ._6_2(undriven_30),
    ._7(undriven_31), ._7_2(undriven_32), .ROW_1(n4_zand_3_out_5), .ROW_2(n4_zand_2_out_5),
    .ROW_3(n4_zand_4_out_5), .ROW_4(n4_zand_5_out_5), .ROW_5(n4_zand_7_out_5), .ROW_6(n4_zand_6_out_5),
    .ROW_7(n4_zand_8_out_5));
  Cell_Array cell_array_6 (
    .ROW_0(n4_zand_9_out_5), ._0(undriven_17), ._0_2(undriven_18), ._1(undriven_19), ._1_2(undriven_20),
    ._2(undriven_21), ._2_2(undriven_22), ._3(undriven_23), ._3_2(undriven_24), ._4(undriven_25),
    ._4_2(undriven_26), ._5(undriven_27), ._5_2(undriven_28), ._6(undriven_29), ._6_2(undriven_30),
    ._7(undriven_31), ._7_2(undriven_32), .ROW_1(n4_zand_11_out_5), .ROW_2(n4_zand_10_out_5),
    .ROW_3(n4_zand_12_out_5), .ROW_4(n4_zand_13_out_5), .ROW_5(n4_zand_15_out_5), .ROW_6(n4_zand_14_out_5),
    .ROW_7(n4_zand_16_out_5));
  Cell_Array cell_array_7 (
    .ROW_0(n4_zand_17_out_5), ._0(undriven_17), ._0_2(undriven_18), ._1(undriven_19), ._1_2(undriven_20),
    ._2(undriven_21), ._2_2(undriven_22), ._3(undriven_23), ._3_2(undriven_24), ._4(undriven_25),
    ._4_2(undriven_26), ._5(undriven_27), ._5_2(undriven_28), ._6(undriven_29), ._6_2(undriven_30),
    ._7(undriven_31), ._7_2(undriven_32), .ROW_1(n4_zand_19_out_5), .ROW_2(n4_zand_18_out_5),
    .ROW_3(n4_zand_20_out_5), .ROW_4(n4_zand_21_out_5), .ROW_5(n4_zand_23_out_5), .ROW_6(n4_zand_22_out_5),
    .ROW_7(n4_zand_24_out_5));
  Cell_Array cell_array_8 (
    .ROW_0(n4_zand_25_out_5), ._0(undriven_17), ._0_2(undriven_18), ._1(undriven_19), ._1_2(undriven_20),
    ._2(undriven_21), ._2_2(undriven_22), ._3(undriven_23), ._3_2(undriven_24), ._4(undriven_25),
    ._4_2(undriven_26), ._5(undriven_27), ._5_2(undriven_28), ._6(undriven_29), ._6_2(undriven_30),
    ._7(undriven_31), ._7_2(undriven_32), .ROW_1(n4_zand_27_out_5), .ROW_2(n4_zand_26_out_5),
    .ROW_3(n4_zand_28_out_5), .ROW_4(n4_zand_29_out_5), .ROW_5(n4_zand_31_out_5), .ROW_6(n4_zand_30_out_5),
    .ROW_7(n4_zand_32_out_5));
  Cell_Array cell_array_9 (
    .ROW_0(n4_zand_1_out_5), ._0(undriven_33), ._0_2(undriven_34), ._1(undriven_35), ._1_2(undriven_36),
    ._2(undriven_37), ._2_2(undriven_38), ._3(undriven_39), ._3_2(undriven_40), ._4(undriven_41),
    ._4_2(undriven_42), ._5(undriven_43), ._5_2(undriven_44), ._6(undriven_45), ._6_2(undriven_46),
    ._7(undriven_47), ._7_2(undriven_48), .ROW_1(n4_zand_3_out_5), .ROW_2(n4_zand_2_out_5),
    .ROW_3(n4_zand_4_out_5), .ROW_4(n4_zand_5_out_5), .ROW_5(n4_zand_7_out_5), .ROW_6(n4_zand_6_out_5),
    .ROW_7(n4_zand_8_out_5));
  Cell_Array cell_array_10 (
    .ROW_0(n4_zand_9_out_5), ._0(undriven_33), ._0_2(undriven_34), ._1(undriven_35), ._1_2(undriven_36),
    ._2(undriven_37), ._2_2(undriven_38), ._3(undriven_39), ._3_2(undriven_40), ._4(undriven_41),
    ._4_2(undriven_42), ._5(undriven_43), ._5_2(undriven_44), ._6(undriven_45), ._6_2(undriven_46),
    ._7(undriven_47), ._7_2(undriven_48), .ROW_1(n4_zand_11_out_5), .ROW_2(n4_zand_10_out_5),
    .ROW_3(n4_zand_12_out_5), .ROW_4(n4_zand_13_out_5), .ROW_5(n4_zand_15_out_5), .ROW_6(n4_zand_14_out_5),
    .ROW_7(n4_zand_16_out_5));
  Cell_Array cell_array_11 (
    .ROW_0(n4_zand_17_out_5), ._0(undriven_33), ._0_2(undriven_34), ._1(undriven_35), ._1_2(undriven_36),
    ._2(undriven_37), ._2_2(undriven_38), ._3(undriven_39), ._3_2(undriven_40), ._4(undriven_41),
    ._4_2(undriven_42), ._5(undriven_43), ._5_2(undriven_44), ._6(undriven_45), ._6_2(undriven_46),
    ._7(undriven_47), ._7_2(undriven_48), .ROW_1(n4_zand_19_out_5), .ROW_2(n4_zand_18_out_5),
    .ROW_3(n4_zand_20_out_5), .ROW_4(n4_zand_21_out_5), .ROW_5(n4_zand_23_out_5), .ROW_6(n4_zand_22_out_5),
    .ROW_7(n4_zand_24_out_5));
  Cell_Array cell_array_12 (
    .ROW_0(n4_zand_25_out_5), ._0(undriven_33), ._0_2(undriven_34), ._1(undriven_35), ._1_2(undriven_36),
    ._2(undriven_37), ._2_2(undriven_38), ._3(undriven_39), ._3_2(undriven_40), ._4(undriven_41),
    ._4_2(undriven_42), ._5(undriven_43), ._5_2(undriven_44), ._6(undriven_45), ._6_2(undriven_46),
    ._7(undriven_47), ._7_2(undriven_48), .ROW_1(n4_zand_27_out_5), .ROW_2(n4_zand_26_out_5),
    .ROW_3(n4_zand_28_out_5), .ROW_4(n4_zand_29_out_5), .ROW_5(n4_zand_31_out_5), .ROW_6(n4_zand_30_out_5),
    .ROW_7(n4_zand_32_out_5));
  Cell_Array cell_array_13 (
    .ROW_0(n4_zand_1_out_5), ._0(undriven_49), ._0_2(undriven_50), ._1(undriven_51), ._1_2(undriven_52),
    ._2(undriven_53), ._2_2(undriven_54), ._3(undriven_55), ._3_2(undriven_56), ._4(undriven_57),
    ._4_2(undriven_58), ._5(undriven_59), ._5_2(undriven_60), ._6(undriven_61), ._6_2(undriven_62),
    ._7(undriven_63), ._7_2(undriven_64), .ROW_1(n4_zand_3_out_5), .ROW_2(n4_zand_2_out_5),
    .ROW_3(n4_zand_4_out_5), .ROW_4(n4_zand_5_out_5), .ROW_5(n4_zand_7_out_5), .ROW_6(n4_zand_6_out_5),
    .ROW_7(n4_zand_8_out_5));
  Cell_Array cell_array_14 (
    .ROW_0(n4_zand_9_out_5), ._0(undriven_49), ._0_2(undriven_50), ._1(undriven_51), ._1_2(undriven_52),
    ._2(undriven_53), ._2_2(undriven_54), ._3(undriven_55), ._3_2(undriven_56), ._4(undriven_57),
    ._4_2(undriven_58), ._5(undriven_59), ._5_2(undriven_60), ._6(undriven_61), ._6_2(undriven_62),
    ._7(undriven_63), ._7_2(undriven_64), .ROW_1(n4_zand_11_out_5), .ROW_2(n4_zand_10_out_5),
    .ROW_3(n4_zand_12_out_5), .ROW_4(n4_zand_13_out_5), .ROW_5(n4_zand_15_out_5), .ROW_6(n4_zand_14_out_5),
    .ROW_7(n4_zand_16_out_5));
  Cell_Array cell_array_15 (
    .ROW_0(n4_zand_17_out_5), ._0(undriven_49), ._0_2(undriven_50), ._1(undriven_51), ._1_2(undriven_52),
    ._2(undriven_53), ._2_2(undriven_54), ._3(undriven_55), ._3_2(undriven_56), ._4(undriven_57),
    ._4_2(undriven_58), ._5(undriven_59), ._5_2(undriven_60), ._6(undriven_61), ._6_2(undriven_62),
    ._7(undriven_63), ._7_2(undriven_64), .ROW_1(n4_zand_19_out_5), .ROW_2(n4_zand_18_out_5),
    .ROW_3(n4_zand_20_out_5), .ROW_4(n4_zand_21_out_5), .ROW_5(n4_zand_23_out_5), .ROW_6(n4_zand_22_out_5),
    .ROW_7(n4_zand_24_out_5));
  Cell_Array cell_array_16 (
    .ROW_0(n4_zand_25_out_5), ._0(undriven_49), ._0_2(undriven_50), ._1(undriven_51), ._1_2(undriven_52),
    ._2(undriven_53), ._2_2(undriven_54), ._3(undriven_55), ._3_2(undriven_56), ._4(undriven_57),
    ._4_2(undriven_58), ._5(undriven_59), ._5_2(undriven_60), ._6(undriven_61), ._6_2(undriven_62),
    ._7(undriven_63), ._7_2(undriven_64), .ROW_1(n4_zand_27_out_5), .ROW_2(n4_zand_26_out_5),
    .ROW_3(n4_zand_28_out_5), .ROW_4(n4_zand_29_out_5), .ROW_5(n4_zand_31_out_5), .ROW_6(n4_zand_30_out_5),
    .ROW_7(n4_zand_32_out_5));

  // Notes on the sheet:
  //   #RWC
  //   #BS4
  //   #BS5
  //   Column Select
  //   R5
  //   Row Select
  //   R5 Reserved for ICache
  //   CHECKOUT!!!!
  //   Column Latches
  //   Row Latches
  //   Byte Select Latches
  //   Reserved for ICache
  //   N.C.
  //   N.C.
endmodule

module Column_Select (
  input  RW,
  input  BS,
  input  nRWC,
  input  Y0,
  input  Y1,
  input  in,
  input  A0,
  input  A1,
  input  A2,
  output IE,
  output nIE,
  output out,
  output _0,
  output _0_2
);

  wire and_2_out, nand_1_out, nand_2_out, nand_3_out, nand_4_out, nand_5_out, nand_6_out, not_1_out,
       not_2_out, not_3_out, not_4_out, not_5_out, not_6_out, not_7_out, not_8_out, not_9_out, not_11_out,
       or_1_out, transistor_1_out, transistor_3_out;

  nand nand_1 (nand_1_out, RW, nand_2_out);
  nand nand_2 (nand_2_out, nand_1_out, nand_3_out);
  not not_1 (not_1_out, in);
  not not_2 (not_2_out, A0);
  not not_3 (not_3_out, A1);
  not not_4 (not_4_out, A2);
  not not_5 (not_5_out, RW);
  not not_6 (not_6_out, not_5_out);
  not not_7 (not_7_out, not_6_out);
  nand nand_3 (nand_3_out, nIE, not_8_out);
  not not_8 (not_8_out, nand_4_out);
  not not_9 (not_9_out, not_7_out);
  nand nand_4 (nand_4_out, nand_6_out, nand_5_out);
  Transistor #(.\type ("n"), .gate("br")) transistor_1 (.in(1'b1), .out(transistor_1_out), .gate(nand_3_out));
  Transistor #(.\type ("n"), .gate("br")) transistor_2 (.in(Y0), .out(transistor_1_out), .gate(nand_5_out));
  Transistor #(.\type ("n"), .gate("br")) transistor_3 (
    .in(transistor_1_out), .out(transistor_3_out), .gate(nand_3_out));
  nand nand_5 (nand_5_out, nand_4_out, nIE);
  nand nand_6 (nand_6_out, nand_2_out, transistor_3_out, transistor_1_out);
  and and_1 (nIE, nRWC, RW);
  Transistor #(.gate("br")) transistor_4 (.in(1'b1), .out(transistor_1_out), .gate(transistor_3_out));
  Transistor #(.\type ("n")) transistor_5 (.in(nIE), .out(transistor_1_out), .gate(transistor_3_out));
  not not_10 (IE, nIE);
  Transistor #(.gate("br")) transistor_6 (.in(1'b1), .out(transistor_3_out), .gate(transistor_1_out));
  Transistor #(.\type ("n")) transistor_7 (.in(nIE), .out(transistor_3_out), .gate(transistor_1_out));
  and and_2 (and_2_out, BS, nIE);
  Transistor #(.\type ("n"), .gate("br")) transistor_8 (
    .in(transistor_3_out), .out(transistor_1_out), .gate(nand_3_out));
  Transistor #(.\type ("n"), .gate("br")) transistor_9 (.in(1'b1), .out(transistor_3_out), .gate(nand_3_out));
  Transistor #(.\type ("n"), .gate("br")) transistor_10 (.in(Y1), .out(transistor_3_out), .gate(nand_5_out));
  or or_1 (or_1_out, not_9_out, nIE);
  not not_11 (not_11_out, transistor_3_out);
  not not_12 (out, not_11_out);

  // Notes on the sheet:
  //   RW_DELAY
  //   #IE
  //   IE
  //   BYTE_EN
  //   Y2
endmodule

module Output_Control (
  input  nRWC,
  input  RW,
  input  in_3,
  input  in_4,
  output LOAD_1,
  output LOAD_CELL
);

  wire and_1_out, nand_1_out, nand_2_out, nand_3_out, nand_5_out, not_1_out;

  nand nand_1 (nand_1_out, RW, nand_2_out);
  nand nand_2 (nand_2_out, nand_1_out, LOAD_1);
  and and_1 (and_1_out, nRWC, RW);
  nand nand_3 (nand_3_out, nand_5_out, LOAD_CELL);
  nand nand_4 (LOAD_CELL, nand_3_out, and_1_out);
  nand nand_5 (nand_5_out, nand_2_out, in_3, in_4);
  not not_1 (not_1_out, nand_3_out);
  nand nand_6 (LOAD_1, and_1_out, not_1_out);

  // Notes on the sheet:
  //   /S
  //   /R
  //   /R
  //   /S
endmodule

module Output_latch (
  input  in_1,
  input  in_2,
  input  RW
);

  Transistor #(.gate("br")) transistor_1 (.in(1'b1), .out(in_2), .gate(in_1));
  Transistor #(.\type ("n")) transistor_2 (.in(RW), .out(in_2), .gate(in_1));
  Transistor #(.gate("br")) transistor_3 (.in(1'b1), .out(in_1), .gate(in_2));
  Transistor #(.\type ("n")) transistor_4 (.in(RW), .out(in_1), .gate(in_2));
endmodule
